// Logisim project Leaderboard.circ as structural Verilog: 4 circuits, main circuit Leaderboard
module HEX2Dec (
  input  [15:0] in_1,
  output [3:0] num0,
  output [3:0] num1,
  output [3:0] num2,
  output [3:0] num3,
  output [3:0] num4
);

  wire [15:0] divider_1_out, divider_1_rem, divider_2_out, divider_2_rem, divider_3_out, divider_3_rem,
       divider_4_out, divider_4_rem, divider_5_rem;

  Divider #(.width(16)) divider_1 (.a(in_1), .b(16'ha), .out(divider_1_out), .rem(divider_1_rem));  // open: upper
  Divider #(.width(16)) divider_2 (
    .a(divider_1_out), .b(16'ha), .out(divider_2_out), .rem(divider_2_rem));  // open: upper
  Bit_Extender #(.in_width(16), .out_width(4)) bit_extender_1 (.in(divider_1_rem), .out(num0));
  Divider #(.width(16)) divider_3 (
    .a(divider_2_out), .b(16'ha), .out(divider_3_out), .rem(divider_3_rem));  // open: upper
  Bit_Extender #(.in_width(16), .out_width(4)) bit_extender_2 (.in(divider_2_rem), .out(num1));
  Divider #(.width(16)) divider_4 (
    .a(divider_3_out), .b(16'ha), .out(divider_4_out), .rem(divider_4_rem));  // open: upper
  Bit_Extender #(.in_width(16), .out_width(4)) bit_extender_3 (.in(divider_3_rem), .out(num2));
  Divider #(.width(16)) divider_5 (.a(divider_4_out), .b(16'ha), .rem(divider_5_rem));  // open: out, upper
  Bit_Extender #(.in_width(16), .out_width(4)) bit_extender_4 (.in(divider_4_rem), .out(num3));
  Bit_Extender #(.in_width(16), .out_width(4)) bit_extender_5 (.in(divider_5_rem), .out(num4));
endmodule

module Leaderboard (
  input  [13:0] recent_result,
  input  losesignal,
  input  tact,
  output [3:0] out_4,
  output [3:0] out_5,
  output [3:0] out_6,
  output [3:0] out_7,
  output [3:0] out_8,
  output [3:0] out_9,
  output [3:0] out_10,
  output [3:0] out_11,
  output [3:0] out_12,
  output [3:0] out_13,
  output [3:0] out_14,
  output [3:0] out_15,
  output [3:0] out_16,
  output [3:0] out_17,
  output [3:0] out_18,
  output [3:0] out_19,
  output [3:0] out_20,
  output [3:0] out_21,
  output [3:0] out_22,
  output [3:0] out_23
);

  wire and_2_out, and_3_out, cdm_8_mark5_1_p1, cdm_8_mark5_1_p3, cdm_8_mark5_1_p4, cdm_8_mark5_1_p6,
       cdm_8_mark5_1_p7, cdm_8_mark5_1_p9, cdm_8_mark5_1_p10, cdm_8_mark5_1_p11, cdm_8_mark5_1_p12, Cl,
       decoder_2_out0, decoder_2_out1, I_Osel, not_1_out, not_2_out, or_1_out, read, read_write, seloutput,
       write;
  wire [3:0] addr1hex, I_Oaddress;
  wire [7:0] cdm_8_mark5_1_p15, cdm_8_mark5_1_p16, controlled_buffer_4_out, I_Odata, \output , PCanchor,
       writetomemory_1_out_7;
  wire [15:0] bit_extender_1_out, bit_extender_2_out, bit_extender_3_out, leaderboardpanel_1_out_4,
       leaderboardpanel_1_out_10, leaderboardpanel_1_out_16, rct16, shifter_1_out;

  // Probe on cdm_8_mark5_1_p4
  // Probe on cdm_8_mark5_1_p3
  // Probe on cdm_8_mark5_1_p6
  and and_1 (I_Osel, seloutput, decoder_2_out1);
  // Probe on PCanchor
  // Probe on cdm_8_mark5_1_p7
  // Probe on cdm_8_mark5_1_p10
  // Probe on cdm_8_mark5_1_p9
  // CdM_8_mark5 cdm_8_mark5_1: pin names not known; wires that end beside it: cdm_8_mark5_1_p1, cdm_8_mark5_1_p1, cdm_8_mark5_1_p3, cdm_8_mark5_1_p4, Cl, cdm_8_mark5_1_p6, cdm_8_mark5_1_p7, PCanchor, cdm_8_mark5_1_p9, cdm_8_mark5_1_p10, cdm_8_mark5_1_p11, cdm_8_mark5_1_p12, read_write, {addr1hex, I_Oaddress}, cdm_8_mark5_1_p15, cdm_8_mark5_1_p16
  Decoder decoder_1 (.out0(read), .out1(write), .sel(read_write), .en(I_Osel));
  Pull_Resistor pull_resistor_1 (.node(read));
  Pull_Resistor pull_resistor_2 (.node(write));
  Decoder decoder_2 (.out0(decoder_2_out0), .out1(decoder_2_out1), .sel(cdm_8_mark5_1_p11), .en(cdm_8_mark5_1_p12));
  not not_1 (not_1_out, read_write);
  assign I_Odata = not_1_out ? cdm_8_mark5_1_p15 : 8'bz;  // Controlled_Buffer controlled_buffer_1
  assign cdm_8_mark5_1_p16 = read_write ? I_Odata : 8'bz;  // Controlled_Buffer controlled_buffer_2
  Demultiplexer #(.select(4), .enable("false")) demultiplexer_1 (
    .out15(seloutput), .in(1'b1), .sel(addr1hex));  // open: out0, out1, out2, out3, out4, out5, out6, out7, out8, out9, out10, out11, out12, out13, out14
  assign Cl = or_1_out ? tact : 1'bz;  // Controlled_Buffer controlled_buffer_3
  and and_2 (and_2_out, decoder_2_out1, I_Osel);
  or or_1 (or_1_out, ~and_3_out, losesignal);  // OR_Gate
  not not_2 (not_2_out, Cl);
  and and_3 (and_3_out, PCanchor[0], ~PCanchor[1], ~PCanchor[2], ~PCanchor[3], ~PCanchor[4], ~PCanchor[5], ~PCanchor[6], ~PCanchor[7]);  // AND_Gate
  ROM rom_1 (.addr({addr1hex, I_Oaddress}), .data(I_Odata), .sel(decoder_2_out0));
  RAM #(.bus("separate")) ram_1 (
    .addr({addr1hex, I_Oaddress}), .din(\output ), .data(I_Odata), .str(write), .sel(and_2_out),
    .clk(not_2_out), .ld(read_write));  // open: clr
  // Probe on I_Odata
  // Probe on {addr1hex, I_Oaddress}
  assign controlled_buffer_4_out = read ? I_Odata : 8'bz;  // Controlled_Buffer controlled_buffer_4
  // Probe on out_4
  // Probe on out_9
  // Probe on out_19
  // Probe on out_5
  // Probe on out_6
  // Probe on out_11
  // Probe on out_10
  // Probe on out_21
  // Probe on out_20
  LeaderboardPanel leaderboardpanel_1 (
    .in_1(controlled_buffer_4_out), .in_2({addr1hex, I_Oaddress}), .in_3(read), .out_5(out_4),
    .out_11(out_9), .out_17(out_19), .out_6(out_5), .out_12(out_10), .out_18(out_20), .out_7(out_6),
    .out_13(out_11), .out_19(out_21), .out_8(out_7), .out_14(out_12), .out_20(out_22), .out_9(out_8),
    .out_15(out_13), .out_21(out_23), .out_4(leaderboardpanel_1_out_4), .out_10(leaderboardpanel_1_out_10),
    .out_16(leaderboardpanel_1_out_16));
  // Probe on out_8
  // Probe on out_7
  // Probe on out_12
  // Probe on out_13
  // Probe on out_22
  // Probe on out_23
  assign bit_extender_1_out = {{8{1'b0}}, {1'b0, recent_result[6:0]}};  // Bit_Extender bit_extender_1
  assign bit_extender_2_out = {{8{1'b0}}, {1'b0, recent_result[13:7]}};  // Bit_Extender bit_extender_2
  assign \output  = write ? writetomemory_1_out_7 : 8'bz;  // Controlled_Buffer controlled_buffer_5
  WriteToMemory writetomemory_1 (
    .in_1({addr1hex, I_Oaddress}), .in_2(write), .top1(leaderboardpanel_1_out_4),
    .top2(leaderboardpanel_1_out_10), .top3(leaderboardpanel_1_out_16), .recent(rct16),
    .out_7(writetomemory_1_out_7));
  Adder #(.width(16)) adder_1 (.a(bit_extender_1_out), .b(shifter_1_out), .out(rct16));  // open: cin, cout
  Shifter #(.width(16)) shifter_1 (.in(bit_extender_2_out), .\dist (4'b1000), .out(shifter_1_out));
  assign bit_extender_3_out = {{2{1'b0}}, recent_result};  // Bit_Extender bit_extender_3
  // Probe on bit_extender_3_out
  HEX2Dec hex2dec_1 (
    .in_1(bit_extender_3_out), .num0(out_18), .num1(out_17), .num2(out_16), .num3(out_15), .num4(out_14));

  // Other names for the same wires on the sheet: rct14[13:0] = recent_result; I_Oaddress[7:4] = addr1hex;
  //   sendrct = losesignal

  // Notes on the sheet:
  //   contents of rom_1 (hex, n*v repeats v):
  //   c3 c7 d0 fa b0 a0 d0 fb b0 a0 d0 f4 b0 a0 d0 f5 b0 a0 d0 f6 b0 a0 d0 f7 b0 a0 d0 f8 b0 a0 d0 f9 b0
  //   a0 d6 24 c7 d0 f4 b0 d2 f5 ba d1 fa b5 71 e5 35 d6 a1 ee 4f 71 e1 4d d1 fb b5 79 e5 42 d6 a1 ee 4b
  //   79 e1 49 d6 1 ee 4b d6 4f ee 4f d6 4f c7 d0 f6 b0 d2 f7 ba d1 fa b5 71 e5 60 d6 c8 ee 7a 71 e1 78 d1
  //   fb b5 79 e5 6d d6 c8 ee 76 79 e1 74 d6 1 ee 76 d6 7a ee 7a d6 7a c7 d0 f8 b0 d2 f9 ba d1 fa b5 71 e5
  //   8b d6 e3 ee a1 71 e1 9f d1 fb b5 79 e5 98 d6 e3 ee 9d 79 e1 9d d6 1 ee a1 d6 1 c7 d0 f6 b0 d1 f8 a4
  //   d0 f7 b0 d1 f9 a4 d0 f4 b0 d1 f6 a4 d0 f5 b0 d1 f7 a4 d0 fa b0 d1 f4 a4 d0 fb b0 d1 f5 a4 d6 1 c7 d0
  //   f6 b0 d1 f8 a4 d0 f7 b0 d1 f9 a4 d0 fa b0 d1 f6 a4 d0 fb b0 d1 f7 a4 d6 1 c7 d0 fa b0 d1 f8 a4 d0 fb
  //   b0 d1 f9 a4 d6 1 d6 1
  //   Score display
endmodule

module LeaderboardPanel (
  input  [7:0] in_1,
  input  [7:0] in_2,
  input  in_3,
  output [15:0] out_4,
  output [3:0] out_5,
  output [3:0] out_6,
  output [3:0] out_7,
  output [3:0] out_8,
  output [3:0] out_9,
  output [15:0] out_10,
  output [3:0] out_11,
  output [3:0] out_12,
  output [3:0] out_13,
  output [3:0] out_14,
  output [3:0] out_15,
  output [15:0] out_16,
  output [3:0] out_17,
  output [3:0] out_18,
  output [3:0] out_19,
  output [3:0] out_20,
  output [3:0] out_21
);

  wire addrptr, and_1_out, enable1_0, enable1_1, enable2_0, enable2_1, enable3_0, enable3_1;
  wire [7:0] multiplexer_1_out, multiplexer_2_out, multiplexer_3_out, multiplexer_4_out, multiplexer_5_out,
       multiplexer_6_out, score1_0, score1_1, score2_0, score2_1, score3_0, score3_1;
  wire [15:0] adder_1_out, adder_2_out, adder_3_out, register_1_q, register_2_q, register_3_q, register_4_q,
       register_5_q, register_6_q, register_7_q, register_8_q, register_9_q, register_10_q, register_11_q,
       register_12_q, score1_0ext, score1_1ext, score2_0ext, score2_1ext, score3_0ext, score3_1ext,
       shifter_1_out, shifter_2_out, shifter_3_out, shifter_4_out, shifter_5_out, shifter_6_out;

  and and_1 (and_1_out, in_2[4], in_2[5], in_2[6], in_2[7]);
  and and_2 (addrptr, in_3, and_1_out);
  Demultiplexer #(.select(4), .width(8)) demultiplexer_1 (
    .out4(score1_0), .out5(score1_1), .out6(score2_0), .out7(score2_1), .out8(score3_0), .out9(score3_1),
    .in(in_1), .sel(in_2[3:0]), .en(in_3));  // open: out0, out1, out2, out3, out10, out11, out12, out13, out14, out15
  Demultiplexer #(.select(4)) demultiplexer_2 (
    .out4(enable1_0), .out5(enable1_1), .out6(enable2_0), .out7(enable2_1), .out8(enable3_0),
    .out9(enable3_1), .in(1'b1), .sel(in_2[3:0]), .en(in_3));  // open: out0, out1, out2, out3, out10, out11, out12, out13, out14, out15
  // Probe on score1_0
  // Probe on score1_1
  // Probe on score2_0
  // Probe on score2_1
  // Probe on score3_0
  // Probe on score3_1
  assign score1_0ext = {{8{1'b0}}, multiplexer_1_out};  // Bit_Extender bit_extender_1
  Multiplexer #(.width(8), .enable("false")) multiplexer_1 (
    .in0({8{1'b0}}), .in1(score1_0), .out(multiplexer_1_out), .sel(enable1_0));
  Multiplexer #(.width(8), .enable("false")) multiplexer_2 (
    .in0({8{1'b0}}), .in1(score1_1), .out(multiplexer_2_out), .sel(enable1_1));
  assign score1_1ext = {{8{1'b0}}, multiplexer_2_out};  // Bit_Extender bit_extender_2
  assign score2_0ext = {{8{1'b0}}, multiplexer_3_out};  // Bit_Extender bit_extender_3
  Multiplexer #(.width(8), .enable("false")) multiplexer_3 (
    .in0({8{1'b0}}), .in1(score2_0), .out(multiplexer_3_out), .sel(enable2_0));
  Multiplexer #(.width(8), .enable("false")) multiplexer_4 (
    .in0({8{1'b0}}), .in1(score2_1), .out(multiplexer_4_out), .sel(enable2_1));
  assign score2_1ext = {{8{1'b0}}, multiplexer_4_out};  // Bit_Extender bit_extender_4
  assign score3_0ext = {{8{1'b0}}, multiplexer_5_out};  // Bit_Extender bit_extender_5
  Multiplexer #(.width(8), .enable("false")) multiplexer_5 (
    .in0({8{1'b0}}), .in1(score3_0), .out(multiplexer_5_out), .sel(enable3_0));
  Multiplexer #(.width(8), .enable("false")) multiplexer_6 (
    .in0({8{1'b0}}), .in1(score3_1), .out(multiplexer_6_out), .sel(enable3_1));
  assign score3_1ext = {{8{1'b0}}, multiplexer_6_out};  // Bit_Extender bit_extender_6
  Shifter #(.width(16)) shifter_1 (.in(score1_0ext), .\dist (4'b0111), .out(shifter_1_out));
  Shifter #(.width(16)) shifter_2 (.in(score2_0ext), .\dist (4'b0111), .out(shifter_2_out));
  Shifter #(.width(16)) shifter_3 (.in(score3_0ext), .\dist (4'b0111), .out(shifter_3_out));
  Register #(.width(16), .trigger("high")) register_1 (
    .D(shifter_1_out), .Q(register_1_q), .clk(enable1_0));  // open: en, clr
  Adder #(.width(16)) adder_1 (.a(register_1_q), .b(register_2_q), .out(adder_1_out));  // open: cin, cout
  Register #(.width(16), .trigger("high")) register_2 (
    .D(score1_1ext), .Q(register_2_q), .clk(enable1_1));  // open: en, clr
  Register #(.width(16), .trigger("high")) register_3 (
    .D(shifter_2_out), .Q(register_3_q), .clk(enable2_0));  // open: en, clr
  Adder #(.width(16)) adder_2 (.a(register_3_q), .b(register_4_q), .out(adder_2_out));  // open: cin, cout
  Register #(.width(16), .trigger("high")) register_4 (
    .D(score2_1ext), .Q(register_4_q), .clk(enable2_1));  // open: en, clr
  Register #(.width(16), .trigger("high")) register_5 (
    .D(shifter_3_out), .Q(register_5_q), .clk(enable3_0));  // open: en, clr
  Adder #(.width(16)) adder_3 (.a(register_5_q), .b(register_6_q), .out(adder_3_out));  // open: cin, cout
  Register #(.width(16), .trigger("high")) register_6 (
    .D(score3_1ext), .Q(register_6_q), .clk(enable3_1));  // open: en, clr
  HEX2Dec hex2dec_1 (.in_1(adder_1_out), .num0(out_9), .num1(out_8), .num2(out_7), .num3(out_6), .num4(out_5));
  HEX2Dec hex2dec_2 (.in_1(adder_2_out), .num0(out_15), .num1(out_14), .num2(out_13), .num3(out_12), .num4(out_11));
  HEX2Dec hex2dec_3 (.in_1(adder_3_out), .num0(out_21), .num1(out_20), .num2(out_19), .num3(out_18), .num4(out_17));
  Shifter #(.width(16)) shifter_4 (.in(score1_0ext), .\dist (4'b1000), .out(shifter_4_out));
  Shifter #(.width(16)) shifter_5 (.in(score2_0ext), .\dist (4'b1000), .out(shifter_5_out));
  Shifter #(.width(16)) shifter_6 (.in(score3_0ext), .\dist (4'b1000), .out(shifter_6_out));
  Register #(.width(16), .trigger("high")) register_7 (
    .D(shifter_4_out), .Q(register_7_q), .clk(enable1_0));  // open: en, clr
  Register #(.width(16), .trigger("high")) register_8 (
    .D(score1_1ext), .Q(register_8_q), .clk(enable1_1));  // open: en, clr
  Register #(.width(16), .trigger("high")) register_9 (
    .D(shifter_5_out), .Q(register_9_q), .clk(enable2_0));  // open: en, clr
  Register #(.width(16), .trigger("high")) register_10 (
    .D(score2_1ext), .Q(register_10_q), .clk(enable2_1));  // open: en, clr
  Register #(.width(16), .trigger("high")) register_11 (
    .D(shifter_6_out), .Q(register_11_q), .clk(enable3_0));  // open: en, clr
  Register #(.width(16), .trigger("high")) register_12 (
    .D(score3_1ext), .Q(register_12_q), .clk(enable3_1));  // open: en, clr
  Adder #(.width(16)) adder_4 (.a(register_7_q), .b(register_8_q), .out(out_4));  // open: cin, cout
  Adder #(.width(16)) adder_5 (.a(register_9_q), .b(register_10_q), .out(out_10));  // open: cin, cout
  Adder #(.width(16)) adder_6 (.a(register_11_q), .b(register_12_q), .out(out_16));  // open: cin, cout

  // Other names for the same wires on the sheet: address[7:0] = in_2; read = in_3; score[7:0] = in_1
endmodule

module WriteToMemory (
  input  [7:0] in_1,
  input  in_2,
  input  [15:0] top1,
  input  [15:0] top2,
  input  [15:0] top3,
  input  [15:0] recent,
  output [7:0] out_7
);

  wire addrptr, and_1_out, defineByte1, defineByte2, defineByte3, defineByteRct, demultiplexer_1_out5,
       demultiplexer_1_out7, demultiplexer_1_out9, demultiplexer_1_out11, enable1, enable2, enable3,
       enablerct, recentptr, top1ptr, top2ptr, top3ptr;
  wire [7:0] bitselector_1_out, bitselector_2_out, bitselector_3_out, bitselector_4_out, register_1_q,
       register_2_q, register_3_q, register_4_q;

  Demultiplexer #(.select(4), .enable("false")) demultiplexer_1 (
    .out4(defineByte1), .out5(demultiplexer_1_out5), .out6(defineByte2), .out7(demultiplexer_1_out7),
    .out8(defineByte3), .out9(demultiplexer_1_out9), .out10(defineByteRct), .out11(demultiplexer_1_out11),
    .in(1'b1), .sel(in_1[3:0]));  // open: out0, out1, out2, out3, out12, out13, out14, out15
  or or_1 (top1ptr, defineByte1, demultiplexer_1_out5);
  and and_1 (and_1_out, in_1[7], in_1[6], in_1[5], in_1[4]);
  and and_2 (addrptr, and_1_out, in_2);
  or or_2 (top2ptr, defineByte2, demultiplexer_1_out7);
  or or_3 (top3ptr, defineByte3, demultiplexer_1_out9);
  or or_4 (recentptr, defineByteRct, demultiplexer_1_out11);
  and and_3 (enable1, top1ptr, in_2);
  and and_4 (enable2, top2ptr, in_2);
  BitSelector #(.width(16), .group(8)) bitselector_1 (.in(top1), .out(bitselector_1_out), .sel(defineByte1));
  BitSelector #(.width(16), .group(8)) bitselector_2 (.in(top2), .out(bitselector_2_out), .sel(defineByte2));
  BitSelector #(.width(16), .group(8)) bitselector_3 (.in(top3), .out(bitselector_3_out), .sel(defineByte3));
  BitSelector #(.width(16), .group(8)) bitselector_4 (.in(recent), .out(bitselector_4_out), .sel(defineByteRct));
  Register register_1 (.D(bitselector_1_out), .Q(register_1_q), .clk(enable1));  // open: en, clr
  assign out_7 = enable1 ? register_1_q : 8'bz;  // Controlled_Buffer controlled_buffer_1
  assign out_7 = enable2 ? register_2_q : 8'bz;  // Controlled_Buffer controlled_buffer_2
  Register register_2 (.D(bitselector_2_out), .Q(register_2_q), .clk(enable2));  // open: en, clr
  assign out_7 = enable3 ? register_3_q : 8'bz;  // Controlled_Buffer controlled_buffer_3
  Register register_3 (.D(bitselector_3_out), .Q(register_3_q), .clk(enable3));  // open: en, clr
  assign out_7 = enablerct ? register_4_q : 8'bz;  // Controlled_Buffer controlled_buffer_4
  Register register_4 (.D(bitselector_4_out), .Q(register_4_q), .clk(enablerct));  // open: en, clr
  and and_5 (enable3, top3ptr, in_2);
  and and_6 (enablerct, recentptr, in_2);

  // Other names for the same wires on the sheet: address[7:0] = in_1; write = in_2
endmodule
