// Logisim project TheFall.circ as structural Verilog: 9 circuits, main circuit StartScreen
module StartScreen (
);

  // IntroductionScreen introductionscreen_1: pin names not known
endmodule

module Game (
);

  wire maincontroller_1_lose_east, maincontroller_1_lose_upper, maincontroller_1_pause,
       maincontroller_1_start, maincontroller_1_tact_2;
  wire [3:0] leaderboard_1_p3, leaderboard_1_p4, leaderboard_1_p5, leaderboard_1_p6, leaderboard_1_p7,
       leaderboard_1_p8, leaderboard_1_p9, leaderboard_1_p10, leaderboard_1_p11, leaderboard_1_p12,
       leaderboard_1_p13, leaderboard_1_p14, leaderboard_1_p15, leaderboard_1_p16, leaderboard_1_p17,
       leaderboard_1_p18, leaderboard_1_p19, leaderboard_1_p20, leaderboard_1_p21, leaderboard_1_p22;
  wire [6:0] keyboard_1_data;
  wire [13:0] maincontroller_1_score;
  wire [29:0] maincontroller_1_out_43, maincontroller_1_out_44, maincontroller_1_out_45,
       maincontroller_1_out_46, maincontroller_1_out_47, maincontroller_1_out_48, maincontroller_1_out_49,
       maincontroller_1_out_50, maincontroller_1_out_51, maincontroller_1_out_52, maincontroller_1_out_53,
       maincontroller_1_out_54, maincontroller_1_out_55, maincontroller_1_out_56, maincontroller_1_out_57,
       maincontroller_1_out_58, maincontroller_1_out_59, maincontroller_1_out_60, maincontroller_1_out_61,
       maincontroller_1_out_62, maincontroller_1_out_63, maincontroller_1_out_64, maincontroller_1_out_65,
       maincontroller_1_out_66, maincontroller_1_out_67, maincontroller_1_out_68, maincontroller_1_out_69,
       maincontroller_1_out_70, maincontroller_1_out_71, maincontroller_1_out_72, maincontroller_1_out_73,
       maincontroller_1_out_74;
  wire [31:0] gsc_1_out_4, gsc_1_out_5, gsc_1_out_6, gsc_1_out_7, gsc_1_out_8, gsc_1_out_9, gsc_1_out_10,
       maincontroller_1_out_7, maincontroller_1_out_8, maincontroller_1_out_9, maincontroller_1_out_10,
       maincontroller_1_out_12, maincontroller_1_out_13, maincontroller_1_out_14, maincontroller_1_out_15,
       maincontroller_1_out_16, maincontroller_1_out_17, maincontroller_1_out_18, maincontroller_1_out_19,
       maincontroller_1_out_20, maincontroller_1_out_21, maincontroller_1_out_22, maincontroller_1_out_23,
       maincontroller_1_out_24, maincontroller_1_out_25, maincontroller_1_out_26, maincontroller_1_out_27,
       maincontroller_1_out_28, maincontroller_1_out_29, maincontroller_1_out_30, maincontroller_1_out_31,
       maincontroller_1_out_32, maincontroller_1_out_33, maincontroller_1_out_34, maincontroller_1_out_35,
       maincontroller_1_out_36, maincontroller_1_out_37, maincontroller_1_out_38, maincontroller_1_out_39;

  DotMatrix #(.inputtype("row"), .matrixcols(32)) dotmatrix_1 (
    .row0(gsc_1_out_4), .row1(gsc_1_out_5), .row2(gsc_1_out_6), .row3(gsc_1_out_7), .row4(gsc_1_out_8),
    .row5(gsc_1_out_9), .row6(gsc_1_out_10));
  GSC gsc_1 (
    .Lose_indicator(maincontroller_1_lose_upper), .Start(maincontroller_1_start),
    .Pause(maincontroller_1_pause), .out_4(gsc_1_out_4), .out_5(gsc_1_out_5), .out_6(gsc_1_out_6),
    .out_7(gsc_1_out_7), .out_8(gsc_1_out_8), .out_9(gsc_1_out_9), .out_10(gsc_1_out_10));
  DotMatrix #(.inputtype("row"), .matrixcols(30), .matrixrows(32), .dotshape("circle")) dotmatrix_2 (
    .row0(maincontroller_1_out_74), .row1(maincontroller_1_out_70), .row2(maincontroller_1_out_66),
    .row3(maincontroller_1_out_62), .row4(maincontroller_1_out_58), .row5(maincontroller_1_out_54),
    .row6(maincontroller_1_out_50), .row7(maincontroller_1_out_46), .row8(maincontroller_1_out_73),
    .row9(maincontroller_1_out_69), .row10(maincontroller_1_out_65), .row11(maincontroller_1_out_61),
    .row12(maincontroller_1_out_57), .row13(maincontroller_1_out_53), .row14(maincontroller_1_out_49),
    .row15(maincontroller_1_out_45), .row16(maincontroller_1_out_72), .row17(maincontroller_1_out_68),
    .row18(maincontroller_1_out_64), .row19(maincontroller_1_out_60), .row20(maincontroller_1_out_56),
    .row21(maincontroller_1_out_52), .row22(maincontroller_1_out_48), .row23(maincontroller_1_out_44),
    .row24(maincontroller_1_out_71), .row25(maincontroller_1_out_67), .row26(maincontroller_1_out_63),
    .row27(maincontroller_1_out_59), .row28(maincontroller_1_out_55), .row29(maincontroller_1_out_51),
    .row30(maincontroller_1_out_47), .row31(maincontroller_1_out_43));
  DotMatrix #(.inputtype("row"), .matrixcols(32), .matrixrows(32)) dotmatrix_3 (
    .row0(maincontroller_1_out_39), .row1(maincontroller_1_out_35), .row2(maincontroller_1_out_31),
    .row3(maincontroller_1_out_27), .row4(maincontroller_1_out_23), .row5(maincontroller_1_out_19),
    .row6(maincontroller_1_out_15), .row7(maincontroller_1_out_10), .row8(maincontroller_1_out_38),
    .row9(maincontroller_1_out_34), .row10(maincontroller_1_out_30), .row11(maincontroller_1_out_26),
    .row12(maincontroller_1_out_22), .row13(maincontroller_1_out_18), .row14(maincontroller_1_out_14),
    .row15(maincontroller_1_out_9), .row16(maincontroller_1_out_37), .row17(maincontroller_1_out_33),
    .row18(maincontroller_1_out_29), .row19(maincontroller_1_out_25), .row20(maincontroller_1_out_21),
    .row21(maincontroller_1_out_17), .row22(maincontroller_1_out_13), .row23(maincontroller_1_out_8),
    .row24(maincontroller_1_out_36), .row25(maincontroller_1_out_32), .row26(maincontroller_1_out_28),
    .row27(maincontroller_1_out_24), .row28(maincontroller_1_out_20), .row29(maincontroller_1_out_16),
    .row30(maincontroller_1_out_12), .row31(maincontroller_1_out_7));
  // DotMatrix #(.inputtype("select"), .matrixcols(31), .matrixrows(32)) dotmatrix_4: pin names not known
  MainController maincontroller_1 (
    .out_7(maincontroller_1_out_7), .out_12(maincontroller_1_out_12), .out_16(maincontroller_1_out_16),
    .out_20(maincontroller_1_out_20), .out_24(maincontroller_1_out_24), .out_28(maincontroller_1_out_28),
    .out_32(maincontroller_1_out_32), .out_36(maincontroller_1_out_36), .out_8(maincontroller_1_out_8),
    .out_13(maincontroller_1_out_13), .out_17(maincontroller_1_out_17), .out_21(maincontroller_1_out_21),
    .out_25(maincontroller_1_out_25), .out_29(maincontroller_1_out_29), .out_33(maincontroller_1_out_33),
    .out_37(maincontroller_1_out_37), .out_9(maincontroller_1_out_9), .out_14(maincontroller_1_out_14),
    .out_18(maincontroller_1_out_18), .out_22(maincontroller_1_out_22), .out_26(maincontroller_1_out_26),
    .out_30(maincontroller_1_out_30), .out_34(maincontroller_1_out_34), .out_38(maincontroller_1_out_38),
    .out_10(maincontroller_1_out_10), .out_15(maincontroller_1_out_15), .out_19(maincontroller_1_out_19),
    .out_23(maincontroller_1_out_23), .out_27(maincontroller_1_out_27), .out_31(maincontroller_1_out_31),
    .out_35(maincontroller_1_out_35), .out_39(maincontroller_1_out_39), .out_43(maincontroller_1_out_43),
    .out_47(maincontroller_1_out_47), .out_51(maincontroller_1_out_51), .out_55(maincontroller_1_out_55),
    .out_59(maincontroller_1_out_59), .out_63(maincontroller_1_out_63), .out_67(maincontroller_1_out_67),
    .out_71(maincontroller_1_out_71), .out_48(maincontroller_1_out_48), .out_52(maincontroller_1_out_52),
    .out_56(maincontroller_1_out_56), .out_60(maincontroller_1_out_60), .out_64(maincontroller_1_out_64),
    .out_68(maincontroller_1_out_68), .out_72(maincontroller_1_out_72), .out_44(maincontroller_1_out_44),
    .out_45(maincontroller_1_out_45), .out_49(maincontroller_1_out_49), .out_53(maincontroller_1_out_53),
    .out_57(maincontroller_1_out_57), .out_61(maincontroller_1_out_61), .out_65(maincontroller_1_out_65),
    .out_69(maincontroller_1_out_69), .out_73(maincontroller_1_out_73), .out_46(maincontroller_1_out_46),
    .out_50(maincontroller_1_out_50), .out_54(maincontroller_1_out_54), .out_58(maincontroller_1_out_58),
    .out_62(maincontroller_1_out_62), .out_66(maincontroller_1_out_66), .out_70(maincontroller_1_out_70),
    .out_74(maincontroller_1_out_74), .score(maincontroller_1_score), .keyboard(keyboard_1_data),
    .Lose_upper(maincontroller_1_lose_upper), .Start(maincontroller_1_start), .Pause(maincontroller_1_pause),
    .Lose_east(maincontroller_1_lose_east), .tact_2(maincontroller_1_tact_2));  // open: out_4, out_5, tact
  // KeyboardScreen keyboardscreen_1: pin names not known
  Keyboard #(.buflen(2)) keyboard_1 (.clk(maincontroller_1_tact_2), .data(keyboard_1_data));  // open: re, clr, avail
  Hex_Digit_Display hex_digit_display_1 (.value(leaderboard_1_p3));  // open: dp
  Hex_Digit_Display hex_digit_display_2 (.value(leaderboard_1_p4));  // open: dp
  Hex_Digit_Display hex_digit_display_3 (.value(leaderboard_1_p6));  // open: dp
  Hex_Digit_Display hex_digit_display_4 (.value(leaderboard_1_p5));  // open: dp
  // Leaderboard leaderboard_1: pin names not known; wires that end beside it: maincontroller_1_lose_east, maincontroller_1_score, leaderboard_1_p3, leaderboard_1_p4, leaderboard_1_p5, leaderboard_1_p6, leaderboard_1_p7, leaderboard_1_p8, leaderboard_1_p9, leaderboard_1_p10, leaderboard_1_p11, leaderboard_1_p12, leaderboard_1_p13, leaderboard_1_p14, leaderboard_1_p15, leaderboard_1_p16, leaderboard_1_p17, leaderboard_1_p18, leaderboard_1_p19, leaderboard_1_p20, leaderboard_1_p21, leaderboard_1_p22
  Hex_Digit_Display hex_digit_display_5 (.value(leaderboard_1_p7));  // open: dp
  Hex_Digit_Display hex_digit_display_6 (.value(leaderboard_1_p8));  // open: dp
  Hex_Digit_Display hex_digit_display_7 (.value(leaderboard_1_p9));  // open: dp
  Hex_Digit_Display hex_digit_display_8 (.value(leaderboard_1_p10));  // open: dp
  Hex_Digit_Display hex_digit_display_9 (.value(leaderboard_1_p14));  // open: dp
  Hex_Digit_Display hex_digit_display_10 (.value(leaderboard_1_p11));  // open: dp
  Hex_Digit_Display hex_digit_display_11 (.value(leaderboard_1_p12));  // open: dp
  Hex_Digit_Display hex_digit_display_12 (.value(leaderboard_1_p15));  // open: dp
  Hex_Digit_Display hex_digit_display_13 (.value(leaderboard_1_p13));  // open: dp
  Hex_Digit_Display hex_digit_display_14 (.value(leaderboard_1_p16));  // open: dp
  Hex_Digit_Display hex_digit_display_15 (.value(leaderboard_1_p20));  // open: dp
  Hex_Digit_Display hex_digit_display_16 (.value(leaderboard_1_p17));  // open: dp
  Hex_Digit_Display hex_digit_display_17 (.value(leaderboard_1_p18));  // open: dp
  Hex_Digit_Display hex_digit_display_18 (.value(leaderboard_1_p21));  // open: dp
  Hex_Digit_Display hex_digit_display_19 (.value(leaderboard_1_p22));  // open: dp
  Hex_Digit_Display hex_digit_display_20 (.value(leaderboard_1_p19));  // open: dp
endmodule

module StateDefiner (
  input  start_stop,
  input  lose,
  output state_of_game
);

  wire not_1_out;

  not not_1 (not_1_out, state_of_game);
  Register #(.width(1)) register_1 (.D(not_1_out), .Q(state_of_game), .clk(start_stop), .clr(lose));  // open: en
endmodule
module MainController (
  input  [6:0] keyboard,
  output tact,
  output tact_2,
  output [30:0] out_4,
  output [31:0] out_5,
  output Lose_upper,
  output [31:0] out_7,
  output [31:0] out_8,
  output [31:0] out_9,
  output [31:0] out_10,
  output Lose_east,
  output [31:0] out_12,
  output [31:0] out_13,
  output [31:0] out_14,
  output [31:0] out_15,
  output [31:0] out_16,
  output [31:0] out_17,
  output [31:0] out_18,
  output [31:0] out_19,
  output [31:0] out_20,
  output [31:0] out_21,
  output [31:0] out_22,
  output [31:0] out_23,
  output [31:0] out_24,
  output [31:0] out_25,
  output [31:0] out_26,
  output [31:0] out_27,
  output [31:0] out_28,
  output [31:0] out_29,
  output [31:0] out_30,
  output [31:0] out_31,
  output [31:0] out_32,
  output [31:0] out_33,
  output [31:0] out_34,
  output [31:0] out_35,
  output [31:0] out_36,
  output [31:0] out_37,
  output [31:0] out_38,
  output [31:0] out_39,
  output Start,
  output Pause,
  output [13:0] score,
  output [29:0] out_43,
  output [29:0] out_44,
  output [29:0] out_45,
  output [29:0] out_46,
  output [29:0] out_47,
  output [29:0] out_48,
  output [29:0] out_49,
  output [29:0] out_50,
  output [29:0] out_51,
  output [29:0] out_52,
  output [29:0] out_53,
  output [29:0] out_54,
  output [29:0] out_55,
  output [29:0] out_56,
  output [29:0] out_57,
  output [29:0] out_58,
  output [29:0] out_59,
  output [29:0] out_60,
  output [29:0] out_61,
  output [29:0] out_62,
  output [29:0] out_63,
  output [29:0] out_64,
  output [29:0] out_65,
  output [29:0] out_66,
  output [29:0] out_67,
  output [29:0] out_68,
  output [29:0] out_69,
  output [29:0] out_70,
  output [29:0] out_71,
  output [29:0] out_72,
  output [29:0] out_73,
  output [29:0] out_74
);

  wire _1m_, _2m_, _2m_a, _3m_, _3m_a, _4m_, _4m_a, _5m_, _5m_a, _6m_, _6m_a, _7m_, _7m_a, _8m_, _8m_a, _9m_,
       _9m_a, _10m_, _10m_a, _11m_, _11m_a, _12m_, _12m_a, _13m_, _13m_a, _14m_, _14m_a, _15m_, _15m_a,
       _16m_, _16m_a, _17m_, _17m_a, _18m_, _18m_a, _19m_, _19m_a, _20m_, _20m_a, _21m_, _21m_a, _22m_,
       _22m_a, _23m_, _23m_a, _24m_, _24m_a, _25m_, _25m_a, _26m_, _26m_a, _27m_, _27m_a, _28m_, _28m_a,
       _29m_, _29m_a, _30m_, _30m_a, _31m_, _31m_a, _32m_, _32m_a, and_1_out, and_3_out,
       collisiondefiner_1_out_3, collisiondefiner_2_out_3, collisiondefiner_3_out_3,
       collisiondefiner_4_out_3, collisiondefiner_5_out_3, collisiondefiner_6_out_3,
       collisiondefiner_7_out_3, collisiondefiner_8_out_3, collisiondefiner_9_out_3,
       collisiondefiner_10_out_3, collisiondefiner_11_out_3, collisiondefiner_12_out_3,
       collisiondefiner_13_out_3, collisiondefiner_14_out_3, collisiondefiner_15_out_3,
       collisiondefiner_16_out_3, collisiondefiner_17_out_3, collisiondefiner_18_out_3,
       collisiondefiner_19_out_3, collisiondefiner_20_out_3, collisiondefiner_21_out_3,
       collisiondefiner_22_out_3, collisiondefiner_23_out_3, collisiondefiner_24_out_3,
       collisiondefiner_25_out_3, collisiondefiner_26_out_3, collisiondefiner_27_out_3,
       collisiondefiner_28_out_3, collisiondefiner_29_out_3, collisiondefiner_30_out_3,
       collisiondefiner_31_out_3, collisiondefiner_32_out_3, collisiondefiner_33_out_3,
       collisiondefiner_34_out_3, collisiondefiner_35_out_3, collisiondefiner_36_out_3,
       collisiondefiner_37_out_3, collisiondefiner_38_out_3, collisiondefiner_39_out_3,
       collisiondefiner_40_out_3, collisiondefiner_41_out_3, collisiondefiner_42_out_3,
       collisiondefiner_43_out_3, collisiondefiner_44_out_3, collisiondefiner_45_out_3,
       collisiondefiner_46_out_3, collisiondefiner_47_out_3, collisiondefiner_48_out_3,
       collisiondefiner_49_out_3, collisiondefiner_50_out_3, collisiondefiner_51_out_3,
       collisiondefiner_52_out_3, collisiondefiner_53_out_3, collisiondefiner_54_out_3,
       collisiondefiner_55_out_3, collisiondefiner_56_out_3, collisiondefiner_57_out_3,
       collisiondefiner_58_out_3, collisiondefiner_59_out_3, collisiondefiner_60_out_3,
       collisiondefiner_61_out_3, collisiondefiner_62_out_3, collisiondefiner_63_out_3,
       collisiondefiner_64_out_3, collisiondefiner_65_out_3, collisiondefiner_66_out_3,
       collisiondefiner_67_out_3, collisiondefiner_68_out_3, collisiondefiner_69_out_3,
       collisiondefiner_70_out_3, collisiondefiner_71_out_3, collisiondefiner_72_out_3,
       collisiondefiner_73_out_3, collisiondefiner_74_out_3, collisiondefiner_75_out_3,
       collisiondefiner_76_out_3, collisiondefiner_77_out_3, collisiondefiner_78_out_3,
       collisiondefiner_79_out_3, collisiondefiner_80_out_3, collisiondefiner_81_out_3,
       collisiondefiner_82_out_3, collisiondefiner_83_out_3, collisiondefiner_84_out_3,
       collisiondefiner_85_out_3, collisiondefiner_86_out_3, collisiondefiner_87_out_3,
       collisiondefiner_88_out_3, collisiondefiner_89_out_3, collisiondefiner_90_out_3,
       collisiondefiner_91_out_3, collisiondefiner_92_out_3, collisiondefiner_93_out_3,
       collisiondefiner_94_out_3, collisiondefiner_95_out_3, collisiondefiner_96_out_3, comparator_1_eq,
       comparator_2_eq, comparator_3_eq, comparator_3_lt, comparator_4_eq, comparator_4_gt, comparator_4_lt,
       comparator_5_eq, comparator_6_eq, d_ff_1_q, d_ff_2_q, demultiplexer_1_out0, demultiplexer_1_out1,
       demultiplexer_1_out2, demultiplexer_1_out3, demultiplexer_1_out4, demultiplexer_1_out5,
       demultiplexer_1_out6, demultiplexer_1_out7, demultiplexer_1_out8, demultiplexer_1_out9,
       demultiplexer_1_out10, demultiplexer_1_out11, demultiplexer_1_out12, demultiplexer_1_out13,
       demultiplexer_1_out14, demultiplexer_1_out15, demultiplexer_1_out16, demultiplexer_1_out17,
       demultiplexer_1_out18, demultiplexer_1_out19, demultiplexer_1_out20, demultiplexer_1_out21,
       demultiplexer_1_out22, demultiplexer_1_out23, demultiplexer_1_out24, demultiplexer_1_out25,
       demultiplexer_1_out26, demultiplexer_1_out27, demultiplexer_1_out28, demultiplexer_1_out29,
       demultiplexer_1_out30, demultiplexer_1_out31, demultiplexer_2_out0, demultiplexer_2_out1,
       demultiplexer_2_out2, demultiplexer_2_out3, demultiplexer_2_out4, demultiplexer_2_out5,
       demultiplexer_2_out6, demultiplexer_2_out7, demultiplexer_2_out8, demultiplexer_2_out9,
       demultiplexer_2_out10, demultiplexer_2_out11, demultiplexer_2_out12, demultiplexer_2_out13,
       demultiplexer_2_out14, demultiplexer_2_out15, demultiplexer_2_out16, demultiplexer_2_out17,
       demultiplexer_2_out18, demultiplexer_2_out19, demultiplexer_2_out20, demultiplexer_2_out21,
       demultiplexer_2_out22, demultiplexer_2_out23, demultiplexer_2_out24, demultiplexer_2_out25,
       demultiplexer_2_out26, demultiplexer_2_out27, demultiplexer_2_out28, demultiplexer_2_out29,
       demultiplexer_2_out30, demultiplexer_2_out31, down, game_state, left, moneycollisiondefiner_1_out_3,
       moneycollisiondefiner_2_out_3, moneycollisiondefiner_3_out_3, moneycollisiondefiner_4_out_3,
       moneycollisiondefiner_5_out_3, moneycollisiondefiner_6_out_3, moneycollisiondefiner_7_out_3,
       moneycollisiondefiner_8_out_3, moneycollisiondefiner_9_out_3, moneycollisiondefiner_10_out_3,
       moneycollisiondefiner_11_out_3, moneycollisiondefiner_12_out_3, moneycollisiondefiner_13_out_3,
       moneycollisiondefiner_14_out_3, moneycollisiondefiner_15_out_3, moneycollisiondefiner_16_out_3,
       moneycollisiondefiner_17_out_3, moneycollisiondefiner_18_out_3, moneycollisiondefiner_19_out_3,
       moneycollisiondefiner_20_out_3, moneycollisiondefiner_21_out_3, moneycollisiondefiner_22_out_3,
       moneycollisiondefiner_23_out_3, moneycollisiondefiner_24_out_3, moneycollisiondefiner_25_out_3,
       moneycollisiondefiner_26_out_3, moneycollisiondefiner_27_out_3, moneycollisiondefiner_28_out_3,
       moneycollisiondefiner_29_out_3, moneycollisiondefiner_30_out_3, moneycollisiondefiner_31_out_3,
       moneycollisiondefiner_32_out_3, moneycollisiondefiner_33_out_3, moneycollisiondefiner_34_out_3,
       moneycollisiondefiner_35_out_3, moneycollisiondefiner_36_out_3, moneycollisiondefiner_37_out_3,
       moneycollisiondefiner_38_out_3, moneycollisiondefiner_39_out_3, moneycollisiondefiner_40_out_3,
       moneycollisiondefiner_41_out_3, moneycollisiondefiner_42_out_3, moneycollisiondefiner_43_out_3,
       moneycollisiondefiner_44_out_3, moneycollisiondefiner_45_out_3, moneycollisiondefiner_46_out_3,
       moneycollisiondefiner_47_out_3, moneycollisiondefiner_48_out_3, moneycollisiondefiner_49_out_3,
       moneycollisiondefiner_50_out_3, moneycollisiondefiner_51_out_3, moneycollisiondefiner_52_out_3,
       moneycollisiondefiner_53_out_3, moneycollisiondefiner_54_out_3, moneycollisiondefiner_55_out_3,
       moneycollisiondefiner_56_out_3, moneycollisiondefiner_57_out_3, moneycollisiondefiner_58_out_3,
       moneycollisiondefiner_59_out_3, moneycollisiondefiner_60_out_3, moneycollisiondefiner_61_out_3,
       moneycollisiondefiner_62_out_3, moneycollisiondefiner_63_out_3, moneycollisiondefiner_64_out_3,
       multiplexer_2_out, multiplexer_69_out, multiplexer_74_out, multiplexer_79_out, multiplexer_80_out,
       multiplexer_84_out, not_1_out, not_2_out, not_3_out, not_4_out, not_5_out, not_6_out, not_7_out,
       not_8_out, not_9_out, not_10_out, not_11_out, not_12_out, not_14_out, not_15_out, not_16_out,
       not_17_out, or_1_out, or_2_out, or_5_out, or_13_out, or_71_out, or_73_out, or_75_out, right, start_t,
       tact_1, tact_2_t, tact_3, tact_4, tact_for_money, tact_for_player, tact_t, tp_or_not, x_cond,
       xor_1_out;
  wire [1:0] adder_2_out, multiplexer_3_out, or_3_out, register_2_q;
  wire [2:0] adder_1_out, multiplexer_1_out, register_1_q;
  wire [3:0] comparator_7_eq;
  wire [4:0] bitfinder_1_index, bitfinder_2_index, bitfinder_3_index, bitfinder_4_index, bitfinder_5_index,
       random_1_out, random_2_out, subtractor_1_out;
  wire [13:0] adder_3_out, multiplexer_68_out;
  wire [29:0] multiplexer_4_out, multiplexer_5_out, multiplexer_6_out, multiplexer_7_out, multiplexer_8_out,
       multiplexer_9_out, multiplexer_10_out, multiplexer_28_out, multiplexer_29_out, multiplexer_30_out,
       multiplexer_31_out, multiplexer_32_out, multiplexer_33_out, multiplexer_34_out, multiplexer_35_out,
       multiplexer_36_out, multiplexer_37_out, multiplexer_38_out, multiplexer_39_out, multiplexer_40_out,
       multiplexer_41_out, multiplexer_42_out, multiplexer_43_out, multiplexer_60_out, multiplexer_61_out,
       multiplexer_62_out, multiplexer_63_out, multiplexer_64_out, multiplexer_65_out, multiplexer_66_out,
       multiplexer_67_out, shifter_1_out;
  wire [30:0] multiplexer_70_out, multiplexer_72_out, multiplexer_75_out, multiplexer_76_out, shifter_2_out,
       shifter_3_out, x_final, x_inverted_alt;
  wire [31:0] multiplexer_11_out, multiplexer_12_out, multiplexer_13_out, multiplexer_14_out,
       multiplexer_15_out, multiplexer_16_out, multiplexer_17_out, multiplexer_20_out, multiplexer_21_out,
       multiplexer_22_out, multiplexer_23_out, multiplexer_24_out, multiplexer_25_out, multiplexer_26_out,
       multiplexer_27_out, multiplexer_44_out, multiplexer_45_out, multiplexer_46_out, multiplexer_47_out,
       multiplexer_48_out, multiplexer_49_out, multiplexer_50_out, multiplexer_51_out, multiplexer_52_out,
       multiplexer_53_out, multiplexer_54_out, multiplexer_55_out, multiplexer_56_out, multiplexer_57_out,
       multiplexer_58_out, multiplexer_59_out, multiplexer_71_out, multiplexer_73_out, multiplexer_77_out,
       multiplexer_78_out, new_y, or_72_out, platformset_1_new_platform, shifter_4_out, shifter_5_out,
       y_final;

  Clock clock_1 (.out(tact));
  not not_1 (not_1_out, d_ff_1_q);
  Multiplexer #(.width(3), .enable("false")) multiplexer_1 (
    .in0(adder_1_out), .in1(3'b000), .out(multiplexer_1_out), .sel(start_t));
  Multiplexer #(.enable("false")) multiplexer_2 (.in0(tact), .in1(1'b0), .out(multiplexer_2_out), .sel(d_ff_1_q));
  not not_2 (not_2_out, d_ff_2_q);
  D_Flip_Flop d_ff_1 (.clk(Pause), .D(not_1_out), .Q(d_ff_1_q));  // open: Qn, preset, en, reset
  Register #(.width(3)) register_1 (.D(multiplexer_1_out), .Q(register_1_q), .clk(tact_t));  // open: en, clr
  Adder #(.width(3)) adder_1 (.a(register_1_q), .b(3'b001), .out(adder_1_out));  // open: cin, cout
  D_Flip_Flop d_ff_2 (.clk(multiplexer_2_out), .D(not_2_out), .Q(d_ff_2_q));  // open: Qn, preset, en, reset
  not not_3 (not_3_out, tact_for_money);
  Random #(.width(5)) random_1 (.clk(tact_t), .out(random_1_out));  // open: next, clr
  Comparator #(.width(3)) comparator_1 (.a(adder_1_out), .b(3'b001), .eq(comparator_1_eq));  // open: gt, lt
  Comparator #(.width(3)) comparator_2 (.a(adder_1_out), .b(3'b101), .eq(comparator_2_eq));  // open: gt, lt
  D_Flip_Flop d_ff_3 (.clk(d_ff_2_q), .D(not_3_out), .Q(tact_for_money));  // open: Qn, preset, en, reset
  D_Flip_Flop d_ff_4 (.clk(tact_for_money), .D(not_4_out), .Q(tact_4));  // open: Qn, preset, en, reset
  not not_4 (not_4_out, tact_4);
  Comparator #(.width(14)) comparator_3 (
    .a(score), .b(14'h3c), .eq(comparator_3_eq), .lt(comparator_3_lt));  // open: gt
  Comparator #(.width(14)) comparator_4 (
    .a(score), .b(14'h14), .gt(comparator_4_gt), .eq(comparator_4_eq), .lt(comparator_4_lt));
  Multiplexer #(.width(2), .enable("false")) multiplexer_3 (
    .in0(adder_2_out), .in1(2'b00), .out(multiplexer_3_out), .sel(start_t));
  Register #(.width(2)) register_2 (.D(multiplexer_3_out), .Q(register_2_q), .clk(tact_t));  // open: en, clr
  Shifter #(.width(30)) shifter_1 (.in(30'h1), .\dist (random_1_out), .out(shifter_1_out));
  Register #(.width(30)) register_3 (.D(shifter_1_out), .Q(out_43), .clk(tact_for_money), .clr(or_1_out));  // open: en
  or or_1 (or_1_out, not_5_out, _1m_, start_t);
  not not_5 (not_5_out, or_2_out);
  or or_2 (or_2_out, comparator_1_eq, comparator_2_eq);
  Multiplexer #(.width(30), .enable("false")) multiplexer_4 (
    .in0(out_43), .in1({30{1'b0}}), .out(multiplexer_4_out), .sel(start_t));
  Register #(.width(30)) register_4 (.D(multiplexer_4_out), .Q(out_47), .clk(tact_t), .clr(_2m_));  // open: en
  Multiplexer #(.width(30), .enable("false")) multiplexer_5 (
    .in0(out_47), .in1({30{1'b0}}), .out(multiplexer_5_out), .sel(start_t));
  Register #(.width(30)) register_5 (.D(multiplexer_5_out), .Q(out_51), .clk(tact_t), .clr(_3m_));  // open: en
  Multiplexer #(.width(30), .enable("false")) multiplexer_6 (
    .in0(out_51), .in1({30{1'b0}}), .out(multiplexer_6_out), .sel(start_t));
  Register #(.width(30)) register_6 (.D(multiplexer_6_out), .Q(out_55), .clk(tact_t), .clr(_4m_));  // open: en
  Register #(.width(30)) register_7 (.D(multiplexer_7_out), .Q(out_59), .clk(tact_t), .clr(_5m_));  // open: en
  Multiplexer #(.width(30), .enable("false")) multiplexer_7 (
    .in0(out_55), .in1({30{1'b0}}), .out(multiplexer_7_out), .sel(start_t));
  Register #(.width(30)) register_8 (.D(multiplexer_8_out), .Q(out_63), .clk(tact_t), .clr(_6m_));  // open: en
  Multiplexer #(.width(30), .enable("false")) multiplexer_8 (
    .in0(out_59), .in1({30{1'b0}}), .out(multiplexer_8_out), .sel(start_t));
  Multiplexer #(.width(30), .enable("false")) multiplexer_9 (
    .in0(out_63), .in1({30{1'b0}}), .out(multiplexer_9_out), .sel(start_t));
  Register #(.width(30)) register_9 (.D(multiplexer_9_out), .Q(out_67), .clk(tact_t), .clr(_7m_));  // open: en
  Multiplexer #(.width(30), .enable("false")) multiplexer_10 (
    .in0(out_67), .in1({30{1'b0}}), .out(multiplexer_10_out), .sel(start_t));
  Register #(.width(30)) register_10 (.D(multiplexer_10_out), .Q(out_71), .clk(tact_t), .clr(_8m_));  // open: en
  D_Flip_Flop d_ff_5 (.clk(tact_4), .D(not_6_out), .Q(tact_3));  // open: Qn, preset, en, reset
  not not_6 (not_6_out, tact_3);
  or or_3 (or_3_out[0], comparator_3_eq, and_1_out);
  and and_1 (and_1_out, comparator_3_lt, comparator_4_gt);
  or or_4 (or_3_out[1], comparator_4_eq, comparator_4_lt);
  Register #(.width(32)) register_11 (
    .D(platformset_1_new_platform), .Q(out_7), .clk(tact_t), .clr(or_5_out));  // open: en
  PlatformSet platformset_1 (.in_1(random_2_out), .new_platform(platformset_1_new_platform));
  Random #(.width(5)) random_2 (.clk(tact_t), .out(random_2_out));  // open: next, clr
  or or_5 (or_5_out, not_7_out, start_t);
  Adder #(.width(2)) adder_2 (.a(register_2_q), .b(2'b01), .out(adder_2_out));  // open: cin, cout
  not not_7 (not_7_out, adder_2_out[1]);
  Register #(.width(32)) register_12 (.D(multiplexer_11_out), .Q(out_12), .clk(tact_t));  // open: en, clr
  Multiplexer #(.width(32), .enable("false")) multiplexer_11 (
    .in0(out_7), .in1({32{1'b0}}), .out(multiplexer_11_out), .sel(start_t));
  Multiplexer #(.width(32), .enable("false")) multiplexer_12 (
    .in0(out_12), .in1(32'h3f8ffc7f), .out(multiplexer_12_out), .sel(start_t));
  Register #(.width(32)) register_13 (.D(multiplexer_12_out), .Q(out_16), .clk(tact_t));  // open: en, clr
  Multiplexer #(.width(32), .enable("false")) multiplexer_13 (
    .in0(out_16), .in1({32{1'b0}}), .out(multiplexer_13_out), .sel(start_t));
  Register #(.width(32)) register_14 (.D(multiplexer_13_out), .Q(out_20), .clk(tact_t));  // open: en, clr
  Multiplexer #(.width(32), .enable("false")) multiplexer_14 (
    .in0(out_20), .in1({32{1'b0}}), .out(multiplexer_14_out), .sel(start_t));
  Register #(.width(32)) register_15 (.D(multiplexer_14_out), .Q(out_24), .clk(tact_t));  // open: en, clr
  Register #(.width(32)) register_16 (.D(multiplexer_15_out), .Q(out_28), .clk(tact_t));  // open: en, clr
  Multiplexer #(.width(32), .enable("false")) multiplexer_15 (
    .in0(out_24), .in1({32{1'b0}}), .out(multiplexer_15_out), .sel(start_t));
  Register #(.width(32)) register_17 (.D(multiplexer_16_out), .Q(out_32), .clk(tact_t));  // open: en, clr
  Multiplexer #(.width(32), .enable("false")) multiplexer_16 (
    .in0(out_28), .in1(32'h3fc7ff1f), .out(multiplexer_16_out), .sel(start_t));
  Multiplexer #(.width(32), .enable("false")) multiplexer_17 (
    .in0(out_32), .in1({32{1'b0}}), .out(multiplexer_17_out), .sel(start_t));
  Register #(.width(32)) register_18 (.D(multiplexer_17_out), .Q(out_36), .clk(tact_t));  // open: en, clr
  D_Flip_Flop d_ff_6 (.clk(tact_3), .D(not_8_out), .Q(tact_2_t));  // open: Qn, preset, en, reset
  not not_8 (not_8_out, tact_2_t);
  Multiplexer #(.select(2), .enable("false")) multiplexer_18 (
    .in0(tact_4), .in1(tact_3), .in2(tact_2_t), .out(tact_for_player), .sel(or_3_out));  // open: in3
  Multiplexer #(.select(2), .enable("false")) multiplexer_19 (
    .in0(tact_3), .in1(tact_2_t), .in2(tact_1), .out(tact_t), .sel(or_3_out));  // open: in3
  D_Flip_Flop d_ff_7 (.clk(tact_2_t), .D(not_9_out), .Q(tact_1));  // open: Qn, preset, en, reset
  not not_9 (not_9_out, tact_1);
  Multiplexer #(.width(32), .enable("false")) multiplexer_20 (
    .in0(out_36), .in1({32{1'b0}}), .out(multiplexer_20_out), .sel(start_t));
  Multiplexer #(.width(32), .enable("false")) multiplexer_21 (
    .in0(out_8), .in1({32{1'b0}}), .out(multiplexer_21_out), .sel(start_t));
  Multiplexer #(.width(32), .enable("false")) multiplexer_22 (
    .in0(out_13), .in1(32'h3c7ff1ff), .out(multiplexer_22_out), .sel(start_t));
  Multiplexer #(.width(32), .enable("false")) multiplexer_23 (
    .in0(out_17), .in1({32{1'b0}}), .out(multiplexer_23_out), .sel(start_t));
  Multiplexer #(.width(32), .enable("false")) multiplexer_24 (
    .in0(out_21), .in1({32{1'b0}}), .out(multiplexer_24_out), .sel(start_t));
  Multiplexer #(.width(32), .enable("false")) multiplexer_25 (
    .in0(out_25), .in1({32{1'b0}}), .out(multiplexer_25_out), .sel(start_t));
  Multiplexer #(.width(32), .enable("false")) multiplexer_26 (
    .in0(out_29), .in1(32'h7fffff8), .out(multiplexer_26_out), .sel(start_t));
  Multiplexer #(.width(32), .enable("false")) multiplexer_27 (
    .in0(out_33), .in1({32{1'b0}}), .out(multiplexer_27_out), .sel(start_t));
  Register #(.width(30)) register_19 (.D(multiplexer_28_out), .Q(out_44), .clk(tact_t), .clr(_9m_));  // open: en
  Multiplexer #(.width(30), .enable("false")) multiplexer_28 (
    .in0(out_71), .in1({30{1'b0}}), .out(multiplexer_28_out), .sel(start_t));
  Register #(.width(30)) register_20 (.D(multiplexer_29_out), .Q(out_48), .clk(tact_t), .clr(_10m_));  // open: en
  Multiplexer #(.width(30), .enable("false")) multiplexer_29 (
    .in0(out_44), .in1({30{1'b0}}), .out(multiplexer_29_out), .sel(start_t));
  Register #(.width(30)) register_21 (.D(multiplexer_30_out), .Q(out_52), .clk(tact_t), .clr(_11m_));  // open: en
  Multiplexer #(.width(30), .enable("false")) multiplexer_30 (
    .in0(out_48), .in1({30{1'b0}}), .out(multiplexer_30_out), .sel(start_t));
  Register #(.width(30)) register_22 (.D(multiplexer_31_out), .Q(out_56), .clk(tact_t), .clr(_12m_));  // open: en
  Multiplexer #(.width(30), .enable("false")) multiplexer_31 (
    .in0(out_52), .in1({30{1'b0}}), .out(multiplexer_31_out), .sel(start_t));
  Multiplexer #(.width(30), .enable("false")) multiplexer_32 (
    .in0(out_56), .in1({30{1'b0}}), .out(multiplexer_32_out), .sel(start_t));
  Register #(.width(30)) register_23 (.D(multiplexer_32_out), .Q(out_60), .clk(tact_t), .clr(_13m_));  // open: en
  Register #(.width(30)) register_24 (.D(multiplexer_33_out), .Q(out_64), .clk(tact_t), .clr(_14m_));  // open: en
  Multiplexer #(.width(30), .enable("false")) multiplexer_33 (
    .in0(out_60), .in1({30{1'b0}}), .out(multiplexer_33_out), .sel(start_t));
  Register #(.width(30)) register_25 (.D(multiplexer_34_out), .Q(out_68), .clk(tact_t), .clr(_15m_));  // open: en
  Multiplexer #(.width(30), .enable("false")) multiplexer_34 (
    .in0(out_64), .in1({30{1'b0}}), .out(multiplexer_34_out), .sel(start_t));
  Multiplexer #(.width(30), .enable("false")) multiplexer_35 (
    .in0(out_68), .in1({30{1'b0}}), .out(multiplexer_35_out), .sel(start_t));
  Register #(.width(30)) register_26 (.D(multiplexer_35_out), .Q(out_72), .clk(tact_t), .clr(_16m_));  // open: en
  Register #(.width(32)) register_27 (.D(multiplexer_20_out), .Q(out_8), .clk(tact_t));  // open: en, clr
  Register #(.width(32)) register_28 (.D(multiplexer_21_out), .Q(out_13), .clk(tact_t));  // open: en, clr
  Register #(.width(32)) register_29 (.D(multiplexer_22_out), .Q(out_17), .clk(tact_t));  // open: en, clr
  Register #(.width(32)) register_30 (.D(multiplexer_23_out), .Q(out_21), .clk(tact_t));  // open: en, clr
  Register #(.width(32)) register_31 (.D(multiplexer_24_out), .Q(out_25), .clk(tact_t));  // open: en, clr
  Register #(.width(32)) register_32 (.D(multiplexer_25_out), .Q(out_29), .clk(tact_t));  // open: en, clr
  Register #(.width(32)) register_33 (.D(multiplexer_26_out), .Q(out_33), .clk(tact_t));  // open: en, clr
  Register #(.width(32)) register_34 (.D(multiplexer_27_out), .Q(out_37), .clk(tact_t));  // open: en, clr
  Multiplexer #(.width(30), .enable("false")) multiplexer_36 (
    .in0(out_72), .in1({30{1'b0}}), .out(multiplexer_36_out), .sel(start_t));
  Multiplexer #(.width(30), .enable("false")) multiplexer_37 (
    .in0(out_45), .in1({30{1'b0}}), .out(multiplexer_37_out), .sel(start_t));
  Multiplexer #(.width(30), .enable("false")) multiplexer_38 (
    .in0(out_49), .in1({30{1'b0}}), .out(multiplexer_38_out), .sel(start_t));
  Multiplexer #(.width(30), .enable("false")) multiplexer_39 (
    .in0(out_53), .in1({30{1'b0}}), .out(multiplexer_39_out), .sel(start_t));
  Multiplexer #(.width(30), .enable("false")) multiplexer_40 (
    .in0(out_57), .in1({30{1'b0}}), .out(multiplexer_40_out), .sel(start_t));
  Multiplexer #(.width(30), .enable("false")) multiplexer_41 (
    .in0(out_61), .in1({30{1'b0}}), .out(multiplexer_41_out), .sel(start_t));
  Multiplexer #(.width(30), .enable("false")) multiplexer_42 (
    .in0(out_65), .in1({30{1'b0}}), .out(multiplexer_42_out), .sel(start_t));
  Multiplexer #(.width(30), .enable("false")) multiplexer_43 (
    .in0(out_69), .in1({30{1'b0}}), .out(multiplexer_43_out), .sel(start_t));
  Register #(.width(32)) register_35 (.D(multiplexer_44_out), .Q(out_9), .clk(tact_t));  // open: en, clr
  Multiplexer #(.width(32), .enable("false")) multiplexer_44 (
    .in0(out_37), .in1({32{1'b0}}), .out(multiplexer_44_out), .sel(start_t));
  Register #(.width(32)) register_36 (.D(multiplexer_45_out), .Q(out_14), .clk(tact_t));  // open: en, clr
  Multiplexer #(.width(32), .enable("false")) multiplexer_45 (
    .in0(out_9), .in1({32{1'b0}}), .out(multiplexer_45_out), .sel(start_t));
  Multiplexer #(.width(32), .enable("false")) multiplexer_46 (
    .in0(out_14), .in1(32'h31ffffe3), .out(multiplexer_46_out), .sel(start_t));
  Register #(.width(32)) register_37 (.D(multiplexer_46_out), .Q(out_18), .clk(tact_t));  // open: en, clr
  Register #(.width(32)) register_38 (.D(multiplexer_47_out), .Q(out_22), .clk(tact_t));  // open: en, clr
  Multiplexer #(.width(32), .enable("false")) multiplexer_47 (
    .in0(out_18), .in1({32{1'b0}}), .out(multiplexer_47_out), .sel(start_t));
  Register #(.width(32)) register_39 (.D(multiplexer_48_out), .Q(out_26), .clk(tact_t));  // open: en, clr
  Multiplexer #(.width(32), .enable("false")) multiplexer_48 (
    .in0(out_22), .in1({32{1'b0}}), .out(multiplexer_48_out), .sel(start_t));
  Multiplexer #(.width(32), .enable("false")) multiplexer_49 (
    .in0(out_26), .in1({32{1'b0}}), .out(multiplexer_49_out), .sel(start_t));
  Register #(.width(32)) register_40 (.D(multiplexer_49_out), .Q(out_30), .clk(tact_t));  // open: en, clr
  Multiplexer #(.width(32), .enable("false")) multiplexer_50 (
    .in0(out_30), .in1(32'h3f8ffc7f), .out(multiplexer_50_out), .sel(start_t));
  Register #(.width(32)) register_41 (.D(multiplexer_50_out), .Q(out_34), .clk(tact_t));  // open: en, clr
  Multiplexer #(.width(32), .enable("false")) multiplexer_51 (
    .in0(out_34), .in1({32{1'b0}}), .out(multiplexer_51_out), .sel(start_t));
  Register #(.width(32)) register_42 (.D(multiplexer_51_out), .Q(out_38), .clk(tact_t));  // open: en, clr
  Register #(.width(30)) register_43 (.D(multiplexer_36_out), .Q(out_45), .clk(tact_t), .clr(_17m_));  // open: en
  Register #(.width(30)) register_44 (.D(multiplexer_37_out), .Q(out_49), .clk(tact_t), .clr(_18m_));  // open: en
  Register #(.width(30)) register_45 (.D(multiplexer_38_out), .Q(out_53), .clk(tact_t), .clr(_19m_));  // open: en
  Register #(.width(30)) register_46 (.D(multiplexer_39_out), .Q(out_57), .clk(tact_t), .clr(_20m_));  // open: en
  Register #(.width(30)) register_47 (.D(multiplexer_40_out), .Q(out_61), .clk(tact_t), .clr(_21m_));  // open: en
  Register #(.width(30)) register_48 (.D(multiplexer_41_out), .Q(out_65), .clk(tact_t), .clr(_22m_));  // open: en
  Register #(.width(30)) register_49 (.D(multiplexer_42_out), .Q(out_69), .clk(tact_t), .clr(_23m_));  // open: en
  Register #(.width(30)) register_50 (.D(multiplexer_43_out), .Q(out_73), .clk(tact_t), .clr(_24m_));  // open: en
  Multiplexer #(.width(32), .enable("false")) multiplexer_52 (
    .in0(out_38), .in1({32{1'b0}}), .out(multiplexer_52_out), .sel(start_t));
  Multiplexer #(.width(32), .enable("false")) multiplexer_53 (
    .in0(out_10), .in1({32{1'b0}}), .out(multiplexer_53_out), .sel(start_t));
  Multiplexer #(.width(32), .enable("false")) multiplexer_54 (
    .in0(out_15), .in1(32'h38fe3f8f), .out(multiplexer_54_out), .sel(start_t));
  Multiplexer #(.width(32), .enable("false")) multiplexer_55 (
    .in0(out_19), .in1({32{1'b0}}), .out(multiplexer_55_out), .sel(start_t));
  Multiplexer #(.width(32), .enable("false")) multiplexer_56 (
    .in0(out_23), .in1({32{1'b0}}), .out(multiplexer_56_out), .sel(start_t));
  Multiplexer #(.width(32), .enable("false")) multiplexer_57 (
    .in0(out_27), .in1({32{1'b0}}), .out(multiplexer_57_out), .sel(start_t));
  Multiplexer #(.width(32), .enable("false")) multiplexer_58 (
    .in0(out_31), .in1(32'h23c7e3f1), .out(multiplexer_58_out), .sel(start_t));
  Multiplexer #(.width(32), .enable("false")) multiplexer_59 (
    .in0(out_35), .in1({32{1'b0}}), .out(multiplexer_59_out), .sel(start_t));
  Multiplexer #(.width(30), .enable("false")) multiplexer_60 (
    .in0(out_73), .in1({30{1'b0}}), .out(multiplexer_60_out), .sel(start_t));
  Multiplexer #(.width(30), .enable("false")) multiplexer_61 (
    .in0(out_46), .in1({30{1'b0}}), .out(multiplexer_61_out), .sel(start_t));
  Multiplexer #(.width(30), .enable("false")) multiplexer_62 (
    .in0(out_50), .in1({30{1'b0}}), .out(multiplexer_62_out), .sel(start_t));
  Multiplexer #(.width(30), .enable("false")) multiplexer_63 (
    .in0(out_54), .in1({30{1'b0}}), .out(multiplexer_63_out), .sel(start_t));
  Multiplexer #(.width(30), .enable("false")) multiplexer_64 (
    .in0(out_58), .in1({30{1'b0}}), .out(multiplexer_64_out), .sel(start_t));
  Multiplexer #(.width(30), .enable("false")) multiplexer_65 (
    .in0(out_62), .in1({30{1'b0}}), .out(multiplexer_65_out), .sel(start_t));
  Multiplexer #(.width(30), .enable("false")) multiplexer_66 (
    .in0(out_66), .in1({30{1'b0}}), .out(multiplexer_66_out), .sel(start_t));
  Multiplexer #(.width(30), .enable("false")) multiplexer_67 (
    .in0(out_70), .in1({30{1'b0}}), .out(multiplexer_67_out), .sel(start_t));
  Register #(.width(32)) register_51 (.D(multiplexer_52_out), .Q(out_10), .clk(tact_t));  // open: en, clr
  Register #(.width(32)) register_52 (.D(multiplexer_53_out), .Q(out_15), .clk(tact_t));  // open: en, clr
  Register #(.width(32)) register_53 (.D(multiplexer_54_out), .Q(out_19), .clk(tact_t));  // open: en, clr
  Register #(.width(32)) register_54 (.D(multiplexer_55_out), .Q(out_23), .clk(tact_t));  // open: en, clr
  Register #(.width(32)) register_55 (.D(multiplexer_56_out), .Q(out_27), .clk(tact_t));  // open: en, clr
  Register #(.width(32)) register_56 (.D(multiplexer_57_out), .Q(out_31), .clk(tact_t));  // open: en, clr
  Register #(.width(32)) register_57 (.D(multiplexer_58_out), .Q(out_35), .clk(tact_t));  // open: en, clr
  Register #(.width(32)) register_58 (.D(multiplexer_59_out), .Q(out_39), .clk(tact_t));  // open: en, clr
  Register #(.width(30)) register_59 (.D(multiplexer_60_out), .Q(out_46), .clk(tact_t), .clr(_25m_));  // open: en
  Register #(.width(30)) register_60 (.D(multiplexer_61_out), .Q(out_50), .clk(tact_t), .clr(_26m_));  // open: en
  Register #(.width(30)) register_61 (.D(multiplexer_62_out), .Q(out_54), .clk(tact_t), .clr(_27m_));  // open: en
  Register #(.width(30)) register_62 (.D(multiplexer_63_out), .Q(out_58), .clk(tact_t), .clr(_28m_));  // open: en
  Register #(.width(30)) register_63 (.D(multiplexer_64_out), .Q(out_62), .clk(tact_t), .clr(_29m_));  // open: en
  Register #(.width(30)) register_64 (.D(multiplexer_65_out), .Q(out_66), .clk(tact_t), .clr(_30m_));  // open: en
  Register #(.width(30)) register_65 (.D(multiplexer_66_out), .Q(out_70), .clk(tact_t), .clr(_31m_));  // open: en
  Register #(.width(30)) register_66 (.D(multiplexer_67_out), .Q(out_74), .clk(tact_t), .clr(_32m_));  // open: en
  Adder #(.width(14)) adder_3 (.a(score), .b(multiplexer_68_out), .out(adder_3_out));  // open: cin, cout
  Multiplexer #(.width(14), .enable("false")) multiplexer_68 (
    .in0(14'h5), .in1(14'h1), .out(multiplexer_68_out), .sel(tp_or_not));
  MoneyCollisionDefiner moneycollisiondefiner_1 (
    .in_1(out_43),
    .in_2({1'b0, out_4[0], out_4[1], out_4[2], out_4[3], out_4[4], out_4[5], out_4[6], out_4[7], out_4[8], out_4[9], out_4[10], out_4[11], out_4[12], out_4[13], out_4[14], out_4[15], out_4[16], out_4[17], out_4[18], out_4[19], out_4[20], out_4[21], out_4[22], out_4[23], out_4[24], out_4[25], out_4[26], out_4[27], out_4[28], out_4[29], out_4[30]}),
    .out_3(moneycollisiondefiner_1_out_3));
  MoneyCollisionDefiner moneycollisiondefiner_2 (
    .in_1(out_47),
    .in_2({1'b0, out_4[0], out_4[1], out_4[2], out_4[3], out_4[4], out_4[5], out_4[6], out_4[7], out_4[8], out_4[9], out_4[10], out_4[11], out_4[12], out_4[13], out_4[14], out_4[15], out_4[16], out_4[17], out_4[18], out_4[19], out_4[20], out_4[21], out_4[22], out_4[23], out_4[24], out_4[25], out_4[26], out_4[27], out_4[28], out_4[29], out_4[30]}),
    .out_3(moneycollisiondefiner_2_out_3));
  MoneyCollisionDefiner moneycollisiondefiner_3 (
    .in_1(out_51),
    .in_2({1'b0, out_4[0], out_4[1], out_4[2], out_4[3], out_4[4], out_4[5], out_4[6], out_4[7], out_4[8], out_4[9], out_4[10], out_4[11], out_4[12], out_4[13], out_4[14], out_4[15], out_4[16], out_4[17], out_4[18], out_4[19], out_4[20], out_4[21], out_4[22], out_4[23], out_4[24], out_4[25], out_4[26], out_4[27], out_4[28], out_4[29], out_4[30]}),
    .out_3(moneycollisiondefiner_3_out_3));
  MoneyCollisionDefiner moneycollisiondefiner_4 (
    .in_1(out_55),
    .in_2({1'b0, out_4[0], out_4[1], out_4[2], out_4[3], out_4[4], out_4[5], out_4[6], out_4[7], out_4[8], out_4[9], out_4[10], out_4[11], out_4[12], out_4[13], out_4[14], out_4[15], out_4[16], out_4[17], out_4[18], out_4[19], out_4[20], out_4[21], out_4[22], out_4[23], out_4[24], out_4[25], out_4[26], out_4[27], out_4[28], out_4[29], out_4[30]}),
    .out_3(moneycollisiondefiner_4_out_3));
  MoneyCollisionDefiner moneycollisiondefiner_5 (
    .in_1(out_59),
    .in_2({1'b0, out_4[0], out_4[1], out_4[2], out_4[3], out_4[4], out_4[5], out_4[6], out_4[7], out_4[8], out_4[9], out_4[10], out_4[11], out_4[12], out_4[13], out_4[14], out_4[15], out_4[16], out_4[17], out_4[18], out_4[19], out_4[20], out_4[21], out_4[22], out_4[23], out_4[24], out_4[25], out_4[26], out_4[27], out_4[28], out_4[29], out_4[30]}),
    .out_3(moneycollisiondefiner_5_out_3));
  MoneyCollisionDefiner moneycollisiondefiner_6 (
    .in_1(out_63),
    .in_2({1'b0, out_4[0], out_4[1], out_4[2], out_4[3], out_4[4], out_4[5], out_4[6], out_4[7], out_4[8], out_4[9], out_4[10], out_4[11], out_4[12], out_4[13], out_4[14], out_4[15], out_4[16], out_4[17], out_4[18], out_4[19], out_4[20], out_4[21], out_4[22], out_4[23], out_4[24], out_4[25], out_4[26], out_4[27], out_4[28], out_4[29], out_4[30]}),
    .out_3(moneycollisiondefiner_6_out_3));
  MoneyCollisionDefiner moneycollisiondefiner_7 (
    .in_1(out_67),
    .in_2({1'b0, out_4[0], out_4[1], out_4[2], out_4[3], out_4[4], out_4[5], out_4[6], out_4[7], out_4[8], out_4[9], out_4[10], out_4[11], out_4[12], out_4[13], out_4[14], out_4[15], out_4[16], out_4[17], out_4[18], out_4[19], out_4[20], out_4[21], out_4[22], out_4[23], out_4[24], out_4[25], out_4[26], out_4[27], out_4[28], out_4[29], out_4[30]}),
    .out_3(moneycollisiondefiner_7_out_3));
  MoneyCollisionDefiner moneycollisiondefiner_8 (
    .in_1(out_71),
    .in_2({1'b0, out_4[0], out_4[1], out_4[2], out_4[3], out_4[4], out_4[5], out_4[6], out_4[7], out_4[8], out_4[9], out_4[10], out_4[11], out_4[12], out_4[13], out_4[14], out_4[15], out_4[16], out_4[17], out_4[18], out_4[19], out_4[20], out_4[21], out_4[22], out_4[23], out_4[24], out_4[25], out_4[26], out_4[27], out_4[28], out_4[29], out_4[30]}),
    .out_3(moneycollisiondefiner_8_out_3));
  MoneyCollisionDefiner moneycollisiondefiner_9 (
    .in_1(out_44),
    .in_2({1'b0, out_4[0], out_4[1], out_4[2], out_4[3], out_4[4], out_4[5], out_4[6], out_4[7], out_4[8], out_4[9], out_4[10], out_4[11], out_4[12], out_4[13], out_4[14], out_4[15], out_4[16], out_4[17], out_4[18], out_4[19], out_4[20], out_4[21], out_4[22], out_4[23], out_4[24], out_4[25], out_4[26], out_4[27], out_4[28], out_4[29], out_4[30]}),
    .out_3(moneycollisiondefiner_9_out_3));
  MoneyCollisionDefiner moneycollisiondefiner_10 (
    .in_1(out_48),
    .in_2({1'b0, out_4[0], out_4[1], out_4[2], out_4[3], out_4[4], out_4[5], out_4[6], out_4[7], out_4[8], out_4[9], out_4[10], out_4[11], out_4[12], out_4[13], out_4[14], out_4[15], out_4[16], out_4[17], out_4[18], out_4[19], out_4[20], out_4[21], out_4[22], out_4[23], out_4[24], out_4[25], out_4[26], out_4[27], out_4[28], out_4[29], out_4[30]}),
    .out_3(moneycollisiondefiner_10_out_3));
  MoneyCollisionDefiner moneycollisiondefiner_11 (
    .in_1(out_52),
    .in_2({1'b0, out_4[0], out_4[1], out_4[2], out_4[3], out_4[4], out_4[5], out_4[6], out_4[7], out_4[8], out_4[9], out_4[10], out_4[11], out_4[12], out_4[13], out_4[14], out_4[15], out_4[16], out_4[17], out_4[18], out_4[19], out_4[20], out_4[21], out_4[22], out_4[23], out_4[24], out_4[25], out_4[26], out_4[27], out_4[28], out_4[29], out_4[30]}),
    .out_3(moneycollisiondefiner_11_out_3));
  MoneyCollisionDefiner moneycollisiondefiner_12 (
    .in_1(out_56),
    .in_2({1'b0, out_4[0], out_4[1], out_4[2], out_4[3], out_4[4], out_4[5], out_4[6], out_4[7], out_4[8], out_4[9], out_4[10], out_4[11], out_4[12], out_4[13], out_4[14], out_4[15], out_4[16], out_4[17], out_4[18], out_4[19], out_4[20], out_4[21], out_4[22], out_4[23], out_4[24], out_4[25], out_4[26], out_4[27], out_4[28], out_4[29], out_4[30]}),
    .out_3(moneycollisiondefiner_12_out_3));
  MoneyCollisionDefiner moneycollisiondefiner_13 (
    .in_1(out_60),
    .in_2({1'b0, out_4[0], out_4[1], out_4[2], out_4[3], out_4[4], out_4[5], out_4[6], out_4[7], out_4[8], out_4[9], out_4[10], out_4[11], out_4[12], out_4[13], out_4[14], out_4[15], out_4[16], out_4[17], out_4[18], out_4[19], out_4[20], out_4[21], out_4[22], out_4[23], out_4[24], out_4[25], out_4[26], out_4[27], out_4[28], out_4[29], out_4[30]}),
    .out_3(moneycollisiondefiner_13_out_3));
  MoneyCollisionDefiner moneycollisiondefiner_14 (
    .in_1(out_64),
    .in_2({1'b0, out_4[0], out_4[1], out_4[2], out_4[3], out_4[4], out_4[5], out_4[6], out_4[7], out_4[8], out_4[9], out_4[10], out_4[11], out_4[12], out_4[13], out_4[14], out_4[15], out_4[16], out_4[17], out_4[18], out_4[19], out_4[20], out_4[21], out_4[22], out_4[23], out_4[24], out_4[25], out_4[26], out_4[27], out_4[28], out_4[29], out_4[30]}),
    .out_3(moneycollisiondefiner_14_out_3));
  MoneyCollisionDefiner moneycollisiondefiner_15 (
    .in_1(out_68),
    .in_2({1'b0, out_4[0], out_4[1], out_4[2], out_4[3], out_4[4], out_4[5], out_4[6], out_4[7], out_4[8], out_4[9], out_4[10], out_4[11], out_4[12], out_4[13], out_4[14], out_4[15], out_4[16], out_4[17], out_4[18], out_4[19], out_4[20], out_4[21], out_4[22], out_4[23], out_4[24], out_4[25], out_4[26], out_4[27], out_4[28], out_4[29], out_4[30]}),
    .out_3(moneycollisiondefiner_15_out_3));
  MoneyCollisionDefiner moneycollisiondefiner_16 (
    .in_1(out_72),
    .in_2({1'b0, out_4[0], out_4[1], out_4[2], out_4[3], out_4[4], out_4[5], out_4[6], out_4[7], out_4[8], out_4[9], out_4[10], out_4[11], out_4[12], out_4[13], out_4[14], out_4[15], out_4[16], out_4[17], out_4[18], out_4[19], out_4[20], out_4[21], out_4[22], out_4[23], out_4[24], out_4[25], out_4[26], out_4[27], out_4[28], out_4[29], out_4[30]}),
    .out_3(moneycollisiondefiner_16_out_3));
  MoneyCollisionDefiner moneycollisiondefiner_17 (
    .in_1(out_45),
    .in_2({1'b0, out_4[0], out_4[1], out_4[2], out_4[3], out_4[4], out_4[5], out_4[6], out_4[7], out_4[8], out_4[9], out_4[10], out_4[11], out_4[12], out_4[13], out_4[14], out_4[15], out_4[16], out_4[17], out_4[18], out_4[19], out_4[20], out_4[21], out_4[22], out_4[23], out_4[24], out_4[25], out_4[26], out_4[27], out_4[28], out_4[29], out_4[30]}),
    .out_3(moneycollisiondefiner_17_out_3));
  MoneyCollisionDefiner moneycollisiondefiner_18 (
    .in_1(out_49),
    .in_2({1'b0, out_4[0], out_4[1], out_4[2], out_4[3], out_4[4], out_4[5], out_4[6], out_4[7], out_4[8], out_4[9], out_4[10], out_4[11], out_4[12], out_4[13], out_4[14], out_4[15], out_4[16], out_4[17], out_4[18], out_4[19], out_4[20], out_4[21], out_4[22], out_4[23], out_4[24], out_4[25], out_4[26], out_4[27], out_4[28], out_4[29], out_4[30]}),
    .out_3(moneycollisiondefiner_18_out_3));
  MoneyCollisionDefiner moneycollisiondefiner_19 (
    .in_1(out_53),
    .in_2({1'b0, out_4[0], out_4[1], out_4[2], out_4[3], out_4[4], out_4[5], out_4[6], out_4[7], out_4[8], out_4[9], out_4[10], out_4[11], out_4[12], out_4[13], out_4[14], out_4[15], out_4[16], out_4[17], out_4[18], out_4[19], out_4[20], out_4[21], out_4[22], out_4[23], out_4[24], out_4[25], out_4[26], out_4[27], out_4[28], out_4[29], out_4[30]}),
    .out_3(moneycollisiondefiner_19_out_3));
  MoneyCollisionDefiner moneycollisiondefiner_20 (
    .in_1(out_57),
    .in_2({1'b0, out_4[0], out_4[1], out_4[2], out_4[3], out_4[4], out_4[5], out_4[6], out_4[7], out_4[8], out_4[9], out_4[10], out_4[11], out_4[12], out_4[13], out_4[14], out_4[15], out_4[16], out_4[17], out_4[18], out_4[19], out_4[20], out_4[21], out_4[22], out_4[23], out_4[24], out_4[25], out_4[26], out_4[27], out_4[28], out_4[29], out_4[30]}),
    .out_3(moneycollisiondefiner_20_out_3));
  MoneyCollisionDefiner moneycollisiondefiner_21 (
    .in_1(out_61),
    .in_2({1'b0, out_4[0], out_4[1], out_4[2], out_4[3], out_4[4], out_4[5], out_4[6], out_4[7], out_4[8], out_4[9], out_4[10], out_4[11], out_4[12], out_4[13], out_4[14], out_4[15], out_4[16], out_4[17], out_4[18], out_4[19], out_4[20], out_4[21], out_4[22], out_4[23], out_4[24], out_4[25], out_4[26], out_4[27], out_4[28], out_4[29], out_4[30]}),
    .out_3(moneycollisiondefiner_21_out_3));
  MoneyCollisionDefiner moneycollisiondefiner_22 (
    .in_1(out_65),
    .in_2({1'b0, out_4[0], out_4[1], out_4[2], out_4[3], out_4[4], out_4[5], out_4[6], out_4[7], out_4[8], out_4[9], out_4[10], out_4[11], out_4[12], out_4[13], out_4[14], out_4[15], out_4[16], out_4[17], out_4[18], out_4[19], out_4[20], out_4[21], out_4[22], out_4[23], out_4[24], out_4[25], out_4[26], out_4[27], out_4[28], out_4[29], out_4[30]}),
    .out_3(moneycollisiondefiner_22_out_3));
  MoneyCollisionDefiner moneycollisiondefiner_23 (
    .in_1(out_69),
    .in_2({1'b0, out_4[0], out_4[1], out_4[2], out_4[3], out_4[4], out_4[5], out_4[6], out_4[7], out_4[8], out_4[9], out_4[10], out_4[11], out_4[12], out_4[13], out_4[14], out_4[15], out_4[16], out_4[17], out_4[18], out_4[19], out_4[20], out_4[21], out_4[22], out_4[23], out_4[24], out_4[25], out_4[26], out_4[27], out_4[28], out_4[29], out_4[30]}),
    .out_3(moneycollisiondefiner_23_out_3));
  MoneyCollisionDefiner moneycollisiondefiner_24 (
    .in_1(out_73),
    .in_2({1'b0, out_4[0], out_4[1], out_4[2], out_4[3], out_4[4], out_4[5], out_4[6], out_4[7], out_4[8], out_4[9], out_4[10], out_4[11], out_4[12], out_4[13], out_4[14], out_4[15], out_4[16], out_4[17], out_4[18], out_4[19], out_4[20], out_4[21], out_4[22], out_4[23], out_4[24], out_4[25], out_4[26], out_4[27], out_4[28], out_4[29], out_4[30]}),
    .out_3(moneycollisiondefiner_24_out_3));
  MoneyCollisionDefiner moneycollisiondefiner_25 (
    .in_1(out_46),
    .in_2({1'b0, out_4[0], out_4[1], out_4[2], out_4[3], out_4[4], out_4[5], out_4[6], out_4[7], out_4[8], out_4[9], out_4[10], out_4[11], out_4[12], out_4[13], out_4[14], out_4[15], out_4[16], out_4[17], out_4[18], out_4[19], out_4[20], out_4[21], out_4[22], out_4[23], out_4[24], out_4[25], out_4[26], out_4[27], out_4[28], out_4[29], out_4[30]}),
    .out_3(moneycollisiondefiner_25_out_3));
  MoneyCollisionDefiner moneycollisiondefiner_26 (
    .in_1(out_50),
    .in_2({1'b0, out_4[0], out_4[1], out_4[2], out_4[3], out_4[4], out_4[5], out_4[6], out_4[7], out_4[8], out_4[9], out_4[10], out_4[11], out_4[12], out_4[13], out_4[14], out_4[15], out_4[16], out_4[17], out_4[18], out_4[19], out_4[20], out_4[21], out_4[22], out_4[23], out_4[24], out_4[25], out_4[26], out_4[27], out_4[28], out_4[29], out_4[30]}),
    .out_3(moneycollisiondefiner_26_out_3));
  MoneyCollisionDefiner moneycollisiondefiner_27 (
    .in_1(out_54),
    .in_2({1'b0, out_4[0], out_4[1], out_4[2], out_4[3], out_4[4], out_4[5], out_4[6], out_4[7], out_4[8], out_4[9], out_4[10], out_4[11], out_4[12], out_4[13], out_4[14], out_4[15], out_4[16], out_4[17], out_4[18], out_4[19], out_4[20], out_4[21], out_4[22], out_4[23], out_4[24], out_4[25], out_4[26], out_4[27], out_4[28], out_4[29], out_4[30]}),
    .out_3(moneycollisiondefiner_27_out_3));
  MoneyCollisionDefiner moneycollisiondefiner_28 (
    .in_1(out_58),
    .in_2({1'b0, out_4[0], out_4[1], out_4[2], out_4[3], out_4[4], out_4[5], out_4[6], out_4[7], out_4[8], out_4[9], out_4[10], out_4[11], out_4[12], out_4[13], out_4[14], out_4[15], out_4[16], out_4[17], out_4[18], out_4[19], out_4[20], out_4[21], out_4[22], out_4[23], out_4[24], out_4[25], out_4[26], out_4[27], out_4[28], out_4[29], out_4[30]}),
    .out_3(moneycollisiondefiner_28_out_3));
  MoneyCollisionDefiner moneycollisiondefiner_29 (
    .in_1(out_62),
    .in_2({1'b0, out_4[0], out_4[1], out_4[2], out_4[3], out_4[4], out_4[5], out_4[6], out_4[7], out_4[8], out_4[9], out_4[10], out_4[11], out_4[12], out_4[13], out_4[14], out_4[15], out_4[16], out_4[17], out_4[18], out_4[19], out_4[20], out_4[21], out_4[22], out_4[23], out_4[24], out_4[25], out_4[26], out_4[27], out_4[28], out_4[29], out_4[30]}),
    .out_3(moneycollisiondefiner_29_out_3));
  MoneyCollisionDefiner moneycollisiondefiner_30 (
    .in_1(out_66),
    .in_2({1'b0, out_4[0], out_4[1], out_4[2], out_4[3], out_4[4], out_4[5], out_4[6], out_4[7], out_4[8], out_4[9], out_4[10], out_4[11], out_4[12], out_4[13], out_4[14], out_4[15], out_4[16], out_4[17], out_4[18], out_4[19], out_4[20], out_4[21], out_4[22], out_4[23], out_4[24], out_4[25], out_4[26], out_4[27], out_4[28], out_4[29], out_4[30]}),
    .out_3(moneycollisiondefiner_30_out_3));
  MoneyCollisionDefiner moneycollisiondefiner_31 (
    .in_1(out_70),
    .in_2({1'b0, out_4[0], out_4[1], out_4[2], out_4[3], out_4[4], out_4[5], out_4[6], out_4[7], out_4[8], out_4[9], out_4[10], out_4[11], out_4[12], out_4[13], out_4[14], out_4[15], out_4[16], out_4[17], out_4[18], out_4[19], out_4[20], out_4[21], out_4[22], out_4[23], out_4[24], out_4[25], out_4[26], out_4[27], out_4[28], out_4[29], out_4[30]}),
    .out_3(moneycollisiondefiner_31_out_3));
  MoneyCollisionDefiner moneycollisiondefiner_32 (
    .in_1(out_74),
    .in_2({1'b0, out_4[0], out_4[1], out_4[2], out_4[3], out_4[4], out_4[5], out_4[6], out_4[7], out_4[8], out_4[9], out_4[10], out_4[11], out_4[12], out_4[13], out_4[14], out_4[15], out_4[16], out_4[17], out_4[18], out_4[19], out_4[20], out_4[21], out_4[22], out_4[23], out_4[24], out_4[25], out_4[26], out_4[27], out_4[28], out_4[29], out_4[30]}),
    .out_3(moneycollisiondefiner_32_out_3));
  xor xor_1 (xor_1_out, tp_or_not, or_13_out);
  Demultiplexer #(.select(5), .enable("false")) demultiplexer_1 (
    .out0(demultiplexer_1_out0), .out1(demultiplexer_1_out1), .out2(demultiplexer_1_out2),
    .out3(demultiplexer_1_out3), .out4(demultiplexer_1_out4), .out5(demultiplexer_1_out5),
    .out6(demultiplexer_1_out6), .out7(demultiplexer_1_out7), .out8(demultiplexer_1_out8),
    .out9(demultiplexer_1_out9), .out10(demultiplexer_1_out10), .out11(demultiplexer_1_out11),
    .out12(demultiplexer_1_out12), .out13(demultiplexer_1_out13), .out14(demultiplexer_1_out14),
    .out15(demultiplexer_1_out15), .out16(demultiplexer_1_out16), .out17(demultiplexer_1_out17),
    .out18(demultiplexer_1_out18), .out19(demultiplexer_1_out19), .out20(demultiplexer_1_out20),
    .out21(demultiplexer_1_out21), .out22(demultiplexer_1_out22), .out23(demultiplexer_1_out23),
    .out24(demultiplexer_1_out24), .out25(demultiplexer_1_out25), .out26(demultiplexer_1_out26),
    .out27(demultiplexer_1_out27), .out28(demultiplexer_1_out28), .out29(demultiplexer_1_out29),
    .out30(demultiplexer_1_out30), .out31(demultiplexer_1_out31), .in(multiplexer_69_out),
    .sel(bitfinder_1_index));
  Multiplexer #(.select(5), .enable("false")) multiplexer_69 (
    .in0(moneycollisiondefiner_1_out_3), .in1(moneycollisiondefiner_2_out_3),
    .in2(moneycollisiondefiner_3_out_3), .in3(moneycollisiondefiner_4_out_3),
    .in4(moneycollisiondefiner_5_out_3), .in5(moneycollisiondefiner_6_out_3),
    .in6(moneycollisiondefiner_7_out_3), .in7(moneycollisiondefiner_8_out_3),
    .in8(moneycollisiondefiner_9_out_3), .in9(moneycollisiondefiner_10_out_3),
    .in10(moneycollisiondefiner_11_out_3), .in11(moneycollisiondefiner_12_out_3),
    .in12(moneycollisiondefiner_13_out_3), .in13(moneycollisiondefiner_14_out_3),
    .in14(moneycollisiondefiner_15_out_3), .in15(moneycollisiondefiner_16_out_3),
    .in16(moneycollisiondefiner_17_out_3), .in17(moneycollisiondefiner_18_out_3),
    .in18(moneycollisiondefiner_19_out_3), .in19(moneycollisiondefiner_20_out_3),
    .in20(moneycollisiondefiner_21_out_3), .in21(moneycollisiondefiner_22_out_3),
    .in22(moneycollisiondefiner_23_out_3), .in23(moneycollisiondefiner_24_out_3),
    .in24(moneycollisiondefiner_25_out_3), .in25(moneycollisiondefiner_26_out_3),
    .in26(moneycollisiondefiner_27_out_3), .in27(moneycollisiondefiner_28_out_3),
    .in28(moneycollisiondefiner_29_out_3), .in29(moneycollisiondefiner_30_out_3),
    .in30(moneycollisiondefiner_31_out_3), .in31(moneycollisiondefiner_32_out_3), .out(multiplexer_69_out),
    .sel(bitfinder_1_index));
  BitFinder #(.width(32), .\type ("high1")) bitfinder_1 (.in(out_5), .index(bitfinder_1_index));  // open: found
  or or_6 (_2m_, _1m_, _2m_a);
  or or_7 (_3m_, _2m_a, _3m_a);
  or or_8 (_4m_, _3m_a, _4m_a);
  or or_9 (_5m_, _4m_a, _5m_a);
  or or_10 (_6m_, _5m_a, _6m_a);
  or or_11 (_7m_, _6m_a, _7m_a);
  or or_12 (_8m_, _7m_a, _8m_a);
  Register #(.width(14)) register_67 (.D(adder_3_out), .Q(score), .clk(xor_1_out), .clr(Start));  // open: en
  or or_13 (or_13_out, multiplexer_69_out, multiplexer_74_out);
  or or_14 (_1m_, demultiplexer_1_out0, demultiplexer_2_out0);
  or or_15 (_2m_a, demultiplexer_1_out1, demultiplexer_2_out1);
  or or_16 (_3m_a, demultiplexer_1_out2, demultiplexer_2_out2);
  or or_17 (_4m_a, demultiplexer_1_out3, demultiplexer_2_out3);
  or or_18 (_5m_a, demultiplexer_1_out4, demultiplexer_2_out4);
  or or_19 (_6m_a, demultiplexer_1_out5, demultiplexer_2_out5);
  or or_20 (_7m_a, demultiplexer_1_out6, demultiplexer_2_out6);
  or or_21 (_8m_a, demultiplexer_1_out7, demultiplexer_2_out7);
  or or_22 (_9m_a, demultiplexer_1_out8, demultiplexer_2_out8);
  or or_23 (_10m_a, demultiplexer_1_out9, demultiplexer_2_out9);
  or or_24 (_11m_a, demultiplexer_1_out10, demultiplexer_2_out10);
  or or_25 (_12m_a, demultiplexer_1_out11, demultiplexer_2_out11);
  or or_26 (_13m_a, demultiplexer_1_out12, demultiplexer_2_out12);
  or or_27 (_14m_a, demultiplexer_1_out13, demultiplexer_2_out13);
  or or_28 (_15m_a, demultiplexer_1_out14, demultiplexer_2_out14);
  or or_29 (_16m_a, demultiplexer_1_out15, demultiplexer_2_out15);
  or or_30 (_17m_a, demultiplexer_1_out16, demultiplexer_2_out16);
  or or_31 (_18m_a, demultiplexer_1_out17, demultiplexer_2_out17);
  or or_32 (_19m_a, demultiplexer_1_out18, demultiplexer_2_out18);
  Demultiplexer #(.select(5), .enable("false")) demultiplexer_2 (
    .out0(demultiplexer_2_out0), .out1(demultiplexer_2_out1), .out2(demultiplexer_2_out2),
    .out3(demultiplexer_2_out3), .out4(demultiplexer_2_out4), .out5(demultiplexer_2_out5),
    .out6(demultiplexer_2_out6), .out7(demultiplexer_2_out7), .out8(demultiplexer_2_out8),
    .out9(demultiplexer_2_out9), .out10(demultiplexer_2_out10), .out11(demultiplexer_2_out11),
    .out12(demultiplexer_2_out12), .out13(demultiplexer_2_out13), .out14(demultiplexer_2_out14),
    .out15(demultiplexer_2_out15), .out16(demultiplexer_2_out16), .out17(demultiplexer_2_out17),
    .out18(demultiplexer_2_out18), .out19(demultiplexer_2_out19), .out20(demultiplexer_2_out20),
    .out21(demultiplexer_2_out21), .out22(demultiplexer_2_out22), .out23(demultiplexer_2_out23),
    .out24(demultiplexer_2_out24), .out25(demultiplexer_2_out25), .out26(demultiplexer_2_out26),
    .out27(demultiplexer_2_out27), .out28(demultiplexer_2_out28), .out29(demultiplexer_2_out29),
    .out30(demultiplexer_2_out30), .out31(demultiplexer_2_out31), .in(multiplexer_74_out),
    .sel(bitfinder_2_index));
  or or_33 (_20m_a, demultiplexer_1_out19, demultiplexer_2_out19);
  or or_34 (_21m_a, demultiplexer_1_out20, demultiplexer_2_out20);
  or or_35 (_22m_a, demultiplexer_1_out21, demultiplexer_2_out21);
  or or_36 (_23m_a, demultiplexer_1_out22, demultiplexer_2_out22);
  or or_37 (_24m_a, demultiplexer_1_out23, demultiplexer_2_out23);
  or or_38 (_25m_a, demultiplexer_1_out24, demultiplexer_2_out24);
  or or_39 (_26m_a, demultiplexer_1_out25, demultiplexer_2_out25);
  or or_40 (_27m_a, demultiplexer_1_out26, demultiplexer_2_out26);
  or or_41 (_28m_a, demultiplexer_1_out27, demultiplexer_2_out27);
  or or_42 (_29m_a, demultiplexer_1_out28, demultiplexer_2_out28);
  or or_43 (_30m_a, demultiplexer_1_out29, demultiplexer_2_out29);
  or or_44 (_31m_a, demultiplexer_1_out30, demultiplexer_2_out30);
  or or_45 (_32m_a, demultiplexer_1_out31, demultiplexer_2_out31);
  or or_46 (_9m_, _8m_a, _9m_a);
  or or_47 (_10m_, _9m_a, _10m_a);
  or or_48 (_11m_, _10m_a, _11m_a);
  or or_49 (_12m_, _11m_a, _12m_a);
  or or_50 (_13m_, _12m_a, _13m_a);
  or or_51 (_14m_, _13m_a, _14m_a);
  or or_52 (_15m_, _14m_a, _15m_a);
  or or_53 (_16m_, _15m_a, _16m_a);
  Multiplexer #(.width(31), .enable("false")) multiplexer_70 (
    .in0(31'hc000), .in1(x_final), .out(multiplexer_70_out), .sel(tp_or_not));
  Multiplexer #(.width(32), .enable("false")) multiplexer_71 (
    .in0(new_y), .in1(y_final), .out(multiplexer_71_out), .sel(tp_or_not));
  MoneyCollisionDefiner moneycollisiondefiner_33 (
    .in_1(out_43),
    .in_2({1'b0, out_4[0], out_4[1], out_4[2], out_4[3], out_4[4], out_4[5], out_4[6], out_4[7], out_4[8], out_4[9], out_4[10], out_4[11], out_4[12], out_4[13], out_4[14], out_4[15], out_4[16], out_4[17], out_4[18], out_4[19], out_4[20], out_4[21], out_4[22], out_4[23], out_4[24], out_4[25], out_4[26], out_4[27], out_4[28], out_4[29], out_4[30]}),
    .out_3(moneycollisiondefiner_33_out_3));
  MoneyCollisionDefiner moneycollisiondefiner_34 (
    .in_1(out_47),
    .in_2({1'b0, out_4[0], out_4[1], out_4[2], out_4[3], out_4[4], out_4[5], out_4[6], out_4[7], out_4[8], out_4[9], out_4[10], out_4[11], out_4[12], out_4[13], out_4[14], out_4[15], out_4[16], out_4[17], out_4[18], out_4[19], out_4[20], out_4[21], out_4[22], out_4[23], out_4[24], out_4[25], out_4[26], out_4[27], out_4[28], out_4[29], out_4[30]}),
    .out_3(moneycollisiondefiner_34_out_3));
  MoneyCollisionDefiner moneycollisiondefiner_35 (
    .in_1(out_51),
    .in_2({1'b0, out_4[0], out_4[1], out_4[2], out_4[3], out_4[4], out_4[5], out_4[6], out_4[7], out_4[8], out_4[9], out_4[10], out_4[11], out_4[12], out_4[13], out_4[14], out_4[15], out_4[16], out_4[17], out_4[18], out_4[19], out_4[20], out_4[21], out_4[22], out_4[23], out_4[24], out_4[25], out_4[26], out_4[27], out_4[28], out_4[29], out_4[30]}),
    .out_3(moneycollisiondefiner_35_out_3));
  MoneyCollisionDefiner moneycollisiondefiner_36 (
    .in_1(out_55),
    .in_2({1'b0, out_4[0], out_4[1], out_4[2], out_4[3], out_4[4], out_4[5], out_4[6], out_4[7], out_4[8], out_4[9], out_4[10], out_4[11], out_4[12], out_4[13], out_4[14], out_4[15], out_4[16], out_4[17], out_4[18], out_4[19], out_4[20], out_4[21], out_4[22], out_4[23], out_4[24], out_4[25], out_4[26], out_4[27], out_4[28], out_4[29], out_4[30]}),
    .out_3(moneycollisiondefiner_36_out_3));
  MoneyCollisionDefiner moneycollisiondefiner_37 (
    .in_1(out_59),
    .in_2({1'b0, out_4[0], out_4[1], out_4[2], out_4[3], out_4[4], out_4[5], out_4[6], out_4[7], out_4[8], out_4[9], out_4[10], out_4[11], out_4[12], out_4[13], out_4[14], out_4[15], out_4[16], out_4[17], out_4[18], out_4[19], out_4[20], out_4[21], out_4[22], out_4[23], out_4[24], out_4[25], out_4[26], out_4[27], out_4[28], out_4[29], out_4[30]}),
    .out_3(moneycollisiondefiner_37_out_3));
  MoneyCollisionDefiner moneycollisiondefiner_38 (
    .in_1(out_63),
    .in_2({1'b0, out_4[0], out_4[1], out_4[2], out_4[3], out_4[4], out_4[5], out_4[6], out_4[7], out_4[8], out_4[9], out_4[10], out_4[11], out_4[12], out_4[13], out_4[14], out_4[15], out_4[16], out_4[17], out_4[18], out_4[19], out_4[20], out_4[21], out_4[22], out_4[23], out_4[24], out_4[25], out_4[26], out_4[27], out_4[28], out_4[29], out_4[30]}),
    .out_3(moneycollisiondefiner_38_out_3));
  MoneyCollisionDefiner moneycollisiondefiner_39 (
    .in_1(out_67),
    .in_2({1'b0, out_4[0], out_4[1], out_4[2], out_4[3], out_4[4], out_4[5], out_4[6], out_4[7], out_4[8], out_4[9], out_4[10], out_4[11], out_4[12], out_4[13], out_4[14], out_4[15], out_4[16], out_4[17], out_4[18], out_4[19], out_4[20], out_4[21], out_4[22], out_4[23], out_4[24], out_4[25], out_4[26], out_4[27], out_4[28], out_4[29], out_4[30]}),
    .out_3(moneycollisiondefiner_39_out_3));
  MoneyCollisionDefiner moneycollisiondefiner_40 (
    .in_1(out_71),
    .in_2({1'b0, out_4[0], out_4[1], out_4[2], out_4[3], out_4[4], out_4[5], out_4[6], out_4[7], out_4[8], out_4[9], out_4[10], out_4[11], out_4[12], out_4[13], out_4[14], out_4[15], out_4[16], out_4[17], out_4[18], out_4[19], out_4[20], out_4[21], out_4[22], out_4[23], out_4[24], out_4[25], out_4[26], out_4[27], out_4[28], out_4[29], out_4[30]}),
    .out_3(moneycollisiondefiner_40_out_3));
  MoneyCollisionDefiner moneycollisiondefiner_41 (
    .in_1(out_44),
    .in_2({1'b0, out_4[0], out_4[1], out_4[2], out_4[3], out_4[4], out_4[5], out_4[6], out_4[7], out_4[8], out_4[9], out_4[10], out_4[11], out_4[12], out_4[13], out_4[14], out_4[15], out_4[16], out_4[17], out_4[18], out_4[19], out_4[20], out_4[21], out_4[22], out_4[23], out_4[24], out_4[25], out_4[26], out_4[27], out_4[28], out_4[29], out_4[30]}),
    .out_3(moneycollisiondefiner_41_out_3));
  MoneyCollisionDefiner moneycollisiondefiner_42 (
    .in_1(out_48),
    .in_2({1'b0, out_4[0], out_4[1], out_4[2], out_4[3], out_4[4], out_4[5], out_4[6], out_4[7], out_4[8], out_4[9], out_4[10], out_4[11], out_4[12], out_4[13], out_4[14], out_4[15], out_4[16], out_4[17], out_4[18], out_4[19], out_4[20], out_4[21], out_4[22], out_4[23], out_4[24], out_4[25], out_4[26], out_4[27], out_4[28], out_4[29], out_4[30]}),
    .out_3(moneycollisiondefiner_42_out_3));
  MoneyCollisionDefiner moneycollisiondefiner_43 (
    .in_1(out_52),
    .in_2({1'b0, out_4[0], out_4[1], out_4[2], out_4[3], out_4[4], out_4[5], out_4[6], out_4[7], out_4[8], out_4[9], out_4[10], out_4[11], out_4[12], out_4[13], out_4[14], out_4[15], out_4[16], out_4[17], out_4[18], out_4[19], out_4[20], out_4[21], out_4[22], out_4[23], out_4[24], out_4[25], out_4[26], out_4[27], out_4[28], out_4[29], out_4[30]}),
    .out_3(moneycollisiondefiner_43_out_3));
  MoneyCollisionDefiner moneycollisiondefiner_44 (
    .in_1(out_56),
    .in_2({1'b0, out_4[0], out_4[1], out_4[2], out_4[3], out_4[4], out_4[5], out_4[6], out_4[7], out_4[8], out_4[9], out_4[10], out_4[11], out_4[12], out_4[13], out_4[14], out_4[15], out_4[16], out_4[17], out_4[18], out_4[19], out_4[20], out_4[21], out_4[22], out_4[23], out_4[24], out_4[25], out_4[26], out_4[27], out_4[28], out_4[29], out_4[30]}),
    .out_3(moneycollisiondefiner_44_out_3));
  MoneyCollisionDefiner moneycollisiondefiner_45 (
    .in_1(out_60),
    .in_2({1'b0, out_4[0], out_4[1], out_4[2], out_4[3], out_4[4], out_4[5], out_4[6], out_4[7], out_4[8], out_4[9], out_4[10], out_4[11], out_4[12], out_4[13], out_4[14], out_4[15], out_4[16], out_4[17], out_4[18], out_4[19], out_4[20], out_4[21], out_4[22], out_4[23], out_4[24], out_4[25], out_4[26], out_4[27], out_4[28], out_4[29], out_4[30]}),
    .out_3(moneycollisiondefiner_45_out_3));
  MoneyCollisionDefiner moneycollisiondefiner_46 (
    .in_1(out_64),
    .in_2({1'b0, out_4[0], out_4[1], out_4[2], out_4[3], out_4[4], out_4[5], out_4[6], out_4[7], out_4[8], out_4[9], out_4[10], out_4[11], out_4[12], out_4[13], out_4[14], out_4[15], out_4[16], out_4[17], out_4[18], out_4[19], out_4[20], out_4[21], out_4[22], out_4[23], out_4[24], out_4[25], out_4[26], out_4[27], out_4[28], out_4[29], out_4[30]}),
    .out_3(moneycollisiondefiner_46_out_3));
  MoneyCollisionDefiner moneycollisiondefiner_47 (
    .in_1(out_68),
    .in_2({1'b0, out_4[0], out_4[1], out_4[2], out_4[3], out_4[4], out_4[5], out_4[6], out_4[7], out_4[8], out_4[9], out_4[10], out_4[11], out_4[12], out_4[13], out_4[14], out_4[15], out_4[16], out_4[17], out_4[18], out_4[19], out_4[20], out_4[21], out_4[22], out_4[23], out_4[24], out_4[25], out_4[26], out_4[27], out_4[28], out_4[29], out_4[30]}),
    .out_3(moneycollisiondefiner_47_out_3));
  MoneyCollisionDefiner moneycollisiondefiner_48 (
    .in_1(out_72),
    .in_2({1'b0, out_4[0], out_4[1], out_4[2], out_4[3], out_4[4], out_4[5], out_4[6], out_4[7], out_4[8], out_4[9], out_4[10], out_4[11], out_4[12], out_4[13], out_4[14], out_4[15], out_4[16], out_4[17], out_4[18], out_4[19], out_4[20], out_4[21], out_4[22], out_4[23], out_4[24], out_4[25], out_4[26], out_4[27], out_4[28], out_4[29], out_4[30]}),
    .out_3(moneycollisiondefiner_48_out_3));
  MoneyCollisionDefiner moneycollisiondefiner_49 (
    .in_1(out_45),
    .in_2({1'b0, out_4[0], out_4[1], out_4[2], out_4[3], out_4[4], out_4[5], out_4[6], out_4[7], out_4[8], out_4[9], out_4[10], out_4[11], out_4[12], out_4[13], out_4[14], out_4[15], out_4[16], out_4[17], out_4[18], out_4[19], out_4[20], out_4[21], out_4[22], out_4[23], out_4[24], out_4[25], out_4[26], out_4[27], out_4[28], out_4[29], out_4[30]}),
    .out_3(moneycollisiondefiner_49_out_3));
  MoneyCollisionDefiner moneycollisiondefiner_50 (
    .in_1(out_49),
    .in_2({1'b0, out_4[0], out_4[1], out_4[2], out_4[3], out_4[4], out_4[5], out_4[6], out_4[7], out_4[8], out_4[9], out_4[10], out_4[11], out_4[12], out_4[13], out_4[14], out_4[15], out_4[16], out_4[17], out_4[18], out_4[19], out_4[20], out_4[21], out_4[22], out_4[23], out_4[24], out_4[25], out_4[26], out_4[27], out_4[28], out_4[29], out_4[30]}),
    .out_3(moneycollisiondefiner_50_out_3));
  MoneyCollisionDefiner moneycollisiondefiner_51 (
    .in_1(out_53),
    .in_2({1'b0, out_4[0], out_4[1], out_4[2], out_4[3], out_4[4], out_4[5], out_4[6], out_4[7], out_4[8], out_4[9], out_4[10], out_4[11], out_4[12], out_4[13], out_4[14], out_4[15], out_4[16], out_4[17], out_4[18], out_4[19], out_4[20], out_4[21], out_4[22], out_4[23], out_4[24], out_4[25], out_4[26], out_4[27], out_4[28], out_4[29], out_4[30]}),
    .out_3(moneycollisiondefiner_51_out_3));
  MoneyCollisionDefiner moneycollisiondefiner_52 (
    .in_1(out_57),
    .in_2({1'b0, out_4[0], out_4[1], out_4[2], out_4[3], out_4[4], out_4[5], out_4[6], out_4[7], out_4[8], out_4[9], out_4[10], out_4[11], out_4[12], out_4[13], out_4[14], out_4[15], out_4[16], out_4[17], out_4[18], out_4[19], out_4[20], out_4[21], out_4[22], out_4[23], out_4[24], out_4[25], out_4[26], out_4[27], out_4[28], out_4[29], out_4[30]}),
    .out_3(moneycollisiondefiner_52_out_3));
  MoneyCollisionDefiner moneycollisiondefiner_53 (
    .in_1(out_61),
    .in_2({1'b0, out_4[0], out_4[1], out_4[2], out_4[3], out_4[4], out_4[5], out_4[6], out_4[7], out_4[8], out_4[9], out_4[10], out_4[11], out_4[12], out_4[13], out_4[14], out_4[15], out_4[16], out_4[17], out_4[18], out_4[19], out_4[20], out_4[21], out_4[22], out_4[23], out_4[24], out_4[25], out_4[26], out_4[27], out_4[28], out_4[29], out_4[30]}),
    .out_3(moneycollisiondefiner_53_out_3));
  MoneyCollisionDefiner moneycollisiondefiner_54 (
    .in_1(out_65),
    .in_2({1'b0, out_4[0], out_4[1], out_4[2], out_4[3], out_4[4], out_4[5], out_4[6], out_4[7], out_4[8], out_4[9], out_4[10], out_4[11], out_4[12], out_4[13], out_4[14], out_4[15], out_4[16], out_4[17], out_4[18], out_4[19], out_4[20], out_4[21], out_4[22], out_4[23], out_4[24], out_4[25], out_4[26], out_4[27], out_4[28], out_4[29], out_4[30]}),
    .out_3(moneycollisiondefiner_54_out_3));
  MoneyCollisionDefiner moneycollisiondefiner_55 (
    .in_1(out_69),
    .in_2({1'b0, out_4[0], out_4[1], out_4[2], out_4[3], out_4[4], out_4[5], out_4[6], out_4[7], out_4[8], out_4[9], out_4[10], out_4[11], out_4[12], out_4[13], out_4[14], out_4[15], out_4[16], out_4[17], out_4[18], out_4[19], out_4[20], out_4[21], out_4[22], out_4[23], out_4[24], out_4[25], out_4[26], out_4[27], out_4[28], out_4[29], out_4[30]}),
    .out_3(moneycollisiondefiner_55_out_3));
  MoneyCollisionDefiner moneycollisiondefiner_56 (
    .in_1(out_73),
    .in_2({1'b0, out_4[0], out_4[1], out_4[2], out_4[3], out_4[4], out_4[5], out_4[6], out_4[7], out_4[8], out_4[9], out_4[10], out_4[11], out_4[12], out_4[13], out_4[14], out_4[15], out_4[16], out_4[17], out_4[18], out_4[19], out_4[20], out_4[21], out_4[22], out_4[23], out_4[24], out_4[25], out_4[26], out_4[27], out_4[28], out_4[29], out_4[30]}),
    .out_3(moneycollisiondefiner_56_out_3));
  MoneyCollisionDefiner moneycollisiondefiner_57 (
    .in_1(out_46),
    .in_2({1'b0, out_4[0], out_4[1], out_4[2], out_4[3], out_4[4], out_4[5], out_4[6], out_4[7], out_4[8], out_4[9], out_4[10], out_4[11], out_4[12], out_4[13], out_4[14], out_4[15], out_4[16], out_4[17], out_4[18], out_4[19], out_4[20], out_4[21], out_4[22], out_4[23], out_4[24], out_4[25], out_4[26], out_4[27], out_4[28], out_4[29], out_4[30]}),
    .out_3(moneycollisiondefiner_57_out_3));
  MoneyCollisionDefiner moneycollisiondefiner_58 (
    .in_1(out_50),
    .in_2({1'b0, out_4[0], out_4[1], out_4[2], out_4[3], out_4[4], out_4[5], out_4[6], out_4[7], out_4[8], out_4[9], out_4[10], out_4[11], out_4[12], out_4[13], out_4[14], out_4[15], out_4[16], out_4[17], out_4[18], out_4[19], out_4[20], out_4[21], out_4[22], out_4[23], out_4[24], out_4[25], out_4[26], out_4[27], out_4[28], out_4[29], out_4[30]}),
    .out_3(moneycollisiondefiner_58_out_3));
  MoneyCollisionDefiner moneycollisiondefiner_59 (
    .in_1(out_54),
    .in_2({1'b0, out_4[0], out_4[1], out_4[2], out_4[3], out_4[4], out_4[5], out_4[6], out_4[7], out_4[8], out_4[9], out_4[10], out_4[11], out_4[12], out_4[13], out_4[14], out_4[15], out_4[16], out_4[17], out_4[18], out_4[19], out_4[20], out_4[21], out_4[22], out_4[23], out_4[24], out_4[25], out_4[26], out_4[27], out_4[28], out_4[29], out_4[30]}),
    .out_3(moneycollisiondefiner_59_out_3));
  MoneyCollisionDefiner moneycollisiondefiner_60 (
    .in_1(out_58),
    .in_2({1'b0, out_4[0], out_4[1], out_4[2], out_4[3], out_4[4], out_4[5], out_4[6], out_4[7], out_4[8], out_4[9], out_4[10], out_4[11], out_4[12], out_4[13], out_4[14], out_4[15], out_4[16], out_4[17], out_4[18], out_4[19], out_4[20], out_4[21], out_4[22], out_4[23], out_4[24], out_4[25], out_4[26], out_4[27], out_4[28], out_4[29], out_4[30]}),
    .out_3(moneycollisiondefiner_60_out_3));
  MoneyCollisionDefiner moneycollisiondefiner_61 (
    .in_1(out_62),
    .in_2({1'b0, out_4[0], out_4[1], out_4[2], out_4[3], out_4[4], out_4[5], out_4[6], out_4[7], out_4[8], out_4[9], out_4[10], out_4[11], out_4[12], out_4[13], out_4[14], out_4[15], out_4[16], out_4[17], out_4[18], out_4[19], out_4[20], out_4[21], out_4[22], out_4[23], out_4[24], out_4[25], out_4[26], out_4[27], out_4[28], out_4[29], out_4[30]}),
    .out_3(moneycollisiondefiner_61_out_3));
  MoneyCollisionDefiner moneycollisiondefiner_62 (
    .in_1(out_66),
    .in_2({1'b0, out_4[0], out_4[1], out_4[2], out_4[3], out_4[4], out_4[5], out_4[6], out_4[7], out_4[8], out_4[9], out_4[10], out_4[11], out_4[12], out_4[13], out_4[14], out_4[15], out_4[16], out_4[17], out_4[18], out_4[19], out_4[20], out_4[21], out_4[22], out_4[23], out_4[24], out_4[25], out_4[26], out_4[27], out_4[28], out_4[29], out_4[30]}),
    .out_3(moneycollisiondefiner_62_out_3));
  MoneyCollisionDefiner moneycollisiondefiner_63 (
    .in_1(out_70),
    .in_2({1'b0, out_4[0], out_4[1], out_4[2], out_4[3], out_4[4], out_4[5], out_4[6], out_4[7], out_4[8], out_4[9], out_4[10], out_4[11], out_4[12], out_4[13], out_4[14], out_4[15], out_4[16], out_4[17], out_4[18], out_4[19], out_4[20], out_4[21], out_4[22], out_4[23], out_4[24], out_4[25], out_4[26], out_4[27], out_4[28], out_4[29], out_4[30]}),
    .out_3(moneycollisiondefiner_63_out_3));
  MoneyCollisionDefiner moneycollisiondefiner_64 (
    .in_1(out_74),
    .in_2({1'b0, out_4[0], out_4[1], out_4[2], out_4[3], out_4[4], out_4[5], out_4[6], out_4[7], out_4[8], out_4[9], out_4[10], out_4[11], out_4[12], out_4[13], out_4[14], out_4[15], out_4[16], out_4[17], out_4[18], out_4[19], out_4[20], out_4[21], out_4[22], out_4[23], out_4[24], out_4[25], out_4[26], out_4[27], out_4[28], out_4[29], out_4[30]}),
    .out_3(moneycollisiondefiner_64_out_3));
  or or_54 (_17m_, _16m_a, _17m_a);
  or or_55 (_18m_, _17m_a, _18m_a);
  or or_56 (_19m_, _18m_a, _19m_a);
  or or_57 (_20m_, _19m_a, _20m_a);
  or or_58 (_21m_, _20m_a, _21m_a);
  or or_59 (_22m_, _21m_a, _22m_a);
  or or_60 (_23m_, _22m_a, _23m_a);
  or or_61 (_24m_, _23m_a, _24m_a);
  Multiplexer #(.width(31), .enable("false")) multiplexer_72 (
    .in0(31'hc000), .in1(multiplexer_70_out), .out(multiplexer_72_out), .sel(game_state));
  Multiplexer #(.width(32), .enable("false")) multiplexer_73 (
    .in0(32'h1800000), .in1(multiplexer_71_out), .out(multiplexer_73_out), .sel(game_state));
  Multiplexer #(.select(5), .enable("false")) multiplexer_74 (
    .in0(moneycollisiondefiner_33_out_3), .in1(moneycollisiondefiner_34_out_3),
    .in2(moneycollisiondefiner_35_out_3), .in3(moneycollisiondefiner_36_out_3),
    .in4(moneycollisiondefiner_37_out_3), .in5(moneycollisiondefiner_38_out_3),
    .in6(moneycollisiondefiner_39_out_3), .in7(moneycollisiondefiner_40_out_3),
    .in8(moneycollisiondefiner_41_out_3), .in9(moneycollisiondefiner_42_out_3),
    .in10(moneycollisiondefiner_43_out_3), .in11(moneycollisiondefiner_44_out_3),
    .in12(moneycollisiondefiner_45_out_3), .in13(moneycollisiondefiner_46_out_3),
    .in14(moneycollisiondefiner_47_out_3), .in15(moneycollisiondefiner_48_out_3),
    .in16(moneycollisiondefiner_49_out_3), .in17(moneycollisiondefiner_50_out_3),
    .in18(moneycollisiondefiner_51_out_3), .in19(moneycollisiondefiner_52_out_3),
    .in20(moneycollisiondefiner_53_out_3), .in21(moneycollisiondefiner_54_out_3),
    .in22(moneycollisiondefiner_55_out_3), .in23(moneycollisiondefiner_56_out_3),
    .in24(moneycollisiondefiner_57_out_3), .in25(moneycollisiondefiner_58_out_3),
    .in26(moneycollisiondefiner_59_out_3), .in27(moneycollisiondefiner_60_out_3),
    .in28(moneycollisiondefiner_61_out_3), .in29(moneycollisiondefiner_62_out_3),
    .in30(moneycollisiondefiner_63_out_3), .in31(moneycollisiondefiner_64_out_3), .out(multiplexer_74_out),
    .sel(bitfinder_2_index));
  BitFinder #(.width(32)) bitfinder_2 (.in(out_5), .index(bitfinder_2_index));  // open: found
  or or_62 (_25m_, _24m_a, _25m_a);
  or or_63 (_26m_, _25m_a, _26m_a);
  or or_64 (_27m_, _26m_a, _27m_a);
  or or_65 (_28m_, _27m_a, _28m_a);
  or or_66 (_29m_, _28m_a, _29m_a);
  or or_67 (_30m_, _29m_a, _30m_a);
  or or_68 (_31m_, _30m_a, _31m_a);
  or or_69 (_32m_, _31m_a, _32m_a);
  Register #(.width(31)) register_68 (.D(multiplexer_72_out), .Q(out_4), .clk(tact_for_player));  // open: en, clr
  Register #(.width(32)) register_69 (.D(multiplexer_73_out), .Q(out_5), .clk(tact_t));  // open: en, clr
  CollisionDefiner collisiondefiner_1 (.in_1(out_7), .in_2({1'b0, x_inverted_alt}), .out_3(collisiondefiner_1_out_3));
  CollisionDefiner collisiondefiner_2 (.in_1(out_12), .in_2({1'b0, x_inverted_alt}), .out_3(collisiondefiner_2_out_3));
  CollisionDefiner collisiondefiner_3 (.in_1(out_16), .in_2({1'b0, x_inverted_alt}), .out_3(collisiondefiner_3_out_3));
  CollisionDefiner collisiondefiner_4 (.in_1(out_20), .in_2({1'b0, x_inverted_alt}), .out_3(collisiondefiner_4_out_3));
  CollisionDefiner collisiondefiner_5 (.in_1(out_24), .in_2({1'b0, x_inverted_alt}), .out_3(collisiondefiner_5_out_3));
  CollisionDefiner collisiondefiner_6 (.in_1(out_28), .in_2({1'b0, x_inverted_alt}), .out_3(collisiondefiner_6_out_3));
  CollisionDefiner collisiondefiner_7 (.in_1(out_32), .in_2({1'b0, x_inverted_alt}), .out_3(collisiondefiner_7_out_3));
  CollisionDefiner collisiondefiner_8 (.in_1(out_36), .in_2({1'b0, x_inverted_alt}), .out_3(collisiondefiner_8_out_3));
  CollisionDefiner collisiondefiner_9 (.in_1(out_8), .in_2({1'b0, x_inverted_alt}), .out_3(collisiondefiner_9_out_3));
  CollisionDefiner collisiondefiner_10 (
    .in_1(out_13), .in_2({1'b0, x_inverted_alt}), .out_3(collisiondefiner_10_out_3));
  CollisionDefiner collisiondefiner_11 (
    .in_1(out_17), .in_2({1'b0, x_inverted_alt}), .out_3(collisiondefiner_11_out_3));
  CollisionDefiner collisiondefiner_12 (
    .in_1(out_21), .in_2({1'b0, x_inverted_alt}), .out_3(collisiondefiner_12_out_3));
  CollisionDefiner collisiondefiner_13 (
    .in_1(out_25), .in_2({1'b0, x_inverted_alt}), .out_3(collisiondefiner_13_out_3));
  CollisionDefiner collisiondefiner_14 (
    .in_1(out_29), .in_2({1'b0, x_inverted_alt}), .out_3(collisiondefiner_14_out_3));
  CollisionDefiner collisiondefiner_15 (
    .in_1(out_33), .in_2({1'b0, x_inverted_alt}), .out_3(collisiondefiner_15_out_3));
  CollisionDefiner collisiondefiner_16 (
    .in_1(out_37), .in_2({1'b0, x_inverted_alt}), .out_3(collisiondefiner_16_out_3));
  CollisionDefiner collisiondefiner_17 (.in_1(out_9), .in_2({1'b0, x_inverted_alt}), .out_3(collisiondefiner_17_out_3));
  CollisionDefiner collisiondefiner_18 (
    .in_1(out_14), .in_2({1'b0, x_inverted_alt}), .out_3(collisiondefiner_18_out_3));
  CollisionDefiner collisiondefiner_19 (
    .in_1(out_18), .in_2({1'b0, x_inverted_alt}), .out_3(collisiondefiner_19_out_3));
  CollisionDefiner collisiondefiner_20 (
    .in_1(out_22), .in_2({1'b0, x_inverted_alt}), .out_3(collisiondefiner_20_out_3));
  CollisionDefiner collisiondefiner_21 (
    .in_1(out_26), .in_2({1'b0, x_inverted_alt}), .out_3(collisiondefiner_21_out_3));
  CollisionDefiner collisiondefiner_22 (
    .in_1(out_30), .in_2({1'b0, x_inverted_alt}), .out_3(collisiondefiner_22_out_3));
  CollisionDefiner collisiondefiner_23 (
    .in_1(out_34), .in_2({1'b0, x_inverted_alt}), .out_3(collisiondefiner_23_out_3));
  CollisionDefiner collisiondefiner_24 (
    .in_1(out_38), .in_2({1'b0, x_inverted_alt}), .out_3(collisiondefiner_24_out_3));
  CollisionDefiner collisiondefiner_25 (
    .in_1(out_10), .in_2({1'b0, x_inverted_alt}), .out_3(collisiondefiner_25_out_3));
  CollisionDefiner collisiondefiner_26 (
    .in_1(out_15), .in_2({1'b0, x_inverted_alt}), .out_3(collisiondefiner_26_out_3));
  CollisionDefiner collisiondefiner_27 (
    .in_1(out_19), .in_2({1'b0, x_inverted_alt}), .out_3(collisiondefiner_27_out_3));
  CollisionDefiner collisiondefiner_28 (
    .in_1(out_23), .in_2({1'b0, x_inverted_alt}), .out_3(collisiondefiner_28_out_3));
  CollisionDefiner collisiondefiner_29 (
    .in_1(out_27), .in_2({1'b0, x_inverted_alt}), .out_3(collisiondefiner_29_out_3));
  CollisionDefiner collisiondefiner_30 (
    .in_1(out_31), .in_2({1'b0, x_inverted_alt}), .out_3(collisiondefiner_30_out_3));
  CollisionDefiner collisiondefiner_31 (
    .in_1(out_35), .in_2({1'b0, x_inverted_alt}), .out_3(collisiondefiner_31_out_3));
  CollisionDefiner collisiondefiner_32 (
    .in_1(out_39), .in_2({1'b0, x_inverted_alt}), .out_3(collisiondefiner_32_out_3));
  BitFinder #(.width(32), .\type ("high1")) bitfinder_3 (.in(out_5), .index(bitfinder_3_index));  // open: found
  Multiplexer #(.width(31), .enable("false")) multiplexer_75 (
    .in0({31{1'b0}}), .in1(shifter_2_out), .out(multiplexer_75_out), .sel(left));
  Shifter #(.width(31), .shift("lr")) shifter_2 (.in(out_4), .\dist (5'b00001), .out(shifter_2_out));
  Multiplexer #(.width(31), .enable("false")) multiplexer_76 (
    .in0({31{1'b0}}), .in1(shifter_3_out), .out(multiplexer_76_out), .sel(right));
  Shifter #(.width(31)) shifter_3 (.in(out_4), .\dist (5'b00001), .out(shifter_3_out));
  Multiplexer #(.width(32), .enable("false")) multiplexer_77 (
    .in0({32{1'b0}}), .in1(shifter_4_out), .out(multiplexer_77_out), .sel(down));
  Shifter #(.width(32), .shift("lr")) shifter_4 (.in(out_5), .\dist (5'b00001), .out(shifter_4_out));
  Multiplexer #(.width(32), .enable("false")) multiplexer_78 (
    .in0({32{1'b0}}), .in1(shifter_5_out), .out(multiplexer_78_out), .sel(not_10_out));
  Shifter #(.width(32)) shifter_5 (.in(out_5), .\dist (5'b00001), .out(shifter_5_out));
  not not_10 (not_10_out, down);
  and and_2 (x_cond, multiplexer_79_out, multiplexer_80_out);
  CollisionDefiner collisiondefiner_33 (.in_1(out_7), .in_2({1'b0, x_inverted_alt}), .out_3(collisiondefiner_33_out_3));
  CollisionDefiner collisiondefiner_34 (
    .in_1(out_12), .in_2({1'b0, x_inverted_alt}), .out_3(collisiondefiner_34_out_3));
  CollisionDefiner collisiondefiner_35 (
    .in_1(out_16), .in_2({1'b0, x_inverted_alt}), .out_3(collisiondefiner_35_out_3));
  CollisionDefiner collisiondefiner_36 (
    .in_1(out_20), .in_2({1'b0, x_inverted_alt}), .out_3(collisiondefiner_36_out_3));
  CollisionDefiner collisiondefiner_37 (
    .in_1(out_24), .in_2({1'b0, x_inverted_alt}), .out_3(collisiondefiner_37_out_3));
  CollisionDefiner collisiondefiner_38 (
    .in_1(out_28), .in_2({1'b0, x_inverted_alt}), .out_3(collisiondefiner_38_out_3));
  CollisionDefiner collisiondefiner_39 (
    .in_1(out_32), .in_2({1'b0, x_inverted_alt}), .out_3(collisiondefiner_39_out_3));
  CollisionDefiner collisiondefiner_40 (
    .in_1(out_36), .in_2({1'b0, x_inverted_alt}), .out_3(collisiondefiner_40_out_3));
  CollisionDefiner collisiondefiner_41 (.in_1(out_8), .in_2({1'b0, x_inverted_alt}), .out_3(collisiondefiner_41_out_3));
  CollisionDefiner collisiondefiner_42 (
    .in_1(out_13), .in_2({1'b0, x_inverted_alt}), .out_3(collisiondefiner_42_out_3));
  CollisionDefiner collisiondefiner_43 (
    .in_1(out_17), .in_2({1'b0, x_inverted_alt}), .out_3(collisiondefiner_43_out_3));
  CollisionDefiner collisiondefiner_44 (
    .in_1(out_21), .in_2({1'b0, x_inverted_alt}), .out_3(collisiondefiner_44_out_3));
  CollisionDefiner collisiondefiner_45 (
    .in_1(out_25), .in_2({1'b0, x_inverted_alt}), .out_3(collisiondefiner_45_out_3));
  CollisionDefiner collisiondefiner_46 (
    .in_1(out_29), .in_2({1'b0, x_inverted_alt}), .out_3(collisiondefiner_46_out_3));
  CollisionDefiner collisiondefiner_47 (
    .in_1(out_33), .in_2({1'b0, x_inverted_alt}), .out_3(collisiondefiner_47_out_3));
  CollisionDefiner collisiondefiner_48 (
    .in_1(out_37), .in_2({1'b0, x_inverted_alt}), .out_3(collisiondefiner_48_out_3));
  CollisionDefiner collisiondefiner_49 (.in_1(out_9), .in_2({1'b0, x_inverted_alt}), .out_3(collisiondefiner_49_out_3));
  Multiplexer #(.select(5), .enable("false")) multiplexer_79 (
    .in0(collisiondefiner_1_out_3), .in1(collisiondefiner_2_out_3), .in2(collisiondefiner_3_out_3),
    .in3(collisiondefiner_4_out_3), .in4(collisiondefiner_5_out_3), .in5(collisiondefiner_6_out_3),
    .in6(collisiondefiner_7_out_3), .in7(collisiondefiner_8_out_3), .in8(collisiondefiner_9_out_3),
    .in9(collisiondefiner_10_out_3), .in10(collisiondefiner_11_out_3), .in11(collisiondefiner_12_out_3),
    .in12(collisiondefiner_13_out_3), .in13(collisiondefiner_14_out_3), .in14(collisiondefiner_15_out_3),
    .in15(collisiondefiner_16_out_3), .in16(collisiondefiner_17_out_3), .in17(collisiondefiner_18_out_3),
    .in18(collisiondefiner_19_out_3), .in19(collisiondefiner_20_out_3), .in20(collisiondefiner_21_out_3),
    .in21(collisiondefiner_22_out_3), .in22(collisiondefiner_23_out_3), .in23(collisiondefiner_24_out_3),
    .in24(collisiondefiner_25_out_3), .in25(collisiondefiner_26_out_3), .in26(collisiondefiner_27_out_3),
    .in27(collisiondefiner_28_out_3), .in28(collisiondefiner_29_out_3), .in29(collisiondefiner_30_out_3),
    .in30(collisiondefiner_31_out_3), .in31(collisiondefiner_32_out_3), .out(multiplexer_79_out),
    .sel(bitfinder_3_index));
  CollisionDefiner collisiondefiner_50 (
    .in_1(out_14), .in_2({1'b0, x_inverted_alt}), .out_3(collisiondefiner_50_out_3));
  CollisionDefiner collisiondefiner_51 (
    .in_1(out_18), .in_2({1'b0, x_inverted_alt}), .out_3(collisiondefiner_51_out_3));
  CollisionDefiner collisiondefiner_52 (
    .in_1(out_22), .in_2({1'b0, x_inverted_alt}), .out_3(collisiondefiner_52_out_3));
  CollisionDefiner collisiondefiner_53 (
    .in_1(out_26), .in_2({1'b0, x_inverted_alt}), .out_3(collisiondefiner_53_out_3));
  CollisionDefiner collisiondefiner_54 (
    .in_1(out_30), .in_2({1'b0, x_inverted_alt}), .out_3(collisiondefiner_54_out_3));
  CollisionDefiner collisiondefiner_55 (
    .in_1(out_34), .in_2({1'b0, x_inverted_alt}), .out_3(collisiondefiner_55_out_3));
  CollisionDefiner collisiondefiner_56 (
    .in_1(out_38), .in_2({1'b0, x_inverted_alt}), .out_3(collisiondefiner_56_out_3));
  CollisionDefiner collisiondefiner_57 (
    .in_1(out_10), .in_2({1'b0, x_inverted_alt}), .out_3(collisiondefiner_57_out_3));
  CollisionDefiner collisiondefiner_58 (
    .in_1(out_15), .in_2({1'b0, x_inverted_alt}), .out_3(collisiondefiner_58_out_3));
  CollisionDefiner collisiondefiner_59 (
    .in_1(out_19), .in_2({1'b0, x_inverted_alt}), .out_3(collisiondefiner_59_out_3));
  CollisionDefiner collisiondefiner_60 (
    .in_1(out_23), .in_2({1'b0, x_inverted_alt}), .out_3(collisiondefiner_60_out_3));
  CollisionDefiner collisiondefiner_61 (
    .in_1(out_27), .in_2({1'b0, x_inverted_alt}), .out_3(collisiondefiner_61_out_3));
  CollisionDefiner collisiondefiner_62 (
    .in_1(out_31), .in_2({1'b0, x_inverted_alt}), .out_3(collisiondefiner_62_out_3));
  CollisionDefiner collisiondefiner_63 (
    .in_1(out_35), .in_2({1'b0, x_inverted_alt}), .out_3(collisiondefiner_63_out_3));
  CollisionDefiner collisiondefiner_64 (
    .in_1(out_39), .in_2({1'b0, x_inverted_alt}), .out_3(collisiondefiner_64_out_3));
  Keyboard #(.buflen(1)) keyboard_1 (.clk(tact));  // open: re, clr, avail, data
  assign {x_inverted_alt[0], x_inverted_alt[1], x_inverted_alt[2], x_inverted_alt[3], x_inverted_alt[4], x_inverted_alt[5], x_inverted_alt[6], x_inverted_alt[7], x_inverted_alt[8], x_inverted_alt[9], x_inverted_alt[10], x_inverted_alt[11], x_inverted_alt[12], x_inverted_alt[13], x_inverted_alt[14], x_inverted_alt[15], x_inverted_alt[16], x_inverted_alt[17], x_inverted_alt[18], x_inverted_alt[19], x_inverted_alt[20], x_inverted_alt[21], x_inverted_alt[22], x_inverted_alt[23], x_inverted_alt[24], x_inverted_alt[25], x_inverted_alt[26], x_inverted_alt[27], x_inverted_alt[28], x_inverted_alt[29], x_inverted_alt[30]} = multiplexer_75_out | multiplexer_76_out;  // OR_Gate or_70, 31 bits wide
  not not_11 (not_11_out, x_inverted_alt[29]);
  not not_12 (not_12_out, x_inverted_alt[0]);
  or or_71 (or_71_out, not_12_out, x_inverted_alt[1]);
  assign or_72_out = multiplexer_77_out | multiplexer_78_out;  // OR_Gate or_72, 32 bits wide
  Multiplexer #(.select(5), .enable("false")) multiplexer_80 (
    .in0(collisiondefiner_33_out_3), .in1(collisiondefiner_34_out_3), .in2(collisiondefiner_35_out_3),
    .in3(collisiondefiner_36_out_3), .in4(collisiondefiner_37_out_3), .in5(collisiondefiner_38_out_3),
    .in6(collisiondefiner_39_out_3), .in7(collisiondefiner_40_out_3), .in8(collisiondefiner_41_out_3),
    .in9(collisiondefiner_42_out_3), .in10(collisiondefiner_43_out_3), .in11(collisiondefiner_44_out_3),
    .in12(collisiondefiner_45_out_3), .in13(collisiondefiner_46_out_3), .in14(collisiondefiner_47_out_3),
    .in15(collisiondefiner_48_out_3), .in16(collisiondefiner_49_out_3), .in17(collisiondefiner_50_out_3),
    .in18(collisiondefiner_51_out_3), .in19(collisiondefiner_52_out_3), .in20(collisiondefiner_53_out_3),
    .in21(collisiondefiner_54_out_3), .in22(collisiondefiner_55_out_3), .in23(collisiondefiner_56_out_3),
    .in24(collisiondefiner_57_out_3), .in25(collisiondefiner_58_out_3), .in26(collisiondefiner_59_out_3),
    .in27(collisiondefiner_60_out_3), .in28(collisiondefiner_61_out_3), .in29(collisiondefiner_62_out_3),
    .in30(collisiondefiner_63_out_3), .in31(collisiondefiner_64_out_3), .out(multiplexer_80_out),
    .sel(bitfinder_4_index));
  BitFinder #(.width(32)) bitfinder_4 (.in(out_5), .index(bitfinder_4_index));  // open: found
  not not_13 (start_t, game_state);
  DotMatrix #(.inputtype("row"), .matrixcols(30), .matrixrows(32), .dotshape("circle")) dotmatrix_1 (
    .row0(out_74), .row1(out_70), .row2(out_66), .row3(out_62), .row4(out_58), .row5(out_54), .row6(out_50),
    .row7(out_46), .row8(out_73), .row9(out_69), .row10(out_65), .row11(out_61), .row12(out_57),
    .row13(out_53), .row14(out_49), .row15(out_45), .row16(out_72), .row17(out_68), .row18(out_64),
    .row19(out_60), .row20(out_56), .row21(out_52), .row22(out_48), .row23(out_44), .row24(out_71),
    .row25(out_67), .row26(out_63), .row27(out_59), .row28(out_55), .row29(out_51), .row30(out_47),
    .row31(out_43));
  DotMatrix #(.inputtype("row"), .matrixcols(32), .matrixrows(32)) dotmatrix_2 (
    .row0(out_39), .row1(out_35), .row2(out_31), .row3(out_27), .row4(out_23), .row5(out_19), .row6(out_15),
    .row7(out_10), .row8(out_38), .row9(out_34), .row10(out_30), .row11(out_26), .row12(out_22),
    .row13(out_18), .row14(out_14), .row15(out_9), .row16(out_37), .row17(out_33), .row18(out_29),
    .row19(out_25), .row20(out_21), .row21(out_17), .row22(out_13), .row23(out_8), .row24(out_36),
    .row25(out_32), .row26(out_28), .row27(out_24), .row28(out_20), .row29(out_16), .row30(out_12),
    .row31(out_7));
  // DotMatrix #(.inputtype("select"), .matrixcols(31), .matrixrows(32)) dotmatrix_3: pin names not known; wires that end beside it: out_4, out_5
  and and_3 (and_3_out, x_cond, or_73_out, or_71_out, not_15_out);
  or or_73 (or_73_out, not_11_out, x_inverted_alt[28]);
  not not_14 (not_14_out, comparator_5_eq);
  Comparator #(.width(32)) comparator_5 (.a(or_72_out), .b({32{1'b0}}), .eq(comparator_5_eq));  // open: gt, lt
  Multiplexer #(.width(31), .enable("false")) multiplexer_81 (
    .in0(out_4),
    .in1({x_inverted_alt[0], x_inverted_alt[1], x_inverted_alt[2], x_inverted_alt[3], x_inverted_alt[4], x_inverted_alt[5], x_inverted_alt[6], x_inverted_alt[7], x_inverted_alt[8], x_inverted_alt[9], x_inverted_alt[10], x_inverted_alt[11], x_inverted_alt[12], x_inverted_alt[13], x_inverted_alt[14], x_inverted_alt[15], x_inverted_alt[16], x_inverted_alt[17], x_inverted_alt[18], x_inverted_alt[19], x_inverted_alt[20], x_inverted_alt[21], x_inverted_alt[22], x_inverted_alt[23], x_inverted_alt[24], x_inverted_alt[25], x_inverted_alt[26], x_inverted_alt[27], x_inverted_alt[28], x_inverted_alt[29], x_inverted_alt[30]}),
    .out(x_final), .sel(and_3_out));
  not not_15 (not_15_out, comparator_6_eq);
  Comparator #(.width(31)) comparator_6 (
    .a({x_inverted_alt[0], x_inverted_alt[1], x_inverted_alt[2], x_inverted_alt[3], x_inverted_alt[4], x_inverted_alt[5], x_inverted_alt[6], x_inverted_alt[7], x_inverted_alt[8], x_inverted_alt[9], x_inverted_alt[10], x_inverted_alt[11], x_inverted_alt[12], x_inverted_alt[13], x_inverted_alt[14], x_inverted_alt[15], x_inverted_alt[16], x_inverted_alt[17], x_inverted_alt[18], x_inverted_alt[19], x_inverted_alt[20], x_inverted_alt[21], x_inverted_alt[22], x_inverted_alt[23], x_inverted_alt[24], x_inverted_alt[25], x_inverted_alt[26], x_inverted_alt[27], x_inverted_alt[28], x_inverted_alt[29], x_inverted_alt[30]}),
    .b({31{1'b0}}), .eq(comparator_6_eq));  // open: gt, lt
  Multiplexer #(.width(32), .enable("false")) multiplexer_82 (
    .in0(out_5), .in1(or_72_out), .out(y_final), .sel(not_14_out));
  StateDefiner statedefiner_1 (.start_stop(Start), .state_of_game(game_state), .lose(Lose_east));
  KIM kim_1 (.keyboard(keyboard), .right(right), .left(left), .start(Start), .pause(Pause));
  CollisionDefiner collisiondefiner_65 (
    .in_1(out_7),
    .in_2({1'b0, x_final[0], x_final[1], x_final[2], x_final[3], x_final[4], x_final[5], x_final[6], x_final[7], x_final[8], x_final[9], x_final[10], x_final[11], x_final[12], x_final[13], x_final[14], x_final[15], x_final[16], x_final[17], x_final[18], x_final[19], x_final[20], x_final[21], x_final[22], x_final[23], x_final[24], x_final[25], x_final[26], x_final[27], x_final[28], x_final[29], x_final[30]}),
    .out_3(collisiondefiner_65_out_3));
  CollisionDefiner collisiondefiner_66 (
    .in_1(out_12),
    .in_2({1'b0, x_final[0], x_final[1], x_final[2], x_final[3], x_final[4], x_final[5], x_final[6], x_final[7], x_final[8], x_final[9], x_final[10], x_final[11], x_final[12], x_final[13], x_final[14], x_final[15], x_final[16], x_final[17], x_final[18], x_final[19], x_final[20], x_final[21], x_final[22], x_final[23], x_final[24], x_final[25], x_final[26], x_final[27], x_final[28], x_final[29], x_final[30]}),
    .out_3(collisiondefiner_66_out_3));
  CollisionDefiner collisiondefiner_67 (
    .in_1(out_16),
    .in_2({1'b0, x_final[0], x_final[1], x_final[2], x_final[3], x_final[4], x_final[5], x_final[6], x_final[7], x_final[8], x_final[9], x_final[10], x_final[11], x_final[12], x_final[13], x_final[14], x_final[15], x_final[16], x_final[17], x_final[18], x_final[19], x_final[20], x_final[21], x_final[22], x_final[23], x_final[24], x_final[25], x_final[26], x_final[27], x_final[28], x_final[29], x_final[30]}),
    .out_3(collisiondefiner_67_out_3));
  CollisionDefiner collisiondefiner_68 (
    .in_1(out_20),
    .in_2({1'b0, x_final[0], x_final[1], x_final[2], x_final[3], x_final[4], x_final[5], x_final[6], x_final[7], x_final[8], x_final[9], x_final[10], x_final[11], x_final[12], x_final[13], x_final[14], x_final[15], x_final[16], x_final[17], x_final[18], x_final[19], x_final[20], x_final[21], x_final[22], x_final[23], x_final[24], x_final[25], x_final[26], x_final[27], x_final[28], x_final[29], x_final[30]}),
    .out_3(collisiondefiner_68_out_3));
  CollisionDefiner collisiondefiner_69 (
    .in_1(out_24),
    .in_2({1'b0, x_final[0], x_final[1], x_final[2], x_final[3], x_final[4], x_final[5], x_final[6], x_final[7], x_final[8], x_final[9], x_final[10], x_final[11], x_final[12], x_final[13], x_final[14], x_final[15], x_final[16], x_final[17], x_final[18], x_final[19], x_final[20], x_final[21], x_final[22], x_final[23], x_final[24], x_final[25], x_final[26], x_final[27], x_final[28], x_final[29], x_final[30]}),
    .out_3(collisiondefiner_69_out_3));
  CollisionDefiner collisiondefiner_70 (
    .in_1(out_28),
    .in_2({1'b0, x_final[0], x_final[1], x_final[2], x_final[3], x_final[4], x_final[5], x_final[6], x_final[7], x_final[8], x_final[9], x_final[10], x_final[11], x_final[12], x_final[13], x_final[14], x_final[15], x_final[16], x_final[17], x_final[18], x_final[19], x_final[20], x_final[21], x_final[22], x_final[23], x_final[24], x_final[25], x_final[26], x_final[27], x_final[28], x_final[29], x_final[30]}),
    .out_3(collisiondefiner_70_out_3));
  CollisionDefiner collisiondefiner_71 (
    .in_1(out_32),
    .in_2({1'b0, x_final[0], x_final[1], x_final[2], x_final[3], x_final[4], x_final[5], x_final[6], x_final[7], x_final[8], x_final[9], x_final[10], x_final[11], x_final[12], x_final[13], x_final[14], x_final[15], x_final[16], x_final[17], x_final[18], x_final[19], x_final[20], x_final[21], x_final[22], x_final[23], x_final[24], x_final[25], x_final[26], x_final[27], x_final[28], x_final[29], x_final[30]}),
    .out_3(collisiondefiner_71_out_3));
  CollisionDefiner collisiondefiner_72 (
    .in_1(out_36),
    .in_2({1'b0, x_final[0], x_final[1], x_final[2], x_final[3], x_final[4], x_final[5], x_final[6], x_final[7], x_final[8], x_final[9], x_final[10], x_final[11], x_final[12], x_final[13], x_final[14], x_final[15], x_final[16], x_final[17], x_final[18], x_final[19], x_final[20], x_final[21], x_final[22], x_final[23], x_final[24], x_final[25], x_final[26], x_final[27], x_final[28], x_final[29], x_final[30]}),
    .out_3(collisiondefiner_72_out_3));
  CollisionDefiner collisiondefiner_73 (
    .in_1(out_8),
    .in_2({1'b0, x_final[0], x_final[1], x_final[2], x_final[3], x_final[4], x_final[5], x_final[6], x_final[7], x_final[8], x_final[9], x_final[10], x_final[11], x_final[12], x_final[13], x_final[14], x_final[15], x_final[16], x_final[17], x_final[18], x_final[19], x_final[20], x_final[21], x_final[22], x_final[23], x_final[24], x_final[25], x_final[26], x_final[27], x_final[28], x_final[29], x_final[30]}),
    .out_3(collisiondefiner_73_out_3));
  CollisionDefiner collisiondefiner_74 (
    .in_1(out_13),
    .in_2({1'b0, x_final[0], x_final[1], x_final[2], x_final[3], x_final[4], x_final[5], x_final[6], x_final[7], x_final[8], x_final[9], x_final[10], x_final[11], x_final[12], x_final[13], x_final[14], x_final[15], x_final[16], x_final[17], x_final[18], x_final[19], x_final[20], x_final[21], x_final[22], x_final[23], x_final[24], x_final[25], x_final[26], x_final[27], x_final[28], x_final[29], x_final[30]}),
    .out_3(collisiondefiner_74_out_3));
  CollisionDefiner collisiondefiner_75 (
    .in_1(out_17),
    .in_2({1'b0, x_final[0], x_final[1], x_final[2], x_final[3], x_final[4], x_final[5], x_final[6], x_final[7], x_final[8], x_final[9], x_final[10], x_final[11], x_final[12], x_final[13], x_final[14], x_final[15], x_final[16], x_final[17], x_final[18], x_final[19], x_final[20], x_final[21], x_final[22], x_final[23], x_final[24], x_final[25], x_final[26], x_final[27], x_final[28], x_final[29], x_final[30]}),
    .out_3(collisiondefiner_75_out_3));
  CollisionDefiner collisiondefiner_76 (
    .in_1(out_21),
    .in_2({1'b0, x_final[0], x_final[1], x_final[2], x_final[3], x_final[4], x_final[5], x_final[6], x_final[7], x_final[8], x_final[9], x_final[10], x_final[11], x_final[12], x_final[13], x_final[14], x_final[15], x_final[16], x_final[17], x_final[18], x_final[19], x_final[20], x_final[21], x_final[22], x_final[23], x_final[24], x_final[25], x_final[26], x_final[27], x_final[28], x_final[29], x_final[30]}),
    .out_3(collisiondefiner_76_out_3));
  CollisionDefiner collisiondefiner_77 (
    .in_1(out_25),
    .in_2({1'b0, x_final[0], x_final[1], x_final[2], x_final[3], x_final[4], x_final[5], x_final[6], x_final[7], x_final[8], x_final[9], x_final[10], x_final[11], x_final[12], x_final[13], x_final[14], x_final[15], x_final[16], x_final[17], x_final[18], x_final[19], x_final[20], x_final[21], x_final[22], x_final[23], x_final[24], x_final[25], x_final[26], x_final[27], x_final[28], x_final[29], x_final[30]}),
    .out_3(collisiondefiner_77_out_3));
  CollisionDefiner collisiondefiner_78 (
    .in_1(out_29),
    .in_2({1'b0, x_final[0], x_final[1], x_final[2], x_final[3], x_final[4], x_final[5], x_final[6], x_final[7], x_final[8], x_final[9], x_final[10], x_final[11], x_final[12], x_final[13], x_final[14], x_final[15], x_final[16], x_final[17], x_final[18], x_final[19], x_final[20], x_final[21], x_final[22], x_final[23], x_final[24], x_final[25], x_final[26], x_final[27], x_final[28], x_final[29], x_final[30]}),
    .out_3(collisiondefiner_78_out_3));
  CollisionDefiner collisiondefiner_79 (
    .in_1(out_33),
    .in_2({1'b0, x_final[0], x_final[1], x_final[2], x_final[3], x_final[4], x_final[5], x_final[6], x_final[7], x_final[8], x_final[9], x_final[10], x_final[11], x_final[12], x_final[13], x_final[14], x_final[15], x_final[16], x_final[17], x_final[18], x_final[19], x_final[20], x_final[21], x_final[22], x_final[23], x_final[24], x_final[25], x_final[26], x_final[27], x_final[28], x_final[29], x_final[30]}),
    .out_3(collisiondefiner_79_out_3));
  CollisionDefiner collisiondefiner_80 (
    .in_1(out_37),
    .in_2({1'b0, x_final[0], x_final[1], x_final[2], x_final[3], x_final[4], x_final[5], x_final[6], x_final[7], x_final[8], x_final[9], x_final[10], x_final[11], x_final[12], x_final[13], x_final[14], x_final[15], x_final[16], x_final[17], x_final[18], x_final[19], x_final[20], x_final[21], x_final[22], x_final[23], x_final[24], x_final[25], x_final[26], x_final[27], x_final[28], x_final[29], x_final[30]}),
    .out_3(collisiondefiner_80_out_3));
  CollisionDefiner collisiondefiner_81 (
    .in_1(out_9),
    .in_2({1'b0, x_final[0], x_final[1], x_final[2], x_final[3], x_final[4], x_final[5], x_final[6], x_final[7], x_final[8], x_final[9], x_final[10], x_final[11], x_final[12], x_final[13], x_final[14], x_final[15], x_final[16], x_final[17], x_final[18], x_final[19], x_final[20], x_final[21], x_final[22], x_final[23], x_final[24], x_final[25], x_final[26], x_final[27], x_final[28], x_final[29], x_final[30]}),
    .out_3(collisiondefiner_81_out_3));
  CollisionDefiner collisiondefiner_82 (
    .in_1(out_14),
    .in_2({1'b0, x_final[0], x_final[1], x_final[2], x_final[3], x_final[4], x_final[5], x_final[6], x_final[7], x_final[8], x_final[9], x_final[10], x_final[11], x_final[12], x_final[13], x_final[14], x_final[15], x_final[16], x_final[17], x_final[18], x_final[19], x_final[20], x_final[21], x_final[22], x_final[23], x_final[24], x_final[25], x_final[26], x_final[27], x_final[28], x_final[29], x_final[30]}),
    .out_3(collisiondefiner_82_out_3));
  CollisionDefiner collisiondefiner_83 (
    .in_1(out_18),
    .in_2({1'b0, x_final[0], x_final[1], x_final[2], x_final[3], x_final[4], x_final[5], x_final[6], x_final[7], x_final[8], x_final[9], x_final[10], x_final[11], x_final[12], x_final[13], x_final[14], x_final[15], x_final[16], x_final[17], x_final[18], x_final[19], x_final[20], x_final[21], x_final[22], x_final[23], x_final[24], x_final[25], x_final[26], x_final[27], x_final[28], x_final[29], x_final[30]}),
    .out_3(collisiondefiner_83_out_3));
  CollisionDefiner collisiondefiner_84 (
    .in_1(out_22),
    .in_2({1'b0, x_final[0], x_final[1], x_final[2], x_final[3], x_final[4], x_final[5], x_final[6], x_final[7], x_final[8], x_final[9], x_final[10], x_final[11], x_final[12], x_final[13], x_final[14], x_final[15], x_final[16], x_final[17], x_final[18], x_final[19], x_final[20], x_final[21], x_final[22], x_final[23], x_final[24], x_final[25], x_final[26], x_final[27], x_final[28], x_final[29], x_final[30]}),
    .out_3(collisiondefiner_84_out_3));
  CollisionDefiner collisiondefiner_85 (
    .in_1(out_26),
    .in_2({1'b0, x_final[0], x_final[1], x_final[2], x_final[3], x_final[4], x_final[5], x_final[6], x_final[7], x_final[8], x_final[9], x_final[10], x_final[11], x_final[12], x_final[13], x_final[14], x_final[15], x_final[16], x_final[17], x_final[18], x_final[19], x_final[20], x_final[21], x_final[22], x_final[23], x_final[24], x_final[25], x_final[26], x_final[27], x_final[28], x_final[29], x_final[30]}),
    .out_3(collisiondefiner_85_out_3));
  CollisionDefiner collisiondefiner_86 (
    .in_1(out_30),
    .in_2({1'b0, x_final[0], x_final[1], x_final[2], x_final[3], x_final[4], x_final[5], x_final[6], x_final[7], x_final[8], x_final[9], x_final[10], x_final[11], x_final[12], x_final[13], x_final[14], x_final[15], x_final[16], x_final[17], x_final[18], x_final[19], x_final[20], x_final[21], x_final[22], x_final[23], x_final[24], x_final[25], x_final[26], x_final[27], x_final[28], x_final[29], x_final[30]}),
    .out_3(collisiondefiner_86_out_3));
  CollisionDefiner collisiondefiner_87 (
    .in_1(out_34),
    .in_2({1'b0, x_final[0], x_final[1], x_final[2], x_final[3], x_final[4], x_final[5], x_final[6], x_final[7], x_final[8], x_final[9], x_final[10], x_final[11], x_final[12], x_final[13], x_final[14], x_final[15], x_final[16], x_final[17], x_final[18], x_final[19], x_final[20], x_final[21], x_final[22], x_final[23], x_final[24], x_final[25], x_final[26], x_final[27], x_final[28], x_final[29], x_final[30]}),
    .out_3(collisiondefiner_87_out_3));
  CollisionDefiner collisiondefiner_88 (
    .in_1(out_38),
    .in_2({1'b0, x_final[0], x_final[1], x_final[2], x_final[3], x_final[4], x_final[5], x_final[6], x_final[7], x_final[8], x_final[9], x_final[10], x_final[11], x_final[12], x_final[13], x_final[14], x_final[15], x_final[16], x_final[17], x_final[18], x_final[19], x_final[20], x_final[21], x_final[22], x_final[23], x_final[24], x_final[25], x_final[26], x_final[27], x_final[28], x_final[29], x_final[30]}),
    .out_3(collisiondefiner_88_out_3));
  CollisionDefiner collisiondefiner_89 (
    .in_1(out_10),
    .in_2({1'b0, x_final[0], x_final[1], x_final[2], x_final[3], x_final[4], x_final[5], x_final[6], x_final[7], x_final[8], x_final[9], x_final[10], x_final[11], x_final[12], x_final[13], x_final[14], x_final[15], x_final[16], x_final[17], x_final[18], x_final[19], x_final[20], x_final[21], x_final[22], x_final[23], x_final[24], x_final[25], x_final[26], x_final[27], x_final[28], x_final[29], x_final[30]}),
    .out_3(collisiondefiner_89_out_3));
  CollisionDefiner collisiondefiner_90 (
    .in_1(out_15),
    .in_2({1'b0, x_final[0], x_final[1], x_final[2], x_final[3], x_final[4], x_final[5], x_final[6], x_final[7], x_final[8], x_final[9], x_final[10], x_final[11], x_final[12], x_final[13], x_final[14], x_final[15], x_final[16], x_final[17], x_final[18], x_final[19], x_final[20], x_final[21], x_final[22], x_final[23], x_final[24], x_final[25], x_final[26], x_final[27], x_final[28], x_final[29], x_final[30]}),
    .out_3(collisiondefiner_90_out_3));
  CollisionDefiner collisiondefiner_91 (
    .in_1(out_19),
    .in_2({1'b0, x_final[0], x_final[1], x_final[2], x_final[3], x_final[4], x_final[5], x_final[6], x_final[7], x_final[8], x_final[9], x_final[10], x_final[11], x_final[12], x_final[13], x_final[14], x_final[15], x_final[16], x_final[17], x_final[18], x_final[19], x_final[20], x_final[21], x_final[22], x_final[23], x_final[24], x_final[25], x_final[26], x_final[27], x_final[28], x_final[29], x_final[30]}),
    .out_3(collisiondefiner_91_out_3));
  CollisionDefiner collisiondefiner_92 (
    .in_1(out_23),
    .in_2({1'b0, x_final[0], x_final[1], x_final[2], x_final[3], x_final[4], x_final[5], x_final[6], x_final[7], x_final[8], x_final[9], x_final[10], x_final[11], x_final[12], x_final[13], x_final[14], x_final[15], x_final[16], x_final[17], x_final[18], x_final[19], x_final[20], x_final[21], x_final[22], x_final[23], x_final[24], x_final[25], x_final[26], x_final[27], x_final[28], x_final[29], x_final[30]}),
    .out_3(collisiondefiner_92_out_3));
  CollisionDefiner collisiondefiner_93 (
    .in_1(out_27),
    .in_2({1'b0, x_final[0], x_final[1], x_final[2], x_final[3], x_final[4], x_final[5], x_final[6], x_final[7], x_final[8], x_final[9], x_final[10], x_final[11], x_final[12], x_final[13], x_final[14], x_final[15], x_final[16], x_final[17], x_final[18], x_final[19], x_final[20], x_final[21], x_final[22], x_final[23], x_final[24], x_final[25], x_final[26], x_final[27], x_final[28], x_final[29], x_final[30]}),
    .out_3(collisiondefiner_93_out_3));
  CollisionDefiner collisiondefiner_94 (
    .in_1(out_31),
    .in_2({1'b0, x_final[0], x_final[1], x_final[2], x_final[3], x_final[4], x_final[5], x_final[6], x_final[7], x_final[8], x_final[9], x_final[10], x_final[11], x_final[12], x_final[13], x_final[14], x_final[15], x_final[16], x_final[17], x_final[18], x_final[19], x_final[20], x_final[21], x_final[22], x_final[23], x_final[24], x_final[25], x_final[26], x_final[27], x_final[28], x_final[29], x_final[30]}),
    .out_3(collisiondefiner_94_out_3));
  CollisionDefiner collisiondefiner_95 (
    .in_1(out_35),
    .in_2({1'b0, x_final[0], x_final[1], x_final[2], x_final[3], x_final[4], x_final[5], x_final[6], x_final[7], x_final[8], x_final[9], x_final[10], x_final[11], x_final[12], x_final[13], x_final[14], x_final[15], x_final[16], x_final[17], x_final[18], x_final[19], x_final[20], x_final[21], x_final[22], x_final[23], x_final[24], x_final[25], x_final[26], x_final[27], x_final[28], x_final[29], x_final[30]}),
    .out_3(collisiondefiner_95_out_3));
  CollisionDefiner collisiondefiner_96 (
    .in_1(out_39),
    .in_2({1'b0, x_final[0], x_final[1], x_final[2], x_final[3], x_final[4], x_final[5], x_final[6], x_final[7], x_final[8], x_final[9], x_final[10], x_final[11], x_final[12], x_final[13], x_final[14], x_final[15], x_final[16], x_final[17], x_final[18], x_final[19], x_final[20], x_final[21], x_final[22], x_final[23], x_final[24], x_final[25], x_final[26], x_final[27], x_final[28], x_final[29], x_final[30]}),
    .out_3(collisiondefiner_96_out_3));
  BitFinder #(.width(32)) bitfinder_5 (.in(out_5), .index(bitfinder_5_index));  // open: found
  Subtractor #(.width(5)) subtractor_1 (
    .a(bitfinder_5_index), .b(5'b00001), .out(subtractor_1_out));  // open: bin, bout
  Multiplexer #(.enable("false")) multiplexer_83 (.in0(1'b0), .in1(multiplexer_84_out), .out(down), .sel(game_state));
  Multiplexer #(.select(5), .enable("false")) multiplexer_84 (
    .in0(collisiondefiner_65_out_3), .in1(collisiondefiner_66_out_3), .in2(collisiondefiner_67_out_3),
    .in3(collisiondefiner_68_out_3), .in4(collisiondefiner_69_out_3), .in5(collisiondefiner_70_out_3),
    .in6(collisiondefiner_71_out_3), .in7(collisiondefiner_72_out_3), .in8(collisiondefiner_73_out_3),
    .in9(collisiondefiner_74_out_3), .in10(collisiondefiner_75_out_3), .in11(collisiondefiner_76_out_3),
    .in12(collisiondefiner_77_out_3), .in13(collisiondefiner_78_out_3), .in14(collisiondefiner_79_out_3),
    .in15(collisiondefiner_80_out_3), .in16(collisiondefiner_81_out_3), .in17(collisiondefiner_82_out_3),
    .in18(collisiondefiner_83_out_3), .in19(collisiondefiner_84_out_3), .in20(collisiondefiner_85_out_3),
    .in21(collisiondefiner_86_out_3), .in22(collisiondefiner_87_out_3), .in23(collisiondefiner_88_out_3),
    .in24(collisiondefiner_89_out_3), .in25(collisiondefiner_90_out_3), .in26(collisiondefiner_91_out_3),
    .in27(collisiondefiner_92_out_3), .in28(collisiondefiner_93_out_3), .in29(collisiondefiner_94_out_3),
    .in30(collisiondefiner_95_out_3), .in31(collisiondefiner_96_out_3), .out(multiplexer_84_out),
    .sel(subtractor_1_out));
  not not_16 (not_16_out, out_5[1]);
  or or_74 (tp_or_not, not_16_out, out_5[2]);
  Comparator #(.width(32)) comparator_7 (.a({32{1'b0}}), .b(out_25), .eq(comparator_7_eq[0]));  // open: gt, lt
  Comparator #(.width(32)) comparator_8 (.a({32{1'b0}}), .b(out_29), .eq(comparator_7_eq[1]));  // open: gt, lt
  Comparator #(.width(32)) comparator_9 (.a({32{1'b0}}), .b(out_33), .eq(comparator_7_eq[2]));  // open: gt, lt
  Comparator #(.width(32)) comparator_10 (.a({32{1'b0}}), .b(out_37), .eq(comparator_7_eq[3]));  // open: gt, lt
  not not_17 (not_17_out, out_5[31]);
  not not_18 (Lose_east, or_75_out);
  or or_75 (or_75_out, not_17_out, out_5[30]);
  Multiplexer #(.select(4), .width(32), .enable("false")) multiplexer_85 (
    .in7(32'h60000), .in11(32'h30000), .in13(32'h18000), .in14(32'hc0000), .out(new_y), .sel(comparator_7_eq));  // open: in0, in1, in2, in3, in4, in5, in6, in8, in9, in10, in12, in15

  assign Lose_upper = Lose_east;
  assign tact_2 = tact;

  // Other names for the same wires on the sheet: _1[31:0] = out_7; _1m[29:0] = out_43; _1m_a = _1m_;
  //   _2[31:0] = out_12; _2m[29:0] = out_47; _3[31:0] = out_16; _3m[29:0] = out_51; _4[31:0] = out_20;
  //   _4m[29:0] = out_55; _5[31:0] = out_24; _5m[29:0] = out_59; _6[31:0] = out_28; _6m[29:0] = out_63;
  //   _7[31:0] = out_32; _7m[29:0] = out_67; _8[31:0] = out_36; _8m[29:0] = out_71; _9[31:0] = out_8;
  //   _9m[29:0] = out_44; _10[31:0] = out_13; _10m[29:0] = out_48; _11[31:0] = out_17; _11m[29:0] = out_52;
  //   _12[31:0] = out_21; _12m[29:0] = out_56; _13[31:0] = out_25; _13m[29:0] = out_60; _14[31:0] = out_29;
  //   _14m[29:0] = out_64; _15[31:0] = out_33; _15m[29:0] = out_68; _16[31:0] = out_37; _16m[29:0] = out_72;
  //   _17[31:0] = out_9; _17m[29:0] = out_45; _18[31:0] = out_14; _18m[29:0] = out_49; _19[31:0] = out_18;
  //   _19m[29:0] = out_53; _20[31:0] = out_22; _20m[29:0] = out_57; _21[31:0] = out_26; _21m[29:0] = out_61;
  //   _22[31:0] = out_30; _22m[29:0] = out_65; _23[31:0] = out_34; _23m[29:0] = out_69; _24[31:0] = out_38;
  //   _24m[29:0] = out_73; _25[31:0] = out_10; _25m[29:0] = out_46; _26[31:0] = out_15; _26m[29:0] = out_50;
  //   _27[31:0] = out_19; _27m[29:0] = out_54; _28[31:0] = out_23; _28m[29:0] = out_58; _29[31:0] = out_27;
  //   _29m[29:0] = out_62; _30[31:0] = out_31; _30m[29:0] = out_66; _31[31:0] = out_35; _31m[29:0] = out_70;
  //   _32[31:0] = out_39; _32m[29:0] = out_74; lose = Lose_east; reg_y[31:0] = out_5; start_alt_1 = game_state;
  //   start_input = Start; tact_for_everything = tact;
  //   x_inverted[30:0] = {x_final[0], x_final[1], x_final[2], x_final[3], x_final[4], x_final[5], x_final[6], x_final[7], x_final[8], x_final[9], x_final[10], x_final[11], x_final[12], x_final[13], x_final[14], x_final[15], x_final[16], x_final[17], x_final[18], x_final[19], x_final[20], x_final[21], x_final[22], x_final[23], x_final[24], x_final[25], x_final[26], x_final[27], x_final[28], x_final[29], x_final[30]};
  //   x_medium[30:0] = {x_inverted_alt[0], x_inverted_alt[1], x_inverted_alt[2], x_inverted_alt[3], x_inverted_alt[4], x_inverted_alt[5], x_inverted_alt[6], x_inverted_alt[7], x_inverted_alt[8], x_inverted_alt[9], x_inverted_alt[10], x_inverted_alt[11], x_inverted_alt[12], x_inverted_alt[13], x_inverted_alt[14], x_inverted_alt[15], x_inverted_alt[16], x_inverted_alt[17], x_inverted_alt[18], x_inverted_alt[19], x_inverted_alt[20], x_inverted_alt[21], x_inverted_alt[22], x_inverted_alt[23], x_inverted_alt[24], x_inverted_alt[25], x_inverted_alt[26], x_inverted_alt[27], x_inverted_alt[28], x_inverted_alt[29], x_inverted_alt[30]};
  //   reg_x[30:0] = out_4;
  //   x_inverted_money[30:0] = {out_4[0], out_4[1], out_4[2], out_4[3], out_4[4], out_4[5], out_4[6], out_4[7], out_4[8], out_4[9], out_4[10], out_4[11], out_4[12], out_4[13], out_4[14], out_4[15], out_4[16], out_4[17], out_4[18], out_4[19], out_4[20], out_4[21], out_4[22], out_4[23], out_4[24], out_4[25], out_4[26], out_4[27], out_4[28], out_4[29], out_4[30]}

  // Notes on the sheet:
  //   Bottom line
  //   Coin line controller
  //   Platform controller
  //   Top line
  //   Сollision avoidance
  //   Character-coin collision
  //   (Score counter)
  //   Character controller
  //   Checking for a gap
  //   Lower border
  //   collision detection
  //   Upper border
  //   collision detection
endmodule

module CollisionDefiner (
  input  [31:0] in_1,
  input  [31:0] in_2,
  output out_3
);

  wire or_1_out;
  wire [31:0] and_1_out;

  assign and_1_out = in_1 & in_2;  // AND_Gate and_1, 32 bits wide
  or or_1 (or_1_out, and_1_out[0], and_1_out[1], and_1_out[2], and_1_out[3], and_1_out[4], and_1_out[5], and_1_out[6], and_1_out[7], and_1_out[8], and_1_out[9], and_1_out[10], and_1_out[11], and_1_out[12], and_1_out[13], and_1_out[14], and_1_out[15], and_1_out[17], and_1_out[18], and_1_out[19], and_1_out[20], and_1_out[21], and_1_out[22], and_1_out[23], and_1_out[24], and_1_out[25], and_1_out[26], and_1_out[27], and_1_out[28], and_1_out[29], and_1_out[30], and_1_out[31], and_1_out[16]);
  not not_1 (out_3, or_1_out);
endmodule

module GSC (
  input  Lose_indicator,
  input  Start,
  input  Pause,
  output [31:0] out_4,
  output [31:0] out_5,
  output [31:0] out_6,
  output [31:0] out_7,
  output [31:0] out_8,
  output [31:0] out_9,
  output [31:0] out_10
);

  wire not_1_out;
  wire [1:0] indicator;

  D_Flip_Flop d_ff_1 (.clk(Pause), .D(not_1_out), .Q(indicator[1]));  // open: Qn, preset, en, reset
  not not_1 (not_1_out, indicator[1]);
  D_Flip_Flop d_ff_2 (
    .clk(Lose_indicator), .D(Lose_indicator), .Q(indicator[0]), .reset(Start));  // open: Qn, preset, en
  Multiplexer #(.select(2), .width(32), .enable("false")) multiplexer_1 (
    .in0({32{1'b0}}), .in1(32'he7bde23e), .in2(32'hf3c91cf0), .in3(32'he7bde23e), .out(out_4), .sel(indicator));
  Multiplexer #(.select(2), .width(32), .enable("false")) multiplexer_2 (
    .in0({32{1'b0}}), .in1(32'h94210508), .in2(32'h92492080), .in3(32'h94210508), .out(out_5), .sel(indicator));
  Multiplexer #(.select(2), .width(32), .enable("false")) multiplexer_3 (
    .in0({32{1'b0}}), .in1(32'h94210888), .in2(32'h92492080), .in3(32'h94210888), .out(out_6), .sel(indicator));
  Multiplexer #(.select(2), .width(32), .enable("false")) multiplexer_4 (
    .in0({32{1'b0}}), .in1(32'h97bdef88), .in2(32'hf3c918e0), .in3(32'h97bdef88), .out(out_7), .sel(indicator));
  Multiplexer #(.select(2), .width(32), .enable("false")) multiplexer_5 (
    .in0({32{1'b0}}), .in1(32'h94210888), .in2(32'h82490480), .in3(32'h94210888), .out(out_8), .sel(indicator));
  Multiplexer #(.select(2), .width(32), .enable("false")) multiplexer_6 (
    .in0({32{1'b0}}), .in1(32'h94210888), .in2(32'h82490480), .in3(32'h94210888), .out(out_9), .sel(indicator));
  Multiplexer #(.select(2), .width(32), .enable("false")) multiplexer_7 (
    .in0({32{1'b0}}), .in1(32'he7a1e888), .in2(32'h824638f0), .in3(32'he7a1e888), .out(out_10),
    .sel(indicator));

  // Other names for the same wires on the sheet: lose = indicator[0]; pause_t = indicator[1]
endmodule

module KIM (
  input  [6:0] keyboard,
  output right,
  output left,
  output start,
  output pause
);

  wire clock_1_out, comparator_1_eq, comparator_2_eq, comparator_3_eq, not_1_out, or_1_out;
  wire [6:0] demultiplexer_1_out0, demultiplexer_1_out1, register_1_q;

  Comparator #(.width(7)) comparator_1 (.a(keyboard), .b(7'b0001010), .eq(comparator_1_eq));  // open: gt, lt
  Comparator #(.width(7)) comparator_2 (.a(keyboard), .b(7'b0100000), .eq(comparator_2_eq));  // open: gt, lt
  Demultiplexer #(.width(7), .enable("false")) demultiplexer_1 (
    .out0(demultiplexer_1_out0), .out1(demultiplexer_1_out1), .in(keyboard), .sel(or_1_out));
  or or_1 (or_1_out, comparator_1_eq, comparator_2_eq);
  Comparator #(.width(7)) comparator_3 (.a(demultiplexer_1_out0), .b({7{1'b0}}), .eq(comparator_3_eq));  // open: gt, lt
  not not_1 (not_1_out, comparator_3_eq);
  Comparator #(.width(7)) comparator_4 (.a(demultiplexer_1_out1), .b(7'b0001010), .eq(start));  // open: gt, lt
  Comparator #(.width(7)) comparator_5 (.a(demultiplexer_1_out1), .b(7'b0100000), .eq(pause));  // open: gt, lt
  Register #(.width(7)) register_1 (
    .D(demultiplexer_1_out0), .en(not_1_out), .Q(register_1_q), .clk(clock_1_out));  // open: clr
  Clock clock_1 (.out(clock_1_out));
  Comparator #(.width(7)) comparator_6 (.a(register_1_q), .b(7'b1100100), .eq(right));  // open: gt, lt
  Comparator #(.width(7)) comparator_7 (.a(register_1_q), .b(7'b1100001), .eq(left));  // open: gt, lt
endmodule

module PlatformSet (
  input  [4:0] in_1,
  output [31:0] new_platform
);

  Multiplexer #(.select(5), .width(32), .enable("false")) multiplexer_1 (
    .in0(32'h7fffff8), .in1(32'h23fffff1), .in2(32'h31ffffe3), .in3(32'h38ffffc7), .in4(32'h3c7fff8f),
    .in5(32'h3e3fff1f), .in6(32'h3f1ffe3f), .in7(32'h3f8ffc7f), .in8(32'h3fc7f8ff), .in9(32'h3fe3f1ff),
    .in10(32'h3ff1e3ff), .in11(32'h3ff8c7ff), .in12(32'h3ffc0fff), .in13(32'h7ff1fff), .in14(32'h23ff8fff),
    .in15(32'h31ffc7ff), .in16(32'h38ffe3ff), .in17(32'h3c7ff1ff), .in18(32'h3e3ff8ff), .in19(32'h3f1ffc7f),
    .in20(32'h3f8ffe3f), .in21(32'h3fc7ff1f), .in22(32'h3fe3ff8f), .in23(32'h3ff1ffc7), .in24(32'h3ff8ffe3),
    .in25(32'h3ffc7ff1), .in26(32'h3ffe3ff8), .in27(32'h23c7e3f1), .in28(32'h200ff1e1), .in29(32'h3ff8c7f1),
    .in30(32'h308fffc7), .in31(32'h38fe3f8f), .out(new_platform), .sel(in_1));
  DotMatrix #(.inputtype("row"), .matrixcols(32), .matrixrows(32)) dotmatrix_1 (
    .row0(32'h7fffff8), .row1(32'h23fffff1), .row2(32'h31ffffe3), .row3(32'h38ffffc7), .row4(32'h3c7fff8f),
    .row5(32'h3e3fff1f), .row6(32'h3f1ffe3f), .row7(32'h3f8ffc7f), .row8(32'h3fc7f8ff), .row9(32'h3fe3f1ff),
    .row10(32'h3ff1e3ff), .row11(32'h3ff8c7ff), .row12(32'h3ffc0fff), .row13(32'h7ff1fff),
    .row14(32'h23ff8fff), .row15(32'h31ffc7ff), .row16(32'h38ffe3ff), .row17(32'h3c7ff1ff),
    .row18(32'h3e3ff8ff), .row19(32'h3f1ffc7f), .row20(32'h3f8ffe3f), .row21(32'h3fc7ff1f),
    .row22(32'h3fe3ff8f), .row23(32'h3ff1ffc7), .row24(32'h3ff8ffe3), .row25(32'h3ffc7ff1),
    .row26(32'h3ffe3ff8), .row27(32'h23c7e3f1), .row28(32'h200ff1e1), .row29(32'h3ff8c7f1),
    .row30(32'h308fffc7), .row31(32'h38fe3f8f));

  // Notes on the sheet:
  //   Platforms visualization
endmodule

module MoneyCollisionDefiner (
  input  [29:0] in_1,
  input  [31:0] in_2,
  output out_3
);

  wire [31:0] and_1_out, bit_extender_1_out;

  assign bit_extender_1_out = {{2{1'b0}}, in_1};  // Bit_Extender bit_extender_1
  assign and_1_out = bit_extender_1_out & in_2;  // AND_Gate and_1, 32 bits wide
  or or_1 (out_3, and_1_out[0], and_1_out[1], and_1_out[2], and_1_out[3], and_1_out[4], and_1_out[5], and_1_out[6], and_1_out[7], and_1_out[8], and_1_out[9], and_1_out[10], and_1_out[11], and_1_out[12], and_1_out[13], and_1_out[14], and_1_out[15], and_1_out[17], and_1_out[18], and_1_out[19], and_1_out[20], and_1_out[21], and_1_out[22], and_1_out[23], and_1_out[24], and_1_out[25], and_1_out[26], and_1_out[27], and_1_out[28], and_1_out[29], and_1_out[30], and_1_out[31], and_1_out[16]);
endmodule
