// Logisim project demo090524.circ as structural Verilog: 9 circuits, main circuit Screen
module main (
);

  wire cdm_8_mark5_1_p1, cdm_8_mark5_1_p2, cdm_8_mark5_1_p4, cdm_8_mark5_1_p6, cdm_8_mark5_1_p7,
       cdm_8_mark5_1_p8, cdm_8_mark5_1_p9, Cl, Code, data, I_Osel, In_out_prime, mem, nand_1_out, not_1_out,
       not_2_out, RAM, res;
  wire [3:0] I_Oadr;
  wire [7:0] cdm_8_mark5_1_p13, cdm_8_mark5_1_p14, I_Odat;
  wire [7:4] cdm_8_mark5_1_p12;

  and and_1 (I_Osel, not_1_out, Cl, data);
  // Probe on cdm_8_mark5_1_p1
  // Probe on cdm_8_mark5_1_p2
  // Probe on cdm_8_mark5_1_p4
  // Probe on cdm_8_mark5_1_p6
  // Probe on nothing
  Clock clock_1 (.out(Cl));
  not not_1 (not_1_out, nand_1_out);
  // Probe on cdm_8_mark5_1_p7
  // Probe on cdm_8_mark5_1_p8
  // CdM_8_mark5 cdm_8_mark5_1: pin names not known; wires that end beside it: cdm_8_mark5_1_p1, cdm_8_mark5_1_p2, Cl, cdm_8_mark5_1_p4, res, cdm_8_mark5_1_p6, cdm_8_mark5_1_p7, cdm_8_mark5_1_p8, cdm_8_mark5_1_p9, mem, In_out_prime, {cdm_8_mark5_1_p12, I_Oadr}, cdm_8_mark5_1_p13, cdm_8_mark5_1_p14
  nand nand_1 (nand_1_out, cdm_8_mark5_1_p12[4], cdm_8_mark5_1_p12[5], cdm_8_mark5_1_p12[6], cdm_8_mark5_1_p12[7]);
  and and_2 (RAM, nand_1_out, data);
  Decoder #(.disabled(0)) decoder_1 (.out0(Code), .out1(data), .sel(cdm_8_mark5_1_p9), .en(mem));
  assign I_Odat = not_2_out ? cdm_8_mark5_1_p13 : 8'bz;  // Controlled_Buffer controlled_buffer_1
  not not_2 (not_2_out, In_out_prime);
  assign cdm_8_mark5_1_p14 = In_out_prime ? I_Odat : 8'bz;  // Controlled_Buffer controlled_buffer_2
  Pull_Resistor pull_resistor_1 (.node(I_Oadr[0]));
  Pull_Resistor pull_resistor_2 (.node(I_Oadr[1]));
  Pull_Resistor pull_resistor_3 (.node(I_Oadr[2]));
  Pull_Resistor pull_resistor_4 (.node(I_Oadr[3]));
  Pull_Resistor pull_resistor_5 (.node(cdm_8_mark5_1_p12[4]));
  Pull_Resistor pull_resistor_6 (.node(cdm_8_mark5_1_p12[5]));
  Pull_Resistor pull_resistor_7 (.node(cdm_8_mark5_1_p12[6]));
  Pull_Resistor pull_resistor_8 (.node(cdm_8_mark5_1_p12[7]));
  ROM rom_1 (.addr({cdm_8_mark5_1_p12, I_Oadr}), .data(I_Odat), .sel(Code));
  RAM ram_1 (.addr({cdm_8_mark5_1_p12, I_Oadr}), .data(I_Odat), .sel(RAM), .clk(Cl), .ld(In_out_prime), .clr(res));

  // Other names for the same wires on the sheet: rd_wr_prime = In_out_prime

  // Notes on the sheet:
  //   instr memory
  //   data memory
endmodule

module Screen (
);

  wire clock_1_out, screen_options_1_lose_east, screen_options_1_pause;
  wire [3:0] leaderboard_1_p3, leaderboard_1_p4, leaderboard_1_p5, leaderboard_1_p6, leaderboard_1_p7,
       leaderboard_1_p8, leaderboard_1_p9, leaderboard_1_p10, leaderboard_1_p11, leaderboard_1_p12,
       leaderboard_1_p13, leaderboard_1_p14, leaderboard_1_p15, leaderboard_1_p16, leaderboard_1_p17,
       leaderboard_1_p18, leaderboard_1_p19, leaderboard_1_p20, leaderboard_1_p21, leaderboard_1_p22;
  wire [6:0] keyboard_1_data;
  wire [13:0] screen_options_1_score;
  wire [29:0] screen_options_1_out_41, screen_options_1_out_42, screen_options_1_out_43,
       screen_options_1_out_44, screen_options_1_out_45, screen_options_1_out_46, screen_options_1_out_47,
       screen_options_1_out_48, screen_options_1_out_49, screen_options_1_out_50, screen_options_1_out_51,
       screen_options_1_out_52, screen_options_1_out_53, screen_options_1_out_54, screen_options_1_out_55,
       screen_options_1_out_56, screen_options_1_out_57, screen_options_1_out_58, screen_options_1_out_59,
       screen_options_1_out_60, screen_options_1_out_61, screen_options_1_out_62, screen_options_1_out_63,
       screen_options_1_out_64, screen_options_1_out_65, screen_options_1_out_66, screen_options_1_out_67,
       screen_options_1_out_68, screen_options_1_out_69, screen_options_1_out_70, screen_options_1_out_71,
       screen_options_1_out_72;
  wire [31:0] info_screen_1_out_4, info_screen_1_out_5, info_screen_1_out_6, info_screen_1_out_7,
       info_screen_1_out_8, info_screen_1_out_9, info_screen_1_out_10, screen_options_1_out_5,
       screen_options_1_out_6, screen_options_1_out_7, screen_options_1_out_8, screen_options_1_out_10,
       screen_options_1_out_11, screen_options_1_out_12, screen_options_1_out_13, screen_options_1_out_14,
       screen_options_1_out_15, screen_options_1_out_16, screen_options_1_out_17, screen_options_1_out_18,
       screen_options_1_out_19, screen_options_1_out_20, screen_options_1_out_21, screen_options_1_out_22,
       screen_options_1_out_23, screen_options_1_out_24, screen_options_1_out_25, screen_options_1_out_26,
       screen_options_1_out_27, screen_options_1_out_28, screen_options_1_out_29, screen_options_1_out_30,
       screen_options_1_out_31, screen_options_1_out_32, screen_options_1_out_33, screen_options_1_out_34,
       screen_options_1_out_35, screen_options_1_out_36, screen_options_1_out_37;

  Clock clock_1 (.out(clock_1_out));
  Keyboard #(.buflen(2)) keyboard_1 (.clk(clock_1_out), .data(keyboard_1_data));  // open: re, clr, avail
  DotMatrix #(.inputtype("row"), .matrixcols(32)) dotmatrix_1 (
    .row0(info_screen_1_out_4), .row1(info_screen_1_out_5), .row2(info_screen_1_out_6),
    .row3(info_screen_1_out_7), .row4(info_screen_1_out_8), .row5(info_screen_1_out_9),
    .row6(info_screen_1_out_10));
  Info_Screen info_screen_1 (
    .Lose_indicator(screen_options_1_pause), .out_4(info_screen_1_out_4), .out_5(info_screen_1_out_5),
    .out_6(info_screen_1_out_6), .out_7(info_screen_1_out_7), .out_8(info_screen_1_out_8),
    .out_9(info_screen_1_out_9), .out_10(info_screen_1_out_10));  // open: Start, Pause
  DotMatrix #(.inputtype("row"), .matrixcols(30), .matrixrows(32), .dotshape("circle")) dotmatrix_2 (
    .row0(screen_options_1_out_72), .row1(screen_options_1_out_68), .row2(screen_options_1_out_64),
    .row3(screen_options_1_out_60), .row4(screen_options_1_out_56), .row5(screen_options_1_out_52),
    .row6(screen_options_1_out_48), .row7(screen_options_1_out_44), .row8(screen_options_1_out_71),
    .row9(screen_options_1_out_67), .row10(screen_options_1_out_63), .row11(screen_options_1_out_59),
    .row12(screen_options_1_out_55), .row13(screen_options_1_out_51), .row14(screen_options_1_out_47),
    .row15(screen_options_1_out_43), .row16(screen_options_1_out_70), .row17(screen_options_1_out_66),
    .row18(screen_options_1_out_62), .row19(screen_options_1_out_58), .row20(screen_options_1_out_54),
    .row21(screen_options_1_out_50), .row22(screen_options_1_out_46), .row23(screen_options_1_out_42),
    .row24(screen_options_1_out_69), .row25(screen_options_1_out_65), .row26(screen_options_1_out_61),
    .row27(screen_options_1_out_57), .row28(screen_options_1_out_53), .row29(screen_options_1_out_49),
    .row30(screen_options_1_out_45), .row31(screen_options_1_out_41));
  DotMatrix #(.inputtype("row"), .matrixcols(32), .matrixrows(32)) dotmatrix_3 (
    .row0(screen_options_1_out_37), .row1(screen_options_1_out_33), .row2(screen_options_1_out_29),
    .row3(screen_options_1_out_25), .row4(screen_options_1_out_21), .row5(screen_options_1_out_17),
    .row6(screen_options_1_out_13), .row7(screen_options_1_out_8), .row8(screen_options_1_out_36),
    .row9(screen_options_1_out_32), .row10(screen_options_1_out_28), .row11(screen_options_1_out_24),
    .row12(screen_options_1_out_20), .row13(screen_options_1_out_16), .row14(screen_options_1_out_12),
    .row15(screen_options_1_out_7), .row16(screen_options_1_out_35), .row17(screen_options_1_out_31),
    .row18(screen_options_1_out_27), .row19(screen_options_1_out_23), .row20(screen_options_1_out_19),
    .row21(screen_options_1_out_15), .row22(screen_options_1_out_11), .row23(screen_options_1_out_6),
    .row24(screen_options_1_out_34), .row25(screen_options_1_out_30), .row26(screen_options_1_out_26),
    .row27(screen_options_1_out_22), .row28(screen_options_1_out_18), .row29(screen_options_1_out_14),
    .row30(screen_options_1_out_10), .row31(screen_options_1_out_5));
  // DotMatrix #(.inputtype("select"), .matrixcols(31), .matrixrows(32)) dotmatrix_4: pin names not known
  Screen_options screen_options_1 (
    .out_5(screen_options_1_out_5), .out_10(screen_options_1_out_10), .out_14(screen_options_1_out_14),
    .out_18(screen_options_1_out_18), .out_22(screen_options_1_out_22), .out_26(screen_options_1_out_26),
    .out_30(screen_options_1_out_30), .out_34(screen_options_1_out_34), .out_6(screen_options_1_out_6),
    .out_11(screen_options_1_out_11), .out_15(screen_options_1_out_15), .out_19(screen_options_1_out_19),
    .out_23(screen_options_1_out_23), .out_27(screen_options_1_out_27), .out_31(screen_options_1_out_31),
    .out_35(screen_options_1_out_35), .out_7(screen_options_1_out_7), .out_12(screen_options_1_out_12),
    .out_16(screen_options_1_out_16), .out_20(screen_options_1_out_20), .out_24(screen_options_1_out_24),
    .out_28(screen_options_1_out_28), .out_32(screen_options_1_out_32), .out_36(screen_options_1_out_36),
    .out_8(screen_options_1_out_8), .out_13(screen_options_1_out_13), .out_17(screen_options_1_out_17),
    .out_21(screen_options_1_out_21), .out_25(screen_options_1_out_25), .out_29(screen_options_1_out_29),
    .out_33(screen_options_1_out_33), .out_37(screen_options_1_out_37), .out_41(screen_options_1_out_41),
    .out_45(screen_options_1_out_45), .out_49(screen_options_1_out_49), .out_53(screen_options_1_out_53),
    .out_57(screen_options_1_out_57), .out_61(screen_options_1_out_61), .out_65(screen_options_1_out_65),
    .out_69(screen_options_1_out_69), .out_46(screen_options_1_out_46), .out_50(screen_options_1_out_50),
    .out_54(screen_options_1_out_54), .out_58(screen_options_1_out_58), .out_62(screen_options_1_out_62),
    .out_66(screen_options_1_out_66), .out_70(screen_options_1_out_70), .out_42(screen_options_1_out_42),
    .out_43(screen_options_1_out_43), .out_47(screen_options_1_out_47), .out_51(screen_options_1_out_51),
    .out_55(screen_options_1_out_55), .out_59(screen_options_1_out_59), .out_63(screen_options_1_out_63),
    .out_67(screen_options_1_out_67), .out_71(screen_options_1_out_71), .out_44(screen_options_1_out_44),
    .out_48(screen_options_1_out_48), .out_52(screen_options_1_out_52), .out_56(screen_options_1_out_56),
    .out_60(screen_options_1_out_60), .out_64(screen_options_1_out_64), .out_68(screen_options_1_out_68),
    .out_72(screen_options_1_out_72), .score(screen_options_1_score), .keyboard(keyboard_1_data),
    .Pause(screen_options_1_pause), .Lose_east(screen_options_1_lose_east));  // open: out_2, out_3, Lose_upper, Start
  Hex_Digit_Display hex_digit_display_1 (.value(leaderboard_1_p4));  // open: dp
  Hex_Digit_Display hex_digit_display_2 (.value(leaderboard_1_p3));  // open: dp
  Hex_Digit_Display hex_digit_display_3 (.value(leaderboard_1_p6));  // open: dp
  Hex_Digit_Display hex_digit_display_4 (.value(leaderboard_1_p5));  // open: dp
  // Leaderboard leaderboard_1: pin names not known; wires that end beside it: screen_options_1_lose_east, screen_options_1_score, leaderboard_1_p3, leaderboard_1_p4, leaderboard_1_p5, leaderboard_1_p6, leaderboard_1_p7, leaderboard_1_p8, leaderboard_1_p9, leaderboard_1_p10, leaderboard_1_p11, leaderboard_1_p12, leaderboard_1_p13, leaderboard_1_p14, leaderboard_1_p15, leaderboard_1_p16, leaderboard_1_p17, leaderboard_1_p18, leaderboard_1_p19, leaderboard_1_p20, leaderboard_1_p21, leaderboard_1_p22
  Hex_Digit_Display hex_digit_display_5 (.value(leaderboard_1_p7));  // open: dp
  Hex_Digit_Display hex_digit_display_6 (.value(leaderboard_1_p8));  // open: dp
  Hex_Digit_Display hex_digit_display_7 (.value(leaderboard_1_p9));  // open: dp
  Hex_Digit_Display hex_digit_display_8 (.value(leaderboard_1_p10));  // open: dp
  Hex_Digit_Display hex_digit_display_9 (.value(leaderboard_1_p11));  // open: dp
  Hex_Digit_Display hex_digit_display_10 (.value(leaderboard_1_p14));  // open: dp
  Hex_Digit_Display hex_digit_display_11 (.value(leaderboard_1_p12));  // open: dp
  Hex_Digit_Display hex_digit_display_12 (.value(leaderboard_1_p15));  // open: dp
  Hex_Digit_Display hex_digit_display_13 (.value(leaderboard_1_p16));  // open: dp
  Hex_Digit_Display hex_digit_display_14 (.value(leaderboard_1_p13));  // open: dp
  Hex_Digit_Display hex_digit_display_15 (.value(leaderboard_1_p17));  // open: dp
  Hex_Digit_Display hex_digit_display_16 (.value(leaderboard_1_p20));  // open: dp
  Hex_Digit_Display hex_digit_display_17 (.value(leaderboard_1_p18));  // open: dp
  Hex_Digit_Display hex_digit_display_18 (.value(leaderboard_1_p21));  // open: dp
  Hex_Digit_Display hex_digit_display_19 (.value(leaderboard_1_p19));  // open: dp
  Hex_Digit_Display hex_digit_display_20 (.value(leaderboard_1_p22));  // open: dp
endmodule

module start_stop (
  input  start_stop,
  input  lose,
  output state_of_game
);

  wire not_1_out;

  not not_1 (not_1_out, state_of_game);
  Register #(.width(1)) register_1 (.D(not_1_out), .Q(state_of_game), .clk(start_stop), .clr(lose));  // open: en
endmodule
module Screen_options (
  input  [6:0] keyboard,
  output [30:0] out_2,
  output [31:0] out_3,
  output Lose_upper,
  output [31:0] out_5,
  output [31:0] out_6,
  output [31:0] out_7,
  output [31:0] out_8,
  output Lose_east,
  output [31:0] out_10,
  output [31:0] out_11,
  output [31:0] out_12,
  output [31:0] out_13,
  output [31:0] out_14,
  output [31:0] out_15,
  output [31:0] out_16,
  output [31:0] out_17,
  output [31:0] out_18,
  output [31:0] out_19,
  output [31:0] out_20,
  output [31:0] out_21,
  output [31:0] out_22,
  output [31:0] out_23,
  output [31:0] out_24,
  output [31:0] out_25,
  output [31:0] out_26,
  output [31:0] out_27,
  output [31:0] out_28,
  output [31:0] out_29,
  output [31:0] out_30,
  output [31:0] out_31,
  output [31:0] out_32,
  output [31:0] out_33,
  output [31:0] out_34,
  output [31:0] out_35,
  output [31:0] out_36,
  output [31:0] out_37,
  output Start,
  output Pause,
  output [13:0] score,
  output [29:0] out_41,
  output [29:0] out_42,
  output [29:0] out_43,
  output [29:0] out_44,
  output [29:0] out_45,
  output [29:0] out_46,
  output [29:0] out_47,
  output [29:0] out_48,
  output [29:0] out_49,
  output [29:0] out_50,
  output [29:0] out_51,
  output [29:0] out_52,
  output [29:0] out_53,
  output [29:0] out_54,
  output [29:0] out_55,
  output [29:0] out_56,
  output [29:0] out_57,
  output [29:0] out_58,
  output [29:0] out_59,
  output [29:0] out_60,
  output [29:0] out_61,
  output [29:0] out_62,
  output [29:0] out_63,
  output [29:0] out_64,
  output [29:0] out_65,
  output [29:0] out_66,
  output [29:0] out_67,
  output [29:0] out_68,
  output [29:0] out_69,
  output [29:0] out_70,
  output [29:0] out_71,
  output [29:0] out_72
);

  wire _1m_, _2m_, _3m_, _4m_, _5m_, _6m_, _7m_, _8m_, _9m_, _10m_, _11m_, _12m_, _13m_, _14m_, _15m_, _16m_,
       _17m_, _18m_, _19m_, _20m_, _21m_, _22m_, _23m_, _24m_, _25m_, _26m_, _27m_, _28m_, _29m_, _30m_,
       _31m_, _32m_, and_1_out, and_3_out, check_for_money_1_out_3, check_for_money_2_out_3,
       check_for_money_3_out_3, check_for_money_4_out_3, check_for_money_5_out_3, check_for_money_6_out_3,
       check_for_money_7_out_3, check_for_money_8_out_3, check_for_money_9_out_3, check_for_money_10_out_3,
       check_for_money_11_out_3, check_for_money_12_out_3, check_for_money_13_out_3,
       check_for_money_14_out_3, check_for_money_15_out_3, check_for_money_16_out_3,
       check_for_money_17_out_3, check_for_money_18_out_3, check_for_money_19_out_3,
       check_for_money_20_out_3, check_for_money_21_out_3, check_for_money_22_out_3,
       check_for_money_23_out_3, check_for_money_24_out_3, check_for_money_25_out_3,
       check_for_money_26_out_3, check_for_money_27_out_3, check_for_money_28_out_3,
       check_for_money_29_out_3, check_for_money_30_out_3, check_for_money_31_out_3,
       check_for_money_32_out_3, check_for_money_33_out_3, check_for_money_34_out_3,
       check_for_money_35_out_3, check_for_money_36_out_3, check_for_money_37_out_3,
       check_for_money_38_out_3, check_for_money_39_out_3, check_for_money_40_out_3,
       check_for_money_41_out_3, check_for_money_42_out_3, check_for_money_43_out_3,
       check_for_money_44_out_3, check_for_money_45_out_3, check_for_money_46_out_3,
       check_for_money_47_out_3, check_for_money_48_out_3, check_for_money_49_out_3,
       check_for_money_50_out_3, check_for_money_51_out_3, check_for_money_52_out_3,
       check_for_money_53_out_3, check_for_money_54_out_3, check_for_money_55_out_3,
       check_for_money_56_out_3, check_for_money_57_out_3, check_for_money_58_out_3,
       check_for_money_59_out_3, check_for_money_60_out_3, check_for_money_61_out_3,
       check_for_money_62_out_3, check_for_money_63_out_3, check_for_money_64_out_3, check_helper_1_out_3,
       check_helper_2_out_3, check_helper_3_out_3, check_helper_4_out_3, check_helper_5_out_3,
       check_helper_6_out_3, check_helper_7_out_3, check_helper_8_out_3, check_helper_9_out_3,
       check_helper_10_out_3, check_helper_11_out_3, check_helper_12_out_3, check_helper_13_out_3,
       check_helper_14_out_3, check_helper_15_out_3, check_helper_16_out_3, check_helper_17_out_3,
       check_helper_18_out_3, check_helper_19_out_3, check_helper_20_out_3, check_helper_21_out_3,
       check_helper_22_out_3, check_helper_23_out_3, check_helper_24_out_3, check_helper_25_out_3,
       check_helper_26_out_3, check_helper_27_out_3, check_helper_28_out_3, check_helper_29_out_3,
       check_helper_30_out_3, check_helper_31_out_3, check_helper_32_out_3, check_helper_33_out_3,
       check_helper_34_out_3, check_helper_35_out_3, check_helper_36_out_3, check_helper_37_out_3,
       check_helper_38_out_3, check_helper_39_out_3, check_helper_40_out_3, check_helper_41_out_3,
       check_helper_42_out_3, check_helper_43_out_3, check_helper_44_out_3, check_helper_45_out_3,
       check_helper_46_out_3, check_helper_47_out_3, check_helper_48_out_3, check_helper_49_out_3,
       check_helper_50_out_3, check_helper_51_out_3, check_helper_52_out_3, check_helper_53_out_3,
       check_helper_54_out_3, check_helper_55_out_3, check_helper_56_out_3, check_helper_57_out_3,
       check_helper_58_out_3, check_helper_59_out_3, check_helper_60_out_3, check_helper_61_out_3,
       check_helper_62_out_3, check_helper_63_out_3, check_helper_64_out_3, check_helper_65_out_3,
       check_helper_66_out_3, check_helper_67_out_3, check_helper_68_out_3, check_helper_69_out_3,
       check_helper_70_out_3, check_helper_71_out_3, check_helper_72_out_3, check_helper_73_out_3,
       check_helper_74_out_3, check_helper_75_out_3, check_helper_76_out_3, check_helper_77_out_3,
       check_helper_78_out_3, check_helper_79_out_3, check_helper_80_out_3, check_helper_81_out_3,
       check_helper_82_out_3, check_helper_83_out_3, check_helper_84_out_3, check_helper_85_out_3,
       check_helper_86_out_3, check_helper_87_out_3, check_helper_88_out_3, check_helper_89_out_3,
       check_helper_90_out_3, check_helper_91_out_3, check_helper_92_out_3, check_helper_93_out_3,
       check_helper_94_out_3, check_helper_95_out_3, check_helper_96_out_3, clock_1_out, clock_2_out,
       comparator_1_eq, comparator_2_eq, comparator_3_eq, comparator_3_lt, comparator_4_eq, comparator_4_gt,
       comparator_4_lt, comparator_5_eq, comparator_6_eq, d_ff_1_q, d_ff_2_q, demultiplexer_1_out0,
       demultiplexer_1_out1, demultiplexer_1_out2, demultiplexer_1_out3, demultiplexer_1_out4,
       demultiplexer_1_out5, demultiplexer_1_out6, demultiplexer_1_out7, demultiplexer_1_out8,
       demultiplexer_1_out9, demultiplexer_1_out10, demultiplexer_1_out11, demultiplexer_1_out12,
       demultiplexer_1_out13, demultiplexer_1_out14, demultiplexer_1_out15, demultiplexer_1_out16,
       demultiplexer_1_out17, demultiplexer_1_out18, demultiplexer_1_out19, demultiplexer_1_out20,
       demultiplexer_1_out21, demultiplexer_1_out22, demultiplexer_1_out23, demultiplexer_1_out24,
       demultiplexer_1_out25, demultiplexer_1_out26, demultiplexer_1_out27, demultiplexer_1_out28,
       demultiplexer_1_out29, demultiplexer_1_out30, demultiplexer_1_out31, demultiplexer_2_out0,
       demultiplexer_2_out1, demultiplexer_2_out2, demultiplexer_2_out3, demultiplexer_2_out4,
       demultiplexer_2_out5, demultiplexer_2_out6, demultiplexer_2_out7, demultiplexer_2_out8,
       demultiplexer_2_out9, demultiplexer_2_out10, demultiplexer_2_out11, demultiplexer_2_out12,
       demultiplexer_2_out13, demultiplexer_2_out14, demultiplexer_2_out15, demultiplexer_2_out16,
       demultiplexer_2_out17, demultiplexer_2_out18, demultiplexer_2_out19, demultiplexer_2_out20,
       demultiplexer_2_out21, demultiplexer_2_out22, demultiplexer_2_out23, demultiplexer_2_out24,
       demultiplexer_2_out25, demultiplexer_2_out26, demultiplexer_2_out27, demultiplexer_2_out28,
       demultiplexer_2_out29, demultiplexer_2_out30, demultiplexer_2_out31, down, game_state, left,
       multiplexer_2_out, multiplexer_70_out, multiplexer_71_out, multiplexer_76_out, multiplexer_81_out,
       multiplexer_82_out, multiplexer_86_out, not_1_out, not_2_out, not_3_out, not_4_out, not_5_out,
       not_6_out, not_7_out, not_8_out, not_9_out, not_11_out, not_12_out, not_13_out, not_14_out,
       not_15_out, not_16_out, not_17_out, or_1_out, or_2_out, or_5_out, or_6_out, or_40_out, or_42_out,
       or_44_out, right, start_t, tact, tact_1, tact_2, tact_3, tact_4, tact_for_money, tact_for_player,
       tp_or_not, x_cond, xor_1_out;
  wire [1:0] adder_2_out, multiplexer_3_out, or_3_out, register_2_q;
  wire [2:0] adder_1_out, multiplexer_1_out, register_1_q;
  wire [3:0] comparator_7_eq;
  wire [4:0] bitfinder_1_index, bitfinder_2_index, bitfinder_3_index, bitfinder_4_index, bitfinder_5_index,
       random_1_out, random_2_out, subtractor_1_out;
  wire [13:0] adder_3_out, multiplexer_68_out, multiplexer_69_out;
  wire [29:0] multiplexer_4_out, multiplexer_5_out, multiplexer_6_out, multiplexer_7_out, multiplexer_8_out,
       multiplexer_9_out, multiplexer_10_out, multiplexer_28_out, multiplexer_29_out, multiplexer_30_out,
       multiplexer_31_out, multiplexer_32_out, multiplexer_33_out, multiplexer_34_out, multiplexer_35_out,
       multiplexer_36_out, multiplexer_37_out, multiplexer_38_out, multiplexer_39_out, multiplexer_40_out,
       multiplexer_41_out, multiplexer_42_out, multiplexer_43_out, multiplexer_60_out, multiplexer_61_out,
       multiplexer_62_out, multiplexer_63_out, multiplexer_64_out, multiplexer_65_out, multiplexer_66_out,
       multiplexer_67_out, shifter_1_out;
  wire [30:0] multiplexer_72_out, multiplexer_74_out, multiplexer_77_out, multiplexer_78_out, shifter_2_out,
       shifter_3_out, x_final, x_inverted_alt;
  wire [31:0] multiplexer_11_out, multiplexer_12_out, multiplexer_13_out, multiplexer_14_out,
       multiplexer_15_out, multiplexer_16_out, multiplexer_17_out, multiplexer_20_out, multiplexer_21_out,
       multiplexer_22_out, multiplexer_23_out, multiplexer_24_out, multiplexer_25_out, multiplexer_26_out,
       multiplexer_27_out, multiplexer_44_out, multiplexer_45_out, multiplexer_46_out, multiplexer_47_out,
       multiplexer_48_out, multiplexer_49_out, multiplexer_50_out, multiplexer_51_out, multiplexer_52_out,
       multiplexer_53_out, multiplexer_54_out, multiplexer_55_out, multiplexer_56_out, multiplexer_57_out,
       multiplexer_58_out, multiplexer_59_out, multiplexer_73_out, multiplexer_75_out, multiplexer_79_out,
       multiplexer_80_out, new_platform_1_new_platform, new_y, or_41_out, shifter_4_out, shifter_5_out,
       y_final;

  Clock clock_1 (.out(clock_1_out));
  not not_1 (not_1_out, d_ff_1_q);
  Multiplexer #(.width(3), .enable("false")) multiplexer_1 (
    .in0(adder_1_out), .in1(3'b000), .out(multiplexer_1_out), .sel(start_t));
  Multiplexer #(.enable("false")) multiplexer_2 (
    .in0(clock_1_out), .in1(1'b0), .out(multiplexer_2_out), .sel(d_ff_1_q));
  not not_2 (not_2_out, d_ff_2_q);
  D_Flip_Flop d_ff_1 (.clk(Pause), .D(not_1_out), .Q(d_ff_1_q));  // open: Qn, preset, en, reset
  Register #(.width(3)) register_1 (.D(multiplexer_1_out), .Q(register_1_q), .clk(tact));  // open: en, clr
  Adder #(.width(3)) adder_1 (.a(register_1_q), .b(3'b001), .out(adder_1_out));  // open: cin, cout
  D_Flip_Flop d_ff_2 (.clk(multiplexer_2_out), .D(not_2_out), .Q(d_ff_2_q));  // open: Qn, preset, en, reset
  not not_3 (not_3_out, tact_for_money);
  Random #(.width(5)) random_1 (.clk(tact), .out(random_1_out));  // open: next, clr
  Comparator #(.width(3)) comparator_1 (.a(adder_1_out), .b(3'b001), .eq(comparator_1_eq));  // open: gt, lt
  Comparator #(.width(3)) comparator_2 (.a(adder_1_out), .b(3'b101), .eq(comparator_2_eq));  // open: gt, lt
  D_Flip_Flop d_ff_3 (.clk(d_ff_2_q), .D(not_3_out), .Q(tact_for_money));  // open: Qn, preset, en, reset
  D_Flip_Flop d_ff_4 (.clk(tact_for_money), .D(not_4_out), .Q(tact_4));  // open: Qn, preset, en, reset
  not not_4 (not_4_out, tact_4);
  Comparator #(.width(14)) comparator_3 (
    .a(score), .b(14'h3c), .eq(comparator_3_eq), .lt(comparator_3_lt));  // open: gt
  Comparator #(.width(14)) comparator_4 (
    .a(score), .b(14'h14), .gt(comparator_4_gt), .eq(comparator_4_eq), .lt(comparator_4_lt));
  Multiplexer #(.width(2), .enable("false")) multiplexer_3 (
    .in0(adder_2_out), .in1(2'b00), .out(multiplexer_3_out), .sel(start_t));
  Register #(.width(2)) register_2 (.D(multiplexer_3_out), .Q(register_2_q), .clk(tact));  // open: en, clr
  Shifter #(.width(30)) shifter_1 (.in(30'h1), .\dist (random_1_out), .out(shifter_1_out));
  Register #(.width(30)) register_3 (.D(shifter_1_out), .Q(out_41), .clk(tact_for_money), .clr(or_1_out));  // open: en
  or or_1 (or_1_out, not_5_out, _1m_, start_t);
  not not_5 (not_5_out, or_2_out);
  or or_2 (or_2_out, comparator_1_eq, comparator_2_eq);
  Multiplexer #(.width(30), .enable("false")) multiplexer_4 (
    .in0(out_41), .in1({30{1'b0}}), .out(multiplexer_4_out), .sel(start_t));
  Register #(.width(30)) register_4 (.D(multiplexer_4_out), .Q(out_45), .clk(tact), .clr(_2m_));  // open: en
  Register #(.width(30)) register_5 (.D(multiplexer_5_out), .Q(out_49), .clk(tact), .clr(_3m_));  // open: en
  Multiplexer #(.width(30), .enable("false")) multiplexer_5 (
    .in0(out_45), .in1({30{1'b0}}), .out(multiplexer_5_out), .sel(start_t));
  Multiplexer #(.width(30), .enable("false")) multiplexer_6 (
    .in0(out_49), .in1({30{1'b0}}), .out(multiplexer_6_out), .sel(start_t));
  Register #(.width(30)) register_6 (.D(multiplexer_6_out), .Q(out_53), .clk(tact), .clr(_4m_));  // open: en
  Multiplexer #(.width(30), .enable("false")) multiplexer_7 (
    .in0(out_53), .in1({30{1'b0}}), .out(multiplexer_7_out), .sel(start_t));
  Register #(.width(30)) register_7 (.D(multiplexer_7_out), .Q(out_57), .clk(tact), .clr(_5m_));  // open: en
  Multiplexer #(.width(30), .enable("false")) multiplexer_8 (
    .in0(out_57), .in1({30{1'b0}}), .out(multiplexer_8_out), .sel(start_t));
  Register #(.width(30)) register_8 (.D(multiplexer_8_out), .Q(out_61), .clk(tact), .clr(_6m_));  // open: en
  Multiplexer #(.width(30), .enable("false")) multiplexer_9 (
    .in0(out_61), .in1({30{1'b0}}), .out(multiplexer_9_out), .sel(start_t));
  Register #(.width(30)) register_9 (.D(multiplexer_9_out), .Q(out_65), .clk(tact), .clr(_7m_));  // open: en
  Multiplexer #(.width(30), .enable("false")) multiplexer_10 (
    .in0(out_65), .in1({30{1'b0}}), .out(multiplexer_10_out), .sel(start_t));
  Register #(.width(30)) register_10 (.D(multiplexer_10_out), .Q(out_69), .clk(tact), .clr(_8m_));  // open: en
  D_Flip_Flop d_ff_5 (.clk(tact_4), .D(not_6_out), .Q(tact_3));  // open: Qn, preset, en, reset
  not not_6 (not_6_out, tact_3);
  or or_3 (or_3_out[0], comparator_3_eq, and_1_out);
  and and_1 (and_1_out, comparator_3_lt, comparator_4_gt);
  or or_4 (or_3_out[1], comparator_4_eq, comparator_4_lt);
  Register #(.width(32)) register_11 (
    .D(new_platform_1_new_platform), .Q(out_5), .clk(tact), .clr(or_5_out));  // open: en
  Random #(.width(5)) random_2 (.clk(tact), .out(random_2_out));  // open: next, clr
  new_platform new_platform_1 (.in_1(random_2_out), .new_platform(new_platform_1_new_platform));
  or or_5 (or_5_out, not_7_out, start_t);
  Adder #(.width(2)) adder_2 (.a(register_2_q), .b(2'b01), .out(adder_2_out));  // open: cin, cout
  not not_7 (not_7_out, adder_2_out[1]);
  Multiplexer #(.width(32), .enable("false")) multiplexer_11 (
    .in0(out_5), .in1({32{1'b0}}), .out(multiplexer_11_out), .sel(start_t));
  Register #(.width(32)) register_12 (.D(multiplexer_11_out), .Q(out_10), .clk(tact));  // open: en, clr
  Register #(.width(32)) register_13 (.D(multiplexer_12_out), .Q(out_14), .clk(tact));  // open: en, clr
  Multiplexer #(.width(32), .enable("false")) multiplexer_12 (
    .in0(out_10), .in1(32'h3f8ffc7f), .out(multiplexer_12_out), .sel(start_t));
  Multiplexer #(.width(32), .enable("false")) multiplexer_13 (
    .in0(out_14), .in1({32{1'b0}}), .out(multiplexer_13_out), .sel(start_t));
  Register #(.width(32)) register_14 (.D(multiplexer_13_out), .Q(out_18), .clk(tact));  // open: en, clr
  Register #(.width(32)) register_15 (.D(multiplexer_14_out), .Q(out_22), .clk(tact));  // open: en, clr
  Multiplexer #(.width(32), .enable("false")) multiplexer_14 (
    .in0(out_18), .in1({32{1'b0}}), .out(multiplexer_14_out), .sel(start_t));
  Register #(.width(32)) register_16 (.D(multiplexer_15_out), .Q(out_26), .clk(tact));  // open: en, clr
  Multiplexer #(.width(32), .enable("false")) multiplexer_15 (
    .in0(out_22), .in1({32{1'b0}}), .out(multiplexer_15_out), .sel(start_t));
  Multiplexer #(.width(32), .enable("false")) multiplexer_16 (
    .in0(out_26), .in1(32'h3fc7ff1f), .out(multiplexer_16_out), .sel(start_t));
  Register #(.width(32)) register_17 (.D(multiplexer_16_out), .Q(out_30), .clk(tact));  // open: en, clr
  Register #(.width(32)) register_18 (.D(multiplexer_17_out), .Q(out_34), .clk(tact));  // open: en, clr
  Multiplexer #(.width(32), .enable("false")) multiplexer_17 (
    .in0(out_30), .in1({32{1'b0}}), .out(multiplexer_17_out), .sel(start_t));
  D_Flip_Flop d_ff_6 (.clk(tact_3), .D(not_8_out), .Q(tact_2));  // open: Qn, preset, en, reset
  not not_8 (not_8_out, tact_2);
  Multiplexer #(.select(2), .enable("false")) multiplexer_18 (
    .in0(tact_4), .in1(tact_3), .in2(tact_2), .out(tact_for_player), .sel(or_3_out));  // open: in3
  Multiplexer #(.select(2), .enable("false")) multiplexer_19 (
    .in0(tact_3), .in1(tact_2), .in2(tact_1), .out(tact), .sel(or_3_out));  // open: in3
  D_Flip_Flop d_ff_7 (.clk(tact_2), .D(not_9_out), .Q(tact_1));  // open: Qn, preset, en, reset
  not not_9 (not_9_out, tact_1);
  Multiplexer #(.width(32), .enable("false")) multiplexer_20 (
    .in0(out_34), .in1({32{1'b0}}), .out(multiplexer_20_out), .sel(start_t));
  Multiplexer #(.width(32), .enable("false")) multiplexer_21 (
    .in0(out_6), .in1({32{1'b0}}), .out(multiplexer_21_out), .sel(start_t));
  Multiplexer #(.width(32), .enable("false")) multiplexer_22 (
    .in0(out_11), .in1(32'h3c7ff1ff), .out(multiplexer_22_out), .sel(start_t));
  Multiplexer #(.width(32), .enable("false")) multiplexer_23 (
    .in0(out_15), .in1({32{1'b0}}), .out(multiplexer_23_out), .sel(start_t));
  Multiplexer #(.width(32), .enable("false")) multiplexer_24 (
    .in0(out_19), .in1({32{1'b0}}), .out(multiplexer_24_out), .sel(start_t));
  Multiplexer #(.width(32), .enable("false")) multiplexer_25 (
    .in0(out_23), .in1({32{1'b0}}), .out(multiplexer_25_out), .sel(start_t));
  Multiplexer #(.width(32), .enable("false")) multiplexer_26 (
    .in0(out_27), .in1(32'h7fffff8), .out(multiplexer_26_out), .sel(start_t));
  Multiplexer #(.width(32), .enable("false")) multiplexer_27 (
    .in0(out_31), .in1({32{1'b0}}), .out(multiplexer_27_out), .sel(start_t));
  Multiplexer #(.width(30), .enable("false")) multiplexer_28 (
    .in0(out_69), .in1({30{1'b0}}), .out(multiplexer_28_out), .sel(start_t));
  Register #(.width(30)) register_19 (.D(multiplexer_28_out), .Q(out_42), .clk(tact), .clr(_9m_));  // open: en
  Register #(.width(30)) register_20 (.D(multiplexer_29_out), .Q(out_46), .clk(tact), .clr(_10m_));  // open: en
  Multiplexer #(.width(30), .enable("false")) multiplexer_29 (
    .in0(out_42), .in1({30{1'b0}}), .out(multiplexer_29_out), .sel(start_t));
  Register #(.width(30)) register_21 (.D(multiplexer_30_out), .Q(out_50), .clk(tact), .clr(_11m_));  // open: en
  Multiplexer #(.width(30), .enable("false")) multiplexer_30 (
    .in0(out_46), .in1({30{1'b0}}), .out(multiplexer_30_out), .sel(start_t));
  Multiplexer #(.width(30), .enable("false")) multiplexer_31 (
    .in0(out_50), .in1({30{1'b0}}), .out(multiplexer_31_out), .sel(start_t));
  Register #(.width(30)) register_22 (.D(multiplexer_31_out), .Q(out_54), .clk(tact), .clr(_12m_));  // open: en
  Register #(.width(30)) register_23 (.D(multiplexer_32_out), .Q(out_58), .clk(tact), .clr(_13m_));  // open: en
  Multiplexer #(.width(30), .enable("false")) multiplexer_32 (
    .in0(out_54), .in1({30{1'b0}}), .out(multiplexer_32_out), .sel(start_t));
  Multiplexer #(.width(30), .enable("false")) multiplexer_33 (
    .in0(out_58), .in1({30{1'b0}}), .out(multiplexer_33_out), .sel(start_t));
  Register #(.width(30)) register_24 (.D(multiplexer_33_out), .Q(out_62), .clk(tact), .clr(_14m_));  // open: en
  Register #(.width(30)) register_25 (.D(multiplexer_34_out), .Q(out_66), .clk(tact), .clr(_15m_));  // open: en
  Multiplexer #(.width(30), .enable("false")) multiplexer_34 (
    .in0(out_62), .in1({30{1'b0}}), .out(multiplexer_34_out), .sel(start_t));
  Register #(.width(30)) register_26 (.D(multiplexer_35_out), .Q(out_70), .clk(tact), .clr(_16m_));  // open: en
  Multiplexer #(.width(30), .enable("false")) multiplexer_35 (
    .in0(out_66), .in1({30{1'b0}}), .out(multiplexer_35_out), .sel(start_t));
  Register #(.width(32)) register_27 (.D(multiplexer_20_out), .Q(out_6), .clk(tact));  // open: en, clr
  Register #(.width(32)) register_28 (.D(multiplexer_21_out), .Q(out_11), .clk(tact));  // open: en, clr
  Register #(.width(32)) register_29 (.D(multiplexer_22_out), .Q(out_15), .clk(tact));  // open: en, clr
  Register #(.width(32)) register_30 (.D(multiplexer_23_out), .Q(out_19), .clk(tact));  // open: en, clr
  Register #(.width(32)) register_31 (.D(multiplexer_24_out), .Q(out_23), .clk(tact));  // open: en, clr
  Register #(.width(32)) register_32 (.D(multiplexer_25_out), .Q(out_27), .clk(tact));  // open: en, clr
  Register #(.width(32)) register_33 (.D(multiplexer_26_out), .Q(out_31), .clk(tact));  // open: en, clr
  Register #(.width(32)) register_34 (.D(multiplexer_27_out), .Q(out_35), .clk(tact));  // open: en, clr
  Multiplexer #(.width(30), .enable("false")) multiplexer_36 (
    .in0(out_70), .in1({30{1'b0}}), .out(multiplexer_36_out), .sel(start_t));
  Multiplexer #(.width(30), .enable("false")) multiplexer_37 (
    .in0(out_43), .in1({30{1'b0}}), .out(multiplexer_37_out), .sel(start_t));
  Multiplexer #(.width(30), .enable("false")) multiplexer_38 (
    .in0(out_47), .in1({30{1'b0}}), .out(multiplexer_38_out), .sel(start_t));
  Multiplexer #(.width(30), .enable("false")) multiplexer_39 (
    .in0(out_51), .in1({30{1'b0}}), .out(multiplexer_39_out), .sel(start_t));
  Multiplexer #(.width(30), .enable("false")) multiplexer_40 (
    .in0(out_55), .in1({30{1'b0}}), .out(multiplexer_40_out), .sel(start_t));
  Multiplexer #(.width(30), .enable("false")) multiplexer_41 (
    .in0(out_59), .in1({30{1'b0}}), .out(multiplexer_41_out), .sel(start_t));
  Multiplexer #(.width(30), .enable("false")) multiplexer_42 (
    .in0(out_63), .in1({30{1'b0}}), .out(multiplexer_42_out), .sel(start_t));
  Multiplexer #(.width(30), .enable("false")) multiplexer_43 (
    .in0(out_67), .in1({30{1'b0}}), .out(multiplexer_43_out), .sel(start_t));
  Multiplexer #(.width(32), .enable("false")) multiplexer_44 (
    .in0(out_35), .in1({32{1'b0}}), .out(multiplexer_44_out), .sel(start_t));
  Register #(.width(32)) register_35 (.D(multiplexer_44_out), .Q(out_7), .clk(tact));  // open: en, clr
  Multiplexer #(.width(32), .enable("false")) multiplexer_45 (
    .in0(out_7), .in1({32{1'b0}}), .out(multiplexer_45_out), .sel(start_t));
  Register #(.width(32)) register_36 (.D(multiplexer_45_out), .Q(out_12), .clk(tact));  // open: en, clr
  Multiplexer #(.width(32), .enable("false")) multiplexer_46 (
    .in0(out_12), .in1(32'h31ffffe3), .out(multiplexer_46_out), .sel(start_t));
  Register #(.width(32)) register_37 (.D(multiplexer_46_out), .Q(out_16), .clk(tact));  // open: en, clr
  Register #(.width(32)) register_38 (.D(multiplexer_47_out), .Q(out_20), .clk(tact));  // open: en, clr
  Multiplexer #(.width(32), .enable("false")) multiplexer_47 (
    .in0(out_16), .in1({32{1'b0}}), .out(multiplexer_47_out), .sel(start_t));
  Multiplexer #(.width(32), .enable("false")) multiplexer_48 (
    .in0(out_20), .in1({32{1'b0}}), .out(multiplexer_48_out), .sel(start_t));
  Register #(.width(32)) register_39 (.D(multiplexer_48_out), .Q(out_24), .clk(tact));  // open: en, clr
  Multiplexer #(.width(32), .enable("false")) multiplexer_49 (
    .in0(out_24), .in1({32{1'b0}}), .out(multiplexer_49_out), .sel(start_t));
  Register #(.width(32)) register_40 (.D(multiplexer_49_out), .Q(out_28), .clk(tact));  // open: en, clr
  Multiplexer #(.width(32), .enable("false")) multiplexer_50 (
    .in0(out_28), .in1(32'h3f8ffc7f), .out(multiplexer_50_out), .sel(start_t));
  Register #(.width(32)) register_41 (.D(multiplexer_50_out), .Q(out_32), .clk(tact));  // open: en, clr
  Register #(.width(32)) register_42 (.D(multiplexer_51_out), .Q(out_36), .clk(tact));  // open: en, clr
  Multiplexer #(.width(32), .enable("false")) multiplexer_51 (
    .in0(out_32), .in1({32{1'b0}}), .out(multiplexer_51_out), .sel(start_t));
  Register #(.width(30)) register_43 (.D(multiplexer_36_out), .Q(out_43), .clk(tact), .clr(_17m_));  // open: en
  Register #(.width(30)) register_44 (.D(multiplexer_37_out), .Q(out_47), .clk(tact), .clr(_18m_));  // open: en
  Register #(.width(30)) register_45 (.D(multiplexer_38_out), .Q(out_51), .clk(tact), .clr(_19m_));  // open: en
  Register #(.width(30)) register_46 (.D(multiplexer_39_out), .Q(out_55), .clk(tact), .clr(_20m_));  // open: en
  Register #(.width(30)) register_47 (.D(multiplexer_40_out), .Q(out_59), .clk(tact), .clr(_21m_));  // open: en
  Register #(.width(30)) register_48 (.D(multiplexer_41_out), .Q(out_63), .clk(tact), .clr(_22m_));  // open: en
  Register #(.width(30)) register_49 (.D(multiplexer_42_out), .Q(out_67), .clk(tact), .clr(_23m_));  // open: en
  Register #(.width(30)) register_50 (.D(multiplexer_43_out), .Q(out_71), .clk(tact), .clr(_24m_));  // open: en
  Multiplexer #(.width(32), .enable("false")) multiplexer_52 (
    .in0(out_36), .in1({32{1'b0}}), .out(multiplexer_52_out), .sel(start_t));
  Multiplexer #(.width(32), .enable("false")) multiplexer_53 (
    .in0(out_8), .in1({32{1'b0}}), .out(multiplexer_53_out), .sel(start_t));
  Multiplexer #(.width(32), .enable("false")) multiplexer_54 (
    .in0(out_13), .in1(32'h38fe3f8f), .out(multiplexer_54_out), .sel(start_t));
  Multiplexer #(.width(32), .enable("false")) multiplexer_55 (
    .in0(out_17), .in1({32{1'b0}}), .out(multiplexer_55_out), .sel(start_t));
  Multiplexer #(.width(32), .enable("false")) multiplexer_56 (
    .in0(out_21), .in1({32{1'b0}}), .out(multiplexer_56_out), .sel(start_t));
  Multiplexer #(.width(32), .enable("false")) multiplexer_57 (
    .in0(out_25), .in1({32{1'b0}}), .out(multiplexer_57_out), .sel(start_t));
  Multiplexer #(.width(32), .enable("false")) multiplexer_58 (
    .in0(out_29), .in1(32'h23c7e3f1), .out(multiplexer_58_out), .sel(start_t));
  Multiplexer #(.width(32), .enable("false")) multiplexer_59 (
    .in0(out_33), .in1({32{1'b0}}), .out(multiplexer_59_out), .sel(start_t));
  Multiplexer #(.width(30), .enable("false")) multiplexer_60 (
    .in0(out_71), .in1({30{1'b0}}), .out(multiplexer_60_out), .sel(start_t));
  Multiplexer #(.width(30), .enable("false")) multiplexer_61 (
    .in0(out_44), .in1({30{1'b0}}), .out(multiplexer_61_out), .sel(start_t));
  Multiplexer #(.width(30), .enable("false")) multiplexer_62 (
    .in0(out_48), .in1({30{1'b0}}), .out(multiplexer_62_out), .sel(start_t));
  Multiplexer #(.width(30), .enable("false")) multiplexer_63 (
    .in0(out_52), .in1({30{1'b0}}), .out(multiplexer_63_out), .sel(start_t));
  Multiplexer #(.width(30), .enable("false")) multiplexer_64 (
    .in0(out_56), .in1({30{1'b0}}), .out(multiplexer_64_out), .sel(start_t));
  Multiplexer #(.width(30), .enable("false")) multiplexer_65 (
    .in0(out_60), .in1({30{1'b0}}), .out(multiplexer_65_out), .sel(start_t));
  Multiplexer #(.width(30), .enable("false")) multiplexer_66 (
    .in0(out_64), .in1({30{1'b0}}), .out(multiplexer_66_out), .sel(start_t));
  Multiplexer #(.width(30), .enable("false")) multiplexer_67 (
    .in0(out_68), .in1({30{1'b0}}), .out(multiplexer_67_out), .sel(start_t));
  Register #(.width(32)) register_51 (.D(multiplexer_52_out), .Q(out_8), .clk(tact));  // open: en, clr
  Register #(.width(32)) register_52 (.D(multiplexer_53_out), .Q(out_13), .clk(tact));  // open: en, clr
  Register #(.width(32)) register_53 (.D(multiplexer_54_out), .Q(out_17), .clk(tact));  // open: en, clr
  Register #(.width(32)) register_54 (.D(multiplexer_55_out), .Q(out_21), .clk(tact));  // open: en, clr
  Register #(.width(32)) register_55 (.D(multiplexer_56_out), .Q(out_25), .clk(tact));  // open: en, clr
  Register #(.width(32)) register_56 (.D(multiplexer_57_out), .Q(out_29), .clk(tact));  // open: en, clr
  Register #(.width(32)) register_57 (.D(multiplexer_58_out), .Q(out_33), .clk(tact));  // open: en, clr
  Register #(.width(32)) register_58 (.D(multiplexer_59_out), .Q(out_37), .clk(tact));  // open: en, clr
  Register #(.width(30)) register_59 (.D(multiplexer_60_out), .Q(out_44), .clk(tact), .clr(_25m_));  // open: en
  Register #(.width(30)) register_60 (.D(multiplexer_61_out), .Q(out_48), .clk(tact), .clr(_26m_));  // open: en
  Register #(.width(30)) register_61 (.D(multiplexer_62_out), .Q(out_52), .clk(tact), .clr(_27m_));  // open: en
  Register #(.width(30)) register_62 (.D(multiplexer_63_out), .Q(out_56), .clk(tact), .clr(_28m_));  // open: en
  Register #(.width(30)) register_63 (.D(multiplexer_64_out), .Q(out_60), .clk(tact), .clr(_29m_));  // open: en
  Register #(.width(30)) register_64 (.D(multiplexer_65_out), .Q(out_64), .clk(tact), .clr(_30m_));  // open: en
  Register #(.width(30)) register_65 (.D(multiplexer_66_out), .Q(out_68), .clk(tact), .clr(_31m_));  // open: en
  Register #(.width(30)) register_66 (.D(multiplexer_67_out), .Q(out_72), .clk(tact), .clr(_32m_));  // open: en
  Adder #(.width(14)) adder_3 (.a(score), .b(multiplexer_68_out), .out(adder_3_out));  // open: cin, cout
  Multiplexer #(.width(14), .enable("false")) multiplexer_68 (
    .in0(14'h5), .in1(14'h1), .out(multiplexer_68_out), .sel(tp_or_not));
  check_for_money check_for_money_1 (
    .in_1(out_41),
    .in_2({1'b0, out_2[0], out_2[1], out_2[2], out_2[3], out_2[4], out_2[5], out_2[6], out_2[7], out_2[8], out_2[9], out_2[10], out_2[11], out_2[12], out_2[13], out_2[14], out_2[15], out_2[16], out_2[17], out_2[18], out_2[19], out_2[20], out_2[21], out_2[22], out_2[23], out_2[24], out_2[25], out_2[26], out_2[27], out_2[28], out_2[29], out_2[30]}),
    .out_3(check_for_money_1_out_3));
  check_for_money check_for_money_2 (
    .in_1(out_45),
    .in_2({1'b0, out_2[0], out_2[1], out_2[2], out_2[3], out_2[4], out_2[5], out_2[6], out_2[7], out_2[8], out_2[9], out_2[10], out_2[11], out_2[12], out_2[13], out_2[14], out_2[15], out_2[16], out_2[17], out_2[18], out_2[19], out_2[20], out_2[21], out_2[22], out_2[23], out_2[24], out_2[25], out_2[26], out_2[27], out_2[28], out_2[29], out_2[30]}),
    .out_3(check_for_money_2_out_3));
  check_for_money check_for_money_3 (
    .in_1(out_49),
    .in_2({1'b0, out_2[0], out_2[1], out_2[2], out_2[3], out_2[4], out_2[5], out_2[6], out_2[7], out_2[8], out_2[9], out_2[10], out_2[11], out_2[12], out_2[13], out_2[14], out_2[15], out_2[16], out_2[17], out_2[18], out_2[19], out_2[20], out_2[21], out_2[22], out_2[23], out_2[24], out_2[25], out_2[26], out_2[27], out_2[28], out_2[29], out_2[30]}),
    .out_3(check_for_money_3_out_3));
  check_for_money check_for_money_4 (
    .in_1(out_53),
    .in_2({1'b0, out_2[0], out_2[1], out_2[2], out_2[3], out_2[4], out_2[5], out_2[6], out_2[7], out_2[8], out_2[9], out_2[10], out_2[11], out_2[12], out_2[13], out_2[14], out_2[15], out_2[16], out_2[17], out_2[18], out_2[19], out_2[20], out_2[21], out_2[22], out_2[23], out_2[24], out_2[25], out_2[26], out_2[27], out_2[28], out_2[29], out_2[30]}),
    .out_3(check_for_money_4_out_3));
  check_for_money check_for_money_5 (
    .in_1(out_57),
    .in_2({1'b0, out_2[0], out_2[1], out_2[2], out_2[3], out_2[4], out_2[5], out_2[6], out_2[7], out_2[8], out_2[9], out_2[10], out_2[11], out_2[12], out_2[13], out_2[14], out_2[15], out_2[16], out_2[17], out_2[18], out_2[19], out_2[20], out_2[21], out_2[22], out_2[23], out_2[24], out_2[25], out_2[26], out_2[27], out_2[28], out_2[29], out_2[30]}),
    .out_3(check_for_money_5_out_3));
  check_for_money check_for_money_6 (
    .in_1(out_61),
    .in_2({1'b0, out_2[0], out_2[1], out_2[2], out_2[3], out_2[4], out_2[5], out_2[6], out_2[7], out_2[8], out_2[9], out_2[10], out_2[11], out_2[12], out_2[13], out_2[14], out_2[15], out_2[16], out_2[17], out_2[18], out_2[19], out_2[20], out_2[21], out_2[22], out_2[23], out_2[24], out_2[25], out_2[26], out_2[27], out_2[28], out_2[29], out_2[30]}),
    .out_3(check_for_money_6_out_3));
  check_for_money check_for_money_7 (
    .in_1(out_65),
    .in_2({1'b0, out_2[0], out_2[1], out_2[2], out_2[3], out_2[4], out_2[5], out_2[6], out_2[7], out_2[8], out_2[9], out_2[10], out_2[11], out_2[12], out_2[13], out_2[14], out_2[15], out_2[16], out_2[17], out_2[18], out_2[19], out_2[20], out_2[21], out_2[22], out_2[23], out_2[24], out_2[25], out_2[26], out_2[27], out_2[28], out_2[29], out_2[30]}),
    .out_3(check_for_money_7_out_3));
  check_for_money check_for_money_8 (
    .in_1(out_69),
    .in_2({1'b0, out_2[0], out_2[1], out_2[2], out_2[3], out_2[4], out_2[5], out_2[6], out_2[7], out_2[8], out_2[9], out_2[10], out_2[11], out_2[12], out_2[13], out_2[14], out_2[15], out_2[16], out_2[17], out_2[18], out_2[19], out_2[20], out_2[21], out_2[22], out_2[23], out_2[24], out_2[25], out_2[26], out_2[27], out_2[28], out_2[29], out_2[30]}),
    .out_3(check_for_money_8_out_3));
  check_for_money check_for_money_9 (
    .in_1(out_42),
    .in_2({1'b0, out_2[0], out_2[1], out_2[2], out_2[3], out_2[4], out_2[5], out_2[6], out_2[7], out_2[8], out_2[9], out_2[10], out_2[11], out_2[12], out_2[13], out_2[14], out_2[15], out_2[16], out_2[17], out_2[18], out_2[19], out_2[20], out_2[21], out_2[22], out_2[23], out_2[24], out_2[25], out_2[26], out_2[27], out_2[28], out_2[29], out_2[30]}),
    .out_3(check_for_money_9_out_3));
  check_for_money check_for_money_10 (
    .in_1(out_46),
    .in_2({1'b0, out_2[0], out_2[1], out_2[2], out_2[3], out_2[4], out_2[5], out_2[6], out_2[7], out_2[8], out_2[9], out_2[10], out_2[11], out_2[12], out_2[13], out_2[14], out_2[15], out_2[16], out_2[17], out_2[18], out_2[19], out_2[20], out_2[21], out_2[22], out_2[23], out_2[24], out_2[25], out_2[26], out_2[27], out_2[28], out_2[29], out_2[30]}),
    .out_3(check_for_money_10_out_3));
  check_for_money check_for_money_11 (
    .in_1(out_50),
    .in_2({1'b0, out_2[0], out_2[1], out_2[2], out_2[3], out_2[4], out_2[5], out_2[6], out_2[7], out_2[8], out_2[9], out_2[10], out_2[11], out_2[12], out_2[13], out_2[14], out_2[15], out_2[16], out_2[17], out_2[18], out_2[19], out_2[20], out_2[21], out_2[22], out_2[23], out_2[24], out_2[25], out_2[26], out_2[27], out_2[28], out_2[29], out_2[30]}),
    .out_3(check_for_money_11_out_3));
  check_for_money check_for_money_12 (
    .in_1(out_54),
    .in_2({1'b0, out_2[0], out_2[1], out_2[2], out_2[3], out_2[4], out_2[5], out_2[6], out_2[7], out_2[8], out_2[9], out_2[10], out_2[11], out_2[12], out_2[13], out_2[14], out_2[15], out_2[16], out_2[17], out_2[18], out_2[19], out_2[20], out_2[21], out_2[22], out_2[23], out_2[24], out_2[25], out_2[26], out_2[27], out_2[28], out_2[29], out_2[30]}),
    .out_3(check_for_money_12_out_3));
  check_for_money check_for_money_13 (
    .in_1(out_58),
    .in_2({1'b0, out_2[0], out_2[1], out_2[2], out_2[3], out_2[4], out_2[5], out_2[6], out_2[7], out_2[8], out_2[9], out_2[10], out_2[11], out_2[12], out_2[13], out_2[14], out_2[15], out_2[16], out_2[17], out_2[18], out_2[19], out_2[20], out_2[21], out_2[22], out_2[23], out_2[24], out_2[25], out_2[26], out_2[27], out_2[28], out_2[29], out_2[30]}),
    .out_3(check_for_money_13_out_3));
  check_for_money check_for_money_14 (
    .in_1(out_62),
    .in_2({1'b0, out_2[0], out_2[1], out_2[2], out_2[3], out_2[4], out_2[5], out_2[6], out_2[7], out_2[8], out_2[9], out_2[10], out_2[11], out_2[12], out_2[13], out_2[14], out_2[15], out_2[16], out_2[17], out_2[18], out_2[19], out_2[20], out_2[21], out_2[22], out_2[23], out_2[24], out_2[25], out_2[26], out_2[27], out_2[28], out_2[29], out_2[30]}),
    .out_3(check_for_money_14_out_3));
  check_for_money check_for_money_15 (
    .in_1(out_66),
    .in_2({1'b0, out_2[0], out_2[1], out_2[2], out_2[3], out_2[4], out_2[5], out_2[6], out_2[7], out_2[8], out_2[9], out_2[10], out_2[11], out_2[12], out_2[13], out_2[14], out_2[15], out_2[16], out_2[17], out_2[18], out_2[19], out_2[20], out_2[21], out_2[22], out_2[23], out_2[24], out_2[25], out_2[26], out_2[27], out_2[28], out_2[29], out_2[30]}),
    .out_3(check_for_money_15_out_3));
  check_for_money check_for_money_16 (
    .in_1(out_70),
    .in_2({1'b0, out_2[0], out_2[1], out_2[2], out_2[3], out_2[4], out_2[5], out_2[6], out_2[7], out_2[8], out_2[9], out_2[10], out_2[11], out_2[12], out_2[13], out_2[14], out_2[15], out_2[16], out_2[17], out_2[18], out_2[19], out_2[20], out_2[21], out_2[22], out_2[23], out_2[24], out_2[25], out_2[26], out_2[27], out_2[28], out_2[29], out_2[30]}),
    .out_3(check_for_money_16_out_3));
  check_for_money check_for_money_17 (
    .in_1(out_43),
    .in_2({1'b0, out_2[0], out_2[1], out_2[2], out_2[3], out_2[4], out_2[5], out_2[6], out_2[7], out_2[8], out_2[9], out_2[10], out_2[11], out_2[12], out_2[13], out_2[14], out_2[15], out_2[16], out_2[17], out_2[18], out_2[19], out_2[20], out_2[21], out_2[22], out_2[23], out_2[24], out_2[25], out_2[26], out_2[27], out_2[28], out_2[29], out_2[30]}),
    .out_3(check_for_money_17_out_3));
  check_for_money check_for_money_18 (
    .in_1(out_47),
    .in_2({1'b0, out_2[0], out_2[1], out_2[2], out_2[3], out_2[4], out_2[5], out_2[6], out_2[7], out_2[8], out_2[9], out_2[10], out_2[11], out_2[12], out_2[13], out_2[14], out_2[15], out_2[16], out_2[17], out_2[18], out_2[19], out_2[20], out_2[21], out_2[22], out_2[23], out_2[24], out_2[25], out_2[26], out_2[27], out_2[28], out_2[29], out_2[30]}),
    .out_3(check_for_money_18_out_3));
  check_for_money check_for_money_19 (
    .in_1(out_51),
    .in_2({1'b0, out_2[0], out_2[1], out_2[2], out_2[3], out_2[4], out_2[5], out_2[6], out_2[7], out_2[8], out_2[9], out_2[10], out_2[11], out_2[12], out_2[13], out_2[14], out_2[15], out_2[16], out_2[17], out_2[18], out_2[19], out_2[20], out_2[21], out_2[22], out_2[23], out_2[24], out_2[25], out_2[26], out_2[27], out_2[28], out_2[29], out_2[30]}),
    .out_3(check_for_money_19_out_3));
  check_for_money check_for_money_20 (
    .in_1(out_55),
    .in_2({1'b0, out_2[0], out_2[1], out_2[2], out_2[3], out_2[4], out_2[5], out_2[6], out_2[7], out_2[8], out_2[9], out_2[10], out_2[11], out_2[12], out_2[13], out_2[14], out_2[15], out_2[16], out_2[17], out_2[18], out_2[19], out_2[20], out_2[21], out_2[22], out_2[23], out_2[24], out_2[25], out_2[26], out_2[27], out_2[28], out_2[29], out_2[30]}),
    .out_3(check_for_money_20_out_3));
  check_for_money check_for_money_21 (
    .in_1(out_59),
    .in_2({1'b0, out_2[0], out_2[1], out_2[2], out_2[3], out_2[4], out_2[5], out_2[6], out_2[7], out_2[8], out_2[9], out_2[10], out_2[11], out_2[12], out_2[13], out_2[14], out_2[15], out_2[16], out_2[17], out_2[18], out_2[19], out_2[20], out_2[21], out_2[22], out_2[23], out_2[24], out_2[25], out_2[26], out_2[27], out_2[28], out_2[29], out_2[30]}),
    .out_3(check_for_money_21_out_3));
  check_for_money check_for_money_22 (
    .in_1(out_63),
    .in_2({1'b0, out_2[0], out_2[1], out_2[2], out_2[3], out_2[4], out_2[5], out_2[6], out_2[7], out_2[8], out_2[9], out_2[10], out_2[11], out_2[12], out_2[13], out_2[14], out_2[15], out_2[16], out_2[17], out_2[18], out_2[19], out_2[20], out_2[21], out_2[22], out_2[23], out_2[24], out_2[25], out_2[26], out_2[27], out_2[28], out_2[29], out_2[30]}),
    .out_3(check_for_money_22_out_3));
  check_for_money check_for_money_23 (
    .in_1(out_67),
    .in_2({1'b0, out_2[0], out_2[1], out_2[2], out_2[3], out_2[4], out_2[5], out_2[6], out_2[7], out_2[8], out_2[9], out_2[10], out_2[11], out_2[12], out_2[13], out_2[14], out_2[15], out_2[16], out_2[17], out_2[18], out_2[19], out_2[20], out_2[21], out_2[22], out_2[23], out_2[24], out_2[25], out_2[26], out_2[27], out_2[28], out_2[29], out_2[30]}),
    .out_3(check_for_money_23_out_3));
  check_for_money check_for_money_24 (
    .in_1(out_71),
    .in_2({1'b0, out_2[0], out_2[1], out_2[2], out_2[3], out_2[4], out_2[5], out_2[6], out_2[7], out_2[8], out_2[9], out_2[10], out_2[11], out_2[12], out_2[13], out_2[14], out_2[15], out_2[16], out_2[17], out_2[18], out_2[19], out_2[20], out_2[21], out_2[22], out_2[23], out_2[24], out_2[25], out_2[26], out_2[27], out_2[28], out_2[29], out_2[30]}),
    .out_3(check_for_money_24_out_3));
  check_for_money check_for_money_25 (
    .in_1(out_44),
    .in_2({1'b0, out_2[0], out_2[1], out_2[2], out_2[3], out_2[4], out_2[5], out_2[6], out_2[7], out_2[8], out_2[9], out_2[10], out_2[11], out_2[12], out_2[13], out_2[14], out_2[15], out_2[16], out_2[17], out_2[18], out_2[19], out_2[20], out_2[21], out_2[22], out_2[23], out_2[24], out_2[25], out_2[26], out_2[27], out_2[28], out_2[29], out_2[30]}),
    .out_3(check_for_money_25_out_3));
  check_for_money check_for_money_26 (
    .in_1(out_48),
    .in_2({1'b0, out_2[0], out_2[1], out_2[2], out_2[3], out_2[4], out_2[5], out_2[6], out_2[7], out_2[8], out_2[9], out_2[10], out_2[11], out_2[12], out_2[13], out_2[14], out_2[15], out_2[16], out_2[17], out_2[18], out_2[19], out_2[20], out_2[21], out_2[22], out_2[23], out_2[24], out_2[25], out_2[26], out_2[27], out_2[28], out_2[29], out_2[30]}),
    .out_3(check_for_money_26_out_3));
  check_for_money check_for_money_27 (
    .in_1(out_52),
    .in_2({1'b0, out_2[0], out_2[1], out_2[2], out_2[3], out_2[4], out_2[5], out_2[6], out_2[7], out_2[8], out_2[9], out_2[10], out_2[11], out_2[12], out_2[13], out_2[14], out_2[15], out_2[16], out_2[17], out_2[18], out_2[19], out_2[20], out_2[21], out_2[22], out_2[23], out_2[24], out_2[25], out_2[26], out_2[27], out_2[28], out_2[29], out_2[30]}),
    .out_3(check_for_money_27_out_3));
  check_for_money check_for_money_28 (
    .in_1(out_56),
    .in_2({1'b0, out_2[0], out_2[1], out_2[2], out_2[3], out_2[4], out_2[5], out_2[6], out_2[7], out_2[8], out_2[9], out_2[10], out_2[11], out_2[12], out_2[13], out_2[14], out_2[15], out_2[16], out_2[17], out_2[18], out_2[19], out_2[20], out_2[21], out_2[22], out_2[23], out_2[24], out_2[25], out_2[26], out_2[27], out_2[28], out_2[29], out_2[30]}),
    .out_3(check_for_money_28_out_3));
  check_for_money check_for_money_29 (
    .in_1(out_60),
    .in_2({1'b0, out_2[0], out_2[1], out_2[2], out_2[3], out_2[4], out_2[5], out_2[6], out_2[7], out_2[8], out_2[9], out_2[10], out_2[11], out_2[12], out_2[13], out_2[14], out_2[15], out_2[16], out_2[17], out_2[18], out_2[19], out_2[20], out_2[21], out_2[22], out_2[23], out_2[24], out_2[25], out_2[26], out_2[27], out_2[28], out_2[29], out_2[30]}),
    .out_3(check_for_money_29_out_3));
  check_for_money check_for_money_30 (
    .in_1(out_64),
    .in_2({1'b0, out_2[0], out_2[1], out_2[2], out_2[3], out_2[4], out_2[5], out_2[6], out_2[7], out_2[8], out_2[9], out_2[10], out_2[11], out_2[12], out_2[13], out_2[14], out_2[15], out_2[16], out_2[17], out_2[18], out_2[19], out_2[20], out_2[21], out_2[22], out_2[23], out_2[24], out_2[25], out_2[26], out_2[27], out_2[28], out_2[29], out_2[30]}),
    .out_3(check_for_money_30_out_3));
  check_for_money check_for_money_31 (
    .in_1(out_68),
    .in_2({1'b0, out_2[0], out_2[1], out_2[2], out_2[3], out_2[4], out_2[5], out_2[6], out_2[7], out_2[8], out_2[9], out_2[10], out_2[11], out_2[12], out_2[13], out_2[14], out_2[15], out_2[16], out_2[17], out_2[18], out_2[19], out_2[20], out_2[21], out_2[22], out_2[23], out_2[24], out_2[25], out_2[26], out_2[27], out_2[28], out_2[29], out_2[30]}),
    .out_3(check_for_money_31_out_3));
  check_for_money check_for_money_32 (
    .in_1(out_72),
    .in_2({1'b0, out_2[0], out_2[1], out_2[2], out_2[3], out_2[4], out_2[5], out_2[6], out_2[7], out_2[8], out_2[9], out_2[10], out_2[11], out_2[12], out_2[13], out_2[14], out_2[15], out_2[16], out_2[17], out_2[18], out_2[19], out_2[20], out_2[21], out_2[22], out_2[23], out_2[24], out_2[25], out_2[26], out_2[27], out_2[28], out_2[29], out_2[30]}),
    .out_3(check_for_money_32_out_3));
  Multiplexer #(.width(14), .enable("false")) multiplexer_69 (
    .in0(adder_3_out), .in1({14{1'b0}}), .out(multiplexer_69_out), .sel(start_t));
  xor xor_1 (xor_1_out, tp_or_not, or_6_out);
  Demultiplexer #(.select(5), .enable("false")) demultiplexer_1 (
    .out0(demultiplexer_1_out0), .out1(demultiplexer_1_out1), .out2(demultiplexer_1_out2),
    .out3(demultiplexer_1_out3), .out4(demultiplexer_1_out4), .out5(demultiplexer_1_out5),
    .out6(demultiplexer_1_out6), .out7(demultiplexer_1_out7), .out8(demultiplexer_1_out8),
    .out9(demultiplexer_1_out9), .out10(demultiplexer_1_out10), .out11(demultiplexer_1_out11),
    .out12(demultiplexer_1_out12), .out13(demultiplexer_1_out13), .out14(demultiplexer_1_out14),
    .out15(demultiplexer_1_out15), .out16(demultiplexer_1_out16), .out17(demultiplexer_1_out17),
    .out18(demultiplexer_1_out18), .out19(demultiplexer_1_out19), .out20(demultiplexer_1_out20),
    .out21(demultiplexer_1_out21), .out22(demultiplexer_1_out22), .out23(demultiplexer_1_out23),
    .out24(demultiplexer_1_out24), .out25(demultiplexer_1_out25), .out26(demultiplexer_1_out26),
    .out27(demultiplexer_1_out27), .out28(demultiplexer_1_out28), .out29(demultiplexer_1_out29),
    .out30(demultiplexer_1_out30), .out31(demultiplexer_1_out31), .in(multiplexer_70_out),
    .sel(bitfinder_1_index));
  Multiplexer #(.select(5), .enable("false")) multiplexer_70 (
    .in0(check_for_money_1_out_3), .in1(check_for_money_2_out_3), .in2(check_for_money_3_out_3),
    .in3(check_for_money_4_out_3), .in4(check_for_money_5_out_3), .in5(check_for_money_6_out_3),
    .in6(check_for_money_7_out_3), .in7(check_for_money_8_out_3), .in8(check_for_money_9_out_3),
    .in9(check_for_money_10_out_3), .in10(check_for_money_11_out_3), .in11(check_for_money_12_out_3),
    .in12(check_for_money_13_out_3), .in13(check_for_money_14_out_3), .in14(check_for_money_15_out_3),
    .in15(check_for_money_16_out_3), .in16(check_for_money_17_out_3), .in17(check_for_money_18_out_3),
    .in18(check_for_money_19_out_3), .in19(check_for_money_20_out_3), .in20(check_for_money_21_out_3),
    .in21(check_for_money_22_out_3), .in22(check_for_money_23_out_3), .in23(check_for_money_24_out_3),
    .in24(check_for_money_25_out_3), .in25(check_for_money_26_out_3), .in26(check_for_money_27_out_3),
    .in27(check_for_money_28_out_3), .in28(check_for_money_29_out_3), .in29(check_for_money_30_out_3),
    .in30(check_for_money_31_out_3), .in31(check_for_money_32_out_3), .out(multiplexer_70_out),
    .sel(bitfinder_1_index));
  BitFinder #(.width(32), .\type ("high1")) bitfinder_1 (.in(out_3), .index(bitfinder_1_index));  // open: found
  Register #(.width(14)) register_67 (.D(multiplexer_69_out), .Q(score), .clk(multiplexer_71_out));  // open: en, clr
  Multiplexer #(.enable("false")) multiplexer_71 (
    .in0(xor_1_out), .in1(tact_for_money), .out(multiplexer_71_out), .sel(start_t));
  or or_6 (or_6_out, multiplexer_70_out, multiplexer_76_out);
  or or_7 (_1m_, demultiplexer_1_out0, demultiplexer_2_out0);
  or or_8 (_2m_, demultiplexer_1_out1, demultiplexer_2_out1);
  or or_9 (_3m_, demultiplexer_1_out2, demultiplexer_2_out2);
  or or_10 (_4m_, demultiplexer_1_out3, demultiplexer_2_out3);
  or or_11 (_5m_, demultiplexer_1_out4, demultiplexer_2_out4);
  or or_12 (_6m_, demultiplexer_1_out5, demultiplexer_2_out5);
  or or_13 (_7m_, demultiplexer_1_out6, demultiplexer_2_out6);
  or or_14 (_8m_, demultiplexer_1_out7, demultiplexer_2_out7);
  or or_15 (_9m_, demultiplexer_1_out8, demultiplexer_2_out8);
  or or_16 (_10m_, demultiplexer_1_out9, demultiplexer_2_out9);
  or or_17 (_11m_, demultiplexer_1_out10, demultiplexer_2_out10);
  or or_18 (_12m_, demultiplexer_1_out11, demultiplexer_2_out11);
  or or_19 (_13m_, demultiplexer_1_out12, demultiplexer_2_out12);
  or or_20 (_14m_, demultiplexer_1_out13, demultiplexer_2_out13);
  or or_21 (_15m_, demultiplexer_1_out14, demultiplexer_2_out14);
  or or_22 (_16m_, demultiplexer_1_out15, demultiplexer_2_out15);
  or or_23 (_17m_, demultiplexer_1_out16, demultiplexer_2_out16);
  or or_24 (_18m_, demultiplexer_1_out17, demultiplexer_2_out17);
  or or_25 (_19m_, demultiplexer_1_out18, demultiplexer_2_out18);
  Demultiplexer #(.select(5), .enable("false")) demultiplexer_2 (
    .out0(demultiplexer_2_out0), .out1(demultiplexer_2_out1), .out2(demultiplexer_2_out2),
    .out3(demultiplexer_2_out3), .out4(demultiplexer_2_out4), .out5(demultiplexer_2_out5),
    .out6(demultiplexer_2_out6), .out7(demultiplexer_2_out7), .out8(demultiplexer_2_out8),
    .out9(demultiplexer_2_out9), .out10(demultiplexer_2_out10), .out11(demultiplexer_2_out11),
    .out12(demultiplexer_2_out12), .out13(demultiplexer_2_out13), .out14(demultiplexer_2_out14),
    .out15(demultiplexer_2_out15), .out16(demultiplexer_2_out16), .out17(demultiplexer_2_out17),
    .out18(demultiplexer_2_out18), .out19(demultiplexer_2_out19), .out20(demultiplexer_2_out20),
    .out21(demultiplexer_2_out21), .out22(demultiplexer_2_out22), .out23(demultiplexer_2_out23),
    .out24(demultiplexer_2_out24), .out25(demultiplexer_2_out25), .out26(demultiplexer_2_out26),
    .out27(demultiplexer_2_out27), .out28(demultiplexer_2_out28), .out29(demultiplexer_2_out29),
    .out30(demultiplexer_2_out30), .out31(demultiplexer_2_out31), .in(multiplexer_76_out),
    .sel(bitfinder_2_index));
  or or_26 (_20m_, demultiplexer_1_out19, demultiplexer_2_out19);
  or or_27 (_21m_, demultiplexer_1_out20, demultiplexer_2_out20);
  or or_28 (_22m_, demultiplexer_1_out21, demultiplexer_2_out21);
  or or_29 (_23m_, demultiplexer_1_out22, demultiplexer_2_out22);
  or or_30 (_24m_, demultiplexer_1_out23, demultiplexer_2_out23);
  or or_31 (_25m_, demultiplexer_1_out24, demultiplexer_2_out24);
  or or_32 (_26m_, demultiplexer_1_out25, demultiplexer_2_out25);
  or or_33 (_27m_, demultiplexer_1_out26, demultiplexer_2_out26);
  or or_34 (_28m_, demultiplexer_1_out27, demultiplexer_2_out27);
  or or_35 (_29m_, demultiplexer_1_out28, demultiplexer_2_out28);
  or or_36 (_30m_, demultiplexer_1_out29, demultiplexer_2_out29);
  or or_37 (_31m_, demultiplexer_1_out30, demultiplexer_2_out30);
  or or_38 (_32m_, demultiplexer_1_out31, demultiplexer_2_out31);
  Multiplexer #(.width(31), .enable("false")) multiplexer_72 (
    .in0(31'hc000), .in1(x_final), .out(multiplexer_72_out), .sel(tp_or_not));
  Multiplexer #(.width(32), .enable("false")) multiplexer_73 (
    .in0(new_y), .in1(y_final), .out(multiplexer_73_out), .sel(tp_or_not));
  Clock clock_2 (.out(clock_2_out));
  Keyboard #(.buflen(1)) keyboard_1 (.clk(clock_2_out));  // open: re, clr, avail, data
  check_for_money check_for_money_33 (
    .in_1(out_41),
    .in_2({1'b0, out_2[0], out_2[1], out_2[2], out_2[3], out_2[4], out_2[5], out_2[6], out_2[7], out_2[8], out_2[9], out_2[10], out_2[11], out_2[12], out_2[13], out_2[14], out_2[15], out_2[16], out_2[17], out_2[18], out_2[19], out_2[20], out_2[21], out_2[22], out_2[23], out_2[24], out_2[25], out_2[26], out_2[27], out_2[28], out_2[29], out_2[30]}),
    .out_3(check_for_money_33_out_3));
  check_for_money check_for_money_34 (
    .in_1(out_45),
    .in_2({1'b0, out_2[0], out_2[1], out_2[2], out_2[3], out_2[4], out_2[5], out_2[6], out_2[7], out_2[8], out_2[9], out_2[10], out_2[11], out_2[12], out_2[13], out_2[14], out_2[15], out_2[16], out_2[17], out_2[18], out_2[19], out_2[20], out_2[21], out_2[22], out_2[23], out_2[24], out_2[25], out_2[26], out_2[27], out_2[28], out_2[29], out_2[30]}),
    .out_3(check_for_money_34_out_3));
  check_for_money check_for_money_35 (
    .in_1(out_49),
    .in_2({1'b0, out_2[0], out_2[1], out_2[2], out_2[3], out_2[4], out_2[5], out_2[6], out_2[7], out_2[8], out_2[9], out_2[10], out_2[11], out_2[12], out_2[13], out_2[14], out_2[15], out_2[16], out_2[17], out_2[18], out_2[19], out_2[20], out_2[21], out_2[22], out_2[23], out_2[24], out_2[25], out_2[26], out_2[27], out_2[28], out_2[29], out_2[30]}),
    .out_3(check_for_money_35_out_3));
  check_for_money check_for_money_36 (
    .in_1(out_53),
    .in_2({1'b0, out_2[0], out_2[1], out_2[2], out_2[3], out_2[4], out_2[5], out_2[6], out_2[7], out_2[8], out_2[9], out_2[10], out_2[11], out_2[12], out_2[13], out_2[14], out_2[15], out_2[16], out_2[17], out_2[18], out_2[19], out_2[20], out_2[21], out_2[22], out_2[23], out_2[24], out_2[25], out_2[26], out_2[27], out_2[28], out_2[29], out_2[30]}),
    .out_3(check_for_money_36_out_3));
  check_for_money check_for_money_37 (
    .in_1(out_57),
    .in_2({1'b0, out_2[0], out_2[1], out_2[2], out_2[3], out_2[4], out_2[5], out_2[6], out_2[7], out_2[8], out_2[9], out_2[10], out_2[11], out_2[12], out_2[13], out_2[14], out_2[15], out_2[16], out_2[17], out_2[18], out_2[19], out_2[20], out_2[21], out_2[22], out_2[23], out_2[24], out_2[25], out_2[26], out_2[27], out_2[28], out_2[29], out_2[30]}),
    .out_3(check_for_money_37_out_3));
  check_for_money check_for_money_38 (
    .in_1(out_61),
    .in_2({1'b0, out_2[0], out_2[1], out_2[2], out_2[3], out_2[4], out_2[5], out_2[6], out_2[7], out_2[8], out_2[9], out_2[10], out_2[11], out_2[12], out_2[13], out_2[14], out_2[15], out_2[16], out_2[17], out_2[18], out_2[19], out_2[20], out_2[21], out_2[22], out_2[23], out_2[24], out_2[25], out_2[26], out_2[27], out_2[28], out_2[29], out_2[30]}),
    .out_3(check_for_money_38_out_3));
  check_for_money check_for_money_39 (
    .in_1(out_65),
    .in_2({1'b0, out_2[0], out_2[1], out_2[2], out_2[3], out_2[4], out_2[5], out_2[6], out_2[7], out_2[8], out_2[9], out_2[10], out_2[11], out_2[12], out_2[13], out_2[14], out_2[15], out_2[16], out_2[17], out_2[18], out_2[19], out_2[20], out_2[21], out_2[22], out_2[23], out_2[24], out_2[25], out_2[26], out_2[27], out_2[28], out_2[29], out_2[30]}),
    .out_3(check_for_money_39_out_3));
  check_for_money check_for_money_40 (
    .in_1(out_69),
    .in_2({1'b0, out_2[0], out_2[1], out_2[2], out_2[3], out_2[4], out_2[5], out_2[6], out_2[7], out_2[8], out_2[9], out_2[10], out_2[11], out_2[12], out_2[13], out_2[14], out_2[15], out_2[16], out_2[17], out_2[18], out_2[19], out_2[20], out_2[21], out_2[22], out_2[23], out_2[24], out_2[25], out_2[26], out_2[27], out_2[28], out_2[29], out_2[30]}),
    .out_3(check_for_money_40_out_3));
  check_for_money check_for_money_41 (
    .in_1(out_42),
    .in_2({1'b0, out_2[0], out_2[1], out_2[2], out_2[3], out_2[4], out_2[5], out_2[6], out_2[7], out_2[8], out_2[9], out_2[10], out_2[11], out_2[12], out_2[13], out_2[14], out_2[15], out_2[16], out_2[17], out_2[18], out_2[19], out_2[20], out_2[21], out_2[22], out_2[23], out_2[24], out_2[25], out_2[26], out_2[27], out_2[28], out_2[29], out_2[30]}),
    .out_3(check_for_money_41_out_3));
  check_for_money check_for_money_42 (
    .in_1(out_46),
    .in_2({1'b0, out_2[0], out_2[1], out_2[2], out_2[3], out_2[4], out_2[5], out_2[6], out_2[7], out_2[8], out_2[9], out_2[10], out_2[11], out_2[12], out_2[13], out_2[14], out_2[15], out_2[16], out_2[17], out_2[18], out_2[19], out_2[20], out_2[21], out_2[22], out_2[23], out_2[24], out_2[25], out_2[26], out_2[27], out_2[28], out_2[29], out_2[30]}),
    .out_3(check_for_money_42_out_3));
  check_for_money check_for_money_43 (
    .in_1(out_50),
    .in_2({1'b0, out_2[0], out_2[1], out_2[2], out_2[3], out_2[4], out_2[5], out_2[6], out_2[7], out_2[8], out_2[9], out_2[10], out_2[11], out_2[12], out_2[13], out_2[14], out_2[15], out_2[16], out_2[17], out_2[18], out_2[19], out_2[20], out_2[21], out_2[22], out_2[23], out_2[24], out_2[25], out_2[26], out_2[27], out_2[28], out_2[29], out_2[30]}),
    .out_3(check_for_money_43_out_3));
  check_for_money check_for_money_44 (
    .in_1(out_54),
    .in_2({1'b0, out_2[0], out_2[1], out_2[2], out_2[3], out_2[4], out_2[5], out_2[6], out_2[7], out_2[8], out_2[9], out_2[10], out_2[11], out_2[12], out_2[13], out_2[14], out_2[15], out_2[16], out_2[17], out_2[18], out_2[19], out_2[20], out_2[21], out_2[22], out_2[23], out_2[24], out_2[25], out_2[26], out_2[27], out_2[28], out_2[29], out_2[30]}),
    .out_3(check_for_money_44_out_3));
  check_for_money check_for_money_45 (
    .in_1(out_58),
    .in_2({1'b0, out_2[0], out_2[1], out_2[2], out_2[3], out_2[4], out_2[5], out_2[6], out_2[7], out_2[8], out_2[9], out_2[10], out_2[11], out_2[12], out_2[13], out_2[14], out_2[15], out_2[16], out_2[17], out_2[18], out_2[19], out_2[20], out_2[21], out_2[22], out_2[23], out_2[24], out_2[25], out_2[26], out_2[27], out_2[28], out_2[29], out_2[30]}),
    .out_3(check_for_money_45_out_3));
  check_for_money check_for_money_46 (
    .in_1(out_62),
    .in_2({1'b0, out_2[0], out_2[1], out_2[2], out_2[3], out_2[4], out_2[5], out_2[6], out_2[7], out_2[8], out_2[9], out_2[10], out_2[11], out_2[12], out_2[13], out_2[14], out_2[15], out_2[16], out_2[17], out_2[18], out_2[19], out_2[20], out_2[21], out_2[22], out_2[23], out_2[24], out_2[25], out_2[26], out_2[27], out_2[28], out_2[29], out_2[30]}),
    .out_3(check_for_money_46_out_3));
  check_for_money check_for_money_47 (
    .in_1(out_66),
    .in_2({1'b0, out_2[0], out_2[1], out_2[2], out_2[3], out_2[4], out_2[5], out_2[6], out_2[7], out_2[8], out_2[9], out_2[10], out_2[11], out_2[12], out_2[13], out_2[14], out_2[15], out_2[16], out_2[17], out_2[18], out_2[19], out_2[20], out_2[21], out_2[22], out_2[23], out_2[24], out_2[25], out_2[26], out_2[27], out_2[28], out_2[29], out_2[30]}),
    .out_3(check_for_money_47_out_3));
  check_for_money check_for_money_48 (
    .in_1(out_70),
    .in_2({1'b0, out_2[0], out_2[1], out_2[2], out_2[3], out_2[4], out_2[5], out_2[6], out_2[7], out_2[8], out_2[9], out_2[10], out_2[11], out_2[12], out_2[13], out_2[14], out_2[15], out_2[16], out_2[17], out_2[18], out_2[19], out_2[20], out_2[21], out_2[22], out_2[23], out_2[24], out_2[25], out_2[26], out_2[27], out_2[28], out_2[29], out_2[30]}),
    .out_3(check_for_money_48_out_3));
  check_for_money check_for_money_49 (
    .in_1(out_43),
    .in_2({1'b0, out_2[0], out_2[1], out_2[2], out_2[3], out_2[4], out_2[5], out_2[6], out_2[7], out_2[8], out_2[9], out_2[10], out_2[11], out_2[12], out_2[13], out_2[14], out_2[15], out_2[16], out_2[17], out_2[18], out_2[19], out_2[20], out_2[21], out_2[22], out_2[23], out_2[24], out_2[25], out_2[26], out_2[27], out_2[28], out_2[29], out_2[30]}),
    .out_3(check_for_money_49_out_3));
  check_for_money check_for_money_50 (
    .in_1(out_47),
    .in_2({1'b0, out_2[0], out_2[1], out_2[2], out_2[3], out_2[4], out_2[5], out_2[6], out_2[7], out_2[8], out_2[9], out_2[10], out_2[11], out_2[12], out_2[13], out_2[14], out_2[15], out_2[16], out_2[17], out_2[18], out_2[19], out_2[20], out_2[21], out_2[22], out_2[23], out_2[24], out_2[25], out_2[26], out_2[27], out_2[28], out_2[29], out_2[30]}),
    .out_3(check_for_money_50_out_3));
  check_for_money check_for_money_51 (
    .in_1(out_51),
    .in_2({1'b0, out_2[0], out_2[1], out_2[2], out_2[3], out_2[4], out_2[5], out_2[6], out_2[7], out_2[8], out_2[9], out_2[10], out_2[11], out_2[12], out_2[13], out_2[14], out_2[15], out_2[16], out_2[17], out_2[18], out_2[19], out_2[20], out_2[21], out_2[22], out_2[23], out_2[24], out_2[25], out_2[26], out_2[27], out_2[28], out_2[29], out_2[30]}),
    .out_3(check_for_money_51_out_3));
  check_for_money check_for_money_52 (
    .in_1(out_55),
    .in_2({1'b0, out_2[0], out_2[1], out_2[2], out_2[3], out_2[4], out_2[5], out_2[6], out_2[7], out_2[8], out_2[9], out_2[10], out_2[11], out_2[12], out_2[13], out_2[14], out_2[15], out_2[16], out_2[17], out_2[18], out_2[19], out_2[20], out_2[21], out_2[22], out_2[23], out_2[24], out_2[25], out_2[26], out_2[27], out_2[28], out_2[29], out_2[30]}),
    .out_3(check_for_money_52_out_3));
  check_for_money check_for_money_53 (
    .in_1(out_59),
    .in_2({1'b0, out_2[0], out_2[1], out_2[2], out_2[3], out_2[4], out_2[5], out_2[6], out_2[7], out_2[8], out_2[9], out_2[10], out_2[11], out_2[12], out_2[13], out_2[14], out_2[15], out_2[16], out_2[17], out_2[18], out_2[19], out_2[20], out_2[21], out_2[22], out_2[23], out_2[24], out_2[25], out_2[26], out_2[27], out_2[28], out_2[29], out_2[30]}),
    .out_3(check_for_money_53_out_3));
  check_for_money check_for_money_54 (
    .in_1(out_63),
    .in_2({1'b0, out_2[0], out_2[1], out_2[2], out_2[3], out_2[4], out_2[5], out_2[6], out_2[7], out_2[8], out_2[9], out_2[10], out_2[11], out_2[12], out_2[13], out_2[14], out_2[15], out_2[16], out_2[17], out_2[18], out_2[19], out_2[20], out_2[21], out_2[22], out_2[23], out_2[24], out_2[25], out_2[26], out_2[27], out_2[28], out_2[29], out_2[30]}),
    .out_3(check_for_money_54_out_3));
  check_for_money check_for_money_55 (
    .in_1(out_67),
    .in_2({1'b0, out_2[0], out_2[1], out_2[2], out_2[3], out_2[4], out_2[5], out_2[6], out_2[7], out_2[8], out_2[9], out_2[10], out_2[11], out_2[12], out_2[13], out_2[14], out_2[15], out_2[16], out_2[17], out_2[18], out_2[19], out_2[20], out_2[21], out_2[22], out_2[23], out_2[24], out_2[25], out_2[26], out_2[27], out_2[28], out_2[29], out_2[30]}),
    .out_3(check_for_money_55_out_3));
  check_for_money check_for_money_56 (
    .in_1(out_71),
    .in_2({1'b0, out_2[0], out_2[1], out_2[2], out_2[3], out_2[4], out_2[5], out_2[6], out_2[7], out_2[8], out_2[9], out_2[10], out_2[11], out_2[12], out_2[13], out_2[14], out_2[15], out_2[16], out_2[17], out_2[18], out_2[19], out_2[20], out_2[21], out_2[22], out_2[23], out_2[24], out_2[25], out_2[26], out_2[27], out_2[28], out_2[29], out_2[30]}),
    .out_3(check_for_money_56_out_3));
  check_for_money check_for_money_57 (
    .in_1(out_44),
    .in_2({1'b0, out_2[0], out_2[1], out_2[2], out_2[3], out_2[4], out_2[5], out_2[6], out_2[7], out_2[8], out_2[9], out_2[10], out_2[11], out_2[12], out_2[13], out_2[14], out_2[15], out_2[16], out_2[17], out_2[18], out_2[19], out_2[20], out_2[21], out_2[22], out_2[23], out_2[24], out_2[25], out_2[26], out_2[27], out_2[28], out_2[29], out_2[30]}),
    .out_3(check_for_money_57_out_3));
  check_for_money check_for_money_58 (
    .in_1(out_48),
    .in_2({1'b0, out_2[0], out_2[1], out_2[2], out_2[3], out_2[4], out_2[5], out_2[6], out_2[7], out_2[8], out_2[9], out_2[10], out_2[11], out_2[12], out_2[13], out_2[14], out_2[15], out_2[16], out_2[17], out_2[18], out_2[19], out_2[20], out_2[21], out_2[22], out_2[23], out_2[24], out_2[25], out_2[26], out_2[27], out_2[28], out_2[29], out_2[30]}),
    .out_3(check_for_money_58_out_3));
  check_for_money check_for_money_59 (
    .in_1(out_52),
    .in_2({1'b0, out_2[0], out_2[1], out_2[2], out_2[3], out_2[4], out_2[5], out_2[6], out_2[7], out_2[8], out_2[9], out_2[10], out_2[11], out_2[12], out_2[13], out_2[14], out_2[15], out_2[16], out_2[17], out_2[18], out_2[19], out_2[20], out_2[21], out_2[22], out_2[23], out_2[24], out_2[25], out_2[26], out_2[27], out_2[28], out_2[29], out_2[30]}),
    .out_3(check_for_money_59_out_3));
  check_for_money check_for_money_60 (
    .in_1(out_56),
    .in_2({1'b0, out_2[0], out_2[1], out_2[2], out_2[3], out_2[4], out_2[5], out_2[6], out_2[7], out_2[8], out_2[9], out_2[10], out_2[11], out_2[12], out_2[13], out_2[14], out_2[15], out_2[16], out_2[17], out_2[18], out_2[19], out_2[20], out_2[21], out_2[22], out_2[23], out_2[24], out_2[25], out_2[26], out_2[27], out_2[28], out_2[29], out_2[30]}),
    .out_3(check_for_money_60_out_3));
  check_for_money check_for_money_61 (
    .in_1(out_60),
    .in_2({1'b0, out_2[0], out_2[1], out_2[2], out_2[3], out_2[4], out_2[5], out_2[6], out_2[7], out_2[8], out_2[9], out_2[10], out_2[11], out_2[12], out_2[13], out_2[14], out_2[15], out_2[16], out_2[17], out_2[18], out_2[19], out_2[20], out_2[21], out_2[22], out_2[23], out_2[24], out_2[25], out_2[26], out_2[27], out_2[28], out_2[29], out_2[30]}),
    .out_3(check_for_money_61_out_3));
  check_for_money check_for_money_62 (
    .in_1(out_64),
    .in_2({1'b0, out_2[0], out_2[1], out_2[2], out_2[3], out_2[4], out_2[5], out_2[6], out_2[7], out_2[8], out_2[9], out_2[10], out_2[11], out_2[12], out_2[13], out_2[14], out_2[15], out_2[16], out_2[17], out_2[18], out_2[19], out_2[20], out_2[21], out_2[22], out_2[23], out_2[24], out_2[25], out_2[26], out_2[27], out_2[28], out_2[29], out_2[30]}),
    .out_3(check_for_money_62_out_3));
  check_for_money check_for_money_63 (
    .in_1(out_68),
    .in_2({1'b0, out_2[0], out_2[1], out_2[2], out_2[3], out_2[4], out_2[5], out_2[6], out_2[7], out_2[8], out_2[9], out_2[10], out_2[11], out_2[12], out_2[13], out_2[14], out_2[15], out_2[16], out_2[17], out_2[18], out_2[19], out_2[20], out_2[21], out_2[22], out_2[23], out_2[24], out_2[25], out_2[26], out_2[27], out_2[28], out_2[29], out_2[30]}),
    .out_3(check_for_money_63_out_3));
  check_for_money check_for_money_64 (
    .in_1(out_72),
    .in_2({1'b0, out_2[0], out_2[1], out_2[2], out_2[3], out_2[4], out_2[5], out_2[6], out_2[7], out_2[8], out_2[9], out_2[10], out_2[11], out_2[12], out_2[13], out_2[14], out_2[15], out_2[16], out_2[17], out_2[18], out_2[19], out_2[20], out_2[21], out_2[22], out_2[23], out_2[24], out_2[25], out_2[26], out_2[27], out_2[28], out_2[29], out_2[30]}),
    .out_3(check_for_money_64_out_3));
  Multiplexer #(.width(31), .enable("false")) multiplexer_74 (
    .in0(31'hc000), .in1(multiplexer_72_out), .out(multiplexer_74_out), .sel(game_state));
  Multiplexer #(.width(32), .enable("false")) multiplexer_75 (
    .in0(32'h1800000), .in1(multiplexer_73_out), .out(multiplexer_75_out), .sel(game_state));
  Multiplexer #(.select(5), .enable("false")) multiplexer_76 (
    .in0(check_for_money_33_out_3), .in1(check_for_money_34_out_3), .in2(check_for_money_35_out_3),
    .in3(check_for_money_36_out_3), .in4(check_for_money_37_out_3), .in5(check_for_money_38_out_3),
    .in6(check_for_money_39_out_3), .in7(check_for_money_40_out_3), .in8(check_for_money_41_out_3),
    .in9(check_for_money_42_out_3), .in10(check_for_money_43_out_3), .in11(check_for_money_44_out_3),
    .in12(check_for_money_45_out_3), .in13(check_for_money_46_out_3), .in14(check_for_money_47_out_3),
    .in15(check_for_money_48_out_3), .in16(check_for_money_49_out_3), .in17(check_for_money_50_out_3),
    .in18(check_for_money_51_out_3), .in19(check_for_money_52_out_3), .in20(check_for_money_53_out_3),
    .in21(check_for_money_54_out_3), .in22(check_for_money_55_out_3), .in23(check_for_money_56_out_3),
    .in24(check_for_money_57_out_3), .in25(check_for_money_58_out_3), .in26(check_for_money_59_out_3),
    .in27(check_for_money_60_out_3), .in28(check_for_money_61_out_3), .in29(check_for_money_62_out_3),
    .in30(check_for_money_63_out_3), .in31(check_for_money_64_out_3), .out(multiplexer_76_out),
    .sel(bitfinder_2_index));
  BitFinder #(.width(32)) bitfinder_2 (.in(out_3), .index(bitfinder_2_index));  // open: found
  Register #(.width(31)) register_68 (.D(multiplexer_74_out), .Q(out_2), .clk(tact_for_player));  // open: en, clr
  Register #(.width(32)) register_69 (.D(multiplexer_75_out), .Q(out_3), .clk(tact));  // open: en, clr
  check_helper check_helper_1 (.in_1(out_5), .in_2({1'b0, x_inverted_alt}), .out_3(check_helper_1_out_3));
  check_helper check_helper_2 (.in_1(out_10), .in_2({1'b0, x_inverted_alt}), .out_3(check_helper_2_out_3));
  check_helper check_helper_3 (.in_1(out_14), .in_2({1'b0, x_inverted_alt}), .out_3(check_helper_3_out_3));
  check_helper check_helper_4 (.in_1(out_18), .in_2({1'b0, x_inverted_alt}), .out_3(check_helper_4_out_3));
  check_helper check_helper_5 (.in_1(out_22), .in_2({1'b0, x_inverted_alt}), .out_3(check_helper_5_out_3));
  check_helper check_helper_6 (.in_1(out_26), .in_2({1'b0, x_inverted_alt}), .out_3(check_helper_6_out_3));
  check_helper check_helper_7 (.in_1(out_30), .in_2({1'b0, x_inverted_alt}), .out_3(check_helper_7_out_3));
  check_helper check_helper_8 (.in_1(out_34), .in_2({1'b0, x_inverted_alt}), .out_3(check_helper_8_out_3));
  check_helper check_helper_9 (.in_1(out_6), .in_2({1'b0, x_inverted_alt}), .out_3(check_helper_9_out_3));
  check_helper check_helper_10 (.in_1(out_11), .in_2({1'b0, x_inverted_alt}), .out_3(check_helper_10_out_3));
  check_helper check_helper_11 (.in_1(out_15), .in_2({1'b0, x_inverted_alt}), .out_3(check_helper_11_out_3));
  check_helper check_helper_12 (.in_1(out_19), .in_2({1'b0, x_inverted_alt}), .out_3(check_helper_12_out_3));
  check_helper check_helper_13 (.in_1(out_23), .in_2({1'b0, x_inverted_alt}), .out_3(check_helper_13_out_3));
  check_helper check_helper_14 (.in_1(out_27), .in_2({1'b0, x_inverted_alt}), .out_3(check_helper_14_out_3));
  check_helper check_helper_15 (.in_1(out_31), .in_2({1'b0, x_inverted_alt}), .out_3(check_helper_15_out_3));
  check_helper check_helper_16 (.in_1(out_35), .in_2({1'b0, x_inverted_alt}), .out_3(check_helper_16_out_3));
  check_helper check_helper_17 (.in_1(out_7), .in_2({1'b0, x_inverted_alt}), .out_3(check_helper_17_out_3));
  check_helper check_helper_18 (.in_1(out_12), .in_2({1'b0, x_inverted_alt}), .out_3(check_helper_18_out_3));
  check_helper check_helper_19 (.in_1(out_16), .in_2({1'b0, x_inverted_alt}), .out_3(check_helper_19_out_3));
  check_helper check_helper_20 (.in_1(out_20), .in_2({1'b0, x_inverted_alt}), .out_3(check_helper_20_out_3));
  check_helper check_helper_21 (.in_1(out_24), .in_2({1'b0, x_inverted_alt}), .out_3(check_helper_21_out_3));
  check_helper check_helper_22 (.in_1(out_28), .in_2({1'b0, x_inverted_alt}), .out_3(check_helper_22_out_3));
  check_helper check_helper_23 (.in_1(out_32), .in_2({1'b0, x_inverted_alt}), .out_3(check_helper_23_out_3));
  check_helper check_helper_24 (.in_1(out_36), .in_2({1'b0, x_inverted_alt}), .out_3(check_helper_24_out_3));
  check_helper check_helper_25 (.in_1(out_8), .in_2({1'b0, x_inverted_alt}), .out_3(check_helper_25_out_3));
  check_helper check_helper_26 (.in_1(out_13), .in_2({1'b0, x_inverted_alt}), .out_3(check_helper_26_out_3));
  check_helper check_helper_27 (.in_1(out_17), .in_2({1'b0, x_inverted_alt}), .out_3(check_helper_27_out_3));
  check_helper check_helper_28 (.in_1(out_21), .in_2({1'b0, x_inverted_alt}), .out_3(check_helper_28_out_3));
  check_helper check_helper_29 (.in_1(out_25), .in_2({1'b0, x_inverted_alt}), .out_3(check_helper_29_out_3));
  check_helper check_helper_30 (.in_1(out_29), .in_2({1'b0, x_inverted_alt}), .out_3(check_helper_30_out_3));
  check_helper check_helper_31 (.in_1(out_33), .in_2({1'b0, x_inverted_alt}), .out_3(check_helper_31_out_3));
  check_helper check_helper_32 (.in_1(out_37), .in_2({1'b0, x_inverted_alt}), .out_3(check_helper_32_out_3));
  BitFinder #(.width(32), .\type ("high1")) bitfinder_3 (.in(out_3), .index(bitfinder_3_index));  // open: found
  not not_10 (start_t, game_state);
  Multiplexer #(.width(31), .enable("false")) multiplexer_77 (
    .in0({31{1'b0}}), .in1(shifter_2_out), .out(multiplexer_77_out), .sel(left));
  Shifter #(.width(31), .shift("lr")) shifter_2 (.in(out_2), .\dist (5'b00001), .out(shifter_2_out));
  Multiplexer #(.width(31), .enable("false")) multiplexer_78 (
    .in0({31{1'b0}}), .in1(shifter_3_out), .out(multiplexer_78_out), .sel(right));
  Shifter #(.width(31)) shifter_3 (.in(out_2), .\dist (5'b00001), .out(shifter_3_out));
  Multiplexer #(.width(32), .enable("false")) multiplexer_79 (
    .in0({32{1'b0}}), .in1(shifter_4_out), .out(multiplexer_79_out), .sel(down));
  Shifter #(.width(32), .shift("lr")) shifter_4 (.in(out_3), .\dist (5'b00001), .out(shifter_4_out));
  Multiplexer #(.width(32), .enable("false")) multiplexer_80 (
    .in0({32{1'b0}}), .in1(shifter_5_out), .out(multiplexer_80_out), .sel(not_11_out));
  Shifter #(.width(32)) shifter_5 (.in(out_3), .\dist (5'b00001), .out(shifter_5_out));
  not not_11 (not_11_out, down);
  and and_2 (x_cond, multiplexer_81_out, multiplexer_82_out);
  check_helper check_helper_33 (.in_1(out_5), .in_2({1'b0, x_inverted_alt}), .out_3(check_helper_33_out_3));
  check_helper check_helper_34 (.in_1(out_10), .in_2({1'b0, x_inverted_alt}), .out_3(check_helper_34_out_3));
  check_helper check_helper_35 (.in_1(out_14), .in_2({1'b0, x_inverted_alt}), .out_3(check_helper_35_out_3));
  check_helper check_helper_36 (.in_1(out_18), .in_2({1'b0, x_inverted_alt}), .out_3(check_helper_36_out_3));
  check_helper check_helper_37 (.in_1(out_22), .in_2({1'b0, x_inverted_alt}), .out_3(check_helper_37_out_3));
  check_helper check_helper_38 (.in_1(out_26), .in_2({1'b0, x_inverted_alt}), .out_3(check_helper_38_out_3));
  check_helper check_helper_39 (.in_1(out_30), .in_2({1'b0, x_inverted_alt}), .out_3(check_helper_39_out_3));
  check_helper check_helper_40 (.in_1(out_34), .in_2({1'b0, x_inverted_alt}), .out_3(check_helper_40_out_3));
  check_helper check_helper_41 (.in_1(out_6), .in_2({1'b0, x_inverted_alt}), .out_3(check_helper_41_out_3));
  check_helper check_helper_42 (.in_1(out_11), .in_2({1'b0, x_inverted_alt}), .out_3(check_helper_42_out_3));
  check_helper check_helper_43 (.in_1(out_15), .in_2({1'b0, x_inverted_alt}), .out_3(check_helper_43_out_3));
  check_helper check_helper_44 (.in_1(out_19), .in_2({1'b0, x_inverted_alt}), .out_3(check_helper_44_out_3));
  check_helper check_helper_45 (.in_1(out_23), .in_2({1'b0, x_inverted_alt}), .out_3(check_helper_45_out_3));
  check_helper check_helper_46 (.in_1(out_27), .in_2({1'b0, x_inverted_alt}), .out_3(check_helper_46_out_3));
  check_helper check_helper_47 (.in_1(out_31), .in_2({1'b0, x_inverted_alt}), .out_3(check_helper_47_out_3));
  check_helper check_helper_48 (.in_1(out_35), .in_2({1'b0, x_inverted_alt}), .out_3(check_helper_48_out_3));
  check_helper check_helper_49 (.in_1(out_7), .in_2({1'b0, x_inverted_alt}), .out_3(check_helper_49_out_3));
  Multiplexer #(.select(5), .enable("false")) multiplexer_81 (
    .in0(check_helper_1_out_3), .in1(check_helper_2_out_3), .in2(check_helper_3_out_3),
    .in3(check_helper_4_out_3), .in4(check_helper_5_out_3), .in5(check_helper_6_out_3),
    .in6(check_helper_7_out_3), .in7(check_helper_8_out_3), .in8(check_helper_9_out_3),
    .in9(check_helper_10_out_3), .in10(check_helper_11_out_3), .in11(check_helper_12_out_3),
    .in12(check_helper_13_out_3), .in13(check_helper_14_out_3), .in14(check_helper_15_out_3),
    .in15(check_helper_16_out_3), .in16(check_helper_17_out_3), .in17(check_helper_18_out_3),
    .in18(check_helper_19_out_3), .in19(check_helper_20_out_3), .in20(check_helper_21_out_3),
    .in21(check_helper_22_out_3), .in22(check_helper_23_out_3), .in23(check_helper_24_out_3),
    .in24(check_helper_25_out_3), .in25(check_helper_26_out_3), .in26(check_helper_27_out_3),
    .in27(check_helper_28_out_3), .in28(check_helper_29_out_3), .in29(check_helper_30_out_3),
    .in30(check_helper_31_out_3), .in31(check_helper_32_out_3), .out(multiplexer_81_out),
    .sel(bitfinder_3_index));
  check_helper check_helper_50 (.in_1(out_12), .in_2({1'b0, x_inverted_alt}), .out_3(check_helper_50_out_3));
  check_helper check_helper_51 (.in_1(out_16), .in_2({1'b0, x_inverted_alt}), .out_3(check_helper_51_out_3));
  check_helper check_helper_52 (.in_1(out_20), .in_2({1'b0, x_inverted_alt}), .out_3(check_helper_52_out_3));
  check_helper check_helper_53 (.in_1(out_24), .in_2({1'b0, x_inverted_alt}), .out_3(check_helper_53_out_3));
  check_helper check_helper_54 (.in_1(out_28), .in_2({1'b0, x_inverted_alt}), .out_3(check_helper_54_out_3));
  check_helper check_helper_55 (.in_1(out_32), .in_2({1'b0, x_inverted_alt}), .out_3(check_helper_55_out_3));
  check_helper check_helper_56 (.in_1(out_36), .in_2({1'b0, x_inverted_alt}), .out_3(check_helper_56_out_3));
  check_helper check_helper_57 (.in_1(out_8), .in_2({1'b0, x_inverted_alt}), .out_3(check_helper_57_out_3));
  check_helper check_helper_58 (.in_1(out_13), .in_2({1'b0, x_inverted_alt}), .out_3(check_helper_58_out_3));
  check_helper check_helper_59 (.in_1(out_17), .in_2({1'b0, x_inverted_alt}), .out_3(check_helper_59_out_3));
  check_helper check_helper_60 (.in_1(out_21), .in_2({1'b0, x_inverted_alt}), .out_3(check_helper_60_out_3));
  check_helper check_helper_61 (.in_1(out_25), .in_2({1'b0, x_inverted_alt}), .out_3(check_helper_61_out_3));
  check_helper check_helper_62 (.in_1(out_29), .in_2({1'b0, x_inverted_alt}), .out_3(check_helper_62_out_3));
  check_helper check_helper_63 (.in_1(out_33), .in_2({1'b0, x_inverted_alt}), .out_3(check_helper_63_out_3));
  check_helper check_helper_64 (.in_1(out_37), .in_2({1'b0, x_inverted_alt}), .out_3(check_helper_64_out_3));
  assign {x_inverted_alt[0], x_inverted_alt[1], x_inverted_alt[2], x_inverted_alt[3], x_inverted_alt[4], x_inverted_alt[5], x_inverted_alt[6], x_inverted_alt[7], x_inverted_alt[8], x_inverted_alt[9], x_inverted_alt[10], x_inverted_alt[11], x_inverted_alt[12], x_inverted_alt[13], x_inverted_alt[14], x_inverted_alt[15], x_inverted_alt[16], x_inverted_alt[17], x_inverted_alt[18], x_inverted_alt[19], x_inverted_alt[20], x_inverted_alt[21], x_inverted_alt[22], x_inverted_alt[23], x_inverted_alt[24], x_inverted_alt[25], x_inverted_alt[26], x_inverted_alt[27], x_inverted_alt[28], x_inverted_alt[29], x_inverted_alt[30]} = multiplexer_77_out | multiplexer_78_out;  // OR_Gate or_39, 31 bits wide
  not not_12 (not_12_out, x_inverted_alt[0]);
  not not_13 (not_13_out, x_inverted_alt[29]);
  or or_40 (or_40_out, not_12_out, x_inverted_alt[1]);
  assign or_41_out = multiplexer_79_out | multiplexer_80_out;  // OR_Gate or_41, 32 bits wide
  Multiplexer #(.select(5), .enable("false")) multiplexer_82 (
    .in0(check_helper_33_out_3), .in1(check_helper_34_out_3), .in2(check_helper_35_out_3),
    .in3(check_helper_36_out_3), .in4(check_helper_37_out_3), .in5(check_helper_38_out_3),
    .in6(check_helper_39_out_3), .in7(check_helper_40_out_3), .in8(check_helper_41_out_3),
    .in9(check_helper_42_out_3), .in10(check_helper_43_out_3), .in11(check_helper_44_out_3),
    .in12(check_helper_45_out_3), .in13(check_helper_46_out_3), .in14(check_helper_47_out_3),
    .in15(check_helper_48_out_3), .in16(check_helper_49_out_3), .in17(check_helper_50_out_3),
    .in18(check_helper_51_out_3), .in19(check_helper_52_out_3), .in20(check_helper_53_out_3),
    .in21(check_helper_54_out_3), .in22(check_helper_55_out_3), .in23(check_helper_56_out_3),
    .in24(check_helper_57_out_3), .in25(check_helper_58_out_3), .in26(check_helper_59_out_3),
    .in27(check_helper_60_out_3), .in28(check_helper_61_out_3), .in29(check_helper_62_out_3),
    .in30(check_helper_63_out_3), .in31(check_helper_64_out_3), .out(multiplexer_82_out),
    .sel(bitfinder_4_index));
  BitFinder #(.width(32)) bitfinder_4 (.in(out_3), .index(bitfinder_4_index));  // open: found
  start_stop start_stop_1 (.start_stop(Start), .state_of_game(game_state), .lose(Lose_east));
  keyboard keyboard_2 (.keyboard(keyboard), .right(right), .left(left), .start(Start), .pause(Pause));
  DotMatrix #(.inputtype("row"), .matrixcols(32), .matrixrows(32)) dotmatrix_1 (
    .row0(out_37), .row1(out_33), .row2(out_29), .row3(out_25), .row4(out_21), .row5(out_17), .row6(out_13),
    .row7(out_8), .row8(out_36), .row9(out_32), .row10(out_28), .row11(out_24), .row12(out_20),
    .row13(out_16), .row14(out_12), .row15(out_7), .row16(out_35), .row17(out_31), .row18(out_27),
    .row19(out_23), .row20(out_19), .row21(out_15), .row22(out_11), .row23(out_6), .row24(out_34),
    .row25(out_30), .row26(out_26), .row27(out_22), .row28(out_18), .row29(out_14), .row30(out_10),
    .row31(out_5));
  DotMatrix #(.inputtype("row"), .matrixcols(30), .matrixrows(32), .dotshape("circle")) dotmatrix_2 (
    .row0(out_72), .row1(out_68), .row2(out_64), .row3(out_60), .row4(out_56), .row5(out_52), .row6(out_48),
    .row7(out_44), .row8(out_71), .row9(out_67), .row10(out_63), .row11(out_59), .row12(out_55),
    .row13(out_51), .row14(out_47), .row15(out_43), .row16(out_70), .row17(out_66), .row18(out_62),
    .row19(out_58), .row20(out_54), .row21(out_50), .row22(out_46), .row23(out_42), .row24(out_69),
    .row25(out_65), .row26(out_61), .row27(out_57), .row28(out_53), .row29(out_49), .row30(out_45),
    .row31(out_41));
  // DotMatrix #(.inputtype("select"), .matrixcols(31), .matrixrows(32)) dotmatrix_3: pin names not known; wires that end beside it: keyboard, out_2, out_3
  and and_3 (and_3_out, x_cond, or_42_out, or_40_out, not_14_out);
  or or_42 (or_42_out, not_13_out, x_inverted_alt[28]);
  Comparator #(.width(32)) comparator_5 (.a(or_41_out), .b({32{1'b0}}), .eq(comparator_5_eq));  // open: gt, lt
  Multiplexer #(.width(31), .enable("false")) multiplexer_83 (
    .in0(out_2),
    .in1({x_inverted_alt[0], x_inverted_alt[1], x_inverted_alt[2], x_inverted_alt[3], x_inverted_alt[4], x_inverted_alt[5], x_inverted_alt[6], x_inverted_alt[7], x_inverted_alt[8], x_inverted_alt[9], x_inverted_alt[10], x_inverted_alt[11], x_inverted_alt[12], x_inverted_alt[13], x_inverted_alt[14], x_inverted_alt[15], x_inverted_alt[16], x_inverted_alt[17], x_inverted_alt[18], x_inverted_alt[19], x_inverted_alt[20], x_inverted_alt[21], x_inverted_alt[22], x_inverted_alt[23], x_inverted_alt[24], x_inverted_alt[25], x_inverted_alt[26], x_inverted_alt[27], x_inverted_alt[28], x_inverted_alt[29], x_inverted_alt[30]}),
    .out(x_final), .sel(and_3_out));
  not not_14 (not_14_out, comparator_6_eq);
  Comparator #(.width(31)) comparator_6 (
    .a({x_inverted_alt[0], x_inverted_alt[1], x_inverted_alt[2], x_inverted_alt[3], x_inverted_alt[4], x_inverted_alt[5], x_inverted_alt[6], x_inverted_alt[7], x_inverted_alt[8], x_inverted_alt[9], x_inverted_alt[10], x_inverted_alt[11], x_inverted_alt[12], x_inverted_alt[13], x_inverted_alt[14], x_inverted_alt[15], x_inverted_alt[16], x_inverted_alt[17], x_inverted_alt[18], x_inverted_alt[19], x_inverted_alt[20], x_inverted_alt[21], x_inverted_alt[22], x_inverted_alt[23], x_inverted_alt[24], x_inverted_alt[25], x_inverted_alt[26], x_inverted_alt[27], x_inverted_alt[28], x_inverted_alt[29], x_inverted_alt[30]}),
    .b({31{1'b0}}), .eq(comparator_6_eq));  // open: gt, lt
  Multiplexer #(.width(32), .enable("false")) multiplexer_84 (
    .in0(out_3), .in1(or_41_out), .out(y_final), .sel(not_15_out));
  not not_15 (not_15_out, comparator_5_eq);
  check_helper check_helper_65 (
    .in_1(out_5),
    .in_2({1'b0, x_final[0], x_final[1], x_final[2], x_final[3], x_final[4], x_final[5], x_final[6], x_final[7], x_final[8], x_final[9], x_final[10], x_final[11], x_final[12], x_final[13], x_final[14], x_final[15], x_final[16], x_final[17], x_final[18], x_final[19], x_final[20], x_final[21], x_final[22], x_final[23], x_final[24], x_final[25], x_final[26], x_final[27], x_final[28], x_final[29], x_final[30]}),
    .out_3(check_helper_65_out_3));
  check_helper check_helper_66 (
    .in_1(out_10),
    .in_2({1'b0, x_final[0], x_final[1], x_final[2], x_final[3], x_final[4], x_final[5], x_final[6], x_final[7], x_final[8], x_final[9], x_final[10], x_final[11], x_final[12], x_final[13], x_final[14], x_final[15], x_final[16], x_final[17], x_final[18], x_final[19], x_final[20], x_final[21], x_final[22], x_final[23], x_final[24], x_final[25], x_final[26], x_final[27], x_final[28], x_final[29], x_final[30]}),
    .out_3(check_helper_66_out_3));
  check_helper check_helper_67 (
    .in_1(out_14),
    .in_2({1'b0, x_final[0], x_final[1], x_final[2], x_final[3], x_final[4], x_final[5], x_final[6], x_final[7], x_final[8], x_final[9], x_final[10], x_final[11], x_final[12], x_final[13], x_final[14], x_final[15], x_final[16], x_final[17], x_final[18], x_final[19], x_final[20], x_final[21], x_final[22], x_final[23], x_final[24], x_final[25], x_final[26], x_final[27], x_final[28], x_final[29], x_final[30]}),
    .out_3(check_helper_67_out_3));
  check_helper check_helper_68 (
    .in_1(out_18),
    .in_2({1'b0, x_final[0], x_final[1], x_final[2], x_final[3], x_final[4], x_final[5], x_final[6], x_final[7], x_final[8], x_final[9], x_final[10], x_final[11], x_final[12], x_final[13], x_final[14], x_final[15], x_final[16], x_final[17], x_final[18], x_final[19], x_final[20], x_final[21], x_final[22], x_final[23], x_final[24], x_final[25], x_final[26], x_final[27], x_final[28], x_final[29], x_final[30]}),
    .out_3(check_helper_68_out_3));
  check_helper check_helper_69 (
    .in_1(out_22),
    .in_2({1'b0, x_final[0], x_final[1], x_final[2], x_final[3], x_final[4], x_final[5], x_final[6], x_final[7], x_final[8], x_final[9], x_final[10], x_final[11], x_final[12], x_final[13], x_final[14], x_final[15], x_final[16], x_final[17], x_final[18], x_final[19], x_final[20], x_final[21], x_final[22], x_final[23], x_final[24], x_final[25], x_final[26], x_final[27], x_final[28], x_final[29], x_final[30]}),
    .out_3(check_helper_69_out_3));
  check_helper check_helper_70 (
    .in_1(out_26),
    .in_2({1'b0, x_final[0], x_final[1], x_final[2], x_final[3], x_final[4], x_final[5], x_final[6], x_final[7], x_final[8], x_final[9], x_final[10], x_final[11], x_final[12], x_final[13], x_final[14], x_final[15], x_final[16], x_final[17], x_final[18], x_final[19], x_final[20], x_final[21], x_final[22], x_final[23], x_final[24], x_final[25], x_final[26], x_final[27], x_final[28], x_final[29], x_final[30]}),
    .out_3(check_helper_70_out_3));
  check_helper check_helper_71 (
    .in_1(out_30),
    .in_2({1'b0, x_final[0], x_final[1], x_final[2], x_final[3], x_final[4], x_final[5], x_final[6], x_final[7], x_final[8], x_final[9], x_final[10], x_final[11], x_final[12], x_final[13], x_final[14], x_final[15], x_final[16], x_final[17], x_final[18], x_final[19], x_final[20], x_final[21], x_final[22], x_final[23], x_final[24], x_final[25], x_final[26], x_final[27], x_final[28], x_final[29], x_final[30]}),
    .out_3(check_helper_71_out_3));
  check_helper check_helper_72 (
    .in_1(out_34),
    .in_2({1'b0, x_final[0], x_final[1], x_final[2], x_final[3], x_final[4], x_final[5], x_final[6], x_final[7], x_final[8], x_final[9], x_final[10], x_final[11], x_final[12], x_final[13], x_final[14], x_final[15], x_final[16], x_final[17], x_final[18], x_final[19], x_final[20], x_final[21], x_final[22], x_final[23], x_final[24], x_final[25], x_final[26], x_final[27], x_final[28], x_final[29], x_final[30]}),
    .out_3(check_helper_72_out_3));
  check_helper check_helper_73 (
    .in_1(out_6),
    .in_2({1'b0, x_final[0], x_final[1], x_final[2], x_final[3], x_final[4], x_final[5], x_final[6], x_final[7], x_final[8], x_final[9], x_final[10], x_final[11], x_final[12], x_final[13], x_final[14], x_final[15], x_final[16], x_final[17], x_final[18], x_final[19], x_final[20], x_final[21], x_final[22], x_final[23], x_final[24], x_final[25], x_final[26], x_final[27], x_final[28], x_final[29], x_final[30]}),
    .out_3(check_helper_73_out_3));
  check_helper check_helper_74 (
    .in_1(out_11),
    .in_2({1'b0, x_final[0], x_final[1], x_final[2], x_final[3], x_final[4], x_final[5], x_final[6], x_final[7], x_final[8], x_final[9], x_final[10], x_final[11], x_final[12], x_final[13], x_final[14], x_final[15], x_final[16], x_final[17], x_final[18], x_final[19], x_final[20], x_final[21], x_final[22], x_final[23], x_final[24], x_final[25], x_final[26], x_final[27], x_final[28], x_final[29], x_final[30]}),
    .out_3(check_helper_74_out_3));
  check_helper check_helper_75 (
    .in_1(out_15),
    .in_2({1'b0, x_final[0], x_final[1], x_final[2], x_final[3], x_final[4], x_final[5], x_final[6], x_final[7], x_final[8], x_final[9], x_final[10], x_final[11], x_final[12], x_final[13], x_final[14], x_final[15], x_final[16], x_final[17], x_final[18], x_final[19], x_final[20], x_final[21], x_final[22], x_final[23], x_final[24], x_final[25], x_final[26], x_final[27], x_final[28], x_final[29], x_final[30]}),
    .out_3(check_helper_75_out_3));
  check_helper check_helper_76 (
    .in_1(out_19),
    .in_2({1'b0, x_final[0], x_final[1], x_final[2], x_final[3], x_final[4], x_final[5], x_final[6], x_final[7], x_final[8], x_final[9], x_final[10], x_final[11], x_final[12], x_final[13], x_final[14], x_final[15], x_final[16], x_final[17], x_final[18], x_final[19], x_final[20], x_final[21], x_final[22], x_final[23], x_final[24], x_final[25], x_final[26], x_final[27], x_final[28], x_final[29], x_final[30]}),
    .out_3(check_helper_76_out_3));
  check_helper check_helper_77 (
    .in_1(out_23),
    .in_2({1'b0, x_final[0], x_final[1], x_final[2], x_final[3], x_final[4], x_final[5], x_final[6], x_final[7], x_final[8], x_final[9], x_final[10], x_final[11], x_final[12], x_final[13], x_final[14], x_final[15], x_final[16], x_final[17], x_final[18], x_final[19], x_final[20], x_final[21], x_final[22], x_final[23], x_final[24], x_final[25], x_final[26], x_final[27], x_final[28], x_final[29], x_final[30]}),
    .out_3(check_helper_77_out_3));
  check_helper check_helper_78 (
    .in_1(out_27),
    .in_2({1'b0, x_final[0], x_final[1], x_final[2], x_final[3], x_final[4], x_final[5], x_final[6], x_final[7], x_final[8], x_final[9], x_final[10], x_final[11], x_final[12], x_final[13], x_final[14], x_final[15], x_final[16], x_final[17], x_final[18], x_final[19], x_final[20], x_final[21], x_final[22], x_final[23], x_final[24], x_final[25], x_final[26], x_final[27], x_final[28], x_final[29], x_final[30]}),
    .out_3(check_helper_78_out_3));
  check_helper check_helper_79 (
    .in_1(out_31),
    .in_2({1'b0, x_final[0], x_final[1], x_final[2], x_final[3], x_final[4], x_final[5], x_final[6], x_final[7], x_final[8], x_final[9], x_final[10], x_final[11], x_final[12], x_final[13], x_final[14], x_final[15], x_final[16], x_final[17], x_final[18], x_final[19], x_final[20], x_final[21], x_final[22], x_final[23], x_final[24], x_final[25], x_final[26], x_final[27], x_final[28], x_final[29], x_final[30]}),
    .out_3(check_helper_79_out_3));
  check_helper check_helper_80 (
    .in_1(out_35),
    .in_2({1'b0, x_final[0], x_final[1], x_final[2], x_final[3], x_final[4], x_final[5], x_final[6], x_final[7], x_final[8], x_final[9], x_final[10], x_final[11], x_final[12], x_final[13], x_final[14], x_final[15], x_final[16], x_final[17], x_final[18], x_final[19], x_final[20], x_final[21], x_final[22], x_final[23], x_final[24], x_final[25], x_final[26], x_final[27], x_final[28], x_final[29], x_final[30]}),
    .out_3(check_helper_80_out_3));
  check_helper check_helper_81 (
    .in_1(out_7),
    .in_2({1'b0, x_final[0], x_final[1], x_final[2], x_final[3], x_final[4], x_final[5], x_final[6], x_final[7], x_final[8], x_final[9], x_final[10], x_final[11], x_final[12], x_final[13], x_final[14], x_final[15], x_final[16], x_final[17], x_final[18], x_final[19], x_final[20], x_final[21], x_final[22], x_final[23], x_final[24], x_final[25], x_final[26], x_final[27], x_final[28], x_final[29], x_final[30]}),
    .out_3(check_helper_81_out_3));
  check_helper check_helper_82 (
    .in_1(out_12),
    .in_2({1'b0, x_final[0], x_final[1], x_final[2], x_final[3], x_final[4], x_final[5], x_final[6], x_final[7], x_final[8], x_final[9], x_final[10], x_final[11], x_final[12], x_final[13], x_final[14], x_final[15], x_final[16], x_final[17], x_final[18], x_final[19], x_final[20], x_final[21], x_final[22], x_final[23], x_final[24], x_final[25], x_final[26], x_final[27], x_final[28], x_final[29], x_final[30]}),
    .out_3(check_helper_82_out_3));
  check_helper check_helper_83 (
    .in_1(out_16),
    .in_2({1'b0, x_final[0], x_final[1], x_final[2], x_final[3], x_final[4], x_final[5], x_final[6], x_final[7], x_final[8], x_final[9], x_final[10], x_final[11], x_final[12], x_final[13], x_final[14], x_final[15], x_final[16], x_final[17], x_final[18], x_final[19], x_final[20], x_final[21], x_final[22], x_final[23], x_final[24], x_final[25], x_final[26], x_final[27], x_final[28], x_final[29], x_final[30]}),
    .out_3(check_helper_83_out_3));
  check_helper check_helper_84 (
    .in_1(out_20),
    .in_2({1'b0, x_final[0], x_final[1], x_final[2], x_final[3], x_final[4], x_final[5], x_final[6], x_final[7], x_final[8], x_final[9], x_final[10], x_final[11], x_final[12], x_final[13], x_final[14], x_final[15], x_final[16], x_final[17], x_final[18], x_final[19], x_final[20], x_final[21], x_final[22], x_final[23], x_final[24], x_final[25], x_final[26], x_final[27], x_final[28], x_final[29], x_final[30]}),
    .out_3(check_helper_84_out_3));
  check_helper check_helper_85 (
    .in_1(out_24),
    .in_2({1'b0, x_final[0], x_final[1], x_final[2], x_final[3], x_final[4], x_final[5], x_final[6], x_final[7], x_final[8], x_final[9], x_final[10], x_final[11], x_final[12], x_final[13], x_final[14], x_final[15], x_final[16], x_final[17], x_final[18], x_final[19], x_final[20], x_final[21], x_final[22], x_final[23], x_final[24], x_final[25], x_final[26], x_final[27], x_final[28], x_final[29], x_final[30]}),
    .out_3(check_helper_85_out_3));
  check_helper check_helper_86 (
    .in_1(out_28),
    .in_2({1'b0, x_final[0], x_final[1], x_final[2], x_final[3], x_final[4], x_final[5], x_final[6], x_final[7], x_final[8], x_final[9], x_final[10], x_final[11], x_final[12], x_final[13], x_final[14], x_final[15], x_final[16], x_final[17], x_final[18], x_final[19], x_final[20], x_final[21], x_final[22], x_final[23], x_final[24], x_final[25], x_final[26], x_final[27], x_final[28], x_final[29], x_final[30]}),
    .out_3(check_helper_86_out_3));
  check_helper check_helper_87 (
    .in_1(out_32),
    .in_2({1'b0, x_final[0], x_final[1], x_final[2], x_final[3], x_final[4], x_final[5], x_final[6], x_final[7], x_final[8], x_final[9], x_final[10], x_final[11], x_final[12], x_final[13], x_final[14], x_final[15], x_final[16], x_final[17], x_final[18], x_final[19], x_final[20], x_final[21], x_final[22], x_final[23], x_final[24], x_final[25], x_final[26], x_final[27], x_final[28], x_final[29], x_final[30]}),
    .out_3(check_helper_87_out_3));
  check_helper check_helper_88 (
    .in_1(out_36),
    .in_2({1'b0, x_final[0], x_final[1], x_final[2], x_final[3], x_final[4], x_final[5], x_final[6], x_final[7], x_final[8], x_final[9], x_final[10], x_final[11], x_final[12], x_final[13], x_final[14], x_final[15], x_final[16], x_final[17], x_final[18], x_final[19], x_final[20], x_final[21], x_final[22], x_final[23], x_final[24], x_final[25], x_final[26], x_final[27], x_final[28], x_final[29], x_final[30]}),
    .out_3(check_helper_88_out_3));
  check_helper check_helper_89 (
    .in_1(out_8),
    .in_2({1'b0, x_final[0], x_final[1], x_final[2], x_final[3], x_final[4], x_final[5], x_final[6], x_final[7], x_final[8], x_final[9], x_final[10], x_final[11], x_final[12], x_final[13], x_final[14], x_final[15], x_final[16], x_final[17], x_final[18], x_final[19], x_final[20], x_final[21], x_final[22], x_final[23], x_final[24], x_final[25], x_final[26], x_final[27], x_final[28], x_final[29], x_final[30]}),
    .out_3(check_helper_89_out_3));
  check_helper check_helper_90 (
    .in_1(out_13),
    .in_2({1'b0, x_final[0], x_final[1], x_final[2], x_final[3], x_final[4], x_final[5], x_final[6], x_final[7], x_final[8], x_final[9], x_final[10], x_final[11], x_final[12], x_final[13], x_final[14], x_final[15], x_final[16], x_final[17], x_final[18], x_final[19], x_final[20], x_final[21], x_final[22], x_final[23], x_final[24], x_final[25], x_final[26], x_final[27], x_final[28], x_final[29], x_final[30]}),
    .out_3(check_helper_90_out_3));
  check_helper check_helper_91 (
    .in_1(out_17),
    .in_2({1'b0, x_final[0], x_final[1], x_final[2], x_final[3], x_final[4], x_final[5], x_final[6], x_final[7], x_final[8], x_final[9], x_final[10], x_final[11], x_final[12], x_final[13], x_final[14], x_final[15], x_final[16], x_final[17], x_final[18], x_final[19], x_final[20], x_final[21], x_final[22], x_final[23], x_final[24], x_final[25], x_final[26], x_final[27], x_final[28], x_final[29], x_final[30]}),
    .out_3(check_helper_91_out_3));
  check_helper check_helper_92 (
    .in_1(out_21),
    .in_2({1'b0, x_final[0], x_final[1], x_final[2], x_final[3], x_final[4], x_final[5], x_final[6], x_final[7], x_final[8], x_final[9], x_final[10], x_final[11], x_final[12], x_final[13], x_final[14], x_final[15], x_final[16], x_final[17], x_final[18], x_final[19], x_final[20], x_final[21], x_final[22], x_final[23], x_final[24], x_final[25], x_final[26], x_final[27], x_final[28], x_final[29], x_final[30]}),
    .out_3(check_helper_92_out_3));
  check_helper check_helper_93 (
    .in_1(out_25),
    .in_2({1'b0, x_final[0], x_final[1], x_final[2], x_final[3], x_final[4], x_final[5], x_final[6], x_final[7], x_final[8], x_final[9], x_final[10], x_final[11], x_final[12], x_final[13], x_final[14], x_final[15], x_final[16], x_final[17], x_final[18], x_final[19], x_final[20], x_final[21], x_final[22], x_final[23], x_final[24], x_final[25], x_final[26], x_final[27], x_final[28], x_final[29], x_final[30]}),
    .out_3(check_helper_93_out_3));
  check_helper check_helper_94 (
    .in_1(out_29),
    .in_2({1'b0, x_final[0], x_final[1], x_final[2], x_final[3], x_final[4], x_final[5], x_final[6], x_final[7], x_final[8], x_final[9], x_final[10], x_final[11], x_final[12], x_final[13], x_final[14], x_final[15], x_final[16], x_final[17], x_final[18], x_final[19], x_final[20], x_final[21], x_final[22], x_final[23], x_final[24], x_final[25], x_final[26], x_final[27], x_final[28], x_final[29], x_final[30]}),
    .out_3(check_helper_94_out_3));
  check_helper check_helper_95 (
    .in_1(out_33),
    .in_2({1'b0, x_final[0], x_final[1], x_final[2], x_final[3], x_final[4], x_final[5], x_final[6], x_final[7], x_final[8], x_final[9], x_final[10], x_final[11], x_final[12], x_final[13], x_final[14], x_final[15], x_final[16], x_final[17], x_final[18], x_final[19], x_final[20], x_final[21], x_final[22], x_final[23], x_final[24], x_final[25], x_final[26], x_final[27], x_final[28], x_final[29], x_final[30]}),
    .out_3(check_helper_95_out_3));
  check_helper check_helper_96 (
    .in_1(out_37),
    .in_2({1'b0, x_final[0], x_final[1], x_final[2], x_final[3], x_final[4], x_final[5], x_final[6], x_final[7], x_final[8], x_final[9], x_final[10], x_final[11], x_final[12], x_final[13], x_final[14], x_final[15], x_final[16], x_final[17], x_final[18], x_final[19], x_final[20], x_final[21], x_final[22], x_final[23], x_final[24], x_final[25], x_final[26], x_final[27], x_final[28], x_final[29], x_final[30]}),
    .out_3(check_helper_96_out_3));
  BitFinder #(.width(32)) bitfinder_5 (.in(out_3), .index(bitfinder_5_index));  // open: found
  Subtractor #(.width(5)) subtractor_1 (
    .a(bitfinder_5_index), .b(5'b00001), .out(subtractor_1_out));  // open: bin, bout
  Multiplexer #(.enable("false")) multiplexer_85 (.in0(1'b0), .in1(multiplexer_86_out), .out(down), .sel(game_state));
  Multiplexer #(.select(5), .enable("false")) multiplexer_86 (
    .in0(check_helper_65_out_3), .in1(check_helper_66_out_3), .in2(check_helper_67_out_3),
    .in3(check_helper_68_out_3), .in4(check_helper_69_out_3), .in5(check_helper_70_out_3),
    .in6(check_helper_71_out_3), .in7(check_helper_72_out_3), .in8(check_helper_73_out_3),
    .in9(check_helper_74_out_3), .in10(check_helper_75_out_3), .in11(check_helper_76_out_3),
    .in12(check_helper_77_out_3), .in13(check_helper_78_out_3), .in14(check_helper_79_out_3),
    .in15(check_helper_80_out_3), .in16(check_helper_81_out_3), .in17(check_helper_82_out_3),
    .in18(check_helper_83_out_3), .in19(check_helper_84_out_3), .in20(check_helper_85_out_3),
    .in21(check_helper_86_out_3), .in22(check_helper_87_out_3), .in23(check_helper_88_out_3),
    .in24(check_helper_89_out_3), .in25(check_helper_90_out_3), .in26(check_helper_91_out_3),
    .in27(check_helper_92_out_3), .in28(check_helper_93_out_3), .in29(check_helper_94_out_3),
    .in30(check_helper_95_out_3), .in31(check_helper_96_out_3), .out(multiplexer_86_out),
    .sel(subtractor_1_out));
  not not_16 (not_16_out, out_3[1]);
  or or_43 (tp_or_not, not_16_out, out_3[2]);
  Comparator #(.width(32)) comparator_7 (.a({32{1'b0}}), .b(out_23), .eq(comparator_7_eq[0]));  // open: gt, lt
  Comparator #(.width(32)) comparator_8 (.a({32{1'b0}}), .b(out_27), .eq(comparator_7_eq[1]));  // open: gt, lt
  Comparator #(.width(32)) comparator_9 (.a({32{1'b0}}), .b(out_31), .eq(comparator_7_eq[2]));  // open: gt, lt
  Comparator #(.width(32)) comparator_10 (.a({32{1'b0}}), .b(out_35), .eq(comparator_7_eq[3]));  // open: gt, lt
  not not_17 (not_17_out, out_3[31]);
  not not_18 (Lose_east, or_44_out);
  or or_44 (or_44_out, not_17_out, out_3[30]);
  Multiplexer #(.select(4), .width(32), .enable("false")) multiplexer_87 (
    .in7(32'h60000), .in11(32'h30000), .in13(32'h18000), .in14(32'hc0000), .out(new_y), .sel(comparator_7_eq));  // open: in0, in1, in2, in3, in4, in5, in6, in8, in9, in10, in12, in15

  assign Lose_upper = Lose_east;

  // Other names for the same wires on the sheet: _1[31:0] = out_5; _1m[29:0] = out_41; _2[31:0] = out_10;
  //   _2m[29:0] = out_45; _3[31:0] = out_14; _3m[29:0] = out_49; _4[31:0] = out_18; _4m[29:0] = out_53;
  //   _5[31:0] = out_22; _5m[29:0] = out_57; _6[31:0] = out_26; _6m[29:0] = out_61; _7[31:0] = out_30;
  //   _7m[29:0] = out_65; _8[31:0] = out_34; _8m[29:0] = out_69; _9[31:0] = out_6; _9m[29:0] = out_42;
  //   _10[31:0] = out_11; _10m[29:0] = out_46; _11[31:0] = out_15; _11m[29:0] = out_50; _12[31:0] = out_19;
  //   _12m[29:0] = out_54; _13[31:0] = out_23; _13m[29:0] = out_58; _14[31:0] = out_27; _14m[29:0] = out_62;
  //   _15[31:0] = out_31; _15m[29:0] = out_66; _16[31:0] = out_35; _16m[29:0] = out_70; _17[31:0] = out_7;
  //   _17m[29:0] = out_43; _18[31:0] = out_12; _18m[29:0] = out_47; _19[31:0] = out_16; _19m[29:0] = out_51;
  //   _20[31:0] = out_20; _20m[29:0] = out_55; _21[31:0] = out_24; _21m[29:0] = out_59; _22[31:0] = out_28;
  //   _22m[29:0] = out_63; _23[31:0] = out_32; _23m[29:0] = out_67; _24[31:0] = out_36; _24m[29:0] = out_71;
  //   _25[31:0] = out_8; _25m[29:0] = out_44; _26[31:0] = out_13; _26m[29:0] = out_48; _27[31:0] = out_17;
  //   _27m[29:0] = out_52; _28[31:0] = out_21; _28m[29:0] = out_56; _29[31:0] = out_25; _29m[29:0] = out_60;
  //   _30[31:0] = out_29; _30m[29:0] = out_64; _31[31:0] = out_33; _31m[29:0] = out_68; _32[31:0] = out_37;
  //   _32m[29:0] = out_72; lose = Lose_east; reg_y[31:0] = out_3; start_alt_1 = game_state; start_input = Start;
  //   x_inverted[30:0] = {x_final[0], x_final[1], x_final[2], x_final[3], x_final[4], x_final[5], x_final[6], x_final[7], x_final[8], x_final[9], x_final[10], x_final[11], x_final[12], x_final[13], x_final[14], x_final[15], x_final[16], x_final[17], x_final[18], x_final[19], x_final[20], x_final[21], x_final[22], x_final[23], x_final[24], x_final[25], x_final[26], x_final[27], x_final[28], x_final[29], x_final[30]};
  //   x_medium[30:0] = {x_inverted_alt[0], x_inverted_alt[1], x_inverted_alt[2], x_inverted_alt[3], x_inverted_alt[4], x_inverted_alt[5], x_inverted_alt[6], x_inverted_alt[7], x_inverted_alt[8], x_inverted_alt[9], x_inverted_alt[10], x_inverted_alt[11], x_inverted_alt[12], x_inverted_alt[13], x_inverted_alt[14], x_inverted_alt[15], x_inverted_alt[16], x_inverted_alt[17], x_inverted_alt[18], x_inverted_alt[19], x_inverted_alt[20], x_inverted_alt[21], x_inverted_alt[22], x_inverted_alt[23], x_inverted_alt[24], x_inverted_alt[25], x_inverted_alt[26], x_inverted_alt[27], x_inverted_alt[28], x_inverted_alt[29], x_inverted_alt[30]};
  //   reg_x[30:0] = out_2;
  //   x_inverted_money[30:0] = {out_2[0], out_2[1], out_2[2], out_2[3], out_2[4], out_2[5], out_2[6], out_2[7], out_2[8], out_2[9], out_2[10], out_2[11], out_2[12], out_2[13], out_2[14], out_2[15], out_2[16], out_2[17], out_2[18], out_2[19], out_2[20], out_2[21], out_2[22], out_2[23], out_2[24], out_2[25], out_2[26], out_2[27], out_2[28], out_2[29], out_2[30]}

  // Notes on the sheet:
  //   Bottom line
  //   Field options
  //   Money Position
  //   Top line
  //   Collecting money 
  //   Сollision avoidance
  //   Player Position
  //   Checking for a hole
  //   Losing indicator
endmodule

module check_helper (
  input  [31:0] in_1,
  input  [31:0] in_2,
  output out_3
);

  wire or_1_out;
  wire [31:0] and_1_out;

  assign and_1_out = in_1 & in_2;  // AND_Gate and_1, 32 bits wide
  or or_1 (or_1_out, and_1_out[0], and_1_out[1], and_1_out[2], and_1_out[3], and_1_out[4], and_1_out[5], and_1_out[6], and_1_out[7], and_1_out[8], and_1_out[9], and_1_out[10], and_1_out[11], and_1_out[12], and_1_out[13], and_1_out[14], and_1_out[15], and_1_out[17], and_1_out[18], and_1_out[19], and_1_out[20], and_1_out[21], and_1_out[22], and_1_out[23], and_1_out[24], and_1_out[25], and_1_out[26], and_1_out[27], and_1_out[28], and_1_out[29], and_1_out[30], and_1_out[31], and_1_out[16]);
  not not_1 (out_3, or_1_out);
endmodule

module Info_Screen (
  input  Lose_indicator,
  input  Start,
  input  Pause,
  output [31:0] out_4,
  output [31:0] out_5,
  output [31:0] out_6,
  output [31:0] out_7,
  output [31:0] out_8,
  output [31:0] out_9,
  output [31:0] out_10
);

  wire not_1_out;
  wire [1:0] indicator;

  D_Flip_Flop d_ff_1 (.clk(Pause), .D(not_1_out), .Q(indicator[1]));  // open: Qn, preset, en, reset
  not not_1 (not_1_out, indicator[1]);
  D_Flip_Flop d_ff_2 (
    .clk(Lose_indicator), .D(Lose_indicator), .Q(indicator[0]), .reset(Start));  // open: Qn, preset, en
  Multiplexer #(.select(2), .width(32), .enable("false")) multiplexer_1 (
    .in0({32{1'b0}}), .in1(32'he7bde23e), .in2(32'hf3c91cf0), .in3(32'he7bde23e), .out(out_4), .sel(indicator));
  Multiplexer #(.select(2), .width(32), .enable("false")) multiplexer_2 (
    .in0({32{1'b0}}), .in1(32'h94210508), .in2(32'h92492080), .in3(32'h94210508), .out(out_5), .sel(indicator));
  Multiplexer #(.select(2), .width(32), .enable("false")) multiplexer_3 (
    .in0({32{1'b0}}), .in1(32'h94210888), .in2(32'h92492080), .in3(32'h94210888), .out(out_6), .sel(indicator));
  Multiplexer #(.select(2), .width(32), .enable("false")) multiplexer_4 (
    .in0({32{1'b0}}), .in1(32'h97bdef88), .in2(32'hf3c918e0), .in3(32'h97bdef88), .out(out_7), .sel(indicator));
  Multiplexer #(.select(2), .width(32), .enable("false")) multiplexer_5 (
    .in0({32{1'b0}}), .in1(32'h94210888), .in2(32'h82490480), .in3(32'h94210888), .out(out_8), .sel(indicator));
  Multiplexer #(.select(2), .width(32), .enable("false")) multiplexer_6 (
    .in0({32{1'b0}}), .in1(32'h94210888), .in2(32'h82490480), .in3(32'h94210888), .out(out_9), .sel(indicator));
  Multiplexer #(.select(2), .width(32), .enable("false")) multiplexer_7 (
    .in0({32{1'b0}}), .in1(32'he7a1e888), .in2(32'h824638f0), .in3(32'he7a1e888), .out(out_10),
    .sel(indicator));

  // Other names for the same wires on the sheet: lose = indicator[0]; pause_t = indicator[1]
endmodule

module keyboard (
  input  [6:0] keyboard,
  output right,
  output left,
  output start,
  output pause
);

  wire clock_1_out, comparator_1_eq, comparator_2_eq, comparator_3_eq, not_1_out, or_1_out;
  wire [6:0] demultiplexer_1_out0, demultiplexer_1_out1, register_1_q;

  Comparator #(.width(7)) comparator_1 (.a(keyboard), .b(7'b0001010), .eq(comparator_1_eq));  // open: gt, lt
  Comparator #(.width(7)) comparator_2 (.a(keyboard), .b(7'b0100000), .eq(comparator_2_eq));  // open: gt, lt
  Demultiplexer #(.width(7), .enable("false")) demultiplexer_1 (
    .out0(demultiplexer_1_out0), .out1(demultiplexer_1_out1), .in(keyboard), .sel(or_1_out));
  or or_1 (or_1_out, comparator_1_eq, comparator_2_eq);
  not not_1 (not_1_out, comparator_3_eq);
  Comparator #(.width(7)) comparator_3 (.a(demultiplexer_1_out0), .b({7{1'b0}}), .eq(comparator_3_eq));  // open: gt, lt
  Comparator #(.width(7)) comparator_4 (.a(demultiplexer_1_out1), .b(7'b0001010), .eq(start));  // open: gt, lt
  Comparator #(.width(7)) comparator_5 (.a(demultiplexer_1_out1), .b(7'b0100000), .eq(pause));  // open: gt, lt
  Register #(.width(7)) register_1 (
    .D(demultiplexer_1_out0), .en(not_1_out), .Q(register_1_q), .clk(clock_1_out));  // open: clr
  Clock clock_1 (.out(clock_1_out));
  Comparator #(.width(7)) comparator_6 (.a(register_1_q), .b(7'b1100100), .eq(right));  // open: gt, lt
  Comparator #(.width(7)) comparator_7 (.a(register_1_q), .b(7'b1100001), .eq(left));  // open: gt, lt
endmodule

module new_platform (
  input  [4:0] in_1,
  output [31:0] new_platform
);

  Multiplexer #(.select(5), .width(32), .enable("false")) multiplexer_1 (
    .in0(32'h7fffff8), .in1(32'h23fffff1), .in2(32'h31ffffe3), .in3(32'h38ffffc7), .in4(32'h3c7fff8f),
    .in5(32'h3e3fff1f), .in6(32'h3f1ffe3f), .in7(32'h3f8ffc7f), .in8(32'h3fc7f8ff), .in9(32'h3fe3f1ff),
    .in10(32'h3ff1e3ff), .in11(32'h3ff8c7ff), .in12(32'h3ffc0fff), .in13(32'h7ff1fff), .in14(32'h23ff8fff),
    .in15(32'h31ffc7ff), .in16(32'h38ffe3ff), .in17(32'h3c7ff1ff), .in18(32'h3e3ff8ff), .in19(32'h3f1ffc7f),
    .in20(32'h3f8ffe3f), .in21(32'h3fc7ff1f), .in22(32'h3fe3ff8f), .in23(32'h3ff1ffc7), .in24(32'h3ff8ffe3),
    .in25(32'h3ffc7ff1), .in26(32'h3ffe3ff8), .in27(32'h23c7e3f1), .in28(32'h200ff1e1), .in29(32'h3ff8c7f1),
    .in30(32'h308fffc7), .in31(32'h38fe3f8f), .out(new_platform), .sel(in_1));
  DotMatrix #(.inputtype("row"), .matrixcols(32), .matrixrows(32)) dotmatrix_1 (
    .row0(32'h7fffff8), .row1(32'h23fffff1), .row2(32'h31ffffe3), .row3(32'h38ffffc7), .row4(32'h3c7fff8f),
    .row5(32'h3e3fff1f), .row6(32'h3f1ffe3f), .row7(32'h3f8ffc7f), .row8(32'h3fc7f8ff), .row9(32'h3fe3f1ff),
    .row10(32'h3ff1e3ff), .row11(32'h3ff8c7ff), .row12(32'h3ffc0fff), .row13(32'h7ff1fff),
    .row14(32'h23ff8fff), .row15(32'h31ffc7ff), .row16(32'h38ffe3ff), .row17(32'h3c7ff1ff),
    .row18(32'h3e3ff8ff), .row19(32'h3f1ffc7f), .row20(32'h3f8ffe3f), .row21(32'h3fc7ff1f),
    .row22(32'h3fe3ff8f), .row23(32'h3ff1ffc7), .row24(32'h3ff8ffe3), .row25(32'h3ffc7ff1),
    .row26(32'h3ffe3ff8), .row27(32'h23c7e3f1), .row28(32'h200ff1e1), .row29(32'h3ff8c7f1),
    .row30(32'h308fffc7), .row31(32'h38fe3f8f));
endmodule

module check_for_money (
  input  [29:0] in_1,
  input  [31:0] in_2,
  output out_3
);

  wire [31:0] and_1_out, bit_extender_1_out;

  assign bit_extender_1_out = {{2{1'b0}}, in_1};  // Bit_Extender bit_extender_1
  assign and_1_out = bit_extender_1_out & in_2;  // AND_Gate and_1, 32 bits wide
  or or_1 (out_3, and_1_out[0], and_1_out[1], and_1_out[2], and_1_out[3], and_1_out[4], and_1_out[5], and_1_out[6], and_1_out[7], and_1_out[8], and_1_out[9], and_1_out[10], and_1_out[11], and_1_out[12], and_1_out[13], and_1_out[14], and_1_out[15], and_1_out[17], and_1_out[18], and_1_out[19], and_1_out[20], and_1_out[21], and_1_out[22], and_1_out[23], and_1_out[24], and_1_out[25], and_1_out[26], and_1_out[27], and_1_out[28], and_1_out[29], and_1_out[30], and_1_out[31], and_1_out[16]);
endmodule
