// Logisim project scheme.circ as structural Verilog: 9 circuits, main circuit Screen
module main (
);

  wire cdm_8_mark5_1_p2, cdm_8_mark5_1_p8, code, data, mem, rd_wr, tact;
  wire [7:0] cdm_8_mark5_1_p5, cdm_8_mark5_1_p6, cdm_8_mark5_1_p7, controlled_buffer_2_out;

  Clock clock_1 (.out(tact));
  // CdM_8_mark5 cdm_8_mark5_1: pin names not known; wires that end beside it: tact, cdm_8_mark5_1_p2, mem, rd_wr, cdm_8_mark5_1_p5, cdm_8_mark5_1_p6, cdm_8_mark5_1_p7, cdm_8_mark5_1_p8
  assign cdm_8_mark5_1_p7 = rd_wr ? controlled_buffer_2_out : 8'bz;  // Controlled_Buffer controlled_buffer_1
  Demultiplexer demultiplexer_1 (.out0(code), .out1(data), .sel(cdm_8_mark5_1_p2), .en(mem));  // open: in
  assign controlled_buffer_2_out = cdm_8_mark5_1_p8 ? cdm_8_mark5_1_p6 : 8'bz;  // Controlled_Buffer controlled_buffer_2
  not not_1 (cdm_8_mark5_1_p8, rd_wr);
  ROM rom_1 ();  // open: addr, data, sel
  ROM rom_2 (.addr(cdm_8_mark5_1_p5), .data(controlled_buffer_2_out), .sel(code));
  RAM ram_1 (.addr(cdm_8_mark5_1_p5), .data(controlled_buffer_2_out), .sel(data), .clk(tact), .ld(rd_wr));  // open: clr

  // Notes on the sheet:
  //   instr memory
  //   data memory
endmodule

module proj (
  input  [23:0] in_1,
  input  in_2,
  input  in_3,
  input  in_4,
  output out_5
);

  wire clock_1_out, down, left, or_1_out, or_3_out, right, up;
  wire [4:0] adder_1_out, adder_2_out, counter_1_q, counter_2_q;
  wire [31:0] demultiplexer_1_out31, demultiplexer_2_out0, demultiplexer_2_out1, demultiplexer_2_out2,
       demultiplexer_2_out3, demultiplexer_2_out4, demultiplexer_2_out5, demultiplexer_2_out6,
       demultiplexer_2_out7, demultiplexer_2_out8, demultiplexer_2_out9, demultiplexer_2_out10,
       demultiplexer_2_out11, demultiplexer_2_out12, demultiplexer_2_out13, demultiplexer_2_out14,
       demultiplexer_2_out15, demultiplexer_2_out16, demultiplexer_2_out17, demultiplexer_2_out18,
       demultiplexer_2_out19, demultiplexer_2_out20, demultiplexer_2_out21, demultiplexer_2_out22,
       demultiplexer_2_out23, demultiplexer_2_out24, demultiplexer_2_out25, demultiplexer_2_out26,
       demultiplexer_2_out27, demultiplexer_2_out28, demultiplexer_2_out29, demultiplexer_2_out30,
       demultiplexer_2_out31;

  Button button_1 (.out(up));
  Button button_2 (.out(left));
  Button button_3 (.out(down));
  Clock clock_1 (.out(clock_1_out));
  Clock _1 ();  // open: out
  Button button_4 (.out(right));
  D_Flip_Flop d_ff_1 (.clk(clock_1_out), .D(in_2), .Q(out_5));  // open: Qn, preset, en, reset
  Adder #(.width(5)) adder_1 (.a(counter_1_q), .b({5{1'b1}}), .out(adder_1_out));  // open: cin, cout
  Counter #(.width(5), .max('h1f)) counter_1 (
    .load(left), .D(adder_1_out), .Q(counter_1_q), .clk(or_1_out));  // open: count, carry, clr
  or or_1 (or_1_out, right, left);
  Demultiplexer #(.select(5)) demultiplexer_1 (
    .out0(demultiplexer_1_out31[31]), .out1(demultiplexer_1_out31[30]), .out2(demultiplexer_1_out31[29]),
    .out3(demultiplexer_1_out31[28]), .out4(demultiplexer_1_out31[27]), .out5(demultiplexer_1_out31[26]),
    .out6(demultiplexer_1_out31[25]), .out7(demultiplexer_1_out31[24]), .out8(demultiplexer_1_out31[23]),
    .out9(demultiplexer_1_out31[22]), .out10(demultiplexer_1_out31[21]), .out11(demultiplexer_1_out31[20]),
    .out12(demultiplexer_1_out31[19]), .out13(demultiplexer_1_out31[18]), .out14(demultiplexer_1_out31[17]),
    .out15(demultiplexer_1_out31[16]), .out16(demultiplexer_1_out31[15]), .out17(demultiplexer_1_out31[14]),
    .out18(demultiplexer_1_out31[13]), .out19(demultiplexer_1_out31[12]), .out20(demultiplexer_1_out31[11]),
    .out21(demultiplexer_1_out31[10]), .out22(demultiplexer_1_out31[9]), .out23(demultiplexer_1_out31[8]),
    .out24(demultiplexer_1_out31[7]), .out25(demultiplexer_1_out31[6]), .out26(demultiplexer_1_out31[5]),
    .out27(demultiplexer_1_out31[4]), .out28(demultiplexer_1_out31[3]), .out29(demultiplexer_1_out31[2]),
    .out30(demultiplexer_1_out31[1]), .out31(demultiplexer_1_out31[0]), .in(1'b1), .sel(counter_1_q));  // open: en
  // OR_Gate or_2 is placed but not wired
  Demultiplexer #(.select(5), .width(32)) demultiplexer_2 (
    .out0(demultiplexer_2_out0), .out1(demultiplexer_2_out1), .out2(demultiplexer_2_out2),
    .out3(demultiplexer_2_out3), .out4(demultiplexer_2_out4), .out5(demultiplexer_2_out5),
    .out6(demultiplexer_2_out6), .out7(demultiplexer_2_out7), .out8(demultiplexer_2_out8),
    .out9(demultiplexer_2_out9), .out10(demultiplexer_2_out10), .out11(demultiplexer_2_out11),
    .out12(demultiplexer_2_out12), .out13(demultiplexer_2_out13), .out14(demultiplexer_2_out14),
    .out15(demultiplexer_2_out15), .out16(demultiplexer_2_out16), .out17(demultiplexer_2_out17),
    .out18(demultiplexer_2_out18), .out19(demultiplexer_2_out19), .out20(demultiplexer_2_out20),
    .out21(demultiplexer_2_out21), .out22(demultiplexer_2_out22), .out23(demultiplexer_2_out23),
    .out24(demultiplexer_2_out24), .out25(demultiplexer_2_out25), .out26(demultiplexer_2_out26),
    .out27(demultiplexer_2_out27), .out28(demultiplexer_2_out28), .out29(demultiplexer_2_out29),
    .out30(demultiplexer_2_out30), .out31(demultiplexer_2_out31), .in(demultiplexer_1_out31),
    .sel(counter_2_q));  // open: en
  Adder #(.width(5)) adder_2 (.a(counter_2_q), .b({5{1'b1}}), .out(adder_2_out));  // open: cin, cout
  Counter #(.width(5), .max('h1f)) counter_2 (
    .load(up), .D(adder_2_out), .Q(counter_2_q), .clk(or_3_out));  // open: count, carry, clr
  or or_3 (or_3_out, up, down);
  DotMatrix #(.inputtype("row"), .matrixcols(6), .matrixrows(4)) dotmatrix_1 (
    .row0(6'b011000), .row1(6'b111100), .row2(6'b111100), .row3(6'b011000));
  DotMatrix #(.inputtype("row"), .matrixcols(32), .matrixrows(32)) dotmatrix_2 (
    .row0(demultiplexer_2_out0), .row1(demultiplexer_2_out1), .row2(demultiplexer_2_out2),
    .row3(demultiplexer_2_out3), .row4(demultiplexer_2_out4), .row5(demultiplexer_2_out5),
    .row6(demultiplexer_2_out6), .row7(demultiplexer_2_out7), .row8(demultiplexer_2_out8),
    .row9(demultiplexer_2_out9), .row10(demultiplexer_2_out10), .row11(demultiplexer_2_out11),
    .row12(demultiplexer_2_out12), .row13(demultiplexer_2_out13), .row14(demultiplexer_2_out14),
    .row15(demultiplexer_2_out15), .row16(demultiplexer_2_out16), .row17(demultiplexer_2_out17),
    .row18(demultiplexer_2_out18), .row19(demultiplexer_2_out19), .row20(demultiplexer_2_out20),
    .row21(demultiplexer_2_out21), .row22(demultiplexer_2_out22), .row23(demultiplexer_2_out23),
    .row24(demultiplexer_2_out24), .row25(demultiplexer_2_out25), .row26(demultiplexer_2_out26),
    .row27(demultiplexer_2_out27), .row28(demultiplexer_2_out28), .row29(demultiplexer_2_out29),
    .row30(demultiplexer_2_out30), .row31(demultiplexer_2_out31));
endmodule

module Screen (
  output [6:0] out_1
);

  wire clock_1_out, game_state, left, lose, right, start, tact;
  wire [31:0] lose_screen_1_out_3, lose_screen_1_out_4, lose_screen_1_out_5, lose_screen_1_out_6,
       lose_screen_1_out_7, lose_screen_1_out_8, lose_screen_1_out_9, screen_options_1_p6,
       screen_options_1_p7, screen_options_1_p8, screen_options_1_p9, screen_options_1_p10,
       screen_options_1_p11, screen_options_1_p12, screen_options_1_p13, screen_options_1_p14,
       screen_options_1_p15, screen_options_1_p16, screen_options_1_p17, screen_options_1_p18,
       screen_options_1_p19, screen_options_1_p20, screen_options_1_p21, screen_options_1_p22,
       screen_options_1_p23, screen_options_1_p24, screen_options_1_p25, screen_options_1_p26,
       screen_options_1_p27, screen_options_1_p28, screen_options_1_p29, screen_options_1_p30,
       screen_options_1_p31, screen_options_1_p32, screen_options_1_p33, screen_options_1_p34,
       screen_options_1_p35, screen_options_1_p36, screen_options_1_p37;

  start_stop start_stop_1 (.start_stop(start), .state_of_game(game_state), .lose(lose));
  Button Start_stop_2 (.out(start));
  Keyboard keyboard_1 (.clk(clock_1_out), .data(out_1));  // open: re, clr, avail
  Clock clock_1 (.out(clock_1_out));
  Button button_1 (.out(right));
  Button button_2 (.out(left));
  DotMatrix #(.inputtype("row"), .matrixcols(32)) dotmatrix_1 (
    .row0(lose_screen_1_out_3), .row1(lose_screen_1_out_4), .row2(lose_screen_1_out_5),
    .row3(lose_screen_1_out_6), .row4(lose_screen_1_out_7), .row5(lose_screen_1_out_8),
    .row6(lose_screen_1_out_9));
  Lose_Screen lose_screen_1 (
    .Lose_indicator(lose), .out_3(lose_screen_1_out_3), .out_4(lose_screen_1_out_4),
    .out_5(lose_screen_1_out_5), .out_6(lose_screen_1_out_6), .out_7(lose_screen_1_out_7),
    .out_8(lose_screen_1_out_8), .out_9(lose_screen_1_out_9), .Start(start));
  DotMatrix #(.inputtype("row"), .matrixcols(32), .matrixrows(32)) dotmatrix_2 (
    .row0(screen_options_1_p6), .row1(screen_options_1_p7), .row2(screen_options_1_p8),
    .row3(screen_options_1_p9), .row4(screen_options_1_p10), .row5(screen_options_1_p11),
    .row6(screen_options_1_p12), .row7(screen_options_1_p13), .row8(screen_options_1_p14),
    .row9(screen_options_1_p15), .row10(screen_options_1_p16), .row11(screen_options_1_p17),
    .row12(screen_options_1_p18), .row13(screen_options_1_p19), .row14(screen_options_1_p20),
    .row15(screen_options_1_p21), .row16(screen_options_1_p22), .row17(screen_options_1_p23),
    .row18(screen_options_1_p24), .row19(screen_options_1_p25), .row20(screen_options_1_p26),
    .row21(screen_options_1_p27), .row22(screen_options_1_p28), .row23(screen_options_1_p29),
    .row24(screen_options_1_p30), .row25(screen_options_1_p31), .row26(screen_options_1_p32),
    .row27(screen_options_1_p33), .row28(screen_options_1_p34), .row29(screen_options_1_p35),
    .row30(screen_options_1_p36), .row31(screen_options_1_p37));
  // DotMatrix #(.inputtype("select"), .matrixcols(31), .matrixrows(32)) dotmatrix_3: pin names not known
  // Screen_options screen_options_1: pin names not known; wires that end beside it: tact, game_state, left, right, lose, screen_options_1_p6, screen_options_1_p7, screen_options_1_p8, screen_options_1_p9, screen_options_1_p10, screen_options_1_p11, screen_options_1_p12, screen_options_1_p13, screen_options_1_p14, screen_options_1_p15, screen_options_1_p16, screen_options_1_p17, screen_options_1_p18, screen_options_1_p19, screen_options_1_p20, screen_options_1_p21, screen_options_1_p22, screen_options_1_p23, screen_options_1_p24, screen_options_1_p25, screen_options_1_p26, screen_options_1_p27, screen_options_1_p28, screen_options_1_p29, screen_options_1_p30, screen_options_1_p31, screen_options_1_p32, screen_options_1_p33, screen_options_1_p34, screen_options_1_p35, screen_options_1_p36, screen_options_1_p37
endmodule

module start_stop (
  input  start_stop,
  input  lose,
  output state_of_game
);

  wire not_1_out;

  not not_1 (not_1_out, state_of_game);
  Register #(.width(1)) register_1 (.D(not_1_out), .Q(state_of_game), .clk(start_stop), .clr(lose));  // open: en
endmodule

module Screen_options (
  input  start,
  input  x_left,
  input  x_right,
  output [30:0] out_4,
  output [31:0] out_5,
  output [31:0] out_6,
  output [31:0] out_7,
  output [31:0] out_8,
  output [31:0] out_9,
  output Lose,
  output [31:0] out_11,
  output [31:0] out_12,
  output [31:0] out_13,
  output [31:0] out_14,
  output [31:0] out_15,
  output [31:0] out_16,
  output [31:0] out_17,
  output [31:0] out_18,
  output [31:0] out_19,
  output [31:0] out_20,
  output [31:0] out_21,
  output [31:0] out_22,
  output [31:0] out_23,
  output [31:0] out_24,
  output [31:0] out_25,
  output [31:0] out_26,
  output [31:0] out_27,
  output [31:0] out_28,
  output [31:0] out_29,
  output [31:0] out_30,
  output [31:0] out_31,
  output [31:0] out_32,
  output [31:0] out_33,
  output [31:0] out_34,
  output [31:0] out_35,
  output [31:0] out_36,
  output [31:0] out_37,
  output [31:0] out_38
);

  wire and_1_out, and_2_out, check_helper_1_out_3, check_helper_2_out_3, check_helper_3_out_3,
       check_helper_4_out_3, check_helper_5_out_3, check_helper_6_out_3, check_helper_7_out_3,
       check_helper_8_out_3, check_helper_9_out_3, check_helper_10_out_3, check_helper_11_out_3,
       check_helper_12_out_3, check_helper_13_out_3, check_helper_14_out_3, check_helper_15_out_3,
       check_helper_16_out_3, check_helper_17_out_3, check_helper_18_out_3, check_helper_19_out_3,
       check_helper_20_out_3, check_helper_21_out_3, check_helper_22_out_3, check_helper_23_out_3,
       check_helper_24_out_3, check_helper_25_out_3, check_helper_26_out_3, check_helper_27_out_3,
       check_helper_28_out_3, check_helper_29_out_3, check_helper_30_out_3, check_helper_31_out_3,
       check_helper_32_out_3, check_helper_33_out_3, check_helper_34_out_3, check_helper_35_out_3,
       check_helper_36_out_3, check_helper_37_out_3, check_helper_38_out_3, check_helper_39_out_3,
       check_helper_40_out_3, check_helper_41_out_3, check_helper_42_out_3, check_helper_43_out_3,
       check_helper_44_out_3, check_helper_45_out_3, check_helper_46_out_3, check_helper_47_out_3,
       check_helper_48_out_3, check_helper_49_out_3, check_helper_50_out_3, check_helper_51_out_3,
       check_helper_52_out_3, check_helper_53_out_3, check_helper_54_out_3, check_helper_55_out_3,
       check_helper_56_out_3, check_helper_57_out_3, check_helper_58_out_3, check_helper_59_out_3,
       check_helper_60_out_3, check_helper_61_out_3, check_helper_62_out_3, check_helper_63_out_3,
       check_helper_64_out_3, d_ff_1_q, down, multiplexer_43_out, not_1_out, not_3_out, not_5_out, not_6_out,
       not_7_out, not_8_out, not_10_out, or_1_out, or_3_out, or_5_out, or_6_out, or_7_out, or_31_0_1_out_2,
       or_32_0_1_out_2, start_alt, start_t, tact, tact_for_player, x_cond;
  wire [1:0] adder_1_out, multiplexer_1_out, register_1_q;
  wire [2:0] random_1_out;
  wire [4:0] bitfinder_1_index, bitfinder_2_index, subtractor_1_out;
  wire [30:0] multiplexer_35_out, multiplexer_37_out, multiplexer_38_out, shifter_1_out, shifter_2_out,
       x_final, x_inverted_alt;
  wire [31:0] multiplexer_2_out, multiplexer_3_out, multiplexer_4_out, multiplexer_5_out, multiplexer_6_out,
       multiplexer_7_out, multiplexer_8_out, multiplexer_9_out, multiplexer_10_out, multiplexer_11_out,
       multiplexer_12_out, multiplexer_13_out, multiplexer_14_out, multiplexer_15_out, multiplexer_16_out,
       multiplexer_17_out, multiplexer_18_out, multiplexer_19_out, multiplexer_20_out, multiplexer_21_out,
       multiplexer_22_out, multiplexer_23_out, multiplexer_24_out, multiplexer_25_out, multiplexer_26_out,
       multiplexer_27_out, multiplexer_28_out, multiplexer_29_out, multiplexer_30_out, multiplexer_31_out,
       multiplexer_32_out, multiplexer_33_out, multiplexer_34_out, multiplexer_39_out, multiplexer_40_out,
       or_4_out, shifter_3_out, shifter_4_out, y_final;

  Clock clock_1 (.out(tact_for_player));
  Random #(.width(3)) random_1 (.clk(tact), .out(random_1_out));  // open: next, clr
  D_Flip_Flop d_ff_1 (.clk(tact_for_player), .D(not_1_out), .Q(d_ff_1_q));  // open: Qn, preset, en, reset
  not not_1 (not_1_out, d_ff_1_q);
  Multiplexer #(.width(2), .enable("false")) multiplexer_1 (
    .in0(adder_1_out), .in1(2'b00), .out(multiplexer_1_out), .sel(start_t));
  not not_2 (tact, d_ff_1_q);
  Multiplexer #(.select(3), .width(32), .enable("false")) multiplexer_2 (
    .in0(32'hfe3ffff), .in1(32'h7fff8ff8), .in2(32'h78ffff1f), .in3(32'h7ffc7ff1), .in4(32'h7f1ff8ff),
    .in5(32'h7fffe3ff), .in6(32'h47fe3fff), .in7(32'h7ff8ffc7), .out(multiplexer_2_out), .sel(random_1_out));
  Register #(.width(2)) register_1 (.D(multiplexer_1_out), .Q(register_1_q), .clk(tact));  // open: en, clr
  Adder #(.width(2)) adder_1 (.a(register_1_q), .b(2'b01), .out(adder_1_out));  // open: cin, cout
  Multiplexer #(.width(32), .enable("false")) multiplexer_3 (
    .in0(out_6), .in1({32{1'b0}}), .out(multiplexer_3_out), .sel(start_t));
  Multiplexer #(.width(32), .enable("false")) multiplexer_4 (
    .in0(out_11), .in1(32'hfe3ffff), .out(multiplexer_4_out), .sel(start_t));
  Multiplexer #(.width(32), .enable("false")) multiplexer_5 (
    .in0(out_15), .in1({32{1'b0}}), .out(multiplexer_5_out), .sel(start_t));
  Multiplexer #(.width(32), .enable("false")) multiplexer_6 (
    .in0(out_19), .in1({32{1'b0}}), .out(multiplexer_6_out), .sel(start_t));
  Multiplexer #(.width(32), .enable("false")) multiplexer_7 (
    .in0(out_23), .in1({32{1'b0}}), .out(multiplexer_7_out), .sel(start_t));
  Multiplexer #(.width(32), .enable("false")) multiplexer_8 (
    .in0(out_27), .in1(32'h7fff8ff8), .out(multiplexer_8_out), .sel(start_t));
  Multiplexer #(.width(32), .enable("false")) multiplexer_9 (
    .in0(out_31), .in1({32{1'b0}}), .out(multiplexer_9_out), .sel(start_t));
  Register #(.width(32)) register_2 (.D(multiplexer_2_out), .en(start_alt), .Q(out_6), .clk(tact), .clr(or_1_out));
  or or_1 (or_1_out, not_3_out, start_t);
  not not_3 (not_3_out, adder_1_out[1]);
  Register #(.width(32)) register_3 (.D(multiplexer_3_out), .en(start_alt), .Q(out_11), .clk(tact));  // open: clr
  Register #(.width(32)) register_4 (.D(multiplexer_4_out), .en(start_alt), .Q(out_15), .clk(tact));  // open: clr
  Register #(.width(32)) register_5 (.D(multiplexer_5_out), .en(start_alt), .Q(out_19), .clk(tact));  // open: clr
  Register #(.width(32)) register_6 (.D(multiplexer_6_out), .en(start_alt), .Q(out_23), .clk(tact));  // open: clr
  Register #(.width(32)) register_7 (.D(multiplexer_7_out), .en(start_alt), .Q(out_27), .clk(tact));  // open: clr
  Register #(.width(32)) register_8 (.D(multiplexer_8_out), .en(start_alt), .Q(out_31), .clk(tact));  // open: clr
  Register #(.width(32)) register_9 (.D(multiplexer_9_out), .en(start_alt), .Q(out_35), .clk(tact));  // open: clr
  not not_4 (start_t, start);
  Register #(.width(32)) register_10 (.D(multiplexer_10_out), .en(start_alt), .Q(out_7), .clk(tact));  // open: clr
  Multiplexer #(.width(32), .enable("false")) multiplexer_10 (
    .in0(out_35), .in1({32{1'b0}}), .out(multiplexer_10_out), .sel(start_t));
  Multiplexer #(.width(32), .enable("false")) multiplexer_11 (
    .in0(out_7), .in1({32{1'b0}}), .out(multiplexer_11_out), .sel(start_t));
  Register #(.width(32)) register_11 (.D(multiplexer_11_out), .en(start_alt), .Q(out_12), .clk(tact));  // open: clr
  Multiplexer #(.width(32), .enable("false")) multiplexer_12 (
    .in0(out_12), .in1(32'h78ffff1f), .out(multiplexer_12_out), .sel(start_t));
  Register #(.width(32)) register_12 (.D(multiplexer_12_out), .en(start_alt), .Q(out_16), .clk(tact));  // open: clr
  Multiplexer #(.width(32), .enable("false")) multiplexer_13 (
    .in0(out_16), .in1({32{1'b0}}), .out(multiplexer_13_out), .sel(start_t));
  Register #(.width(32)) register_13 (.D(multiplexer_13_out), .en(start_alt), .Q(out_20), .clk(tact));  // open: clr
  Multiplexer #(.width(32), .enable("false")) multiplexer_14 (
    .in0(out_20), .in1({32{1'b0}}), .out(multiplexer_14_out), .sel(start_t));
  Register #(.width(32)) register_14 (.D(multiplexer_14_out), .en(start_alt), .Q(out_24), .clk(tact));  // open: clr
  Register #(.width(32)) register_15 (.D(multiplexer_15_out), .en(start_alt), .Q(out_28), .clk(tact));  // open: clr
  Multiplexer #(.width(32), .enable("false")) multiplexer_15 (
    .in0(out_24), .in1({32{1'b0}}), .out(multiplexer_15_out), .sel(start_t));
  Register #(.width(32)) register_16 (.D(multiplexer_16_out), .en(start_alt), .Q(out_32), .clk(tact));  // open: clr
  Multiplexer #(.width(32), .enable("false")) multiplexer_16 (
    .in0(out_28), .in1(32'h7ffc7ff1), .out(multiplexer_16_out), .sel(start_t));
  Register #(.width(32)) register_17 (.D(multiplexer_17_out), .en(start_alt), .Q(out_36), .clk(tact));  // open: clr
  Multiplexer #(.width(32), .enable("false")) multiplexer_17 (
    .in0(out_32), .in1({32{1'b0}}), .out(multiplexer_17_out), .sel(start_t));
  DotMatrix #(.inputtype("row"), .matrixcols(32), .matrixrows(16)) dotmatrix_1 (
    .row0(32'hfe3ffff), .row1(32'h7fff8ff8), .row2(32'h78ffff1f), .row3(32'h7ffc7ff1), .row4(32'h7f1ff8ff),
    .row5(32'h7fffe3ff), .row6(32'h47fe3fff), .row7(32'h7ff8ffc7));  // open: row8, row9, row10, row11, row12, row13, row14, row15
  Multiplexer #(.width(32), .enable("false")) multiplexer_18 (
    .in0(out_36), .in1({32{1'b0}}), .out(multiplexer_18_out), .sel(start_t));
  Multiplexer #(.width(32), .enable("false")) multiplexer_19 (
    .in0(out_8), .in1({32{1'b0}}), .out(multiplexer_19_out), .sel(start_t));
  Multiplexer #(.width(32), .enable("false")) multiplexer_20 (
    .in0(out_13), .in1(32'h7ff8ffc7), .out(multiplexer_20_out), .sel(start_t));
  Multiplexer #(.width(32), .enable("false")) multiplexer_21 (
    .in0(out_17), .in1({32{1'b0}}), .out(multiplexer_21_out), .sel(start_t));
  Multiplexer #(.width(32), .enable("false")) multiplexer_22 (
    .in0(out_21), .in1({32{1'b0}}), .out(multiplexer_22_out), .sel(start_t));
  Multiplexer #(.width(32), .enable("false")) multiplexer_23 (
    .in0(out_25), .in1({32{1'b0}}), .out(multiplexer_23_out), .sel(start_t));
  Multiplexer #(.width(32), .enable("false")) multiplexer_24 (
    .in0(out_29), .in1(32'h7fffe3ff), .out(multiplexer_24_out), .sel(start_t));
  Multiplexer #(.width(32), .enable("false")) multiplexer_25 (
    .in0(out_33), .in1({32{1'b0}}), .out(multiplexer_25_out), .sel(start_t));
  Register #(.width(32)) register_18 (.D(multiplexer_18_out), .en(start_alt), .Q(out_8), .clk(tact));  // open: clr
  Register #(.width(32)) register_19 (.D(multiplexer_19_out), .en(start_alt), .Q(out_13), .clk(tact));  // open: clr
  Register #(.width(32)) register_20 (.D(multiplexer_20_out), .en(start_alt), .Q(out_17), .clk(tact));  // open: clr
  Register #(.width(32)) register_21 (.D(multiplexer_21_out), .en(start_alt), .Q(out_21), .clk(tact));  // open: clr
  Register #(.width(32)) register_22 (.D(multiplexer_22_out), .en(start_alt), .Q(out_25), .clk(tact));  // open: clr
  Register #(.width(32)) register_23 (.D(multiplexer_23_out), .en(start_alt), .Q(out_29), .clk(tact));  // open: clr
  Register #(.width(32)) register_24 (.D(multiplexer_24_out), .en(start_alt), .Q(out_33), .clk(tact));  // open: clr
  Register #(.width(32)) register_25 (.D(multiplexer_25_out), .en(start_alt), .Q(out_37), .clk(tact));  // open: clr
  Multiplexer #(.width(32), .enable("false")) multiplexer_26 (
    .in0(out_37), .in1({32{1'b0}}), .out(multiplexer_26_out), .sel(start_t));
  Register #(.width(32)) register_26 (.D(multiplexer_26_out), .en(start_alt), .Q(out_9), .clk(tact));  // open: clr
  Multiplexer #(.width(32), .enable("false")) multiplexer_27 (
    .in0(out_9), .in1({32{1'b0}}), .out(multiplexer_27_out), .sel(start_t));
  Register #(.width(32)) register_27 (.D(multiplexer_27_out), .en(start_alt), .Q(out_14), .clk(tact));  // open: clr
  Register #(.width(32)) register_28 (.D(multiplexer_28_out), .en(start_alt), .Q(out_18), .clk(tact));  // open: clr
  Multiplexer #(.width(32), .enable("false")) multiplexer_28 (
    .in0(out_14), .in1(32'h47fe3fff), .out(multiplexer_28_out), .sel(start_t));
  Multiplexer #(.width(32), .enable("false")) multiplexer_29 (
    .in0(out_18), .in1({32{1'b0}}), .out(multiplexer_29_out), .sel(start_t));
  Register #(.width(32)) register_29 (.D(multiplexer_29_out), .en(start_alt), .Q(out_22), .clk(tact));  // open: clr
  Register #(.width(32)) register_30 (.D(multiplexer_30_out), .en(start_alt), .Q(out_26), .clk(tact));  // open: clr
  Multiplexer #(.width(32), .enable("false")) multiplexer_30 (
    .in0(out_22), .in1({32{1'b0}}), .out(multiplexer_30_out), .sel(start_t));
  Register #(.width(32)) register_31 (.D(multiplexer_31_out), .en(start_alt), .Q(out_30), .clk(tact));  // open: clr
  Multiplexer #(.width(32), .enable("false")) multiplexer_31 (
    .in0(out_26), .in1({32{1'b0}}), .out(multiplexer_31_out), .sel(start_t));
  Multiplexer #(.width(32), .enable("false")) multiplexer_32 (
    .in0(out_30), .in1(32'h7f1ff8ff), .out(multiplexer_32_out), .sel(start_t));
  Register #(.width(32)) register_32 (.D(multiplexer_32_out), .en(start_alt), .Q(out_34), .clk(tact));  // open: clr
  Multiplexer #(.width(32), .enable("false")) multiplexer_33 (
    .in0(out_34), .in1({32{1'b0}}), .out(multiplexer_33_out), .sel(start_t));
  Register #(.width(32)) register_33 (.D(multiplexer_33_out), .en(start_alt), .Q(out_38), .clk(tact));  // open: clr
  Multiplexer #(.width(32), .enable("false")) multiplexer_34 (
    .in0(32'h1800000), .in1(y_final), .out(multiplexer_34_out), .sel(start));
  Multiplexer #(.width(31), .enable("false")) multiplexer_35 (
    .in0(31'hc000), .in1(x_final), .out(multiplexer_35_out), .sel(start));
  Register #(.width(31)) register_34 (.D(multiplexer_35_out), .Q(out_4), .clk(tact_for_player));  // open: en, clr
  Register #(.width(32)) register_35 (.D(multiplexer_34_out), .Q(out_5), .clk(tact));  // open: en, clr
  check_helper check_helper_1 (.in_1(out_6), .in_2({1'b0, x_inverted_alt}), .out_3(check_helper_1_out_3));
  check_helper check_helper_2 (.in_1(out_11), .in_2({1'b0, x_inverted_alt}), .out_3(check_helper_2_out_3));
  check_helper check_helper_3 (.in_1(out_15), .in_2({1'b0, x_inverted_alt}), .out_3(check_helper_3_out_3));
  check_helper check_helper_4 (.in_1(out_19), .in_2({1'b0, x_inverted_alt}), .out_3(check_helper_4_out_3));
  check_helper check_helper_5 (.in_1(out_23), .in_2({1'b0, x_inverted_alt}), .out_3(check_helper_5_out_3));
  check_helper check_helper_6 (.in_1(out_27), .in_2({1'b0, x_inverted_alt}), .out_3(check_helper_6_out_3));
  check_helper check_helper_7 (.in_1(out_31), .in_2({1'b0, x_inverted_alt}), .out_3(check_helper_7_out_3));
  check_helper check_helper_8 (.in_1(out_35), .in_2({1'b0, x_inverted_alt}), .out_3(check_helper_8_out_3));
  check_helper check_helper_9 (.in_1(out_7), .in_2({1'b0, x_inverted_alt}), .out_3(check_helper_9_out_3));
  check_helper check_helper_10 (.in_1(out_12), .in_2({1'b0, x_inverted_alt}), .out_3(check_helper_10_out_3));
  check_helper check_helper_11 (.in_1(out_16), .in_2({1'b0, x_inverted_alt}), .out_3(check_helper_11_out_3));
  check_helper check_helper_12 (.in_1(out_20), .in_2({1'b0, x_inverted_alt}), .out_3(check_helper_12_out_3));
  check_helper check_helper_13 (.in_1(out_24), .in_2({1'b0, x_inverted_alt}), .out_3(check_helper_13_out_3));
  check_helper check_helper_14 (.in_1(out_28), .in_2({1'b0, x_inverted_alt}), .out_3(check_helper_14_out_3));
  check_helper check_helper_15 (.in_1(out_32), .in_2({1'b0, x_inverted_alt}), .out_3(check_helper_15_out_3));
  check_helper check_helper_16 (.in_1(out_36), .in_2({1'b0, x_inverted_alt}), .out_3(check_helper_16_out_3));
  Multiplexer #(.select(5), .enable("false")) multiplexer_36 (
    .in0(check_helper_1_out_3), .in1(check_helper_2_out_3), .in2(check_helper_3_out_3),
    .in3(check_helper_4_out_3), .in4(check_helper_5_out_3), .in5(check_helper_6_out_3),
    .in6(check_helper_7_out_3), .in7(check_helper_8_out_3), .in8(check_helper_9_out_3),
    .in9(check_helper_10_out_3), .in10(check_helper_11_out_3), .in11(check_helper_12_out_3),
    .in12(check_helper_13_out_3), .in13(check_helper_14_out_3), .in14(check_helper_15_out_3),
    .in15(check_helper_16_out_3), .in16(check_helper_17_out_3), .in17(check_helper_18_out_3),
    .in18(check_helper_19_out_3), .in19(check_helper_20_out_3), .in20(check_helper_21_out_3),
    .in21(check_helper_22_out_3), .in22(check_helper_23_out_3), .in23(check_helper_24_out_3),
    .in24(check_helper_25_out_3), .in25(check_helper_26_out_3), .in26(check_helper_27_out_3),
    .in27(check_helper_28_out_3), .in28(check_helper_29_out_3), .in29(check_helper_30_out_3),
    .in30(check_helper_31_out_3), .in31(check_helper_32_out_3), .out(x_cond), .sel(bitfinder_1_index));
  check_helper check_helper_17 (.in_1(out_8), .in_2({1'b0, x_inverted_alt}), .out_3(check_helper_17_out_3));
  check_helper check_helper_18 (.in_1(out_13), .in_2({1'b0, x_inverted_alt}), .out_3(check_helper_18_out_3));
  check_helper check_helper_19 (.in_1(out_17), .in_2({1'b0, x_inverted_alt}), .out_3(check_helper_19_out_3));
  check_helper check_helper_20 (.in_1(out_21), .in_2({1'b0, x_inverted_alt}), .out_3(check_helper_20_out_3));
  check_helper check_helper_21 (.in_1(out_25), .in_2({1'b0, x_inverted_alt}), .out_3(check_helper_21_out_3));
  check_helper check_helper_22 (.in_1(out_29), .in_2({1'b0, x_inverted_alt}), .out_3(check_helper_22_out_3));
  check_helper check_helper_23 (.in_1(out_33), .in_2({1'b0, x_inverted_alt}), .out_3(check_helper_23_out_3));
  check_helper check_helper_24 (.in_1(out_37), .in_2({1'b0, x_inverted_alt}), .out_3(check_helper_24_out_3));
  check_helper check_helper_25 (.in_1(out_9), .in_2({1'b0, x_inverted_alt}), .out_3(check_helper_25_out_3));
  check_helper check_helper_26 (.in_1(out_14), .in_2({1'b0, x_inverted_alt}), .out_3(check_helper_26_out_3));
  check_helper check_helper_27 (.in_1(out_18), .in_2({1'b0, x_inverted_alt}), .out_3(check_helper_27_out_3));
  check_helper check_helper_28 (.in_1(out_22), .in_2({1'b0, x_inverted_alt}), .out_3(check_helper_28_out_3));
  check_helper check_helper_29 (.in_1(out_26), .in_2({1'b0, x_inverted_alt}), .out_3(check_helper_29_out_3));
  check_helper check_helper_30 (.in_1(out_30), .in_2({1'b0, x_inverted_alt}), .out_3(check_helper_30_out_3));
  check_helper check_helper_31 (.in_1(out_34), .in_2({1'b0, x_inverted_alt}), .out_3(check_helper_31_out_3));
  check_helper check_helper_32 (.in_1(out_38), .in_2({1'b0, x_inverted_alt}), .out_3(check_helper_32_out_3));
  BitFinder #(.width(32), .\type ("high1")) bitfinder_1 (.in(out_5), .index(bitfinder_1_index));  // open: found
  Multiplexer #(.width(31), .enable("false")) multiplexer_37 (
    .in0({31{1'b0}}), .in1(shifter_1_out), .out(multiplexer_37_out), .sel(x_left));
  Shifter #(.width(31), .shift("lr")) shifter_1 (.in(out_4), .\dist (5'b00001), .out(shifter_1_out));
  Multiplexer #(.width(31), .enable("false")) multiplexer_38 (
    .in0({31{1'b0}}), .in1(shifter_2_out), .out(multiplexer_38_out), .sel(x_right));
  Shifter #(.width(31)) shifter_2 (.in(out_4), .\dist (5'b00001), .out(shifter_2_out));
  Shifter #(.width(32), .shift("lr")) shifter_3 (.in(out_5), .\dist (5'b00001), .out(shifter_3_out));
  Shifter #(.width(32)) shifter_4 (.in(out_5), .\dist (5'b00001), .out(shifter_4_out));
  not not_5 (not_5_out, down);
  assign {x_inverted_alt[0], x_inverted_alt[1], x_inverted_alt[2], x_inverted_alt[3], x_inverted_alt[4], x_inverted_alt[5], x_inverted_alt[6], x_inverted_alt[7], x_inverted_alt[8], x_inverted_alt[9], x_inverted_alt[10], x_inverted_alt[11], x_inverted_alt[12], x_inverted_alt[13], x_inverted_alt[14], x_inverted_alt[15], x_inverted_alt[16], x_inverted_alt[17], x_inverted_alt[18], x_inverted_alt[19], x_inverted_alt[20], x_inverted_alt[21], x_inverted_alt[22], x_inverted_alt[23], x_inverted_alt[24], x_inverted_alt[25], x_inverted_alt[26], x_inverted_alt[27], x_inverted_alt[28], x_inverted_alt[29], x_inverted_alt[30]} = multiplexer_37_out | multiplexer_38_out;  // OR_Gate or_2, 31 bits wide
  not not_6 (not_6_out, x_inverted_alt[0]);
  or or_3 (or_3_out, not_6_out, x_inverted_alt[1]);
  Multiplexer #(.width(32), .enable("false")) multiplexer_39 (
    .in0({32{1'b0}}), .in1(shifter_3_out), .out(multiplexer_39_out), .sel(down));
  assign or_4_out = multiplexer_39_out | multiplexer_40_out;  // OR_Gate or_4, 32 bits wide
  Multiplexer #(.width(32), .enable("false")) multiplexer_40 (
    .in0({32{1'b0}}), .in1(shifter_4_out), .out(multiplexer_40_out), .sel(not_5_out));
  or_31_0 or_31_0_1 (
    ._1_ch({x_inverted_alt[0], x_inverted_alt[1], x_inverted_alt[2], x_inverted_alt[3], x_inverted_alt[4], x_inverted_alt[5], x_inverted_alt[6], x_inverted_alt[7], x_inverted_alt[8], x_inverted_alt[9], x_inverted_alt[10], x_inverted_alt[11], x_inverted_alt[12], x_inverted_alt[13], x_inverted_alt[14], x_inverted_alt[15], x_inverted_alt[16], x_inverted_alt[17], x_inverted_alt[18], x_inverted_alt[19], x_inverted_alt[20], x_inverted_alt[21], x_inverted_alt[22], x_inverted_alt[23], x_inverted_alt[24], x_inverted_alt[25], x_inverted_alt[26], x_inverted_alt[27], x_inverted_alt[28], x_inverted_alt[29], x_inverted_alt[30]}),
    .out_2(or_31_0_1_out_2));
  not not_7 (not_7_out, x_inverted_alt[30]);
  or or_5 (or_5_out, not_7_out, x_inverted_alt[29]);
  not not_8 (not_8_out, or_4_out[0]);
  or or_6 (or_6_out, not_8_out, or_4_out[1]);
  Multiplexer #(.width(31), .enable("false")) multiplexer_41 (
    .in0(out_4),
    .in1({x_inverted_alt[0], x_inverted_alt[1], x_inverted_alt[2], x_inverted_alt[3], x_inverted_alt[4], x_inverted_alt[5], x_inverted_alt[6], x_inverted_alt[7], x_inverted_alt[8], x_inverted_alt[9], x_inverted_alt[10], x_inverted_alt[11], x_inverted_alt[12], x_inverted_alt[13], x_inverted_alt[14], x_inverted_alt[15], x_inverted_alt[16], x_inverted_alt[17], x_inverted_alt[18], x_inverted_alt[19], x_inverted_alt[20], x_inverted_alt[21], x_inverted_alt[22], x_inverted_alt[23], x_inverted_alt[24], x_inverted_alt[25], x_inverted_alt[26], x_inverted_alt[27], x_inverted_alt[28], x_inverted_alt[29], x_inverted_alt[30]}),
    .out(x_final), .sel(and_1_out));
  and and_1 (and_1_out, or_31_0_1_out_2, x_cond, or_5_out, or_3_out);
  Multiplexer #(.width(32), .enable("false")) multiplexer_42 (
    .in0(out_5), .in1(or_4_out), .out(y_final), .sel(and_2_out));
  and and_2 (and_2_out, or_32_0_1_out_2, or_6_out);
  or_32_0 or_32_0_1 (._1_ch(or_4_out), .out_2(or_32_0_1_out_2));
  check_helper check_helper_33 (
    .in_1(out_6),
    .in_2({1'b0, x_final[0], x_final[1], x_final[2], x_final[3], x_final[4], x_final[5], x_final[6], x_final[7], x_final[8], x_final[9], x_final[10], x_final[11], x_final[12], x_final[13], x_final[14], x_final[15], x_final[16], x_final[17], x_final[18], x_final[19], x_final[20], x_final[21], x_final[22], x_final[23], x_final[24], x_final[25], x_final[26], x_final[27], x_final[28], x_final[29], x_final[30]}),
    .out_3(check_helper_33_out_3));
  check_helper check_helper_34 (
    .in_1(out_11),
    .in_2({1'b0, x_final[0], x_final[1], x_final[2], x_final[3], x_final[4], x_final[5], x_final[6], x_final[7], x_final[8], x_final[9], x_final[10], x_final[11], x_final[12], x_final[13], x_final[14], x_final[15], x_final[16], x_final[17], x_final[18], x_final[19], x_final[20], x_final[21], x_final[22], x_final[23], x_final[24], x_final[25], x_final[26], x_final[27], x_final[28], x_final[29], x_final[30]}),
    .out_3(check_helper_34_out_3));
  check_helper check_helper_35 (
    .in_1(out_15),
    .in_2({1'b0, x_final[0], x_final[1], x_final[2], x_final[3], x_final[4], x_final[5], x_final[6], x_final[7], x_final[8], x_final[9], x_final[10], x_final[11], x_final[12], x_final[13], x_final[14], x_final[15], x_final[16], x_final[17], x_final[18], x_final[19], x_final[20], x_final[21], x_final[22], x_final[23], x_final[24], x_final[25], x_final[26], x_final[27], x_final[28], x_final[29], x_final[30]}),
    .out_3(check_helper_35_out_3));
  check_helper check_helper_36 (
    .in_1(out_19),
    .in_2({1'b0, x_final[0], x_final[1], x_final[2], x_final[3], x_final[4], x_final[5], x_final[6], x_final[7], x_final[8], x_final[9], x_final[10], x_final[11], x_final[12], x_final[13], x_final[14], x_final[15], x_final[16], x_final[17], x_final[18], x_final[19], x_final[20], x_final[21], x_final[22], x_final[23], x_final[24], x_final[25], x_final[26], x_final[27], x_final[28], x_final[29], x_final[30]}),
    .out_3(check_helper_36_out_3));
  check_helper check_helper_37 (
    .in_1(out_23),
    .in_2({1'b0, x_final[0], x_final[1], x_final[2], x_final[3], x_final[4], x_final[5], x_final[6], x_final[7], x_final[8], x_final[9], x_final[10], x_final[11], x_final[12], x_final[13], x_final[14], x_final[15], x_final[16], x_final[17], x_final[18], x_final[19], x_final[20], x_final[21], x_final[22], x_final[23], x_final[24], x_final[25], x_final[26], x_final[27], x_final[28], x_final[29], x_final[30]}),
    .out_3(check_helper_37_out_3));
  check_helper check_helper_38 (
    .in_1(out_27),
    .in_2({1'b0, x_final[0], x_final[1], x_final[2], x_final[3], x_final[4], x_final[5], x_final[6], x_final[7], x_final[8], x_final[9], x_final[10], x_final[11], x_final[12], x_final[13], x_final[14], x_final[15], x_final[16], x_final[17], x_final[18], x_final[19], x_final[20], x_final[21], x_final[22], x_final[23], x_final[24], x_final[25], x_final[26], x_final[27], x_final[28], x_final[29], x_final[30]}),
    .out_3(check_helper_38_out_3));
  check_helper check_helper_39 (
    .in_1(out_31),
    .in_2({1'b0, x_final[0], x_final[1], x_final[2], x_final[3], x_final[4], x_final[5], x_final[6], x_final[7], x_final[8], x_final[9], x_final[10], x_final[11], x_final[12], x_final[13], x_final[14], x_final[15], x_final[16], x_final[17], x_final[18], x_final[19], x_final[20], x_final[21], x_final[22], x_final[23], x_final[24], x_final[25], x_final[26], x_final[27], x_final[28], x_final[29], x_final[30]}),
    .out_3(check_helper_39_out_3));
  check_helper check_helper_40 (
    .in_1(out_35),
    .in_2({1'b0, x_final[0], x_final[1], x_final[2], x_final[3], x_final[4], x_final[5], x_final[6], x_final[7], x_final[8], x_final[9], x_final[10], x_final[11], x_final[12], x_final[13], x_final[14], x_final[15], x_final[16], x_final[17], x_final[18], x_final[19], x_final[20], x_final[21], x_final[22], x_final[23], x_final[24], x_final[25], x_final[26], x_final[27], x_final[28], x_final[29], x_final[30]}),
    .out_3(check_helper_40_out_3));
  check_helper check_helper_41 (
    .in_1(out_7),
    .in_2({1'b0, x_final[0], x_final[1], x_final[2], x_final[3], x_final[4], x_final[5], x_final[6], x_final[7], x_final[8], x_final[9], x_final[10], x_final[11], x_final[12], x_final[13], x_final[14], x_final[15], x_final[16], x_final[17], x_final[18], x_final[19], x_final[20], x_final[21], x_final[22], x_final[23], x_final[24], x_final[25], x_final[26], x_final[27], x_final[28], x_final[29], x_final[30]}),
    .out_3(check_helper_41_out_3));
  check_helper check_helper_42 (
    .in_1(out_12),
    .in_2({1'b0, x_final[0], x_final[1], x_final[2], x_final[3], x_final[4], x_final[5], x_final[6], x_final[7], x_final[8], x_final[9], x_final[10], x_final[11], x_final[12], x_final[13], x_final[14], x_final[15], x_final[16], x_final[17], x_final[18], x_final[19], x_final[20], x_final[21], x_final[22], x_final[23], x_final[24], x_final[25], x_final[26], x_final[27], x_final[28], x_final[29], x_final[30]}),
    .out_3(check_helper_42_out_3));
  check_helper check_helper_43 (
    .in_1(out_16),
    .in_2({1'b0, x_final[0], x_final[1], x_final[2], x_final[3], x_final[4], x_final[5], x_final[6], x_final[7], x_final[8], x_final[9], x_final[10], x_final[11], x_final[12], x_final[13], x_final[14], x_final[15], x_final[16], x_final[17], x_final[18], x_final[19], x_final[20], x_final[21], x_final[22], x_final[23], x_final[24], x_final[25], x_final[26], x_final[27], x_final[28], x_final[29], x_final[30]}),
    .out_3(check_helper_43_out_3));
  check_helper check_helper_44 (
    .in_1(out_20),
    .in_2({1'b0, x_final[0], x_final[1], x_final[2], x_final[3], x_final[4], x_final[5], x_final[6], x_final[7], x_final[8], x_final[9], x_final[10], x_final[11], x_final[12], x_final[13], x_final[14], x_final[15], x_final[16], x_final[17], x_final[18], x_final[19], x_final[20], x_final[21], x_final[22], x_final[23], x_final[24], x_final[25], x_final[26], x_final[27], x_final[28], x_final[29], x_final[30]}),
    .out_3(check_helper_44_out_3));
  check_helper check_helper_45 (
    .in_1(out_24),
    .in_2({1'b0, x_final[0], x_final[1], x_final[2], x_final[3], x_final[4], x_final[5], x_final[6], x_final[7], x_final[8], x_final[9], x_final[10], x_final[11], x_final[12], x_final[13], x_final[14], x_final[15], x_final[16], x_final[17], x_final[18], x_final[19], x_final[20], x_final[21], x_final[22], x_final[23], x_final[24], x_final[25], x_final[26], x_final[27], x_final[28], x_final[29], x_final[30]}),
    .out_3(check_helper_45_out_3));
  check_helper check_helper_46 (
    .in_1(out_28),
    .in_2({1'b0, x_final[0], x_final[1], x_final[2], x_final[3], x_final[4], x_final[5], x_final[6], x_final[7], x_final[8], x_final[9], x_final[10], x_final[11], x_final[12], x_final[13], x_final[14], x_final[15], x_final[16], x_final[17], x_final[18], x_final[19], x_final[20], x_final[21], x_final[22], x_final[23], x_final[24], x_final[25], x_final[26], x_final[27], x_final[28], x_final[29], x_final[30]}),
    .out_3(check_helper_46_out_3));
  check_helper check_helper_47 (
    .in_1(out_32),
    .in_2({1'b0, x_final[0], x_final[1], x_final[2], x_final[3], x_final[4], x_final[5], x_final[6], x_final[7], x_final[8], x_final[9], x_final[10], x_final[11], x_final[12], x_final[13], x_final[14], x_final[15], x_final[16], x_final[17], x_final[18], x_final[19], x_final[20], x_final[21], x_final[22], x_final[23], x_final[24], x_final[25], x_final[26], x_final[27], x_final[28], x_final[29], x_final[30]}),
    .out_3(check_helper_47_out_3));
  check_helper check_helper_48 (
    .in_1(out_36),
    .in_2({1'b0, x_final[0], x_final[1], x_final[2], x_final[3], x_final[4], x_final[5], x_final[6], x_final[7], x_final[8], x_final[9], x_final[10], x_final[11], x_final[12], x_final[13], x_final[14], x_final[15], x_final[16], x_final[17], x_final[18], x_final[19], x_final[20], x_final[21], x_final[22], x_final[23], x_final[24], x_final[25], x_final[26], x_final[27], x_final[28], x_final[29], x_final[30]}),
    .out_3(check_helper_48_out_3));
  Multiplexer #(.select(5), .enable("false")) multiplexer_43 (
    .in0(check_helper_33_out_3), .in1(check_helper_34_out_3), .in2(check_helper_35_out_3),
    .in3(check_helper_36_out_3), .in4(check_helper_37_out_3), .in5(check_helper_38_out_3),
    .in6(check_helper_39_out_3), .in7(check_helper_40_out_3), .in8(check_helper_41_out_3),
    .in9(check_helper_42_out_3), .in10(check_helper_43_out_3), .in11(check_helper_44_out_3),
    .in12(check_helper_45_out_3), .in13(check_helper_46_out_3), .in14(check_helper_47_out_3),
    .in15(check_helper_48_out_3), .in16(check_helper_49_out_3), .in17(check_helper_50_out_3),
    .in18(check_helper_51_out_3), .in19(check_helper_52_out_3), .in20(check_helper_53_out_3),
    .in21(check_helper_54_out_3), .in22(check_helper_55_out_3), .in23(check_helper_56_out_3),
    .in24(check_helper_57_out_3), .in25(check_helper_58_out_3), .in26(check_helper_59_out_3),
    .in27(check_helper_60_out_3), .in28(check_helper_61_out_3), .in29(check_helper_62_out_3),
    .in30(check_helper_63_out_3), .in31(check_helper_64_out_3), .out(multiplexer_43_out),
    .sel(subtractor_1_out));
  check_helper check_helper_49 (
    .in_1(out_8),
    .in_2({1'b0, x_final[0], x_final[1], x_final[2], x_final[3], x_final[4], x_final[5], x_final[6], x_final[7], x_final[8], x_final[9], x_final[10], x_final[11], x_final[12], x_final[13], x_final[14], x_final[15], x_final[16], x_final[17], x_final[18], x_final[19], x_final[20], x_final[21], x_final[22], x_final[23], x_final[24], x_final[25], x_final[26], x_final[27], x_final[28], x_final[29], x_final[30]}),
    .out_3(check_helper_49_out_3));
  check_helper check_helper_50 (
    .in_1(out_13),
    .in_2({1'b0, x_final[0], x_final[1], x_final[2], x_final[3], x_final[4], x_final[5], x_final[6], x_final[7], x_final[8], x_final[9], x_final[10], x_final[11], x_final[12], x_final[13], x_final[14], x_final[15], x_final[16], x_final[17], x_final[18], x_final[19], x_final[20], x_final[21], x_final[22], x_final[23], x_final[24], x_final[25], x_final[26], x_final[27], x_final[28], x_final[29], x_final[30]}),
    .out_3(check_helper_50_out_3));
  check_helper check_helper_51 (
    .in_1(out_17),
    .in_2({1'b0, x_final[0], x_final[1], x_final[2], x_final[3], x_final[4], x_final[5], x_final[6], x_final[7], x_final[8], x_final[9], x_final[10], x_final[11], x_final[12], x_final[13], x_final[14], x_final[15], x_final[16], x_final[17], x_final[18], x_final[19], x_final[20], x_final[21], x_final[22], x_final[23], x_final[24], x_final[25], x_final[26], x_final[27], x_final[28], x_final[29], x_final[30]}),
    .out_3(check_helper_51_out_3));
  check_helper check_helper_52 (
    .in_1(out_21),
    .in_2({1'b0, x_final[0], x_final[1], x_final[2], x_final[3], x_final[4], x_final[5], x_final[6], x_final[7], x_final[8], x_final[9], x_final[10], x_final[11], x_final[12], x_final[13], x_final[14], x_final[15], x_final[16], x_final[17], x_final[18], x_final[19], x_final[20], x_final[21], x_final[22], x_final[23], x_final[24], x_final[25], x_final[26], x_final[27], x_final[28], x_final[29], x_final[30]}),
    .out_3(check_helper_52_out_3));
  check_helper check_helper_53 (
    .in_1(out_25),
    .in_2({1'b0, x_final[0], x_final[1], x_final[2], x_final[3], x_final[4], x_final[5], x_final[6], x_final[7], x_final[8], x_final[9], x_final[10], x_final[11], x_final[12], x_final[13], x_final[14], x_final[15], x_final[16], x_final[17], x_final[18], x_final[19], x_final[20], x_final[21], x_final[22], x_final[23], x_final[24], x_final[25], x_final[26], x_final[27], x_final[28], x_final[29], x_final[30]}),
    .out_3(check_helper_53_out_3));
  check_helper check_helper_54 (
    .in_1(out_29),
    .in_2({1'b0, x_final[0], x_final[1], x_final[2], x_final[3], x_final[4], x_final[5], x_final[6], x_final[7], x_final[8], x_final[9], x_final[10], x_final[11], x_final[12], x_final[13], x_final[14], x_final[15], x_final[16], x_final[17], x_final[18], x_final[19], x_final[20], x_final[21], x_final[22], x_final[23], x_final[24], x_final[25], x_final[26], x_final[27], x_final[28], x_final[29], x_final[30]}),
    .out_3(check_helper_54_out_3));
  check_helper check_helper_55 (
    .in_1(out_33),
    .in_2({1'b0, x_final[0], x_final[1], x_final[2], x_final[3], x_final[4], x_final[5], x_final[6], x_final[7], x_final[8], x_final[9], x_final[10], x_final[11], x_final[12], x_final[13], x_final[14], x_final[15], x_final[16], x_final[17], x_final[18], x_final[19], x_final[20], x_final[21], x_final[22], x_final[23], x_final[24], x_final[25], x_final[26], x_final[27], x_final[28], x_final[29], x_final[30]}),
    .out_3(check_helper_55_out_3));
  check_helper check_helper_56 (
    .in_1(out_37),
    .in_2({1'b0, x_final[0], x_final[1], x_final[2], x_final[3], x_final[4], x_final[5], x_final[6], x_final[7], x_final[8], x_final[9], x_final[10], x_final[11], x_final[12], x_final[13], x_final[14], x_final[15], x_final[16], x_final[17], x_final[18], x_final[19], x_final[20], x_final[21], x_final[22], x_final[23], x_final[24], x_final[25], x_final[26], x_final[27], x_final[28], x_final[29], x_final[30]}),
    .out_3(check_helper_56_out_3));
  check_helper check_helper_57 (
    .in_1(out_9),
    .in_2({1'b0, x_final[0], x_final[1], x_final[2], x_final[3], x_final[4], x_final[5], x_final[6], x_final[7], x_final[8], x_final[9], x_final[10], x_final[11], x_final[12], x_final[13], x_final[14], x_final[15], x_final[16], x_final[17], x_final[18], x_final[19], x_final[20], x_final[21], x_final[22], x_final[23], x_final[24], x_final[25], x_final[26], x_final[27], x_final[28], x_final[29], x_final[30]}),
    .out_3(check_helper_57_out_3));
  check_helper check_helper_58 (
    .in_1(out_14),
    .in_2({1'b0, x_final[0], x_final[1], x_final[2], x_final[3], x_final[4], x_final[5], x_final[6], x_final[7], x_final[8], x_final[9], x_final[10], x_final[11], x_final[12], x_final[13], x_final[14], x_final[15], x_final[16], x_final[17], x_final[18], x_final[19], x_final[20], x_final[21], x_final[22], x_final[23], x_final[24], x_final[25], x_final[26], x_final[27], x_final[28], x_final[29], x_final[30]}),
    .out_3(check_helper_58_out_3));
  check_helper check_helper_59 (
    .in_1(out_18),
    .in_2({1'b0, x_final[0], x_final[1], x_final[2], x_final[3], x_final[4], x_final[5], x_final[6], x_final[7], x_final[8], x_final[9], x_final[10], x_final[11], x_final[12], x_final[13], x_final[14], x_final[15], x_final[16], x_final[17], x_final[18], x_final[19], x_final[20], x_final[21], x_final[22], x_final[23], x_final[24], x_final[25], x_final[26], x_final[27], x_final[28], x_final[29], x_final[30]}),
    .out_3(check_helper_59_out_3));
  check_helper check_helper_60 (
    .in_1(out_22),
    .in_2({1'b0, x_final[0], x_final[1], x_final[2], x_final[3], x_final[4], x_final[5], x_final[6], x_final[7], x_final[8], x_final[9], x_final[10], x_final[11], x_final[12], x_final[13], x_final[14], x_final[15], x_final[16], x_final[17], x_final[18], x_final[19], x_final[20], x_final[21], x_final[22], x_final[23], x_final[24], x_final[25], x_final[26], x_final[27], x_final[28], x_final[29], x_final[30]}),
    .out_3(check_helper_60_out_3));
  check_helper check_helper_61 (
    .in_1(out_26),
    .in_2({1'b0, x_final[0], x_final[1], x_final[2], x_final[3], x_final[4], x_final[5], x_final[6], x_final[7], x_final[8], x_final[9], x_final[10], x_final[11], x_final[12], x_final[13], x_final[14], x_final[15], x_final[16], x_final[17], x_final[18], x_final[19], x_final[20], x_final[21], x_final[22], x_final[23], x_final[24], x_final[25], x_final[26], x_final[27], x_final[28], x_final[29], x_final[30]}),
    .out_3(check_helper_61_out_3));
  check_helper check_helper_62 (
    .in_1(out_30),
    .in_2({1'b0, x_final[0], x_final[1], x_final[2], x_final[3], x_final[4], x_final[5], x_final[6], x_final[7], x_final[8], x_final[9], x_final[10], x_final[11], x_final[12], x_final[13], x_final[14], x_final[15], x_final[16], x_final[17], x_final[18], x_final[19], x_final[20], x_final[21], x_final[22], x_final[23], x_final[24], x_final[25], x_final[26], x_final[27], x_final[28], x_final[29], x_final[30]}),
    .out_3(check_helper_62_out_3));
  check_helper check_helper_63 (
    .in_1(out_34),
    .in_2({1'b0, x_final[0], x_final[1], x_final[2], x_final[3], x_final[4], x_final[5], x_final[6], x_final[7], x_final[8], x_final[9], x_final[10], x_final[11], x_final[12], x_final[13], x_final[14], x_final[15], x_final[16], x_final[17], x_final[18], x_final[19], x_final[20], x_final[21], x_final[22], x_final[23], x_final[24], x_final[25], x_final[26], x_final[27], x_final[28], x_final[29], x_final[30]}),
    .out_3(check_helper_63_out_3));
  check_helper check_helper_64 (
    .in_1(out_38),
    .in_2({1'b0, x_final[0], x_final[1], x_final[2], x_final[3], x_final[4], x_final[5], x_final[6], x_final[7], x_final[8], x_final[9], x_final[10], x_final[11], x_final[12], x_final[13], x_final[14], x_final[15], x_final[16], x_final[17], x_final[18], x_final[19], x_final[20], x_final[21], x_final[22], x_final[23], x_final[24], x_final[25], x_final[26], x_final[27], x_final[28], x_final[29], x_final[30]}),
    .out_3(check_helper_64_out_3));
  BitFinder #(.width(32)) bitfinder_2 (.in(out_5), .index(bitfinder_2_index));  // open: found
  Subtractor #(.width(5)) subtractor_1 (
    .a(bitfinder_2_index), .b(5'b00001), .out(subtractor_1_out));  // open: bin, bout
  Multiplexer #(.enable("false")) multiplexer_44 (.in0(1'b0), .in1(multiplexer_43_out), .out(down), .sel(start));
  DotMatrix #(.inputtype("row"), .matrixcols(32), .matrixrows(32)) dotmatrix_2 (
    .row0(out_38), .row1(out_34), .row2(out_30), .row3(out_26), .row4(out_22), .row5(out_18), .row6(out_14),
    .row7(out_9), .row8(out_37), .row9(out_33), .row10(out_29), .row11(out_25), .row12(out_21),
    .row13(out_17), .row14(out_13), .row15(out_8), .row16(out_36), .row17(out_32), .row18(out_28),
    .row19(out_24), .row20(out_20), .row21(out_16), .row22(out_12), .row23(out_7), .row24(out_35),
    .row25(out_31), .row26(out_27), .row27(out_23), .row28(out_19), .row29(out_15), .row30(out_11),
    .row31(out_6));
  // DotMatrix #(.inputtype("select"), .matrixcols(31), .matrixrows(32)) dotmatrix_3: pin names not known; wires that end beside it: out_4, out_5
  not not_9 (Lose, or_7_out);
  or or_7 (or_7_out, not_10_out, out_5[30]);
  not not_10 (not_10_out, out_5[31]);

  // Other names for the same wires on the sheet: _1[31:0] = out_6; _2[31:0] = out_11; _3[31:0] = out_15;
  //   _4[31:0] = out_19; _5[31:0] = out_23; _6[31:0] = out_27; _7[31:0] = out_31; _8[31:0] = out_35; _9[31:0] = out_7;
  //   _10[31:0] = out_12; _11[31:0] = out_16; _12[31:0] = out_20; _13[31:0] = out_24; _14[31:0] = out_28;
  //   _15[31:0] = out_32; _16[31:0] = out_36; _17[31:0] = out_8; _18[31:0] = out_13; _19[31:0] = out_17;
  //   _20[31:0] = out_21; _21[31:0] = out_25; _22[31:0] = out_29; _23[31:0] = out_33; _24[31:0] = out_37;
  //   _25[31:0] = out_9; _26[31:0] = out_14; _27[31:0] = out_18; _28[31:0] = out_22; _29[31:0] = out_26;
  //   _30[31:0] = out_30; _31[31:0] = out_34; _32[31:0] = out_38; left = x_left; reg_x[30:0] = out_4;
  //   reg_y[31:0] = out_5; right = x_right; start_alt_1 = start;
  //   x_inverted[30:0] = {x_final[0], x_final[1], x_final[2], x_final[3], x_final[4], x_final[5], x_final[6], x_final[7], x_final[8], x_final[9], x_final[10], x_final[11], x_final[12], x_final[13], x_final[14], x_final[15], x_final[16], x_final[17], x_final[18], x_final[19], x_final[20], x_final[21], x_final[22], x_final[23], x_final[24], x_final[25], x_final[26], x_final[27], x_final[28], x_final[29], x_final[30]};
  //   x_medium[30:0] = {x_inverted_alt[0], x_inverted_alt[1], x_inverted_alt[2], x_inverted_alt[3], x_inverted_alt[4], x_inverted_alt[5], x_inverted_alt[6], x_inverted_alt[7], x_inverted_alt[8], x_inverted_alt[9], x_inverted_alt[10], x_inverted_alt[11], x_inverted_alt[12], x_inverted_alt[13], x_inverted_alt[14], x_inverted_alt[15], x_inverted_alt[16], x_inverted_alt[17], x_inverted_alt[18], x_inverted_alt[19], x_inverted_alt[20], x_inverted_alt[21], x_inverted_alt[22], x_inverted_alt[23], x_inverted_alt[24], x_inverted_alt[25], x_inverted_alt[26], x_inverted_alt[27], x_inverted_alt[28], x_inverted_alt[29], x_inverted_alt[30]}

  // Notes on the sheet:
  //   Field options
  //   Bottom line
  //   Top line
  //   Сollision avoidance
  //   Player Position
  //   Checking for a hole
  //   Losing indicator
endmodule

module or_31_0 (
  input  [30:0] _1_ch,
  output out_2
);

  or or_1 (out_2, _1_ch[0], _1_ch[1], _1_ch[2], _1_ch[3], _1_ch[4], _1_ch[5], _1_ch[6], _1_ch[7], _1_ch[8], _1_ch[9], _1_ch[10], _1_ch[11], _1_ch[12], _1_ch[13], _1_ch[14], _1_ch[15], _1_ch[16], _1_ch[17], _1_ch[18], _1_ch[19], _1_ch[20], _1_ch[21], _1_ch[22], _1_ch[23], _1_ch[24], _1_ch[25], _1_ch[26], _1_ch[27], _1_ch[28], _1_ch[29], _1_ch[30]);
endmodule

module or_32_0 (
  input  [31:0] _1_ch,
  output out_2
);

  or or_1 (out_2, _1_ch[0], _1_ch[1], _1_ch[2], _1_ch[3], _1_ch[4], _1_ch[5], _1_ch[6], _1_ch[7], _1_ch[8], _1_ch[9], _1_ch[10], _1_ch[11], _1_ch[12], _1_ch[13], _1_ch[14], _1_ch[15], _1_ch[17], _1_ch[18], _1_ch[19], _1_ch[20], _1_ch[21], _1_ch[22], _1_ch[23], _1_ch[24], _1_ch[25], _1_ch[26], _1_ch[27], _1_ch[28], _1_ch[29], _1_ch[30], _1_ch[31], _1_ch[16]);
endmodule

module check_helper (
  input  [31:0] in_1,
  input  [31:0] in_2,
  output out_3
);

  wire or_1_out;
  wire [31:0] and_1_out;

  assign and_1_out = in_1 & in_2;  // AND_Gate and_1, 32 bits wide
  or or_1 (or_1_out, and_1_out[0], and_1_out[1], and_1_out[2], and_1_out[3], and_1_out[4], and_1_out[5], and_1_out[6], and_1_out[7], and_1_out[8], and_1_out[9], and_1_out[10], and_1_out[11], and_1_out[12], and_1_out[13], and_1_out[14], and_1_out[15], and_1_out[17], and_1_out[18], and_1_out[19], and_1_out[20], and_1_out[21], and_1_out[22], and_1_out[23], and_1_out[24], and_1_out[25], and_1_out[26], and_1_out[27], and_1_out[28], and_1_out[29], and_1_out[30], and_1_out[31], and_1_out[16]);
  not not_1 (out_3, or_1_out);
endmodule

module Lose_Screen (
  input  Lose_indicator,
  input  Start,
  output [31:0] out_3,
  output [31:0] out_4,
  output [31:0] out_5,
  output [31:0] out_6,
  output [31:0] out_7,
  output [31:0] out_8,
  output [31:0] out_9
);

  wire [31:31] lose;

  D_Flip_Flop d_ff_1 (.clk(Lose_indicator), .D(Lose_indicator), .Q(lose[31]), .reset(Start));  // open: Qn, preset, en
  assign out_3 = 32'he7bde23e & {32{lose[31]}};  // AND_Gate and_1, 32 bits wide
  assign out_4 = 32'h94210508 & {32{lose[31]}};  // AND_Gate and_2, 32 bits wide
  assign out_5 = 32'h94210888 & {32{lose[31]}};  // AND_Gate and_3, 32 bits wide
  assign out_6 = 32'h97bdef88 & {32{lose[31]}};  // AND_Gate and_4, 32 bits wide
  assign out_7 = 32'h94210888 & {32{lose[31]}};  // AND_Gate and_5, 32 bits wide
  assign out_8 = 32'h94210888 & {32{lose[31]}};  // AND_Gate and_6, 32 bits wide
  assign out_9 = 32'he7a1e888 & {32{lose[31]}};  // AND_Gate and_7, 32 bits wide

  // Other names for the same wires on the sheet: lose[30:0] = {31{lose[31]}}
endmodule
